// Logisim project cpu各阶段汇总.circ as structural Verilog: 38 circuits, main circuit ◇24+4条扩展指令电路
module \单周期MIPS  (
  input  IR1,
  input  IR2,
  input  IR3,
  output RegWrite,
  output MemWrite,
  output [31:0] PC,
  output [31:0] IR,
  output [31:0] RDin,
  output [31:0] MDin,
  output [31:0] LedData
);

  wire and_1_out, and_2_out, and_3_out, and_4_out, CLK, comparator_1_eq, Go, IR1_t, IR2_t, IR3_t, IRA, IRB,
       IRC, mips_alu_1_equal, not_1_out, not_3_out, or_1_out, or_2_out, or_6_out, PCok, register_2_q, RST,
       SignedExt, Syscall, W1, W2, W3, \单周期硬布线控制器_1_alu_src , \单周期硬布线控制器_1_beq , \单周期硬布线控制器_1_bne ,
       \单周期硬布线控制器_1_jal , \单周期硬布线控制器_1_jmp , \单周期硬布线控制器_1_jr , \单周期硬布线控制器_1_memtoreg , \单周期硬布线控制器_1_regdst ;
  wire [3:0] \单周期硬布线控制器_1_alu_op ;
  wire [4:0] multiplexer_4_out, multiplexer_5_out, multiplexer_6_out, multiplexer_7_out;
  wire [15:0] \总周期数 ;
  wire [31:0] adder_1_out, adder_2_out, bit_extender_1_out, bit_extender_2_out, bit_extender_3_out,
       mips_alu_1_result, multiplexer_3_out, multiplexer_8_out, multiplexer_9_out, multiplexer_11_out, PC1,
       PC2, R1, ram_1_data, shifter_1_out, shifter_2_out;

  Clock #(.highDuration(1), .lowDuration(1)) clock_1 (.out(CLK));
  Button _1 (.out(IRA));
  Button _2 (.out(IRB));
  Button _3 (.out(IRC));
  Button \u_总复位  (.out(RST));
  Button \u_继续运行  (.out(Go));
  LED #(.active("true")) led_1 (.in(W1));
  LED #(.active("true")) led_2 (.in(W2));
  LED #(.active("true")) led_3 (.in(W3));
  Multiplexer #(.select(1), .width(32), .disabled("Z"), .enable("false")) multiplexer_1 (
    .in0(adder_1_out), .in1(adder_2_out), .out(PC1), .sel(or_6_out));
  Multiplexer #(.select(1), .width(32), .disabled("Z"), .enable("false")) multiplexer_2 (
    .in0(PC1), .in1(shifter_2_out), .out(PC2), .sel(or_1_out));
  Multiplexer #(.select(1), .width(32), .disabled("Z"), .enable("false")) multiplexer_3 (
    .in0(PC2), .in1(R1), .out(multiplexer_3_out), .sel(\单周期硬布线控制器_1_jr ));
  Comparator #(.width(32), .mode("twosComplement")) comparator_1 (
    .a(MDin), .b(32'h22), .eq(comparator_1_eq));  // open: gt, lt
  not not_1 (not_1_out, comparator_1_eq);
  Hex_Digit_Display hex_digit_display_1 (.value(LedData[27:24]));  // open: dp
  Hex_Digit_Display hex_digit_display_2 (.value(LedData[31:28]));  // open: dp
  or or_1 (or_1_out, \单周期硬布线控制器_1_jal , \单周期硬布线控制器_1_jmp );
  Register #(.width(32), .trigger("rising"), .Select("low")) u_PC (
    .D(multiplexer_3_out), .en(PCok), .Q(PC), .clk(CLK), .clr(RST));
  and and_1 (and_1_out, comparator_1_eq, Syscall);
  and and_2 (and_2_out, not_1_out, Syscall);
  Hex_Digit_Display hex_digit_display_3 (.value(LedData[23:20]));  // open: dp
  Hex_Digit_Display hex_digit_display_4 (.value(LedData[19:16]));  // open: dp
  Adder #(.width(32)) adder_1 (.a(PC), .b(32'h4), .out(adder_1_out));  // open: cin, cout
  Register #(.width(32), .trigger("rising"), .Select("low")) register_1 (
    .D(R1), .en(and_1_out), .Q(LedData), .clk(CLK), .clr(RST));
  not not_2 (PCok, register_2_q);
  Register #(.width(1), .trigger("rising"), .Select("low")) register_2 (
    .D(Syscall), .en(and_2_out), .Q(register_2_q), .clk(CLK), .clr(or_2_out));
  or or_2 (or_2_out, Go, RST);
  Hex_Digit_Display hex_digit_display_5 (.value(LedData[15:12]));  // open: dp
  Hex_Digit_Display hex_digit_display_6 (.value(LedData[11:8]));  // open: dp
  Counter #(.width(16), .max('hffff), .ongoal("wrap"), .trigger("rising"), .behavior("old")) counter_1 (
    .count(PCok), .Q(\总周期数 ), .clk(CLK), .clr(RST));  // open: load, D, carry, preset
  ROM #(.addrWidth(10), .dataWidth(32), .Select("high")) rom_1 (.addr(PC[11:2]), .data(IR));
  Hex_Digit_Display hex_digit_display_7 (.value(LedData[7:4]));  // open: dp
  Hex_Digit_Display hex_digit_display_8 (.value(LedData[3:0]));  // open: dp
  // Probe on \总周期数 
  Multiplexer #(.select(1), .width(5), .disabled("Z"), .enable("false")) multiplexer_4 (
    .in0(IR[25:21]), .in1(5'b00100), .out(multiplexer_4_out), .sel(Syscall));
  Multiplexer #(.select(1), .width(5), .disabled("Z"), .enable("false")) multiplexer_5 (
    .in0(IR[20:16]), .in1(5'b00010), .out(multiplexer_5_out), .sel(Syscall));
  Multiplexer #(.select(1), .width(5), .disabled("Z"), .enable("false")) multiplexer_6 (
    .in0(IR[20:16]), .in1(IR[15:11]), .out(multiplexer_6_out), .sel(\单周期硬布线控制器_1_regdst ));
  Multiplexer #(.select(1), .width(5), .disabled("Z"), .enable("false")) multiplexer_7 (
    .in0(multiplexer_6_out), .in1({5{1'b1}}), .out(multiplexer_7_out), .sel(\单周期硬布线控制器_1_jal ));
  assign bit_extender_1_out = {{16{1'b0}}, IR[15:0]};  // Bit_Extender bit_extender_1
  assign bit_extender_2_out = {{16{IR[15]}}, IR[15:0]};  // Bit_Extender bit_extender_2
  assign bit_extender_3_out = {{6{IR[25]}}, IR[25:0]};  // Bit_Extender bit_extender_3
  or or_3 (IR1_t, IR1, IRA);
  \单周期硬布线控制器  \u_单周期硬布线控制器_1  (
    .OP(IR[31:26]), .Func(IR[5:0]), .ALU_OP(\单周期硬布线控制器_1_alu_op ), .MemToReg(\单周期硬布线控制器_1_memtoreg ),
    .MemWrite(MemWrite), .ALU_SRC(\单周期硬布线控制器_1_alu_src ), .RegWrite(RegWrite), .SysCALL(Syscall),
    .SignedExt(SignedExt), .RegDst(\单周期硬布线控制器_1_regdst ), .Beq(\单周期硬布线控制器_1_beq ), .Bne(\单周期硬布线控制器_1_bne ),
    .JR(\单周期硬布线控制器_1_jr ), .JMP(\单周期硬布线控制器_1_jmp ), .JAL(\单周期硬布线控制器_1_jal ));
  Multiplexer #(.select(1), .width(32), .disabled("Z"), .enable("false")) multiplexer_8 (
    .in0(bit_extender_1_out), .in1(bit_extender_2_out), .out(multiplexer_8_out), .sel(SignedExt));
  MIPS_Regifile mips_regifile_1 (
    .Din(RDin), .Clk(CLK), .R1(R1), .R2(MDin), .WE(RegWrite), .W_num(multiplexer_7_out),
    .R1_num(multiplexer_4_out), .R2_num(multiplexer_5_out));
  or or_4 (IR2_t, IR2, IRB);
  Multiplexer #(.select(1), .width(32), .disabled("Z"), .enable("false")) multiplexer_9 (
    .in0(MDin), .in1(multiplexer_8_out), .out(multiplexer_9_out), .sel(\单周期硬布线控制器_1_alu_src ));
  Multiplexer #(.select(1), .width(32), .disabled("Z"), .enable("false")) multiplexer_10 (
    .in0(multiplexer_11_out), .in1(adder_1_out), .out(RDin), .sel(\单周期硬布线控制器_1_jal ));
  Shifter #(.width(32), .shift("ll")) shifter_1 (.in(multiplexer_8_out), .\dist (5'b00010), .out(shifter_1_out));
  Shifter #(.width(32), .shift("ll")) shifter_2 (.in(bit_extender_3_out), .\dist (5'b00010), .out(shifter_2_out));
  or or_5 (IR3_t, IR3, IRC);
  not not_3 (not_3_out, mips_alu_1_equal);
  MIPS_ALU mips_alu_1 (
    .X(R1), .Y(multiplexer_9_out), .AluOP(\单周期硬布线控制器_1_alu_op ), .Equal(mips_alu_1_equal),
    .Result(mips_alu_1_result), .shamt(IR[10:6]));  // open: Result_2
  and and_3 (and_3_out, mips_alu_1_equal, \单周期硬布线控制器_1_beq );
  and and_4 (and_4_out, not_3_out, \单周期硬布线控制器_1_bne );
  Adder #(.width(32)) adder_2 (.a(shifter_1_out), .b(adder_1_out), .out(adder_2_out));  // open: cin, cout
  or or_6 (or_6_out, and_3_out, and_4_out);
  RAM #(.addrWidth(10), .dataWidth(32), .bus("separate"), .Select("high")) ram_1 (
    .addr(mips_alu_1_result[11:2]), .din(MDin), .data(ram_1_data), .str(MemWrite), .clk(CLK), .clr(RST));  // open: sel, ld
  Multiplexer #(.select(1), .width(32), .disabled("Z"), .enable("false")) multiplexer_11 (
    .in0(mips_alu_1_result), .in1(ram_1_data), .out(multiplexer_11_out), .sel(\单周期硬布线控制器_1_memtoreg ));

  // Other names for the same wires on the sheet: R2[31:0] = MDin

  // Notes on the sheet:
  //   中断源
  //   总复位信号应将除ROM以外所有存储组件全部清零
  //   中断等待指示
  //   数码管输出
  //   指令存储器
  //   指令字
  //   contents of rom_1 (hex, n*v repeats v):
  //   20110001 8000c05 20110001 20120002 20130003 8000c09 20110001 20120002 20130003 8000c0d 20110001
  //   20120002 20130003 8000c11 20110001 20120002 20130003 c000cb8 20100001 20110001 118fc0 112020
  //   20020022 c 118882 12200001 8000c15 112020 20020022 c 20110001 118880 112020 20020022 c 12200001
  //   8000c1f 20110001 118fc0 112020 20020022 c 1188c3 112020 20020022 c 118903 112020 20020022 c 118903
  //   112020 20020022 c 118903 112020 20020022 c 118903 112020 20020022 c 118903 112020 20020022 c 118903
  //   112020 20020022 c 118903 112020 20020022 c 20100001 109fc0 139fc3 8021 2012000c 24160003 26100001
  //   3210000f 20080008 20090001 139900 2709825 132020 20020022 c 1094022 1500fff9 22100001 2018000f
  //   2188024 108700 20080008 20090001 139902 2709825 132021 20020022 c 1094022 1500fff9 108702 2c9b022
  //   12c00001 8000c50 4020 1084027 84400 3508ffff 82021 20020022 c 2010ffff 20110000 ae300000 22100001
  //   22310004 ae300000 22100001 22310004 ae300000 22100001 22310004 ae300000 22100001 22310004 ae300000
  //   22100001 22310004 ae300000 22100001 22310004 ae300000 22100001 22310004 ae300000 22100001 22310004
  //   ae300000 22100001 22310004 ae300000 22100001 22310004 ae300000 22100001 22310004 ae300000 22100001
  //   22310004 ae300000 22100001 22310004 ae300000 22100001 22310004 ae300000 22100001 22310004 ae300000
  //   22100001 22310004 22100001 8020 2011003c 8e130000 8e340000 274402a 11000002 ae330000 ae140000
  //   2231fffc 1611fff8 102020 20020022 c 22100004 2011003c 1611fff2 20020032 c 20100000 22100001 102020
  //   20020022 c 22100002 102020 20020022 c 22100003 102020 20020022 c 22100004 102020 20020022 c 22100005
  //   102020 20020022 c 22100006 102020 20020022 c 22100007 102020 20020022 c 22100008 102020 20020022
  //   20020022 c 3e00008
  //   数码管输出应该用寄存器锁存，否则显示数据只能一闪而过
  //   OP
  //   Func
  //   rs
  //   rt
  //   rd
  //   JMP
  //   JR
  //   OP
  //   Func
  //   Beq
  //   Bne
  //   MemToReg
  //   MemWrite
  //   AluOP
  //   AluSrcB
  //   RegWrite
  //   JAL
  //   RegDst
  //   Syscall
  //   数据存储器
  //   为方便自动评测，需要输出PC，IR，寄存器堆写如数据RDin
  //   RAM写使能MemWrite、RAM写入数据MDin等信号
endmodule

// 单周期硬布线控制器
module \单周期硬布线控制器  (
  input  [5:0] OP,
  input  [5:0] Func,
  output [3:0] ALU_OP,
  output MemToReg,
  output MemWrite,
  output ALU_SRC,
  output RegWrite,
  output SysCALL,
  output SignedExt,
  output RegDst,
  output Beq,
  output Bne,
  output JR,
  output JMP,
  output JAL
);

  \运算控制器自动生成  \u_运算控制器自动生成_1  (
    .OP0(OP[0]), .OP1(OP[1]), .OP2(OP[2]), .OP3(OP[3]), .OP4(OP[4]), .OP5(OP[5]), .F0(Func[0]), .F1(Func[1]),
    .F2(Func[2]), .F3(Func[3]), .F4(Func[4]), .F5(Func[5]), .S0(ALU_OP[0]), .S1(ALU_OP[1]), .S2(ALU_OP[2]),
    .S3(ALU_OP[3]));
  \控制信号自动生成  \u_控制信号自动生成_1  (
    .OP0(OP[0]), .OP1(OP[1]), .OP2(OP[2]), .OP3(OP[3]), .OP4(OP[4]), .OP5(OP[5]), .F0(Func[0]), .F1(Func[1]),
    .F2(Func[2]), .F3(Func[3]), .F4(Func[4]), .F5(Func[5]), .MemToReg(MemToReg), .MemWrite(MemWrite),
    .ALU_SRC(ALU_SRC), .RegWrite(RegWrite), .SysCALL(SysCALL), .SignedExt(SignedExt), .RegDst(RegDst),
    .BEQ(Beq), .BNE(Bne), .JR(JR), .JUMP(JMP), .JAL(JAL));

  // Other names for the same wires on the sheet: OP_CODE[5:0] = OP

  // Notes on the sheet:
  //   运算器控制器，根据指令生成运算器功能选择信号
  //   控制信号生成，产生数据通路需要的其他控制信号
endmodule

// 运算控制器自动生成
module \运算控制器自动生成  (
  input  OP0,
  input  OP1,
  input  OP2,
  input  OP3,
  input  OP4,
  input  OP5,
  input  F0,
  input  F1,
  input  F2,
  input  F3,
  input  F4,
  input  F5,
  output S0,
  output S1,
  output S2,
  output S3
);

  wire and_1_out, and_2_out, and_3_out, and_4_out, and_5_out, and_6_out, and_7_out, and_8_out, and_9_out,
       and_10_out, and_11_out, and_12_out, and_13_out, and_14_out, and_15_out, and_16_out, and_17_out,
       and_18_out, and_19_out, and_20_out, and_21_out, and_22_out, and_23_out, and_24_out, and_25_out,
       and_26_out, and_27_out, and_28_out, and_29_out, and_30_out, and_31_out, and_32_out, and_33_out,
       and_34_out, not_1_out, not_2_out, not_3_out, not_4_out, not_5_out, not_6_out, not_7_out, not_8_out,
       not_9_out, not_10_out, not_11_out, not_12_out, not_13_out, not_14_out, not_15_out, not_16_out,
       not_17_out, not_18_out, not_19_out, not_20_out, not_21_out, not_22_out, not_23_out, not_24_out,
       not_25_out, not_26_out, not_27_out, not_28_out, not_29_out, not_30_out, not_31_out, not_32_out,
       not_33_out, not_34_out, not_35_out, not_36_out, not_37_out, not_38_out, not_39_out, not_40_out,
       not_41_out, not_42_out, not_43_out, not_44_out, not_45_out, not_46_out, not_47_out, not_48_out,
       not_49_out, not_50_out, not_51_out, not_52_out, not_53_out, not_54_out, not_55_out, not_56_out,
       not_57_out, not_58_out, not_59_out, not_60_out, not_61_out, not_62_out, not_63_out, not_64_out,
       not_65_out, not_66_out, not_67_out, not_68_out, not_69_out, not_70_out, not_71_out, not_72_out,
       not_73_out, not_74_out, not_75_out, not_76_out, not_77_out, not_78_out, not_79_out, not_80_out,
       not_81_out, not_82_out, not_83_out, not_84_out, not_85_out, not_86_out, not_87_out, not_88_out,
       not_89_out, not_90_out, not_91_out, not_92_out, not_93_out, not_94_out, not_95_out, not_96_out,
       not_97_out, not_98_out, not_99_out, not_100_out, not_101_out, not_102_out, not_103_out, not_104_out,
       not_105_out, not_106_out, not_107_out, not_108_out, not_109_out, not_110_out, not_111_out,
       not_112_out, not_113_out, not_114_out, not_115_out, not_116_out, not_117_out, not_118_out,
       not_119_out, not_120_out, not_121_out, not_122_out, not_123_out, not_124_out, not_125_out,
       not_126_out, not_127_out, not_128_out, not_129_out, not_130_out, not_131_out, not_132_out,
       not_133_out, not_134_out, not_135_out, not_136_out, not_137_out, not_138_out, not_139_out,
       not_140_out, not_141_out, not_142_out, not_143_out, not_144_out, not_145_out, not_146_out,
       not_147_out, not_148_out, not_149_out, not_150_out, not_151_out, not_152_out, not_153_out,
       not_154_out, not_155_out, not_156_out, not_157_out, not_158_out, not_159_out, not_160_out,
       not_161_out, not_162_out, not_163_out, not_164_out, not_165_out, not_166_out, not_167_out,
       not_168_out, not_169_out, not_170_out, not_171_out, not_172_out, not_173_out, not_174_out,
       not_175_out, not_176_out, not_177_out, not_178_out, not_179_out, not_180_out, not_181_out,
       not_182_out, not_183_out, not_184_out, not_185_out, not_186_out, not_187_out, not_188_out,
       not_189_out, not_190_out, not_191_out, not_192_out, not_193_out, not_194_out, not_195_out,
       not_196_out, not_197_out, not_198_out, not_199_out, not_200_out, not_201_out, not_202_out,
       not_203_out, not_204_out, not_205_out, not_206_out, not_207_out, not_208_out, not_209_out,
       not_210_out, not_211_out, not_212_out, not_213_out, not_214_out, not_215_out, not_216_out,
       not_217_out, not_218_out, not_219_out, not_220_out, not_221_out, not_222_out, not_223_out,
       not_224_out, not_225_out, not_226_out, not_227_out, not_228_out, not_229_out, not_230_out,
       not_231_out, not_232_out, not_233_out, not_234_out, not_235_out, not_236_out;

  not not_1 (not_1_out, OP5);
  not not_2 (not_2_out, OP4);
  not not_3 (not_3_out, OP3);
  not not_4 (not_4_out, OP2);
  not not_5 (not_5_out, OP1);
  not not_6 (not_6_out, OP0);
  not not_7 (not_7_out, F5);
  not not_8 (not_8_out, F4);
  not not_9 (not_9_out, F3);
  not not_10 (not_10_out, F2);
  not not_11 (not_11_out, OP5);
  not not_12 (not_12_out, OP4);
  not not_13 (not_13_out, OP3);
  not not_14 (not_14_out, OP2);
  not not_15 (not_15_out, OP1);
  not not_16 (not_16_out, OP0);
  not not_17 (not_17_out, F4);
  not not_18 (not_18_out, F3);
  not not_19 (not_19_out, F2);
  not not_20 (not_20_out, F1);
  not not_21 (not_21_out, F0);
  not not_22 (not_22_out, OP5);
  not not_23 (not_23_out, OP4);
  not not_24 (not_24_out, OP3);
  not not_25 (not_25_out, OP2);
  not not_26 (not_26_out, OP1);
  not not_27 (not_27_out, OP0);
  not not_28 (not_28_out, F4);
  not not_29 (not_29_out, F3);
  not not_30 (not_30_out, F2);
  not not_31 (not_31_out, F1);
  not not_32 (not_32_out, OP5);
  not not_33 (not_33_out, OP4);
  not not_34 (not_34_out, OP3);
  not not_35 (not_35_out, OP2);
  not not_36 (not_36_out, OP1);
  not not_37 (not_37_out, OP0);
  not not_38 (not_38_out, F4);
  not not_39 (not_39_out, F3);
  not not_40 (not_40_out, F1);
  not not_41 (not_41_out, F0);
  not not_42 (not_42_out, OP5);
  not not_43 (not_43_out, OP4);
  not not_44 (not_44_out, OP3);
  not not_45 (not_45_out, OP2);
  not not_46 (not_46_out, OP1);
  not not_47 (not_47_out, OP0);
  not not_48 (not_48_out, F4);
  not not_49 (not_49_out, F2);
  not not_50 (not_50_out, F0);
  not not_51 (not_51_out, OP5);
  not not_52 (not_52_out, OP4);
  not not_53 (not_53_out, OP2);
  not not_54 (not_54_out, OP1);
  not not_55 (not_55_out, OP0);
  not not_56 (not_56_out, OP5);
  not not_57 (not_57_out, OP4);
  not not_58 (not_58_out, OP1);
  not not_59 (not_59_out, OP0);
  not not_60 (not_60_out, OP5);
  not not_61 (not_61_out, OP4);
  not not_62 (not_62_out, OP2);
  not not_63 (not_63_out, OP1);
  not not_64 (not_64_out, OP5);
  not not_65 (not_65_out, OP4);
  not not_66 (not_66_out, OP2);
  not not_67 (not_67_out, OP0);
  not not_68 (not_68_out, OP4);
  not not_69 (not_69_out, OP3);
  not not_70 (not_70_out, OP2);
  not not_71 (not_71_out, OP4);
  not not_72 (not_72_out, OP2);
  not not_73 (not_73_out, OP5);
  not not_74 (not_74_out, OP4);
  not not_75 (not_75_out, OP3);
  not not_76 (not_76_out, OP2);
  not not_77 (not_77_out, OP1);
  not not_78 (not_78_out, OP0);
  not not_79 (not_79_out, F5);
  not not_80 (not_80_out, F4);
  not not_81 (not_81_out, F3);
  not not_82 (not_82_out, F2);
  not not_83 (not_83_out, F0);
  not not_84 (not_84_out, OP5);
  not not_85 (not_85_out, OP4);
  not not_86 (not_86_out, OP3);
  not not_87 (not_87_out, OP2);
  not not_88 (not_88_out, OP1);
  not not_89 (not_89_out, OP0);
  not not_90 (not_90_out, F4);
  not not_91 (not_91_out, F3);
  not not_92 (not_92_out, F2);
  not not_93 (not_93_out, F0);
  not not_94 (not_94_out, OP5);
  not not_95 (not_95_out, OP4);
  not not_96 (not_96_out, OP3);
  not not_97 (not_97_out, OP2);
  not not_98 (not_98_out, OP1);
  not not_99 (not_99_out, OP0);
  not not_100 (not_100_out, F4);
  not not_101 (not_101_out, F3);
  not not_102 (not_102_out, F1);
  not not_103 (not_103_out, F0);
  not not_104 (not_104_out, OP5);
  not not_105 (not_105_out, OP4);
  not not_106 (not_106_out, OP3);
  not not_107 (not_107_out, OP2);
  not not_108 (not_108_out, OP1);
  not not_109 (not_109_out, OP0);
  not not_110 (not_110_out, F4);
  not not_111 (not_111_out, F3);
  not not_112 (not_112_out, OP5);
  not not_113 (not_113_out, OP4);
  not not_114 (not_114_out, OP3);
  not not_115 (not_115_out, OP2);
  not not_116 (not_116_out, OP1);
  not not_117 (not_117_out, OP0);
  not not_118 (not_118_out, F4);
  not not_119 (not_119_out, F2);
  not not_120 (not_120_out, F0);
  not not_121 (not_121_out, OP5);
  not not_122 (not_122_out, OP4);
  not not_123 (not_123_out, OP1);
  not not_124 (not_124_out, OP0);
  not not_125 (not_125_out, OP5);
  not not_126 (not_126_out, OP4);
  not not_127 (not_127_out, OP2);
  not not_128 (not_128_out, OP0);
  not not_129 (not_129_out, OP5);
  not not_130 (not_130_out, OP4);
  not not_131 (not_131_out, OP3);
  not not_132 (not_132_out, OP2);
  not not_133 (not_133_out, OP1);
  not not_134 (not_134_out, OP0);
  not not_135 (not_135_out, F4);
  not not_136 (not_136_out, F3);
  not not_137 (not_137_out, F2);
  not not_138 (not_138_out, F1);
  not not_139 (not_139_out, F0);
  not not_140 (not_140_out, OP5);
  not not_141 (not_141_out, OP4);
  not not_142 (not_142_out, OP3);
  not not_143 (not_143_out, OP2);
  not not_144 (not_144_out, OP1);
  not not_145 (not_145_out, OP0);
  not not_146 (not_146_out, F4);
  not not_147 (not_147_out, F3);
  not not_148 (not_148_out, F2);
  not not_149 (not_149_out, F1);
  not not_150 (not_150_out, OP5);
  not not_151 (not_151_out, OP4);
  not not_152 (not_152_out, OP3);
  not not_153 (not_153_out, OP2);
  not not_154 (not_154_out, OP1);
  not not_155 (not_155_out, OP0);
  not not_156 (not_156_out, F4);
  not not_157 (not_157_out, F3);
  not not_158 (not_158_out, F2);
  not not_159 (not_159_out, F0);
  not not_160 (not_160_out, OP5);
  not not_161 (not_161_out, OP4);
  not not_162 (not_162_out, OP3);
  not not_163 (not_163_out, OP2);
  not not_164 (not_164_out, OP1);
  not not_165 (not_165_out, OP0);
  not not_166 (not_166_out, F4);
  not not_167 (not_167_out, F3);
  not not_168 (not_168_out, F1);
  not not_169 (not_169_out, F0);
  not not_170 (not_170_out, OP5);
  not not_171 (not_171_out, OP4);
  not not_172 (not_172_out, OP3);
  not not_173 (not_173_out, OP2);
  not not_174 (not_174_out, OP1);
  not not_175 (not_175_out, OP0);
  not not_176 (not_176_out, F4);
  not not_177 (not_177_out, F2);
  not not_178 (not_178_out, OP5);
  not not_179 (not_179_out, OP4);
  not not_180 (not_180_out, OP2);
  not not_181 (not_181_out, OP1);
  not not_182 (not_182_out, OP0);
  not not_183 (not_183_out, OP5);
  not not_184 (not_184_out, OP4);
  not not_185 (not_185_out, OP1);
  not not_186 (not_186_out, OP0);
  not not_187 (not_187_out, OP5);
  not not_188 (not_188_out, OP4);
  not not_189 (not_189_out, OP2);
  not not_190 (not_190_out, OP1);
  not not_191 (not_191_out, OP4);
  not not_192 (not_192_out, OP3);
  not not_193 (not_193_out, OP2);
  not not_194 (not_194_out, OP4);
  not not_195 (not_195_out, OP2);
  not not_196 (not_196_out, OP5);
  not not_197 (not_197_out, OP4);
  not not_198 (not_198_out, OP3);
  not not_199 (not_199_out, OP2);
  not not_200 (not_200_out, OP1);
  not not_201 (not_201_out, OP0);
  not not_202 (not_202_out, F4);
  not not_203 (not_203_out, F3);
  not not_204 (not_204_out, F1);
  not not_205 (not_205_out, OP5);
  not not_206 (not_206_out, OP4);
  not not_207 (not_207_out, OP3);
  not not_208 (not_208_out, OP2);
  not not_209 (not_209_out, OP1);
  not not_210 (not_210_out, OP0);
  not not_211 (not_211_out, F4);
  not not_212 (not_212_out, F3);
  not not_213 (not_213_out, OP5);
  not not_214 (not_214_out, OP4);
  not not_215 (not_215_out, OP3);
  not not_216 (not_216_out, OP2);
  not not_217 (not_217_out, OP1);
  not not_218 (not_218_out, OP0);
  not not_219 (not_219_out, F4);
  not not_220 (not_220_out, F2);
  not not_221 (not_221_out, F0);
  not not_222 (not_222_out, OP5);
  not not_223 (not_223_out, OP4);
  not not_224 (not_224_out, OP3);
  not not_225 (not_225_out, OP2);
  not not_226 (not_226_out, OP1);
  not not_227 (not_227_out, OP0);
  not not_228 (not_228_out, F4);
  not not_229 (not_229_out, F2);
  not not_230 (not_230_out, OP5);
  not not_231 (not_231_out, OP4);
  not not_232 (not_232_out, OP2);
  not not_233 (not_233_out, OP0);
  not not_234 (not_234_out, OP5);
  not not_235 (not_235_out, OP4);
  not not_236 (not_236_out, OP1);
  and and_1 (and_1_out, not_1_out, not_2_out, not_3_out, not_4_out, not_5_out, not_6_out, not_7_out, not_8_out, not_9_out, not_10_out, F1, F0);
  and and_2 (and_2_out, not_11_out, not_12_out, not_13_out, not_14_out, not_15_out, not_16_out, F5, not_17_out, not_18_out, not_19_out, not_20_out, not_21_out);
  and and_3 (and_3_out, not_22_out, not_23_out, not_24_out, not_25_out, not_26_out, not_27_out, F5, not_28_out, not_29_out, not_30_out, not_31_out, F0);
  and and_4 (and_4_out, not_32_out, not_33_out, not_34_out, not_35_out, not_36_out, not_37_out, F5, not_38_out, not_39_out, F2, not_40_out, not_41_out);
  and and_5 (and_5_out, not_42_out, not_43_out, not_44_out, not_45_out, not_46_out, not_47_out, F5, not_48_out, F3, not_49_out, F1, not_50_out);
  and and_6 (and_6_out, not_51_out, not_52_out, OP3, not_53_out, not_54_out, not_55_out);
  and and_7 (and_7_out, not_56_out, not_57_out, OP3, OP2, not_58_out, not_59_out);
  and and_8 (and_8_out, not_60_out, not_61_out, OP3, not_62_out, not_63_out, OP0);
  and and_9 (and_9_out, not_64_out, not_65_out, OP3, not_66_out, OP1, not_67_out);
  and and_10 (and_10_out, OP5, not_68_out, not_69_out, not_70_out, OP1, OP0);
  and and_11 (and_11_out, OP5, not_71_out, OP3, not_72_out, OP1, OP0);
  and and_12 (and_12_out, not_73_out, not_74_out, not_75_out, not_76_out, not_77_out, not_78_out, not_79_out, not_80_out, not_81_out, not_82_out, F1, not_83_out);
  and and_13 (and_13_out, not_84_out, not_85_out, not_86_out, not_87_out, not_88_out, not_89_out, F5, not_90_out, not_91_out, not_92_out, F1, not_93_out);
  and and_14 (and_14_out, not_94_out, not_95_out, not_96_out, not_97_out, not_98_out, not_99_out, F5, not_100_out, not_101_out, F2, not_102_out, not_103_out);
  and and_15 (and_15_out, not_104_out, not_105_out, not_106_out, not_107_out, not_108_out, not_109_out, F5, not_110_out, not_111_out, F2, F1, F0);
  and and_16 (and_16_out, not_112_out, not_113_out, not_114_out, not_115_out, not_116_out, not_117_out, F5, not_118_out, F3, not_119_out, F1, not_120_out);
  and and_17 (and_17_out, not_121_out, not_122_out, OP3, OP2, not_123_out, not_124_out);
  and and_18 (and_18_out, not_125_out, not_126_out, OP3, not_127_out, OP1, not_128_out);
  and and_19 (and_19_out, not_129_out, not_130_out, not_131_out, not_132_out, not_133_out, not_134_out, F5, not_135_out, not_136_out, not_137_out, not_138_out, not_139_out);
  and and_20 (and_20_out, not_140_out, not_141_out, not_142_out, not_143_out, not_144_out, not_145_out, F5, not_146_out, not_147_out, not_148_out, not_149_out, F0);
  and and_21 (and_21_out, not_150_out, not_151_out, not_152_out, not_153_out, not_154_out, not_155_out, F5, not_156_out, not_157_out, not_158_out, F1, not_159_out);
  and and_22 (and_22_out, not_160_out, not_161_out, not_162_out, not_163_out, not_164_out, not_165_out, F5, not_166_out, not_167_out, F2, not_168_out, not_169_out);
  and and_23 (and_23_out, not_170_out, not_171_out, not_172_out, not_173_out, not_174_out, not_175_out, F5, not_176_out, F3, not_177_out, F1, F0);
  and and_24 (and_24_out, not_178_out, not_179_out, OP3, not_180_out, not_181_out, not_182_out);
  and and_25 (and_25_out, not_183_out, not_184_out, OP3, OP2, not_185_out, not_186_out);
  and and_26 (and_26_out, not_187_out, not_188_out, OP3, not_189_out, not_190_out, OP0);
  and and_27 (and_27_out, OP5, not_191_out, not_192_out, not_193_out, OP1, OP0);
  and and_28 (and_28_out, OP5, not_194_out, OP3, not_195_out, OP1, OP0);
  and and_29 (and_29_out, not_196_out, not_197_out, not_198_out, not_199_out, not_200_out, not_201_out, F5, not_202_out, not_203_out, F2, not_204_out, F0);
  and and_30 (and_30_out, not_205_out, not_206_out, not_207_out, not_208_out, not_209_out, not_210_out, F5, not_211_out, not_212_out, F2, F1, F0);
  and and_31 (and_31_out, not_213_out, not_214_out, not_215_out, not_216_out, not_217_out, not_218_out, F5, not_219_out, F3, not_220_out, F1, not_221_out);
  and and_32 (and_32_out, not_222_out, not_223_out, not_224_out, not_225_out, not_226_out, not_227_out, F5, not_228_out, F3, not_229_out, F1, F0);
  and and_33 (and_33_out, not_230_out, not_231_out, OP3, not_232_out, OP1, not_233_out);
  and and_34 (and_34_out, not_234_out, not_235_out, OP3, OP2, not_236_out, OP0);
  or or_1 (S0, and_1_out, and_2_out, and_3_out, and_4_out, and_5_out, and_6_out, and_7_out, and_8_out, and_9_out, and_10_out, and_11_out);
  or or_2 (S1, and_12_out, and_13_out, and_14_out, and_15_out, and_16_out, and_17_out, and_18_out);
  or or_3 (S2, and_19_out, and_20_out, and_21_out, and_22_out, and_23_out, and_24_out, and_25_out, and_26_out, and_27_out, and_28_out);
  or or_4 (S3, and_29_out, and_30_out, and_31_out, and_32_out, and_33_out, and_34_out);
endmodule

// 控制信号生成
module \控制信号自动生成  (
  input  OP0,
  input  OP1,
  input  OP2,
  input  OP3,
  input  OP4,
  input  OP5,
  input  F0,
  input  F1,
  input  F2,
  input  F3,
  input  F4,
  input  F5,
  output MemToReg,
  output MemWrite,
  output ALU_SRC,
  output RegWrite,
  output SysCALL,
  output SignedExt,
  output RegDst,
  output BEQ,
  output BNE,
  output JR,
  output JUMP,
  output JAL
);

  wire and_3_out, and_4_out, and_5_out, and_6_out, and_7_out, and_8_out, and_9_out, and_10_out, and_11_out,
       and_12_out, and_13_out, and_14_out, and_15_out, and_16_out, and_17_out, and_18_out, and_19_out,
       and_20_out, and_21_out, and_22_out, and_23_out, and_24_out, and_25_out, and_26_out, and_27_out,
       and_29_out, and_30_out, and_31_out, and_32_out, and_33_out, and_34_out, and_35_out, and_36_out,
       and_37_out, and_38_out, and_39_out, and_40_out, and_41_out, and_42_out, and_43_out, and_44_out,
       and_45_out, and_46_out, not_1_out, not_2_out, not_3_out, not_4_out, not_5_out, not_6_out, not_7_out,
       not_8_out, not_9_out, not_10_out, not_11_out, not_12_out, not_13_out, not_14_out, not_15_out,
       not_16_out, not_17_out, not_18_out, not_19_out, not_20_out, not_21_out, not_22_out, not_23_out,
       not_24_out, not_25_out, not_26_out, not_27_out, not_28_out, not_29_out, not_30_out, not_31_out,
       not_32_out, not_33_out, not_34_out, not_35_out, not_36_out, not_37_out, not_38_out, not_39_out,
       not_40_out, not_41_out, not_42_out, not_43_out, not_44_out, not_45_out, not_46_out, not_47_out,
       not_48_out, not_49_out, not_50_out, not_51_out, not_52_out, not_53_out, not_54_out, not_55_out,
       not_56_out, not_57_out, not_58_out, not_59_out, not_60_out, not_61_out, not_62_out, not_63_out,
       not_64_out, not_65_out, not_66_out, not_67_out, not_68_out, not_69_out, not_70_out, not_71_out,
       not_72_out, not_73_out, not_74_out, not_75_out, not_76_out, not_77_out, not_78_out, not_79_out,
       not_80_out, not_81_out, not_82_out, not_83_out, not_84_out, not_85_out, not_86_out, not_87_out,
       not_88_out, not_89_out, not_90_out, not_91_out, not_92_out, not_93_out, not_94_out, not_95_out,
       not_96_out, not_97_out, not_98_out, not_99_out, not_100_out, not_101_out, not_102_out, not_103_out,
       not_104_out, not_105_out, not_106_out, not_107_out, not_108_out, not_109_out, not_110_out,
       not_111_out, not_112_out, not_113_out, not_114_out, not_115_out, not_116_out, not_117_out,
       not_118_out, not_119_out, not_120_out, not_121_out, not_122_out, not_123_out, not_124_out,
       not_125_out, not_126_out, not_127_out, not_128_out, not_129_out, not_130_out, not_131_out,
       not_132_out, not_133_out, not_134_out, not_135_out, not_136_out, not_137_out, not_138_out,
       not_139_out, not_140_out, not_141_out, not_142_out, not_143_out, not_144_out, not_145_out,
       not_146_out, not_147_out, not_148_out, not_149_out, not_150_out, not_151_out, not_152_out,
       not_153_out, not_154_out, not_155_out, not_156_out, not_157_out, not_158_out, not_159_out,
       not_160_out, not_161_out, not_162_out, not_163_out, not_164_out, not_165_out, not_166_out,
       not_167_out, not_168_out, not_169_out, not_170_out, not_171_out, not_172_out, not_173_out,
       not_174_out, not_175_out, not_176_out, not_177_out, not_178_out, not_179_out, not_180_out,
       not_181_out, not_182_out, not_183_out, not_184_out, not_185_out, not_186_out, not_187_out,
       not_188_out, not_189_out, not_190_out, not_191_out, not_192_out, not_193_out, not_194_out,
       not_195_out, not_196_out, not_197_out, not_198_out, not_199_out, not_200_out, not_201_out,
       not_202_out, not_203_out, not_204_out, not_205_out, not_206_out, not_207_out, not_208_out,
       not_209_out, not_210_out, not_211_out, not_212_out, not_213_out, not_214_out, not_215_out,
       not_216_out, not_217_out, not_218_out, not_219_out, not_220_out, not_221_out, not_222_out,
       not_223_out, not_224_out, not_225_out, not_226_out, not_227_out, not_228_out, not_229_out,
       not_230_out, not_231_out, not_232_out, not_233_out, not_234_out, not_235_out, not_236_out,
       not_237_out, not_238_out, not_239_out, not_240_out, not_241_out, not_242_out, not_243_out,
       not_244_out, not_245_out, not_246_out, not_247_out, not_248_out, not_249_out, not_250_out,
       not_251_out, not_252_out, not_253_out, not_254_out, not_255_out, not_256_out, not_257_out,
       not_258_out, not_259_out, not_260_out, not_261_out, not_262_out, not_263_out, not_264_out,
       not_265_out, not_266_out, not_267_out, not_268_out, not_269_out, not_270_out, not_271_out,
       not_272_out, not_273_out, not_274_out, not_275_out, not_276_out, not_277_out, not_278_out,
       not_279_out, not_280_out, not_281_out, not_282_out, not_283_out, not_284_out, not_285_out,
       not_286_out, not_287_out, not_288_out, not_289_out, not_290_out, not_291_out, not_292_out,
       not_293_out, not_294_out, not_295_out, not_296_out, not_297_out, not_298_out, not_299_out,
       not_300_out, not_301_out, not_302_out, not_303_out, not_304_out, not_305_out, not_306_out,
       not_307_out, not_308_out, not_309_out, not_310_out, not_311_out, not_312_out, not_313_out,
       not_314_out, not_315_out, not_316_out, not_317_out, not_318_out, not_319_out, not_320_out,
       not_321_out, not_322_out, not_323_out, not_324_out, not_325_out, not_326_out, not_327_out,
       not_328_out, not_329_out, not_330_out, not_331_out, not_332_out, not_333_out, not_334_out,
       not_335_out, not_336_out, not_337_out, not_338_out, not_339_out;

  not not_1 (not_1_out, OP4);
  not not_2 (not_2_out, OP3);
  not not_3 (not_3_out, OP2);
  not not_4 (not_4_out, OP4);
  not not_5 (not_5_out, OP2);
  not not_6 (not_6_out, OP5);
  not not_7 (not_7_out, OP4);
  not not_8 (not_8_out, OP2);
  not not_9 (not_9_out, OP1);
  not not_10 (not_10_out, OP0);
  not not_11 (not_11_out, OP5);
  not not_12 (not_12_out, OP4);
  not not_13 (not_13_out, OP1);
  not not_14 (not_14_out, OP0);
  not not_15 (not_15_out, OP5);
  not not_16 (not_16_out, OP4);
  not not_17 (not_17_out, OP2);
  not not_18 (not_18_out, OP1);
  not not_19 (not_19_out, OP5);
  not not_20 (not_20_out, OP4);
  not not_21 (not_21_out, OP2);
  not not_22 (not_22_out, OP0);
  not not_23 (not_23_out, OP5);
  not not_24 (not_24_out, OP4);
  not not_25 (not_25_out, OP1);
  not not_26 (not_26_out, OP4);
  not not_27 (not_27_out, OP3);
  not not_28 (not_28_out, OP2);
  not not_29 (not_29_out, OP4);
  not not_30 (not_30_out, OP2);
  not not_31 (not_31_out, OP5);
  not not_32 (not_32_out, OP4);
  not not_33 (not_33_out, OP3);
  not not_34 (not_34_out, OP2);
  not not_35 (not_35_out, OP1);
  not not_36 (not_36_out, OP0);
  not not_37 (not_37_out, F5);
  not not_38 (not_38_out, F4);
  not not_39 (not_39_out, F3);
  not not_40 (not_40_out, F2);
  not not_41 (not_41_out, F1);
  not not_42 (not_42_out, F0);
  not not_43 (not_43_out, OP5);
  not not_44 (not_44_out, OP4);
  not not_45 (not_45_out, OP3);
  not not_46 (not_46_out, OP2);
  not not_47 (not_47_out, OP1);
  not not_48 (not_48_out, OP0);
  not not_49 (not_49_out, F5);
  not not_50 (not_50_out, F4);
  not not_51 (not_51_out, F3);
  not not_52 (not_52_out, F2);
  not not_53 (not_53_out, OP5);
  not not_54 (not_54_out, OP4);
  not not_55 (not_55_out, OP3);
  not not_56 (not_56_out, OP2);
  not not_57 (not_57_out, OP1);
  not not_58 (not_58_out, OP0);
  not not_59 (not_59_out, F5);
  not not_60 (not_60_out, F4);
  not not_61 (not_61_out, F3);
  not not_62 (not_62_out, F2);
  not not_63 (not_63_out, F0);
  not not_64 (not_64_out, OP5);
  not not_65 (not_65_out, OP4);
  not not_66 (not_66_out, OP3);
  not not_67 (not_67_out, OP2);
  not not_68 (not_68_out, OP1);
  not not_69 (not_69_out, OP0);
  not not_70 (not_70_out, F4);
  not not_71 (not_71_out, F3);
  not not_72 (not_72_out, F2);
  not not_73 (not_73_out, F1);
  not not_74 (not_74_out, F0);
  not not_75 (not_75_out, OP5);
  not not_76 (not_76_out, OP4);
  not not_77 (not_77_out, OP3);
  not not_78 (not_78_out, OP2);
  not not_79 (not_79_out, OP1);
  not not_80 (not_80_out, OP0);
  not not_81 (not_81_out, F4);
  not not_82 (not_82_out, F3);
  not not_83 (not_83_out, F2);
  not not_84 (not_84_out, F1);
  not not_85 (not_85_out, OP5);
  not not_86 (not_86_out, OP4);
  not not_87 (not_87_out, OP3);
  not not_88 (not_88_out, OP2);
  not not_89 (not_89_out, OP1);
  not not_90 (not_90_out, OP0);
  not not_91 (not_91_out, F4);
  not not_92 (not_92_out, F3);
  not not_93 (not_93_out, F2);
  not not_94 (not_94_out, F0);
  not not_95 (not_95_out, OP5);
  not not_96 (not_96_out, OP4);
  not not_97 (not_97_out, OP3);
  not not_98 (not_98_out, OP2);
  not not_99 (not_99_out, OP1);
  not not_100 (not_100_out, OP0);
  not not_101 (not_101_out, F4);
  not not_102 (not_102_out, F3);
  not not_103 (not_103_out, F1);
  not not_104 (not_104_out, F0);
  not not_105 (not_105_out, OP5);
  not not_106 (not_106_out, OP4);
  not not_107 (not_107_out, OP3);
  not not_108 (not_108_out, OP2);
  not not_109 (not_109_out, OP1);
  not not_110 (not_110_out, OP0);
  not not_111 (not_111_out, F4);
  not not_112 (not_112_out, F3);
  not not_113 (not_113_out, F1);
  not not_114 (not_114_out, OP5);
  not not_115 (not_115_out, OP4);
  not not_116 (not_116_out, OP3);
  not not_117 (not_117_out, OP2);
  not not_118 (not_118_out, OP1);
  not not_119 (not_119_out, OP0);
  not not_120 (not_120_out, F4);
  not not_121 (not_121_out, F3);
  not not_122 (not_122_out, OP5);
  not not_123 (not_123_out, OP4);
  not not_124 (not_124_out, OP3);
  not not_125 (not_125_out, OP2);
  not not_126 (not_126_out, OP1);
  not not_127 (not_127_out, OP0);
  not not_128 (not_128_out, F4);
  not not_129 (not_129_out, F2);
  not not_130 (not_130_out, F0);
  not not_131 (not_131_out, OP5);
  not not_132 (not_132_out, OP4);
  not not_133 (not_133_out, OP3);
  not not_134 (not_134_out, OP2);
  not not_135 (not_135_out, OP1);
  not not_136 (not_136_out, OP0);
  not not_137 (not_137_out, F4);
  not not_138 (not_138_out, F2);
  not not_139 (not_139_out, OP5);
  not not_140 (not_140_out, OP4);
  not not_141 (not_141_out, OP3);
  not not_142 (not_142_out, OP2);
  not not_143 (not_143_out, OP5);
  not not_144 (not_144_out, OP4);
  not not_145 (not_145_out, OP2);
  not not_146 (not_146_out, OP1);
  not not_147 (not_147_out, OP0);
  not not_148 (not_148_out, OP5);
  not not_149 (not_149_out, OP4);
  not not_150 (not_150_out, OP1);
  not not_151 (not_151_out, OP0);
  not not_152 (not_152_out, OP5);
  not not_153 (not_153_out, OP4);
  not not_154 (not_154_out, OP2);
  not not_155 (not_155_out, OP1);
  not not_156 (not_156_out, OP5);
  not not_157 (not_157_out, OP4);
  not not_158 (not_158_out, OP2);
  not not_159 (not_159_out, OP0);
  not not_160 (not_160_out, OP5);
  not not_161 (not_161_out, OP4);
  not not_162 (not_162_out, OP1);
  not not_163 (not_163_out, OP4);
  not not_164 (not_164_out, OP3);
  not not_165 (not_165_out, OP2);
  not not_166 (not_166_out, OP5);
  not not_167 (not_167_out, OP4);
  not not_168 (not_168_out, OP3);
  not not_169 (not_169_out, OP2);
  not not_170 (not_170_out, OP1);
  not not_171 (not_171_out, OP0);
  not not_172 (not_172_out, F5);
  not not_173 (not_173_out, F4);
  not not_174 (not_174_out, F1);
  not not_175 (not_175_out, F0);
  not not_176 (not_176_out, OP5);
  not not_177 (not_177_out, OP4);
  not not_178 (not_178_out, OP3);
  not not_179 (not_179_out, OP1);
  not not_180 (not_180_out, OP0);
  not not_181 (not_181_out, OP5);
  not not_182 (not_182_out, OP4);
  not not_183 (not_183_out, OP3);
  not not_184 (not_184_out, OP1);
  not not_185 (not_185_out, OP5);
  not not_186 (not_186_out, OP4);
  not not_187 (not_187_out, OP2);
  not not_188 (not_188_out, OP1);
  not not_189 (not_189_out, OP0);
  not not_190 (not_190_out, OP5);
  not not_191 (not_191_out, OP4);
  not not_192 (not_192_out, OP2);
  not not_193 (not_193_out, OP1);
  not not_194 (not_194_out, OP5);
  not not_195 (not_195_out, OP4);
  not not_196 (not_196_out, OP2);
  not not_197 (not_197_out, OP0);
  not not_198 (not_198_out, OP4);
  not not_199 (not_199_out, OP3);
  not not_200 (not_200_out, OP2);
  not not_201 (not_201_out, OP4);
  not not_202 (not_202_out, OP2);
  not not_203 (not_203_out, OP5);
  not not_204 (not_204_out, OP4);
  not not_205 (not_205_out, OP3);
  not not_206 (not_206_out, OP2);
  not not_207 (not_207_out, OP1);
  not not_208 (not_208_out, OP0);
  not not_209 (not_209_out, F5);
  not not_210 (not_210_out, F4);
  not not_211 (not_211_out, F3);
  not not_212 (not_212_out, F2);
  not not_213 (not_213_out, F1);
  not not_214 (not_214_out, F0);
  not not_215 (not_215_out, OP5);
  not not_216 (not_216_out, OP4);
  not not_217 (not_217_out, OP3);
  not not_218 (not_218_out, OP2);
  not not_219 (not_219_out, OP1);
  not not_220 (not_220_out, OP0);
  not not_221 (not_221_out, F5);
  not not_222 (not_222_out, F4);
  not not_223 (not_223_out, F3);
  not not_224 (not_224_out, F2);
  not not_225 (not_225_out, OP5);
  not not_226 (not_226_out, OP4);
  not not_227 (not_227_out, OP3);
  not not_228 (not_228_out, OP2);
  not not_229 (not_229_out, OP1);
  not not_230 (not_230_out, OP0);
  not not_231 (not_231_out, F5);
  not not_232 (not_232_out, F4);
  not not_233 (not_233_out, F3);
  not not_234 (not_234_out, F2);
  not not_235 (not_235_out, F0);
  not not_236 (not_236_out, OP5);
  not not_237 (not_237_out, OP4);
  not not_238 (not_238_out, OP3);
  not not_239 (not_239_out, OP2);
  not not_240 (not_240_out, OP1);
  not not_241 (not_241_out, OP0);
  not not_242 (not_242_out, F4);
  not not_243 (not_243_out, F3);
  not not_244 (not_244_out, F2);
  not not_245 (not_245_out, F1);
  not not_246 (not_246_out, F0);
  not not_247 (not_247_out, OP5);
  not not_248 (not_248_out, OP4);
  not not_249 (not_249_out, OP3);
  not not_250 (not_250_out, OP2);
  not not_251 (not_251_out, OP1);
  not not_252 (not_252_out, OP0);
  not not_253 (not_253_out, F4);
  not not_254 (not_254_out, F3);
  not not_255 (not_255_out, F2);
  not not_256 (not_256_out, F1);
  not not_257 (not_257_out, OP5);
  not not_258 (not_258_out, OP4);
  not not_259 (not_259_out, OP3);
  not not_260 (not_260_out, OP2);
  not not_261 (not_261_out, OP1);
  not not_262 (not_262_out, OP0);
  not not_263 (not_263_out, F4);
  not not_264 (not_264_out, F3);
  not not_265 (not_265_out, F2);
  not not_266 (not_266_out, F0);
  not not_267 (not_267_out, OP5);
  not not_268 (not_268_out, OP4);
  not not_269 (not_269_out, OP3);
  not not_270 (not_270_out, OP2);
  not not_271 (not_271_out, OP1);
  not not_272 (not_272_out, OP0);
  not not_273 (not_273_out, F4);
  not not_274 (not_274_out, F3);
  not not_275 (not_275_out, F1);
  not not_276 (not_276_out, F0);
  not not_277 (not_277_out, OP5);
  not not_278 (not_278_out, OP4);
  not not_279 (not_279_out, OP3);
  not not_280 (not_280_out, OP2);
  not not_281 (not_281_out, OP1);
  not not_282 (not_282_out, OP0);
  not not_283 (not_283_out, F4);
  not not_284 (not_284_out, F3);
  not not_285 (not_285_out, F1);
  not not_286 (not_286_out, OP5);
  not not_287 (not_287_out, OP4);
  not not_288 (not_288_out, OP3);
  not not_289 (not_289_out, OP2);
  not not_290 (not_290_out, OP1);
  not not_291 (not_291_out, OP0);
  not not_292 (not_292_out, F4);
  not not_293 (not_293_out, F3);
  not not_294 (not_294_out, OP5);
  not not_295 (not_295_out, OP4);
  not not_296 (not_296_out, OP3);
  not not_297 (not_297_out, OP2);
  not not_298 (not_298_out, OP1);
  not not_299 (not_299_out, OP0);
  not not_300 (not_300_out, F4);
  not not_301 (not_301_out, F2);
  not not_302 (not_302_out, F0);
  not not_303 (not_303_out, OP5);
  not not_304 (not_304_out, OP4);
  not not_305 (not_305_out, OP3);
  not not_306 (not_306_out, OP2);
  not not_307 (not_307_out, OP1);
  not not_308 (not_308_out, OP0);
  not not_309 (not_309_out, F4);
  not not_310 (not_310_out, F2);
  not not_311 (not_311_out, OP5);
  not not_312 (not_312_out, OP4);
  not not_313 (not_313_out, OP3);
  not not_314 (not_314_out, OP1);
  not not_315 (not_315_out, OP0);
  not not_316 (not_316_out, OP5);
  not not_317 (not_317_out, OP4);
  not not_318 (not_318_out, OP3);
  not not_319 (not_319_out, OP1);
  not not_320 (not_320_out, OP5);
  not not_321 (not_321_out, OP4);
  not not_322 (not_322_out, OP3);
  not not_323 (not_323_out, OP2);
  not not_324 (not_324_out, OP1);
  not not_325 (not_325_out, OP0);
  not not_326 (not_326_out, F5);
  not not_327 (not_327_out, F4);
  not not_328 (not_328_out, F2);
  not not_329 (not_329_out, F1);
  not not_330 (not_330_out, F0);
  not not_331 (not_331_out, OP5);
  not not_332 (not_332_out, OP4);
  not not_333 (not_333_out, OP3);
  not not_334 (not_334_out, OP2);
  not not_335 (not_335_out, OP0);
  not not_336 (not_336_out, OP5);
  not not_337 (not_337_out, OP4);
  not not_338 (not_338_out, OP3);
  not not_339 (not_339_out, OP2);
  and and_1 (MemToReg, OP5, not_1_out, not_2_out, not_3_out, OP1, OP0);
  and and_2 (MemWrite, OP5, not_4_out, OP3, not_5_out, OP1, OP0);
  and and_3 (and_3_out, not_6_out, not_7_out, OP3, not_8_out, not_9_out, not_10_out);
  and and_4 (and_4_out, not_11_out, not_12_out, OP3, OP2, not_13_out, not_14_out);
  and and_5 (and_5_out, not_15_out, not_16_out, OP3, not_17_out, not_18_out, OP0);
  and and_6 (and_6_out, not_19_out, not_20_out, OP3, not_21_out, OP1, not_22_out);
  and and_7 (and_7_out, not_23_out, not_24_out, OP3, OP2, not_25_out, OP0);
  and and_8 (and_8_out, OP5, not_26_out, not_27_out, not_28_out, OP1, OP0);
  and and_9 (and_9_out, OP5, not_29_out, OP3, not_30_out, OP1, OP0);
  and and_10 (and_10_out, not_31_out, not_32_out, not_33_out, not_34_out, not_35_out, not_36_out, not_37_out, not_38_out, not_39_out, not_40_out, not_41_out, not_42_out);
  and and_11 (and_11_out, not_43_out, not_44_out, not_45_out, not_46_out, not_47_out, not_48_out, not_49_out, not_50_out, not_51_out, not_52_out, F1, F0);
  and and_12 (and_12_out, not_53_out, not_54_out, not_55_out, not_56_out, not_57_out, not_58_out, not_59_out, not_60_out, not_61_out, not_62_out, F1, not_63_out);
  and and_13 (and_13_out, not_64_out, not_65_out, not_66_out, not_67_out, not_68_out, not_69_out, F5, not_70_out, not_71_out, not_72_out, not_73_out, not_74_out);
  and and_14 (and_14_out, not_75_out, not_76_out, not_77_out, not_78_out, not_79_out, not_80_out, F5, not_81_out, not_82_out, not_83_out, not_84_out, F0);
  and and_15 (and_15_out, not_85_out, not_86_out, not_87_out, not_88_out, not_89_out, not_90_out, F5, not_91_out, not_92_out, not_93_out, F1, not_94_out);
  and and_16 (and_16_out, not_95_out, not_96_out, not_97_out, not_98_out, not_99_out, not_100_out, F5, not_101_out, not_102_out, F2, not_103_out, not_104_out);
  and and_17 (and_17_out, not_105_out, not_106_out, not_107_out, not_108_out, not_109_out, not_110_out, F5, not_111_out, not_112_out, F2, not_113_out, F0);
  and and_18 (and_18_out, not_114_out, not_115_out, not_116_out, not_117_out, not_118_out, not_119_out, F5, not_120_out, not_121_out, F2, F1, F0);
  and and_19 (and_19_out, not_122_out, not_123_out, not_124_out, not_125_out, not_126_out, not_127_out, F5, not_128_out, F3, not_129_out, F1, not_130_out);
  and and_20 (and_20_out, not_131_out, not_132_out, not_133_out, not_134_out, not_135_out, not_136_out, F5, not_137_out, F3, not_138_out, F1, F0);
  and and_21 (and_21_out, not_139_out, not_140_out, not_141_out, not_142_out, OP1, OP0);
  and and_22 (and_22_out, not_143_out, not_144_out, OP3, not_145_out, not_146_out, not_147_out);
  and and_23 (and_23_out, not_148_out, not_149_out, OP3, OP2, not_150_out, not_151_out);
  and and_24 (and_24_out, not_152_out, not_153_out, OP3, not_154_out, not_155_out, OP0);
  and and_25 (and_25_out, not_156_out, not_157_out, OP3, not_158_out, OP1, not_159_out);
  and and_26 (and_26_out, not_160_out, not_161_out, OP3, OP2, not_162_out, OP0);
  and and_27 (and_27_out, OP5, not_163_out, not_164_out, not_165_out, OP1, OP0);
  and and_28 (SysCALL, not_166_out, not_167_out, not_168_out, not_169_out, not_170_out, not_171_out, not_172_out, not_173_out, F3, F2, not_174_out, not_175_out);
  and and_29 (and_29_out, not_176_out, not_177_out, not_178_out, OP2, not_179_out, not_180_out);
  and and_30 (and_30_out, not_181_out, not_182_out, not_183_out, OP2, not_184_out, OP0);
  and and_31 (and_31_out, not_185_out, not_186_out, OP3, not_187_out, not_188_out, not_189_out);
  and and_32 (and_32_out, not_190_out, not_191_out, OP3, not_192_out, not_193_out, OP0);
  and and_33 (and_33_out, not_194_out, not_195_out, OP3, not_196_out, OP1, not_197_out);
  and and_34 (and_34_out, OP5, not_198_out, not_199_out, not_200_out, OP1, OP0);
  and and_35 (and_35_out, OP5, not_201_out, OP3, not_202_out, OP1, OP0);
  and and_36 (and_36_out, not_203_out, not_204_out, not_205_out, not_206_out, not_207_out, not_208_out, not_209_out, not_210_out, not_211_out, not_212_out, not_213_out, not_214_out);
  and and_37 (and_37_out, not_215_out, not_216_out, not_217_out, not_218_out, not_219_out, not_220_out, not_221_out, not_222_out, not_223_out, not_224_out, F1, F0);
  and and_38 (and_38_out, not_225_out, not_226_out, not_227_out, not_228_out, not_229_out, not_230_out, not_231_out, not_232_out, not_233_out, not_234_out, F1, not_235_out);
  and and_39 (and_39_out, not_236_out, not_237_out, not_238_out, not_239_out, not_240_out, not_241_out, F5, not_242_out, not_243_out, not_244_out, not_245_out, not_246_out);
  and and_40 (and_40_out, not_247_out, not_248_out, not_249_out, not_250_out, not_251_out, not_252_out, F5, not_253_out, not_254_out, not_255_out, not_256_out, F0);
  and and_41 (and_41_out, not_257_out, not_258_out, not_259_out, not_260_out, not_261_out, not_262_out, F5, not_263_out, not_264_out, not_265_out, F1, not_266_out);
  and and_42 (and_42_out, not_267_out, not_268_out, not_269_out, not_270_out, not_271_out, not_272_out, F5, not_273_out, not_274_out, F2, not_275_out, not_276_out);
  and and_43 (and_43_out, not_277_out, not_278_out, not_279_out, not_280_out, not_281_out, not_282_out, F5, not_283_out, not_284_out, F2, not_285_out, F0);
  and and_44 (and_44_out, not_286_out, not_287_out, not_288_out, not_289_out, not_290_out, not_291_out, F5, not_292_out, not_293_out, F2, F1, F0);
  and and_45 (and_45_out, not_294_out, not_295_out, not_296_out, not_297_out, not_298_out, not_299_out, F5, not_300_out, F3, not_301_out, F1, not_302_out);
  and and_46 (and_46_out, not_303_out, not_304_out, not_305_out, not_306_out, not_307_out, not_308_out, F5, not_309_out, F3, not_310_out, F1, F0);
  and and_47 (BEQ, not_311_out, not_312_out, not_313_out, OP2, not_314_out, not_315_out);
  and and_48 (BNE, not_316_out, not_317_out, not_318_out, OP2, not_319_out, OP0);
  and and_49 (JR, not_320_out, not_321_out, not_322_out, not_323_out, not_324_out, not_325_out, not_326_out, not_327_out, F3, not_328_out, not_329_out, not_330_out);
  and and_50 (JUMP, not_331_out, not_332_out, not_333_out, not_334_out, OP1, not_335_out);
  and and_51 (JAL, not_336_out, not_337_out, not_338_out, not_339_out, OP1, OP0);
  or or_1 (ALU_SRC, and_3_out, and_4_out, and_5_out, and_6_out, and_7_out, and_8_out, and_9_out);
  or or_2 (SignedExt, and_29_out, and_30_out, and_31_out, and_32_out, and_33_out, and_34_out, and_35_out);
  or or_3 (RegDst, and_36_out, and_37_out, and_38_out, and_39_out, and_40_out, and_41_out, and_42_out, and_43_out, and_44_out, and_45_out, and_46_out);
  or or_4 (RegWrite, and_10_out, and_11_out, and_12_out, and_13_out, and_14_out, and_15_out, and_16_out, and_17_out, and_18_out, and_19_out, and_20_out, and_21_out, and_22_out, and_23_out, and_24_out, and_25_out, and_26_out, and_27_out);
endmodule

module \_24_4条扩展指令电路  (
  input  IR1,
  input  IR2,
  input  IR3,
  output RegWrite,
  output MemWrite,
  output [31:0] PC,
  output [31:0] IR,
  output [31:0] RDin,
  output [31:0] MDin,
  output [31:0] LedData
);

  wire and_1_out, and_2_out, and_3_out, and_4_out, and_5_out, CLK, comparator_1_eq, Go, IR1_t, IR2_t, IR3_t,
       IRA, IRB, IRC, lbu, lui, mips_alu_1_equal, \n24_4条扩展指令控制器_1_alu_src , \n24_4条扩展指令控制器_1_beq ,
       \n24_4条扩展指令控制器_1_bgez , \n24_4条扩展指令控制器_1_bne , \n24_4条扩展指令控制器_1_jal , \n24_4条扩展指令控制器_1_jmp ,
       \n24_4条扩展指令控制器_1_jr , \n24_4条扩展指令控制器_1_memtoreg , \n24_4条扩展指令控制器_1_regdst , not_1_out, not_3_out,
       not_4_out, or_1_out, or_2_out, or_6_out, PCok, register_2_q, RST, SignedExt, Syscall, W1, W2, W3;
  wire [3:0] \n24_4条扩展指令控制器_1_alu_op ;
  wire [4:0] multiplexer_4_out, multiplexer_5_out, multiplexer_6_out, multiplexer_7_out;
  wire [15:0] \总周期数 ;
  wire [31:0] adder_1_out, adder_2_out, bit_extender_1_out, bit_extender_2_out, bit_extender_3_out,
       mips_alu_1_result, multiplexer_3_out, multiplexer_8_out, multiplexer_9_out, multiplexer_11_out,
       multiplexer_12_out, multiplexer_13_out, multiplexer_14_out, PC1, PC2, R1, ram_1_data, shifter_1_out,
       shifter_2_out, shifter_3_out;

  Clock #(.highDuration(1), .lowDuration(1)) clock_1 (.out(CLK));
  Button _1 (.out(IRA));
  Button _2 (.out(IRB));
  Button _3 (.out(IRC));
  Button \u_总复位  (.out(RST));
  Multiplexer #(.select(1), .width(32), .disabled("Z"), .enable("false")) multiplexer_1 (
    .in0(adder_1_out), .in1(adder_2_out), .out(PC1), .sel(or_6_out));
  Multiplexer #(.select(1), .width(32), .disabled("Z"), .enable("false")) multiplexer_2 (
    .in0(PC1), .in1(shifter_3_out), .out(PC2), .sel(or_1_out));
  Multiplexer #(.select(1), .width(32), .disabled("Z"), .enable("false")) multiplexer_3 (
    .in0(PC2), .in1(R1), .out(multiplexer_3_out), .sel(\n24_4条扩展指令控制器_1_jr ));
  Button \u_继续运行  (.out(Go));
  LED #(.active("true")) led_1 (.in(W1));
  LED #(.active("true")) led_2 (.in(W2));
  LED #(.active("true")) led_3 (.in(W3));
  Register #(.width(32), .trigger("rising"), .Select("low")) u_PC (
    .D(multiplexer_3_out), .en(PCok), .Q(PC), .clk(CLK), .clr(RST));
  Comparator #(.width(32), .mode("twosComplement")) comparator_1 (
    .a(MDin), .b(32'h22), .eq(comparator_1_eq));  // open: gt, lt
  not not_1 (not_1_out, comparator_1_eq);
  Hex_Digit_Display hex_digit_display_1 (.value(LedData[27:24]));  // open: dp
  Hex_Digit_Display hex_digit_display_2 (.value(LedData[31:28]));  // open: dp
  or or_1 (or_1_out, \n24_4条扩展指令控制器_1_jal , \n24_4条扩展指令控制器_1_jmp );
  Adder #(.width(32)) adder_1 (.a(PC), .b(32'h4), .out(adder_1_out));  // open: cin, cout
  Register #(.width(32), .trigger("rising"), .Select("low")) register_1 (
    .D(R1), .en(and_1_out), .Q(LedData), .clk(CLK), .clr(RST));
  and and_1 (and_1_out, comparator_1_eq, Syscall);
  Register #(.width(1), .trigger("rising"), .Select("low")) register_2 (
    .D(Syscall), .en(and_2_out), .Q(register_2_q), .clk(CLK), .clr(or_2_out));
  and and_2 (and_2_out, not_1_out, Syscall);
  or or_2 (or_2_out, Go, RST);
  Hex_Digit_Display hex_digit_display_3 (.value(LedData[19:16]));  // open: dp
  Hex_Digit_Display hex_digit_display_4 (.value(LedData[23:20]));  // open: dp
  Counter #(.width(16), .max('hffff), .ongoal("wrap"), .trigger("rising"), .behavior("old")) counter_1 (
    .count(PCok), .Q(\总周期数 ), .clk(CLK), .clr(RST));  // open: load, D, carry, preset
  ROM #(.addrWidth(10), .dataWidth(32), .Select("high")) rom_1 (.addr(PC[11:2]), .data(IR));
  not not_2 (PCok, register_2_q);
  Hex_Digit_Display hex_digit_display_5 (.value(LedData[15:12]));  // open: dp
  Hex_Digit_Display hex_digit_display_6 (.value(LedData[11:8]));  // open: dp
  Hex_Digit_Display hex_digit_display_7 (.value(LedData[7:4]));  // open: dp
  Hex_Digit_Display hex_digit_display_8 (.value(LedData[3:0]));  // open: dp
  // Probe on \总周期数 
  Multiplexer #(.select(1), .width(5), .disabled("Z"), .enable("false")) multiplexer_4 (
    .in0(IR[25:21]), .in1(5'b00100), .out(multiplexer_4_out), .sel(Syscall));
  Multiplexer #(.select(1), .width(5), .disabled("Z"), .enable("false")) multiplexer_5 (
    .in0(IR[20:16]), .in1(5'b00010), .out(multiplexer_5_out), .sel(Syscall));
  Multiplexer #(.select(1), .width(5), .disabled("Z"), .enable("false")) multiplexer_6 (
    .in0(IR[20:16]), .in1(IR[15:11]), .out(multiplexer_6_out), .sel(\n24_4条扩展指令控制器_1_regdst ));
  assign bit_extender_1_out = {{16{1'b0}}, IR[15:0]};  // Bit_Extender bit_extender_1
  assign bit_extender_2_out = {{16{IR[15]}}, IR[15:0]};  // Bit_Extender bit_extender_2
  assign bit_extender_3_out = {{6{IR[25]}}, IR[25:0]};  // Bit_Extender bit_extender_3
  \_24_4条扩展指令控制器  \u_24_4条扩展指令控制器_1  (
    .Func(IR[5:0]), .OP(IR[31:26]), .ALU_OP(\n24_4条扩展指令控制器_1_alu_op ), .MemToReg(\n24_4条扩展指令控制器_1_memtoreg ),
    .MemWrite(MemWrite), .ALU_SRC(\n24_4条扩展指令控制器_1_alu_src ), .RegWrite(RegWrite), .SysCALL(Syscall),
    .SignedExt(SignedExt), .RegDst(\n24_4条扩展指令控制器_1_regdst ), .JR(\n24_4条扩展指令控制器_1_jr ),
    .JMP(\n24_4条扩展指令控制器_1_jmp ), .Beq(\n24_4条扩展指令控制器_1_beq ), .JAL(\n24_4条扩展指令控制器_1_jal ),
    .Bne(\n24_4条扩展指令控制器_1_bne ), .LUI(lui), .LBU(lbu), .BGEZ(\n24_4条扩展指令控制器_1_bgez ));
  Multiplexer #(.select(1), .width(5), .disabled("Z"), .enable("false")) multiplexer_7 (
    .in0(multiplexer_6_out), .in1({5{1'b1}}), .out(multiplexer_7_out), .sel(\n24_4条扩展指令控制器_1_jal ));
  Multiplexer #(.select(1), .width(32), .disabled("Z"), .enable("false")) multiplexer_8 (
    .in0(bit_extender_1_out), .in1(bit_extender_2_out), .out(multiplexer_8_out), .sel(SignedExt));
  or or_3 (IR1_t, IR1, IRA);
  MIPS_Regifile mips_regifile_1 (
    .Din(RDin), .Clk(CLK), .R1(R1), .R2(MDin), .WE(RegWrite), .W_num(multiplexer_7_out),
    .R1_num(multiplexer_4_out), .R2_num(multiplexer_5_out));
  or or_4 (IR2_t, IR2, IRB);
  Multiplexer #(.select(1), .width(32), .disabled("Z"), .enable("false")) multiplexer_9 (
    .in0(MDin), .in1(multiplexer_8_out), .out(multiplexer_9_out), .sel(\n24_4条扩展指令控制器_1_alu_src ));
  Multiplexer #(.select(1), .width(32), .disabled("Z"), .enable("false")) multiplexer_10 (
    .in0(multiplexer_12_out), .in1(adder_1_out), .out(RDin), .sel(\n24_4条扩展指令控制器_1_jal ));
  Shifter #(.width(32), .shift("ll")) shifter_1 (.in(multiplexer_8_out), .\dist (5'b00010), .out(shifter_1_out));
  Shifter #(.width(32), .shift("ll")) shifter_2 (.in(bit_extender_1_out), .\dist (5'b10000), .out(shifter_2_out));
  Shifter #(.width(32), .shift("ll")) shifter_3 (.in(bit_extender_3_out), .\dist (5'b00010), .out(shifter_3_out));
  or or_5 (IR3_t, IR3, IRC);
  Multiplexer #(.select(1), .width(32), .disabled("Z"), .enable("false")) multiplexer_11 (
    .in0(multiplexer_9_out), .in1({32{1'b0}}), .out(multiplexer_11_out), .sel(\n24_4条扩展指令控制器_1_bgez ));
  MIPS_ALU mips_alu_1 (
    .X(R1), .Y(multiplexer_11_out), .AluOP(\n24_4条扩展指令控制器_1_alu_op ), .Equal(mips_alu_1_equal),
    .Result(mips_alu_1_result), .shamt(IR[10:6]));  // open: Result_2
  not not_3 (not_3_out, mips_alu_1_result[0]);
  not not_4 (not_4_out, mips_alu_1_equal);
  Multiplexer #(.select(1), .width(32), .disabled("Z"), .enable("false")) multiplexer_12 (
    .in0(multiplexer_14_out), .in1(shifter_2_out), .out(multiplexer_12_out), .sel(lui));
  Adder #(.width(32)) adder_2 (.a(shifter_1_out), .b(adder_1_out), .out(adder_2_out));  // open: cin, cout
  and and_3 (and_3_out, not_3_out, \n24_4条扩展指令控制器_1_bgez );
  and and_4 (and_4_out, mips_alu_1_equal, \n24_4条扩展指令控制器_1_beq );
  and and_5 (and_5_out, not_4_out, \n24_4条扩展指令控制器_1_bne );
  RAM #(.addrWidth(10), .dataWidth(32), .bus("separate"), .Select("high")) ram_1 (
    .addr(mips_alu_1_result[11:2]), .din(MDin), .data(ram_1_data), .str(MemWrite), .clk(CLK), .clr(RST));  // open: sel, ld
  or or_6 (or_6_out, and_3_out, and_4_out, and_5_out);
  Multiplexer #(.select(1), .width(32), .disabled("Z"), .enable("false")) multiplexer_13 (
    .in0(ram_1_data), .in1({{24{1'b0}}, ram_1_data[7:0]}), .out(multiplexer_13_out), .sel(lbu));
  Multiplexer #(.select(1), .width(32), .disabled("Z"), .enable("false")) multiplexer_14 (
    .in0(mips_alu_1_result), .in1(multiplexer_13_out), .out(multiplexer_14_out),
    .sel(\n24_4条扩展指令控制器_1_memtoreg ));

  // Other names for the same wires on the sheet: R2[31:0] = MDin

  // Notes on the sheet:
  //   中断源
  //   总复位信号应将除ROM以外所有存储组件全部清零
  //   中断等待指示
  //   数码管输出
  //   指令存储器
  //   contents of rom_1 (hex, n*v repeats v):
  //   20110001 8100005 20110001 20120002 20130003 8100009 20110001 20120002 20130003 810000d 20110001
  //   20120002 20130003 8100011 20110001 20120002 20130003 c1000fc 20100001 20110001 118fc0 112020
  //   20020022 c 118882 12200001 8100015 112020 20020022 c 20110001 118880 112020 20020022 c 12200001
  //   810001f 20110001 118fc0 112020 20020022 c 1188c3 112020 20020022 c 118903 112020 20020022 c 118903
  //   112020 20020022 c 118903 112020 20020022 c 118903 112020 20020022 c 118903 112020 20020022 c 118903
  //   112020 20020022 c 118903 112020 20020022 c 20100001 109fc0 139fc3 8021 2012000c 24160003 26100001
  //   3210000f 20080008 20090001 139900 2709825 132020 20020022 c 1094022 1500fff9 22100001 2018000f
  //   2188024 108700 20080008 20090001 139902 2709825 132021 20020022 c 1094022 1500fff9 108702 2c9b022
  //   12c00001 8100050 4020 1084027 84400 3508ffff 82021 20020022 c 2010ffff 20110000 ae300000 22100001
  //   22310004 ae300000 22100001 22310004 ae300000 22100001 22310004 ae300000 22100001 22310004 ae300000
  //   22100001 22310004 ae300000 22100001 22310004 ae300000 22100001 22310004 ae300000 22100001 22310004
  //   ae300000 22100001 22310004 ae300000 22100001 22310004 ae300000 22100001 22310004 ae300000 22100001
  //   22310004 ae300000 22100001 22310004 ae300000 22100001 22310004 ae300000 22100001 22310004 ae300000
  //   22100001 22310004 22100001 8020 2011003c 8e130000 8e340000 274402a 11000002 ae330000 ae140000
  //   2231fffc 1611fff8 102020 20020022 c 22100004 2011003c 1611fff2 20020032 c 20080001 20110010 112020
  //   20020022 c 200b0020 2288823 112020 20020022 c 216bffff 1560fffa 2002000a c 200b0008 3c11fedc
  //   3631ffff 112020 20020022 c 3c11ba98 112020 c 3c117654 112020 c 3c113210 112020 c 216bffff 1560fff0
  //   2002000a c 20090000 200b0020 34118483 20120401 118c00 129400 36318281 22520401 ad310000 2328820
  //   21290004 216bffff 1560fffb 20020022 200b0020 20090000 91310000 112020 20020022 c 21290004 216bffff
  //   1560fff9 2002000a c 2011000f 112020 20020022 c 2231ffff 621fffb 2002000a c 2002000a c 20100000
  //   22100001 102020 20020022 c 22100002 102020 20020022 c 22100003 102020 20020022 c 22100004 102020
  //   20020022 c 22100005 102020 20020022 c 22100006 102020 20020022 c 22100007 102020 20020022 c 22100008
  //   102020 20020022 20020022 c 3e00008
  //   OP
  //   Func
  //   rs
  //   指令字
  //   rt
  //   rd
  //   数码管输出应该用寄存器锁存，否则显示数据只能一闪而过
  //   JMP
  //   JR
  //   OP
  //   Func
  //   Syscall
  //   Beq
  //   Bgez
  //   Bne
  //   MemToReg
  //   MemWrite
  //   AluOP
  //   AluSrcB
  //   RegWrite
  //   JAL
  //   RegDst
  //   数据存储器
  //   为方便自动评测，需要输出PC，IR，寄存器堆写如数据RDin
  //   RAM写使能MemWrite、RAM写入数据MDin等信号
endmodule

// 24+4条扩展指令控制器
module \_24_4条扩展指令控制器  (
  input  [5:0] OP,
  input  [5:0] Func,
  output [3:0] ALU_OP,
  output MemToReg,
  output MemWrite,
  output ALU_SRC,
  output RegWrite,
  output SysCALL,
  output SignedExt,
  output RegDst,
  output Beq,
  output Bne,
  output JR,
  output JMP,
  output JAL,
  output LUI,
  output LBU,
  output BGEZ
);

  \_24_4条扩展指令运算信号生成  \u_24_4条扩展指令运算信号生成_1  (
    .OP0(OP[0]), .OP1(OP[1]), .OP2(OP[2]), .OP3(OP[3]), .OP4(OP[4]), .OP5(OP[5]), .F0(Func[0]), .F1(Func[1]),
    .F2(Func[2]), .F3(Func[3]), .F4(Func[4]), .F5(Func[5]), .S0(ALU_OP[0]), .S1(ALU_OP[1]), .S2(ALU_OP[2]),
    .S3(ALU_OP[3]));
  \_24_4条扩展指令控制信号生成  \u_24_4条扩展指令控制信号生成_1  (
    .OP0(OP[0]), .OP1(OP[1]), .OP2(OP[2]), .OP3(OP[3]), .OP4(OP[4]), .OP5(OP[5]), .F0(Func[0]), .F1(Func[1]),
    .F2(Func[2]), .F3(Func[3]), .F4(Func[4]), .F5(Func[5]), .MemToReg(MemToReg), .MemWrite(MemWrite),
    .ALU_SRC(ALU_SRC), .RegWrite(RegWrite), .SysCALL(SysCALL), .SignedExt(SignedExt), .RegDst(RegDst),
    .BEQ(Beq), .BNE(Bne), .JR(JR), .JUMP(JMP), .JAL(JAL), .LUI(LUI), .LBU(LBU), .BGEZ(BGEZ));

  // Other names for the same wires on the sheet: OP_CODE[5:0] = OP

  // Notes on the sheet:
  //   运算器控制器，根据指令生成运算器功能选择信号
  //   控制信号生成，产生数据通路需要的其他控制信号
endmodule

// 24+4条扩展指令运算信号
module \_24_4条扩展指令运算信号生成  (
  input  OP0,
  input  OP1,
  input  OP2,
  input  OP3,
  input  OP4,
  input  OP5,
  input  F0,
  input  F1,
  input  F2,
  input  F3,
  input  F4,
  input  F5,
  output S0,
  output S1,
  output S2,
  output S3
);

  wire and_1_out, and_2_out, and_3_out, and_4_out, and_5_out, and_6_out, and_7_out, and_8_out, and_9_out,
       and_10_out, and_11_out, and_12_out, and_13_out, and_14_out, and_15_out, and_16_out, and_17_out,
       and_18_out, and_19_out, and_20_out, and_21_out, and_22_out, and_23_out, and_24_out, and_25_out,
       and_26_out, and_27_out, and_28_out, and_29_out, and_30_out, and_31_out, and_32_out, and_33_out,
       and_34_out, and_35_out, and_36_out, and_37_out, and_38_out, and_39_out, and_40_out, and_41_out,
       not_1_out, not_2_out, not_3_out, not_4_out, not_5_out, not_6_out, not_7_out, not_8_out, not_9_out,
       not_10_out, not_11_out, not_12_out, not_13_out, not_14_out, not_15_out, not_16_out, not_17_out,
       not_18_out, not_19_out, not_20_out, not_21_out, not_22_out, not_23_out, not_24_out, not_25_out,
       not_26_out, not_27_out, not_28_out, not_29_out, not_30_out, not_31_out, not_32_out, not_33_out,
       not_34_out, not_35_out, not_36_out, not_37_out, not_38_out, not_39_out, not_40_out, not_41_out,
       not_42_out, not_43_out, not_44_out, not_45_out, not_46_out, not_47_out, not_48_out, not_49_out,
       not_50_out, not_51_out, not_52_out, not_53_out, not_54_out, not_55_out, not_56_out, not_57_out,
       not_58_out, not_59_out, not_60_out, not_61_out, not_62_out, not_63_out, not_64_out, not_65_out,
       not_66_out, not_67_out, not_68_out, not_69_out, not_70_out, not_71_out, not_72_out, not_73_out,
       not_74_out, not_75_out, not_76_out, not_77_out, not_78_out, not_79_out, not_80_out, not_81_out,
       not_82_out, not_83_out, not_84_out, not_85_out, not_86_out, not_87_out, not_88_out, not_89_out,
       not_90_out, not_91_out, not_92_out, not_93_out, not_94_out, not_95_out, not_96_out, not_97_out,
       not_98_out, not_99_out, not_100_out, not_101_out, not_102_out, not_103_out, not_104_out, not_105_out,
       not_106_out, not_107_out, not_108_out, not_109_out, not_110_out, not_111_out, not_112_out,
       not_113_out, not_114_out, not_115_out, not_116_out, not_117_out, not_118_out, not_119_out,
       not_120_out, not_121_out, not_122_out, not_123_out, not_124_out, not_125_out, not_126_out,
       not_127_out, not_128_out, not_129_out, not_130_out, not_131_out, not_132_out, not_133_out,
       not_134_out, not_135_out, not_136_out, not_137_out, not_138_out, not_139_out, not_140_out,
       not_141_out, not_142_out, not_143_out, not_144_out, not_145_out, not_146_out, not_147_out,
       not_148_out, not_149_out, not_150_out, not_151_out, not_152_out, not_153_out, not_154_out,
       not_155_out, not_156_out, not_157_out, not_158_out, not_159_out, not_160_out, not_161_out,
       not_162_out, not_163_out, not_164_out, not_165_out, not_166_out, not_167_out, not_168_out,
       not_169_out, not_170_out, not_171_out, not_172_out, not_173_out, not_174_out, not_175_out,
       not_176_out, not_177_out, not_178_out, not_179_out, not_180_out, not_181_out, not_182_out,
       not_183_out, not_184_out, not_185_out, not_186_out, not_187_out, not_188_out, not_189_out,
       not_190_out, not_191_out, not_192_out, not_193_out, not_194_out, not_195_out, not_196_out,
       not_197_out, not_198_out, not_199_out, not_200_out, not_201_out, not_202_out, not_203_out,
       not_204_out, not_205_out, not_206_out, not_207_out, not_208_out, not_209_out, not_210_out,
       not_211_out, not_212_out, not_213_out, not_214_out, not_215_out, not_216_out, not_217_out,
       not_218_out, not_219_out, not_220_out, not_221_out, not_222_out, not_223_out, not_224_out,
       not_225_out, not_226_out, not_227_out, not_228_out, not_229_out, not_230_out, not_231_out,
       not_232_out, not_233_out, not_234_out, not_235_out, not_236_out, not_237_out, not_238_out,
       not_239_out, not_240_out, not_241_out, not_242_out, not_243_out, not_244_out, not_245_out,
       not_246_out, not_247_out, not_248_out, not_249_out, not_250_out, not_251_out, not_252_out,
       not_253_out, not_254_out, not_255_out, not_256_out, not_257_out, not_258_out, not_259_out,
       not_260_out, not_261_out, not_262_out, not_263_out, not_264_out, not_265_out, not_266_out,
       not_267_out, not_268_out, not_269_out, not_270_out, not_271_out, not_272_out, not_273_out,
       not_274_out, not_275_out, not_276_out, not_277_out;

  not not_1 (not_1_out, OP5);
  not not_2 (not_2_out, OP4);
  not not_3 (not_3_out, OP3);
  not not_4 (not_4_out, OP2);
  not not_5 (not_5_out, OP1);
  not not_6 (not_6_out, OP0);
  not not_7 (not_7_out, F5);
  not not_8 (not_8_out, F4);
  not not_9 (not_9_out, F3);
  not not_10 (not_10_out, F2);
  not not_11 (not_11_out, OP5);
  not not_12 (not_12_out, OP4);
  not not_13 (not_13_out, OP3);
  not not_14 (not_14_out, OP2);
  not not_15 (not_15_out, OP1);
  not not_16 (not_16_out, OP0);
  not not_17 (not_17_out, F4);
  not not_18 (not_18_out, F3);
  not not_19 (not_19_out, F2);
  not not_20 (not_20_out, F1);
  not not_21 (not_21_out, F0);
  not not_22 (not_22_out, OP5);
  not not_23 (not_23_out, OP4);
  not not_24 (not_24_out, OP3);
  not not_25 (not_25_out, OP2);
  not not_26 (not_26_out, OP1);
  not not_27 (not_27_out, OP0);
  not not_28 (not_28_out, F4);
  not not_29 (not_29_out, F3);
  not not_30 (not_30_out, F2);
  not not_31 (not_31_out, F1);
  not not_32 (not_32_out, OP5);
  not not_33 (not_33_out, OP4);
  not not_34 (not_34_out, OP3);
  not not_35 (not_35_out, OP2);
  not not_36 (not_36_out, OP1);
  not not_37 (not_37_out, OP0);
  not not_38 (not_38_out, F4);
  not not_39 (not_39_out, F3);
  not not_40 (not_40_out, F1);
  not not_41 (not_41_out, F0);
  not not_42 (not_42_out, OP5);
  not not_43 (not_43_out, OP4);
  not not_44 (not_44_out, OP3);
  not not_45 (not_45_out, OP2);
  not not_46 (not_46_out, OP1);
  not not_47 (not_47_out, OP0);
  not not_48 (not_48_out, F4);
  not not_49 (not_49_out, F2);
  not not_50 (not_50_out, F0);
  not not_51 (not_51_out, OP5);
  not not_52 (not_52_out, OP4);
  not not_53 (not_53_out, OP2);
  not not_54 (not_54_out, OP1);
  not not_55 (not_55_out, OP0);
  not not_56 (not_56_out, OP5);
  not not_57 (not_57_out, OP4);
  not not_58 (not_58_out, OP1);
  not not_59 (not_59_out, OP0);
  not not_60 (not_60_out, OP5);
  not not_61 (not_61_out, OP4);
  not not_62 (not_62_out, OP2);
  not not_63 (not_63_out, OP1);
  not not_64 (not_64_out, OP5);
  not not_65 (not_65_out, OP4);
  not not_66 (not_66_out, OP2);
  not not_67 (not_67_out, OP0);
  not not_68 (not_68_out, OP4);
  not not_69 (not_69_out, OP3);
  not not_70 (not_70_out, OP2);
  not not_71 (not_71_out, OP4);
  not not_72 (not_72_out, OP2);
  not not_73 (not_73_out, OP4);
  not not_74 (not_74_out, OP3);
  not not_75 (not_75_out, OP1);
  not not_76 (not_76_out, OP0);
  not not_77 (not_77_out, OP5);
  not not_78 (not_78_out, OP4);
  not not_79 (not_79_out, OP3);
  not not_80 (not_80_out, OP2);
  not not_81 (not_81_out, OP1);
  not not_82 (not_82_out, OP5);
  not not_83 (not_83_out, OP4);
  not not_84 (not_84_out, OP3);
  not not_85 (not_85_out, OP2);
  not not_86 (not_86_out, OP1);
  not not_87 (not_87_out, OP0);
  not not_88 (not_88_out, F5);
  not not_89 (not_89_out, F4);
  not not_90 (not_90_out, F3);
  not not_91 (not_91_out, F2);
  not not_92 (not_92_out, F0);
  not not_93 (not_93_out, OP5);
  not not_94 (not_94_out, OP4);
  not not_95 (not_95_out, OP3);
  not not_96 (not_96_out, OP2);
  not not_97 (not_97_out, OP1);
  not not_98 (not_98_out, OP0);
  not not_99 (not_99_out, F4);
  not not_100 (not_100_out, F3);
  not not_101 (not_101_out, F2);
  not not_102 (not_102_out, F0);
  not not_103 (not_103_out, OP5);
  not not_104 (not_104_out, OP4);
  not not_105 (not_105_out, OP3);
  not not_106 (not_106_out, OP2);
  not not_107 (not_107_out, OP1);
  not not_108 (not_108_out, OP0);
  not not_109 (not_109_out, F4);
  not not_110 (not_110_out, F3);
  not not_111 (not_111_out, F1);
  not not_112 (not_112_out, F0);
  not not_113 (not_113_out, OP5);
  not not_114 (not_114_out, OP4);
  not not_115 (not_115_out, OP3);
  not not_116 (not_116_out, OP2);
  not not_117 (not_117_out, OP1);
  not not_118 (not_118_out, OP0);
  not not_119 (not_119_out, F4);
  not not_120 (not_120_out, F3);
  not not_121 (not_121_out, OP5);
  not not_122 (not_122_out, OP4);
  not not_123 (not_123_out, OP3);
  not not_124 (not_124_out, OP2);
  not not_125 (not_125_out, OP1);
  not not_126 (not_126_out, OP0);
  not not_127 (not_127_out, F4);
  not not_128 (not_128_out, F2);
  not not_129 (not_129_out, F0);
  not not_130 (not_130_out, OP5);
  not not_131 (not_131_out, OP4);
  not not_132 (not_132_out, OP1);
  not not_133 (not_133_out, OP0);
  not not_134 (not_134_out, OP5);
  not not_135 (not_135_out, OP4);
  not not_136 (not_136_out, OP2);
  not not_137 (not_137_out, OP0);
  not not_138 (not_138_out, OP5);
  not not_139 (not_139_out, OP4);
  not not_140 (not_140_out, OP3);
  not not_141 (not_141_out, OP2);
  not not_142 (not_142_out, OP1);
  not not_143 (not_143_out, OP0);
  not not_144 (not_144_out, F4);
  not not_145 (not_145_out, F3);
  not not_146 (not_146_out, F2);
  not not_147 (not_147_out, OP5);
  not not_148 (not_148_out, OP4);
  not not_149 (not_149_out, OP3);
  not not_150 (not_150_out, OP2);
  not not_151 (not_151_out, OP1);
  not not_152 (not_152_out, OP5);
  not not_153 (not_153_out, OP4);
  not not_154 (not_154_out, OP3);
  not not_155 (not_155_out, OP2);
  not not_156 (not_156_out, OP1);
  not not_157 (not_157_out, OP0);
  not not_158 (not_158_out, F4);
  not not_159 (not_159_out, F3);
  not not_160 (not_160_out, F2);
  not not_161 (not_161_out, F1);
  not not_162 (not_162_out, F0);
  not not_163 (not_163_out, OP5);
  not not_164 (not_164_out, OP4);
  not not_165 (not_165_out, OP3);
  not not_166 (not_166_out, OP2);
  not not_167 (not_167_out, OP1);
  not not_168 (not_168_out, OP0);
  not not_169 (not_169_out, F4);
  not not_170 (not_170_out, F3);
  not not_171 (not_171_out, F2);
  not not_172 (not_172_out, F1);
  not not_173 (not_173_out, OP5);
  not not_174 (not_174_out, OP4);
  not not_175 (not_175_out, OP3);
  not not_176 (not_176_out, OP2);
  not not_177 (not_177_out, OP1);
  not not_178 (not_178_out, OP0);
  not not_179 (not_179_out, F4);
  not not_180 (not_180_out, F3);
  not not_181 (not_181_out, F2);
  not not_182 (not_182_out, F0);
  not not_183 (not_183_out, OP5);
  not not_184 (not_184_out, OP4);
  not not_185 (not_185_out, OP3);
  not not_186 (not_186_out, OP2);
  not not_187 (not_187_out, OP1);
  not not_188 (not_188_out, OP0);
  not not_189 (not_189_out, F4);
  not not_190 (not_190_out, F3);
  not not_191 (not_191_out, F1);
  not not_192 (not_192_out, F0);
  not not_193 (not_193_out, OP5);
  not not_194 (not_194_out, OP4);
  not not_195 (not_195_out, OP3);
  not not_196 (not_196_out, OP2);
  not not_197 (not_197_out, OP1);
  not not_198 (not_198_out, OP0);
  not not_199 (not_199_out, F4);
  not not_200 (not_200_out, F2);
  not not_201 (not_201_out, OP5);
  not not_202 (not_202_out, OP4);
  not not_203 (not_203_out, OP2);
  not not_204 (not_204_out, OP1);
  not not_205 (not_205_out, OP0);
  not not_206 (not_206_out, OP5);
  not not_207 (not_207_out, OP4);
  not not_208 (not_208_out, OP1);
  not not_209 (not_209_out, OP0);
  not not_210 (not_210_out, OP5);
  not not_211 (not_211_out, OP4);
  not not_212 (not_212_out, OP2);
  not not_213 (not_213_out, OP1);
  not not_214 (not_214_out, OP4);
  not not_215 (not_215_out, OP3);
  not not_216 (not_216_out, OP2);
  not not_217 (not_217_out, OP4);
  not not_218 (not_218_out, OP2);
  not not_219 (not_219_out, OP5);
  not not_220 (not_220_out, OP4);
  not not_221 (not_221_out, OP3);
  not not_222 (not_222_out, OP2);
  not not_223 (not_223_out, OP1);
  not not_224 (not_224_out, OP0);
  not not_225 (not_225_out, F4);
  not not_226 (not_226_out, F3);
  not not_227 (not_227_out, F2);
  not not_228 (not_228_out, OP4);
  not not_229 (not_229_out, OP3);
  not not_230 (not_230_out, OP1);
  not not_231 (not_231_out, OP0);
  not not_232 (not_232_out, OP5);
  not not_233 (not_233_out, OP4);
  not not_234 (not_234_out, OP3);
  not not_235 (not_235_out, OP2);
  not not_236 (not_236_out, OP1);
  not not_237 (not_237_out, OP0);
  not not_238 (not_238_out, F4);
  not not_239 (not_239_out, F3);
  not not_240 (not_240_out, F1);
  not not_241 (not_241_out, OP5);
  not not_242 (not_242_out, OP4);
  not not_243 (not_243_out, OP3);
  not not_244 (not_244_out, OP2);
  not not_245 (not_245_out, OP1);
  not not_246 (not_246_out, OP0);
  not not_247 (not_247_out, F4);
  not not_248 (not_248_out, F3);
  not not_249 (not_249_out, OP5);
  not not_250 (not_250_out, OP4);
  not not_251 (not_251_out, OP3);
  not not_252 (not_252_out, OP2);
  not not_253 (not_253_out, OP1);
  not not_254 (not_254_out, OP0);
  not not_255 (not_255_out, F4);
  not not_256 (not_256_out, F2);
  not not_257 (not_257_out, F0);
  not not_258 (not_258_out, OP5);
  not not_259 (not_259_out, OP4);
  not not_260 (not_260_out, OP3);
  not not_261 (not_261_out, OP2);
  not not_262 (not_262_out, OP1);
  not not_263 (not_263_out, OP0);
  not not_264 (not_264_out, F4);
  not not_265 (not_265_out, F2);
  not not_266 (not_266_out, OP5);
  not not_267 (not_267_out, OP4);
  not not_268 (not_268_out, OP2);
  not not_269 (not_269_out, OP0);
  not not_270 (not_270_out, OP5);
  not not_271 (not_271_out, OP4);
  not not_272 (not_272_out, OP1);
  not not_273 (not_273_out, OP5);
  not not_274 (not_274_out, OP4);
  not not_275 (not_275_out, OP3);
  not not_276 (not_276_out, OP2);
  not not_277 (not_277_out, OP1);
  and and_1 (and_1_out, not_1_out, not_2_out, not_3_out, not_4_out, not_5_out, not_6_out, not_7_out, not_8_out, not_9_out, not_10_out, F1, F0);
  and and_2 (and_2_out, not_11_out, not_12_out, not_13_out, not_14_out, not_15_out, not_16_out, F5, not_17_out, not_18_out, not_19_out, not_20_out, not_21_out);
  and and_3 (and_3_out, not_22_out, not_23_out, not_24_out, not_25_out, not_26_out, not_27_out, F5, not_28_out, not_29_out, not_30_out, not_31_out, F0);
  and and_4 (and_4_out, not_32_out, not_33_out, not_34_out, not_35_out, not_36_out, not_37_out, F5, not_38_out, not_39_out, F2, not_40_out, not_41_out);
  and and_5 (and_5_out, not_42_out, not_43_out, not_44_out, not_45_out, not_46_out, not_47_out, F5, not_48_out, F3, not_49_out, F1, not_50_out);
  and and_6 (and_6_out, not_51_out, not_52_out, OP3, not_53_out, not_54_out, not_55_out);
  and and_7 (and_7_out, not_56_out, not_57_out, OP3, OP2, not_58_out, not_59_out);
  and and_8 (and_8_out, not_60_out, not_61_out, OP3, not_62_out, not_63_out, OP0);
  and and_9 (and_9_out, not_64_out, not_65_out, OP3, not_66_out, OP1, not_67_out);
  and and_10 (and_10_out, OP5, not_68_out, not_69_out, not_70_out, OP1, OP0);
  and and_11 (and_11_out, OP5, not_71_out, OP3, not_72_out, OP1, OP0);
  and and_12 (and_12_out, OP5, not_73_out, not_74_out, OP2, not_75_out, not_76_out);
  and and_13 (and_13_out, not_77_out, not_78_out, not_79_out, not_80_out, not_81_out, OP0);
  and and_14 (and_14_out, not_82_out, not_83_out, not_84_out, not_85_out, not_86_out, not_87_out, not_88_out, not_89_out, not_90_out, not_91_out, F1, not_92_out);
  and and_15 (and_15_out, not_93_out, not_94_out, not_95_out, not_96_out, not_97_out, not_98_out, F5, not_99_out, not_100_out, not_101_out, F1, not_102_out);
  and and_16 (and_16_out, not_103_out, not_104_out, not_105_out, not_106_out, not_107_out, not_108_out, F5, not_109_out, not_110_out, F2, not_111_out, not_112_out);
  and and_17 (and_17_out, not_113_out, not_114_out, not_115_out, not_116_out, not_117_out, not_118_out, F5, not_119_out, not_120_out, F2, F1, F0);
  and and_18 (and_18_out, not_121_out, not_122_out, not_123_out, not_124_out, not_125_out, not_126_out, F5, not_127_out, F3, not_128_out, F1, not_129_out);
  and and_19 (and_19_out, not_130_out, not_131_out, OP3, OP2, not_132_out, not_133_out);
  and and_20 (and_20_out, not_134_out, not_135_out, OP3, not_136_out, OP1, not_137_out);
  and and_21 (and_21_out, not_138_out, not_139_out, not_140_out, not_141_out, not_142_out, not_143_out, F5, not_144_out, not_145_out, not_146_out, F1, F0);
  and and_22 (and_22_out, not_147_out, not_148_out, not_149_out, not_150_out, not_151_out, OP0);
  and and_23 (and_23_out, not_152_out, not_153_out, not_154_out, not_155_out, not_156_out, not_157_out, F5, not_158_out, not_159_out, not_160_out, not_161_out, not_162_out);
  and and_24 (and_24_out, not_163_out, not_164_out, not_165_out, not_166_out, not_167_out, not_168_out, F5, not_169_out, not_170_out, not_171_out, not_172_out, F0);
  and and_25 (and_25_out, not_173_out, not_174_out, not_175_out, not_176_out, not_177_out, not_178_out, F5, not_179_out, not_180_out, not_181_out, F1, not_182_out);
  and and_26 (and_26_out, not_183_out, not_184_out, not_185_out, not_186_out, not_187_out, not_188_out, F5, not_189_out, not_190_out, F2, not_191_out, not_192_out);
  and and_27 (and_27_out, not_193_out, not_194_out, not_195_out, not_196_out, not_197_out, not_198_out, F5, not_199_out, F3, not_200_out, F1, F0);
  and and_28 (and_28_out, not_201_out, not_202_out, OP3, not_203_out, not_204_out, not_205_out);
  and and_29 (and_29_out, not_206_out, not_207_out, OP3, OP2, not_208_out, not_209_out);
  and and_30 (and_30_out, not_210_out, not_211_out, OP3, not_212_out, not_213_out, OP0);
  and and_31 (and_31_out, OP5, not_214_out, not_215_out, not_216_out, OP1, OP0);
  and and_32 (and_32_out, OP5, not_217_out, OP3, not_218_out, OP1, OP0);
  and and_33 (and_33_out, not_219_out, not_220_out, not_221_out, not_222_out, not_223_out, not_224_out, F5, not_225_out, not_226_out, not_227_out, F1, F0);
  and and_34 (and_34_out, OP5, not_228_out, not_229_out, OP2, not_230_out, not_231_out);
  and and_35 (and_35_out, not_232_out, not_233_out, not_234_out, not_235_out, not_236_out, not_237_out, F5, not_238_out, not_239_out, F2, not_240_out, F0);
  and and_36 (and_36_out, not_241_out, not_242_out, not_243_out, not_244_out, not_245_out, not_246_out, F5, not_247_out, not_248_out, F2, F1, F0);
  and and_37 (and_37_out, not_249_out, not_250_out, not_251_out, not_252_out, not_253_out, not_254_out, F5, not_255_out, F3, not_256_out, F1, not_257_out);
  and and_38 (and_38_out, not_258_out, not_259_out, not_260_out, not_261_out, not_262_out, not_263_out, F5, not_264_out, F3, not_265_out, F1, F0);
  and and_39 (and_39_out, not_266_out, not_267_out, OP3, not_268_out, OP1, not_269_out);
  and and_40 (and_40_out, not_270_out, not_271_out, OP3, OP2, not_272_out, OP0);
  and and_41 (and_41_out, not_273_out, not_274_out, not_275_out, not_276_out, not_277_out, OP0);
  or or_1 (S1, and_14_out, and_15_out, and_16_out, and_17_out, and_18_out, and_19_out, and_20_out, and_21_out, and_22_out);
  or or_2 (S3, and_35_out, and_36_out, and_37_out, and_38_out, and_39_out, and_40_out, and_41_out);
  or or_3 (S0, and_1_out, and_2_out, and_3_out, and_4_out, and_5_out, and_6_out, and_7_out, and_8_out, and_9_out, and_10_out, and_11_out, and_12_out, and_13_out);
  or or_4 (S2, and_23_out, and_24_out, and_25_out, and_26_out, and_27_out, and_28_out, and_29_out, and_30_out, and_31_out, and_32_out, and_33_out, and_34_out);
endmodule

// 24+4条扩展指令控制信号
module \_24_4条扩展指令控制信号生成  (
  input  OP0,
  input  OP1,
  input  OP2,
  input  OP3,
  input  OP4,
  input  OP5,
  input  F0,
  input  F1,
  input  F2,
  input  F3,
  input  F4,
  input  F5,
  output MemToReg,
  output MemWrite,
  output ALU_SRC,
  output RegWrite,
  output SysCALL,
  output SignedExt,
  output RegDst,
  output BEQ,
  output BNE,
  output JR,
  output JUMP,
  output JAL,
  output LUI,
  output LBU,
  output BGEZ
);

  wire and_1_out, and_2_out, and_4_out, and_5_out, and_6_out, and_7_out, and_8_out, and_9_out, and_10_out,
       and_11_out, and_12_out, and_13_out, and_14_out, and_15_out, and_16_out, and_17_out, and_18_out,
       and_20_out, and_21_out, and_22_out, and_23_out, and_24_out, and_25_out, and_26_out, and_27_out,
       and_28_out, and_29_out, not_1_out, not_2_out, not_3_out, not_4_out, not_5_out, not_6_out, not_7_out,
       not_8_out, not_9_out, not_10_out, not_11_out, not_12_out, not_13_out, not_14_out, not_15_out,
       not_16_out, not_17_out, not_18_out, not_19_out, not_20_out, not_21_out, not_22_out, not_23_out,
       not_24_out, not_25_out, not_26_out, not_27_out, not_28_out, not_29_out, not_30_out, not_31_out,
       not_32_out, not_33_out, not_34_out, not_35_out, not_36_out, not_37_out, not_38_out, not_39_out,
       not_40_out, not_41_out, not_42_out, not_43_out, not_44_out, not_45_out, not_46_out, not_47_out,
       not_48_out, not_49_out, not_50_out, not_51_out, not_52_out, not_53_out, not_54_out, not_55_out,
       not_56_out, not_57_out, not_58_out, not_59_out, not_60_out, not_61_out, not_62_out, not_63_out,
       not_64_out, not_65_out, not_66_out, not_67_out, not_68_out, not_69_out, not_70_out, not_71_out,
       not_72_out, not_73_out, not_74_out, not_75_out, not_76_out, not_77_out, not_78_out, not_79_out,
       not_80_out, not_81_out, not_82_out, not_83_out, not_84_out, not_85_out, not_86_out, not_87_out,
       not_88_out, not_89_out, not_90_out, not_91_out, not_92_out, not_93_out, not_94_out, not_95_out,
       not_96_out, not_97_out, not_98_out, not_99_out, not_100_out, not_101_out, not_102_out, not_103_out,
       not_104_out, not_105_out, not_106_out, not_107_out, not_108_out, not_109_out, not_110_out,
       not_111_out, not_112_out, not_113_out, not_114_out, not_115_out, not_116_out, not_117_out,
       not_118_out, not_119_out, not_120_out, not_121_out, not_122_out, not_123_out, not_124_out,
       not_125_out, not_126_out, not_127_out, not_128_out, not_129_out, not_130_out, not_131_out,
       not_132_out, not_133_out, not_134_out, not_135_out, not_136_out, not_137_out, not_138_out,
       not_139_out, not_140_out, not_141_out, not_142_out, not_143_out, not_144_out, not_145_out,
       not_146_out, not_147_out, not_148_out, not_149_out, not_150_out, not_151_out, not_152_out,
       not_153_out, not_154_out, not_155_out, not_156_out, not_157_out, not_158_out, not_159_out,
       not_160_out, not_161_out, not_162_out, not_163_out, not_164_out, not_165_out, not_166_out,
       not_167_out, not_168_out, not_169_out, not_170_out, not_171_out, not_172_out, not_173_out,
       not_174_out, not_175_out, not_176_out, not_177_out, not_178_out, not_179_out, not_180_out,
       not_181_out, not_182_out, not_183_out, not_184_out, not_185_out, not_186_out, not_187_out,
       not_188_out, not_189_out, not_190_out, not_191_out;

  not not_1 (not_1_out, OP0);
  not not_2 (not_2_out, OP1);
  not not_3 (not_3_out, OP3);
  not not_4 (not_4_out, OP4);
  not not_5 (not_5_out, OP2);
  not not_6 (not_6_out, OP3);
  not not_7 (not_7_out, OP4);
  not not_8 (not_8_out, OP2);
  not not_9 (not_9_out, OP4);
  not not_10 (not_10_out, OP0);
  not not_11 (not_11_out, OP2);
  not not_12 (not_12_out, OP4);
  not not_13 (not_13_out, OP5);
  not not_14 (not_14_out, OP1);
  not not_15 (not_15_out, OP4);
  not not_16 (not_16_out, OP5);
  not not_17 (not_17_out, OP0);
  not not_18 (not_18_out, OP1);
  not not_19 (not_19_out, OP3);
  not not_20 (not_20_out, OP4);
  not not_21 (not_21_out, OP4);
  not not_22 (not_22_out, OP5);
  not not_23 (not_23_out, OP2);
  not not_24 (not_24_out, OP4);
  not not_25 (not_25_out, OP0);
  not not_26 (not_26_out, OP1);
  not not_27 (not_27_out, OP2);
  not not_28 (not_28_out, OP4);
  not not_29 (not_29_out, OP5);
  not not_30 (not_30_out, F0);
  not not_31 (not_31_out, F2);
  not not_32 (not_32_out, F3);
  not not_33 (not_33_out, F4);
  not not_34 (not_34_out, OP0);
  not not_35 (not_35_out, OP1);
  not not_36 (not_36_out, OP2);
  not not_37 (not_37_out, OP4);
  not not_38 (not_38_out, OP5);
  not not_39 (not_39_out, F1);
  not not_40 (not_40_out, F3);
  not not_41 (not_41_out, F4);
  not not_42 (not_42_out, OP0);
  not not_43 (not_43_out, OP1);
  not not_44 (not_44_out, OP2);
  not not_45 (not_45_out, OP4);
  not not_46 (not_46_out, OP5);
  not not_47 (not_47_out, F2);
  not not_48 (not_48_out, F3);
  not not_49 (not_49_out, F4);
  not not_50 (not_50_out, OP0);
  not not_51 (not_51_out, OP1);
  not not_52 (not_52_out, OP2);
  not not_53 (not_53_out, OP4);
  not not_54 (not_54_out, OP5);
  not not_55 (not_55_out, F2);
  not not_56 (not_56_out, F4);
  not not_57 (not_57_out, OP0);
  not not_58 (not_58_out, OP1);
  not not_59 (not_59_out, OP2);
  not not_60 (not_60_out, OP4);
  not not_61 (not_61_out, OP5);
  not not_62 (not_62_out, F3);
  not not_63 (not_63_out, F4);
  not not_64 (not_64_out, OP0);
  not not_65 (not_65_out, OP2);
  not not_66 (not_66_out, OP4);
  not not_67 (not_67_out, OP5);
  not not_68 (not_68_out, OP1);
  not not_69 (not_69_out, OP4);
  not not_70 (not_70_out, OP5);
  not not_71 (not_71_out, OP0);
  not not_72 (not_72_out, OP1);
  not not_73 (not_73_out, OP3);
  not not_74 (not_74_out, OP4);
  not not_75 (not_75_out, OP4);
  not not_76 (not_76_out, OP5);
  not not_77 (not_77_out, OP2);
  not not_78 (not_78_out, OP3);
  not not_79 (not_79_out, OP4);
  not not_80 (not_80_out, OP0);
  not not_81 (not_81_out, OP1);
  not not_82 (not_82_out, OP2);
  not not_83 (not_83_out, OP3);
  not not_84 (not_84_out, OP4);
  not not_85 (not_85_out, OP5);
  not not_86 (not_86_out, F0);
  not not_87 (not_87_out, F1);
  not not_88 (not_88_out, F4);
  not not_89 (not_89_out, F5);
  not not_90 (not_90_out, OP0);
  not not_91 (not_91_out, OP2);
  not not_92 (not_92_out, OP4);
  not not_93 (not_93_out, OP5);
  not not_94 (not_94_out, OP0);
  not not_95 (not_95_out, OP1);
  not not_96 (not_96_out, OP3);
  not not_97 (not_97_out, OP4);
  not not_98 (not_98_out, OP1);
  not not_99 (not_99_out, OP3);
  not not_100 (not_100_out, OP4);
  not not_101 (not_101_out, OP5);
  not not_102 (not_102_out, OP1);
  not not_103 (not_103_out, OP2);
  not not_104 (not_104_out, OP4);
  not not_105 (not_105_out, OP5);
  not not_106 (not_106_out, OP2);
  not not_107 (not_107_out, OP4);
  not not_108 (not_108_out, OP0);
  not not_109 (not_109_out, OP1);
  not not_110 (not_110_out, OP2);
  not not_111 (not_111_out, OP3);
  not not_112 (not_112_out, OP4);
  not not_113 (not_113_out, OP5);
  not not_114 (not_114_out, F0);
  not not_115 (not_115_out, F2);
  not not_116 (not_116_out, F3);
  not not_117 (not_117_out, F4);
  not not_118 (not_118_out, OP0);
  not not_119 (not_119_out, OP1);
  not not_120 (not_120_out, OP2);
  not not_121 (not_121_out, OP3);
  not not_122 (not_122_out, OP4);
  not not_123 (not_123_out, OP5);
  not not_124 (not_124_out, F1);
  not not_125 (not_125_out, F3);
  not not_126 (not_126_out, F4);
  not not_127 (not_127_out, OP0);
  not not_128 (not_128_out, OP1);
  not not_129 (not_129_out, OP2);
  not not_130 (not_130_out, OP3);
  not not_131 (not_131_out, OP4);
  not not_132 (not_132_out, OP5);
  not not_133 (not_133_out, F2);
  not not_134 (not_134_out, F3);
  not not_135 (not_135_out, F4);
  not not_136 (not_136_out, OP0);
  not not_137 (not_137_out, OP1);
  not not_138 (not_138_out, OP2);
  not not_139 (not_139_out, OP3);
  not not_140 (not_140_out, OP4);
  not not_141 (not_141_out, OP5);
  not not_142 (not_142_out, F2);
  not not_143 (not_143_out, F4);
  not not_144 (not_144_out, OP0);
  not not_145 (not_145_out, OP1);
  not not_146 (not_146_out, OP2);
  not not_147 (not_147_out, OP3);
  not not_148 (not_148_out, OP4);
  not not_149 (not_149_out, OP5);
  not not_150 (not_150_out, F3);
  not not_151 (not_151_out, F4);
  not not_152 (not_152_out, OP0);
  not not_153 (not_153_out, OP1);
  not not_154 (not_154_out, OP3);
  not not_155 (not_155_out, OP4);
  not not_156 (not_156_out, OP5);
  not not_157 (not_157_out, OP1);
  not not_158 (not_158_out, OP3);
  not not_159 (not_159_out, OP4);
  not not_160 (not_160_out, OP5);
  not not_161 (not_161_out, OP0);
  not not_162 (not_162_out, OP1);
  not not_163 (not_163_out, OP2);
  not not_164 (not_164_out, OP3);
  not not_165 (not_165_out, OP4);
  not not_166 (not_166_out, OP5);
  not not_167 (not_167_out, F0);
  not not_168 (not_168_out, F1);
  not not_169 (not_169_out, F2);
  not not_170 (not_170_out, F4);
  not not_171 (not_171_out, F5);
  not not_172 (not_172_out, OP0);
  not not_173 (not_173_out, OP2);
  not not_174 (not_174_out, OP3);
  not not_175 (not_175_out, OP4);
  not not_176 (not_176_out, OP5);
  not not_177 (not_177_out, OP2);
  not not_178 (not_178_out, OP3);
  not not_179 (not_179_out, OP4);
  not not_180 (not_180_out, OP5);
  not not_181 (not_181_out, OP5);
  not not_182 (not_182_out, OP4);
  not not_183 (not_183_out, OP4);
  not not_184 (not_184_out, OP3);
  not not_185 (not_185_out, OP1);
  not not_186 (not_186_out, OP0);
  not not_187 (not_187_out, OP5);
  not not_188 (not_188_out, OP4);
  not not_189 (not_189_out, OP3);
  not not_190 (not_190_out, OP2);
  not not_191 (not_191_out, OP1);
  and and_1 (and_1_out, not_1_out, not_2_out, OP2, not_3_out, not_4_out, OP5);
  and and_2 (and_2_out, OP0, OP1, not_5_out, not_6_out, not_7_out, OP5);
  and and_3 (MemWrite, OP0, OP1, not_8_out, OP3, not_9_out, OP5);
  and and_4 (and_4_out, not_10_out, not_11_out, OP3, not_12_out, not_13_out);
  and and_5 (and_5_out, not_14_out, OP3, not_15_out, not_16_out);
  and and_6 (and_6_out, not_17_out, not_18_out, OP2, not_19_out, not_20_out, OP5);
  and and_7 (and_7_out, OP0, OP2, OP3, not_21_out, not_22_out);
  and and_8 (and_8_out, OP0, OP1, not_23_out, not_24_out, OP5);
  and and_9 (and_9_out, not_25_out, not_26_out, not_27_out, not_28_out, not_29_out, not_30_out, not_31_out, not_32_out, not_33_out);
  and and_10 (and_10_out, not_34_out, not_35_out, not_36_out, not_37_out, not_38_out, not_39_out, not_40_out, not_41_out, F5);
  and and_11 (and_11_out, not_42_out, not_43_out, not_44_out, not_45_out, not_46_out, F1, not_47_out, not_48_out, not_49_out);
  and and_12 (and_12_out, not_50_out, not_51_out, not_52_out, not_53_out, not_54_out, F1, not_55_out, not_56_out, F5);
  and and_13 (and_13_out, not_57_out, not_58_out, not_59_out, not_60_out, not_61_out, F0, not_62_out, not_63_out, F5);
  and and_14 (and_14_out, not_64_out, not_65_out, OP3, not_66_out, not_67_out);
  and and_15 (and_15_out, not_68_out, OP3, not_69_out, not_70_out);
  and and_16 (and_16_out, not_71_out, not_72_out, OP2, not_73_out, not_74_out, OP5);
  and and_17 (and_17_out, OP0, OP2, OP3, not_75_out, not_76_out);
  and and_18 (and_18_out, OP0, OP1, not_77_out, not_78_out, not_79_out);
  and and_19 (SysCALL, not_80_out, not_81_out, not_82_out, not_83_out, not_84_out, not_85_out, not_86_out, not_87_out, F2, F3, not_88_out, not_89_out);
  and and_20 (and_20_out, not_90_out, not_91_out, OP3, not_92_out, not_93_out);
  and and_21 (and_21_out, not_94_out, not_95_out, OP2, not_96_out, not_97_out);
  and and_22 (and_22_out, not_98_out, OP2, not_99_out, not_100_out, not_101_out);
  and and_23 (and_23_out, OP0, not_102_out, not_103_out, not_104_out, not_105_out);
  and and_24 (and_24_out, OP0, OP1, not_106_out, not_107_out, OP5);
  and and_25 (and_25_out, not_108_out, not_109_out, not_110_out, not_111_out, not_112_out, not_113_out, not_114_out, not_115_out, not_116_out, not_117_out);
  and and_26 (and_26_out, not_118_out, not_119_out, not_120_out, not_121_out, not_122_out, not_123_out, not_124_out, not_125_out, not_126_out, F5);
  and and_27 (and_27_out, not_127_out, not_128_out, not_129_out, not_130_out, not_131_out, not_132_out, F1, not_133_out, not_134_out, not_135_out);
  and and_28 (and_28_out, not_136_out, not_137_out, not_138_out, not_139_out, not_140_out, not_141_out, F1, not_142_out, not_143_out, F5);
  and and_29 (and_29_out, not_144_out, not_145_out, not_146_out, not_147_out, not_148_out, not_149_out, F0, not_150_out, not_151_out, F5);
  and and_30 (BEQ, not_152_out, not_153_out, OP2, not_154_out, not_155_out, not_156_out);
  and and_31 (BNE, OP0, not_157_out, OP2, not_158_out, not_159_out, not_160_out);
  and and_32 (JR, not_161_out, not_162_out, not_163_out, not_164_out, not_165_out, not_166_out, not_167_out, not_168_out, not_169_out, F3, not_170_out, not_171_out);
  and and_33 (JUMP, not_172_out, OP1, not_173_out, not_174_out, not_175_out, not_176_out);
  and and_34 (JAL, OP0, OP1, not_177_out, not_178_out, not_179_out, not_180_out);
  and and_35 (LUI, not_181_out, not_182_out, OP3, OP2, OP1, OP0);
  and and_36 (LBU, OP5, not_183_out, not_184_out, OP2, not_185_out, not_186_out);
  and and_37 (BGEZ, not_187_out, not_188_out, not_189_out, not_190_out, not_191_out, OP0);
  or or_1 (MemToReg, and_1_out, and_2_out);
  or or_2 (ALU_SRC, and_4_out, and_5_out, and_6_out, and_7_out, and_8_out);
  or or_3 (RegWrite, and_9_out, and_10_out, and_11_out, and_12_out, and_13_out, and_14_out, and_15_out, and_16_out, and_17_out, and_18_out);
  or or_4 (SignedExt, and_20_out, and_21_out, and_22_out, and_23_out, and_24_out);
  or or_5 (RegDst, and_25_out, and_26_out, and_27_out, and_28_out, and_29_out);
endmodule
module \_27_4条扩展指令电路  (
  input  IR1,
  input  IR2,
  input  IR3,
  output RegWrite,
  output MemWrite,
  output [31:0] PC,
  output [31:0] IR,
  output [31:0] RDin,
  output [31:0] MDin,
  output [31:0] LedData
);

  wire and_1_out, and_2_out, and_3_out, and_4_out, and_5_out, CLK, comparator_1_eq, ERET, Go, IR1_t, IR2_t,
       IR3_t, IRA, IRB, IRC, lbu, lui, MFC0, mips_alu_1_equal, MTC0, \n27_4条扩展指令控制器_1_alu_src ,
       \n27_4条扩展指令控制器_1_beq , \n27_4条扩展指令控制器_1_bgez , \n27_4条扩展指令控制器_1_bne , \n27_4条扩展指令控制器_1_jal ,
       \n27_4条扩展指令控制器_1_jmp , \n27_4条扩展指令控制器_1_jr , \n27_4条扩展指令控制器_1_memtoreg , \n27_4条扩展指令控制器_1_regdst ,
       not_1_out, not_3_out, not_4_out, or_1_out, or_2_out, or_6_out, PCok, register_2_q, RST, SignedExt,
       Syscall, W1, W2, W3;
  wire [3:0] \n27_4条扩展指令控制器_1_alu_op ;
  wire [4:0] multiplexer_4_out, multiplexer_5_out, multiplexer_6_out, multiplexer_7_out;
  wire [15:0] \总周期数 ;
  wire [31:0] adder_1_out, adder_2_out, bit_extender_1_out, bit_extender_2_out, bit_extender_3_out,
       mips_alu_1_result, multiplexer_3_out, multiplexer_8_out, multiplexer_9_out, multiplexer_11_out,
       multiplexer_12_out, multiplexer_13_out, multiplexer_14_out, PC1, PC2, R1, ram_1_data, shifter_1_out,
       shifter_2_out, shifter_3_out;

  Clock #(.highDuration(1), .lowDuration(1)) clock_1 (.out(CLK));
  Button _1 (.out(IRA));
  Button _2 (.out(IRB));
  Button _3 (.out(IRC));
  Button \u_总复位  (.out(RST));
  Button \u_继续运行  (.out(Go));
  LED #(.active("true")) led_1 (.in(W1));
  LED #(.active("true")) led_2 (.in(W2));
  LED #(.active("true")) led_3 (.in(W3));
  Multiplexer #(.select(1), .width(32), .disabled("Z"), .enable("false")) multiplexer_1 (
    .in0(adder_1_out), .in1(adder_2_out), .out(PC1), .sel(or_6_out));
  Multiplexer #(.select(1), .width(32), .disabled("Z"), .enable("false")) multiplexer_2 (
    .in0(PC1), .in1(shifter_3_out), .out(PC2), .sel(or_1_out));
  Register #(.width(32), .trigger("rising"), .Select("low")) u_PC (
    .D(multiplexer_3_out), .en(PCok), .Q(PC), .clk(CLK), .clr(RST));
  Multiplexer #(.select(1), .width(32), .disabled("Z"), .enable("false")) multiplexer_3 (
    .in0(PC2), .in1(R1), .out(multiplexer_3_out), .sel(\n27_4条扩展指令控制器_1_jr ));
  Comparator #(.width(32), .mode("twosComplement")) comparator_1 (
    .a(MDin), .b(32'h22), .eq(comparator_1_eq));  // open: gt, lt
  not not_1 (not_1_out, comparator_1_eq);
  Hex_Digit_Display hex_digit_display_1 (.value(LedData[31:28]));  // open: dp
  Hex_Digit_Display hex_digit_display_2 (.value(LedData[27:24]));  // open: dp
  or or_1 (or_1_out, \n27_4条扩展指令控制器_1_jal , \n27_4条扩展指令控制器_1_jmp );
  and and_1 (and_1_out, comparator_1_eq, Syscall);
  and and_2 (and_2_out, not_1_out, Syscall);
  Hex_Digit_Display hex_digit_display_3 (.value(LedData[23:20]));  // open: dp
  Hex_Digit_Display hex_digit_display_4 (.value(LedData[19:16]));  // open: dp
  Counter #(.width(16), .max('hffff), .ongoal("wrap"), .trigger("rising"), .behavior("old")) counter_1 (
    .count(PCok), .Q(\总周期数 ), .clk(CLK), .clr(RST));  // open: load, D, carry, preset
  Adder #(.width(32)) adder_1 (.a(PC), .b(32'h4), .out(adder_1_out));  // open: cin, cout
  Register #(.width(32), .trigger("rising"), .Select("low")) register_1 (
    .D(R1), .en(and_1_out), .Q(LedData), .clk(CLK), .clr(RST));
  Register #(.width(1), .trigger("rising"), .Select("low")) register_2 (
    .D(Syscall), .en(and_2_out), .Q(register_2_q), .clk(CLK), .clr(or_2_out));
  not not_2 (PCok, register_2_q);
  or or_2 (or_2_out, Go, RST);
  Hex_Digit_Display hex_digit_display_5 (.value(LedData[15:12]));  // open: dp
  Hex_Digit_Display hex_digit_display_6 (.value(LedData[11:8]));  // open: dp
  ROM #(.addrWidth(10), .dataWidth(32), .Select("high")) rom_1 (.addr(PC[11:2]), .data(IR));
  Hex_Digit_Display hex_digit_display_7 (.value(LedData[7:4]));  // open: dp
  Hex_Digit_Display hex_digit_display_8 (.value(LedData[3:0]));  // open: dp
  // Probe on \总周期数 
  Multiplexer #(.select(1), .width(5), .disabled("Z"), .enable("false")) multiplexer_4 (
    .in0(IR[25:21]), .in1(5'b00100), .out(multiplexer_4_out), .sel(Syscall));
  Multiplexer #(.select(1), .width(5), .disabled("Z"), .enable("false")) multiplexer_5 (
    .in0(IR[20:16]), .in1(5'b00010), .out(multiplexer_5_out), .sel(Syscall));
  Multiplexer #(.select(1), .width(5), .disabled("Z"), .enable("false")) multiplexer_6 (
    .in0(IR[20:16]), .in1(IR[15:11]), .out(multiplexer_6_out), .sel(\n27_4条扩展指令控制器_1_regdst ));
  Multiplexer #(.select(1), .width(5), .disabled("Z"), .enable("false")) multiplexer_7 (
    .in0(multiplexer_6_out), .in1({5{1'b1}}), .out(multiplexer_7_out), .sel(\n27_4条扩展指令控制器_1_jal ));
  assign bit_extender_1_out = {{16{1'b0}}, IR[15:0]};  // Bit_Extender bit_extender_1
  assign bit_extender_2_out = {{16{IR[15]}}, IR[15:0]};  // Bit_Extender bit_extender_2
  assign bit_extender_3_out = {{6{IR[25]}}, IR[25:0]};  // Bit_Extender bit_extender_3
  or or_3 (IR1_t, IR1, IRA);
  \_27_4条扩展指令控制器  \u_27_4条扩展指令控制器_1  (
    .OP(IR[31:26]), .Func(IR[5:0]), .ALU_OP(\n27_4条扩展指令控制器_1_alu_op ), .MemToReg(\n27_4条扩展指令控制器_1_memtoreg ),
    .MemWrite(MemWrite), .ALU_SRC(\n27_4条扩展指令控制器_1_alu_src ), .SysCALL(Syscall), .SignedExt(SignedExt),
    .RegDst(\n27_4条扩展指令控制器_1_regdst ), .Beq(\n27_4条扩展指令控制器_1_beq ), .Bne(\n27_4条扩展指令控制器_1_bne ),
    .JR(\n27_4条扩展指令控制器_1_jr ), .JMP(\n27_4条扩展指令控制器_1_jmp ), .JAL(\n27_4条扩展指令控制器_1_jal ), .LUI(lui),
    .LBU(lbu), .BGEZ(\n27_4条扩展指令控制器_1_bgez ), .MTC0(MTC0), .MFMT(IR[25:21]), .ERET(ERET), .MFC0(MFC0),
    .RegWrite(RegWrite));
  MIPS_Regifile mips_regifile_1 (
    .Din(RDin), .Clk(CLK), .R1(R1), .R2(MDin), .WE(RegWrite), .W_num(multiplexer_7_out),
    .R1_num(multiplexer_4_out), .R2_num(multiplexer_5_out));
  Multiplexer #(.select(1), .width(32), .disabled("Z"), .enable("false")) multiplexer_8 (
    .in0(bit_extender_1_out), .in1(bit_extender_2_out), .out(multiplexer_8_out), .sel(SignedExt));
  or or_4 (IR2_t, IR2, IRB);
  Multiplexer #(.select(1), .width(32), .disabled("Z"), .enable("false")) multiplexer_9 (
    .in0(MDin), .in1(multiplexer_8_out), .out(multiplexer_9_out), .sel(\n27_4条扩展指令控制器_1_alu_src ));
  Multiplexer #(.select(1), .width(32), .disabled("Z"), .enable("false")) multiplexer_10 (
    .in0(multiplexer_12_out), .in1(adder_1_out), .out(RDin), .sel(\n27_4条扩展指令控制器_1_jal ));
  Shifter #(.width(32), .shift("ll")) shifter_1 (.in(multiplexer_8_out), .\dist (5'b00010), .out(shifter_1_out));
  Shifter #(.width(32), .shift("ll")) shifter_2 (.in(bit_extender_1_out), .\dist (5'b10000), .out(shifter_2_out));
  Shifter #(.width(32), .shift("ll")) shifter_3 (.in(bit_extender_3_out), .\dist (5'b00010), .out(shifter_3_out));
  or or_5 (IR3_t, IR3, IRC);
  Multiplexer #(.select(1), .width(32), .disabled("Z"), .enable("false")) multiplexer_11 (
    .in0(multiplexer_9_out), .in1({32{1'b0}}), .out(multiplexer_11_out), .sel(\n27_4条扩展指令控制器_1_bgez ));
  MIPS_ALU mips_alu_1 (
    .X(R1), .Y(multiplexer_11_out), .AluOP(\n27_4条扩展指令控制器_1_alu_op ), .Equal(mips_alu_1_equal),
    .Result(mips_alu_1_result), .shamt(IR[10:6]));  // open: Result_2
  not not_3 (not_3_out, mips_alu_1_result[0]);
  not not_4 (not_4_out, mips_alu_1_equal);
  Multiplexer #(.select(1), .width(32), .disabled("Z"), .enable("false")) multiplexer_12 (
    .in0(multiplexer_14_out), .in1(shifter_2_out), .out(multiplexer_12_out), .sel(lui));
  Adder #(.width(32)) adder_2 (.a(shifter_1_out), .b(adder_1_out), .out(adder_2_out));  // open: cin, cout
  and and_3 (and_3_out, not_3_out, \n27_4条扩展指令控制器_1_bgez );
  and and_4 (and_4_out, mips_alu_1_equal, \n27_4条扩展指令控制器_1_beq );
  and and_5 (and_5_out, not_4_out, \n27_4条扩展指令控制器_1_bne );
  RAM #(.addrWidth(10), .dataWidth(32), .bus("separate"), .Select("high")) ram_1 (
    .addr(mips_alu_1_result[11:2]), .din(MDin), .data(ram_1_data), .str(MemWrite), .clk(CLK), .clr(RST));  // open: sel, ld
  or or_6 (or_6_out, and_3_out, and_4_out, and_5_out);
  Multiplexer #(.select(1), .width(32), .disabled("Z"), .enable("false")) multiplexer_13 (
    .in0(ram_1_data), .in1({{24{1'b0}}, ram_1_data[7:0]}), .out(multiplexer_13_out), .sel(lbu));
  Multiplexer #(.select(1), .width(32), .disabled("Z"), .enable("false")) multiplexer_14 (
    .in0(mips_alu_1_result), .in1(multiplexer_13_out), .out(multiplexer_14_out),
    .sel(\n27_4条扩展指令控制器_1_memtoreg ));

  // Other names for the same wires on the sheet: R2[31:0] = MDin

  // Notes on the sheet:
  //   中断源
  //   总复位信号应将除ROM以外所有存储组件全部清零
  //   中断等待指示
  //   数码管输出
  //   指令存储器
  //   OP
  //   rs
  //   指令字
  //   contents of rom_1 (hex, n*v repeats v):
  //   20110001 8100005 20110001 20120002 20130003 8100009 20110001 20120002 20130003 810000d 20110001
  //   20120002 20130003 8100011 20110001 20120002 20130003 c1000fc 20100001 20110001 118fc0 112020
  //   20020022 c 118882 12200001 8100015 112020 20020022 c 20110001 118880 112020 20020022 c 12200001
  //   810001f 20110001 118fc0 112020 20020022 c 1188c3 112020 20020022 c 118903 112020 20020022 c 118903
  //   112020 20020022 c 118903 112020 20020022 c 118903 112020 20020022 c 118903 112020 20020022 c 118903
  //   112020 20020022 c 118903 112020 20020022 c 20100001 109fc0 139fc3 8021 2012000c 24160003 26100001
  //   3210000f 20080008 20090001 139900 2709825 132020 20020022 c 1094022 1500fff9 22100001 2018000f
  //   2188024 108700 20080008 20090001 139902 2709825 132021 20020022 c 1094022 1500fff9 108702 2c9b022
  //   12c00001 8100050 4020 1084027 84400 3508ffff 82021 20020022 c 2010ffff 20110000 ae300000 22100001
  //   22310004 ae300000 22100001 22310004 ae300000 22100001 22310004 ae300000 22100001 22310004 ae300000
  //   22100001 22310004 ae300000 22100001 22310004 ae300000 22100001 22310004 ae300000 22100001 22310004
  //   ae300000 22100001 22310004 ae300000 22100001 22310004 ae300000 22100001 22310004 ae300000 22100001
  //   22310004 ae300000 22100001 22310004 ae300000 22100001 22310004 ae300000 22100001 22310004 ae300000
  //   22100001 22310004 22100001 8020 2011003c 8e130000 8e340000 274402a 11000002 ae330000 ae140000
  //   2231fffc 1611fff8 102020 20020022 c 22100004 2011003c 1611fff2 20020032 c 20080001 20110010 112020
  //   20020022 c 200b0020 2288823 112020 20020022 c 216bffff 1560fffa 2002000a c 200b0008 3c11fedc
  //   3631ffff 112020 20020022 c 3c11ba98 112020 c 3c117654 112020 c 3c113210 112020 c 216bffff 1560fff0
  //   2002000a c 20090000 200b0020 34118483 20120401 118c00 129400 36318281 22520401 ad310000 2328820
  //   21290004 216bffff 1560fffb 20020022 200b0020 20090000 91310000 112020 20020022 c 21290004 216bffff
  //   1560fff9 2002000a c 2011000f 112020 20020022 c 2231ffff 621fffb 2002000a c 2002000a c 20100000
  //   22100001 102020 20020022 c 22100002 102020 20020022 c 22100003 102020 20020022 c 22100004 102020
  //   20020022 c 22100005 102020 20020022 c 22100006 102020 20020022 c 22100007 102020 20020022 c 22100008
  //   102020 20020022 20020022 c 3e00008
  //   rt
  //   rd
  //   数码管输出应该用寄存器锁存，否则显示数据只能一闪而过
  //   OP
  //   Func
  //   MF/MT
  //   Func
  //   MF/MT
  //   JMP
  //   JR
  //   Syscall
  //   Beq
  //   Bgez
  //   Bne
  //   MemToReg
  //   MemWrite
  //   AluOP
  //   AluSrcB
  //   RegWrite
  //   JAL
  //   RegDst
  //   ERET
  //   数据存储器
  //   为方便自动评测，需要输出PC，IR，寄存器堆写如数据RDin
  //   RAM写使能MemWrite、RAM写入数据MDin等信号
endmodule

// 27+4条扩展指令控制器
module \_27_4条扩展指令控制器  (
  input  [5:0] OP,
  input  [5:0] Func,
  input  [4:0] MFMT,
  output [3:0] ALU_OP,
  output MemToReg,
  output MemWrite,
  output ALU_SRC,
  output SysCALL,
  output SignedExt,
  output RegDst,
  output Beq,
  output Bne,
  output JR,
  output JMP,
  output JAL,
  output LUI,
  output LBU,
  output BGEZ,
  output MFC0,
  output MTC0,
  output ERET,
  output RegWrite
);

  wire \n24_4条扩展指令控制信号生成_1_regwrite ;

  \_24_4条扩展指令运算信号生成  \u_24_4条扩展指令运算信号生成_1  (
    .OP0(OP[0]), .OP1(OP[1]), .OP2(OP[2]), .OP3(OP[3]), .OP4(OP[4]), .OP5(OP[5]), .F0(Func[0]), .F1(Func[1]),
    .F2(Func[2]), .F3(Func[3]), .F4(Func[4]), .F5(Func[5]), .S0(ALU_OP[0]), .S1(ALU_OP[1]), .S2(ALU_OP[2]),
    .S3(ALU_OP[3]));
  \_24_4条扩展指令控制信号生成  \u_24_4条扩展指令控制信号生成_1  (
    .OP0(OP[0]), .OP1(OP[1]), .OP2(OP[2]), .OP3(OP[3]), .OP4(OP[4]), .OP5(OP[5]), .F0(Func[0]), .F1(Func[1]),
    .F2(Func[2]), .F3(Func[3]), .F4(Func[4]), .F5(Func[5]), .MemToReg(MemToReg), .MemWrite(MemWrite),
    .ALU_SRC(ALU_SRC), .RegWrite(\n24_4条扩展指令控制信号生成_1_regwrite ), .SysCALL(SysCALL), .SignedExt(SignedExt),
    .RegDst(RegDst), .BEQ(Beq), .BNE(Bne), .JR(JR), .JUMP(JMP), .JAL(JAL), .LUI(LUI), .LBU(LBU), .BGEZ(BGEZ));
  \_27_4条指令扩展信号自动生成  \u_27_4条指令扩展信号自动生成_1  (
    .OP0(OP[0]), .OP1(OP[1]), .OP2(OP[2]), .OP3(OP[3]), .OP4(OP[4]), .OP5(OP[5]), .F0(Func[0]), .F1(Func[1]),
    .F2(Func[2]), .F3(Func[3]), .F4(Func[4]), .F5(Func[5]), .MFMT0(MFMT[0]), .MFMT1(MFMT[1]),
    .MFMT2(MFMT[2]), .MFMT3(MFMT[3]), .MFMT4(MFMT[4]), .MFC0(MFC0), .MTC0(MTC0), .ERET(ERET));
  or or_1 (RegWrite, MFC0, \n24_4条扩展指令控制信号生成_1_regwrite );

  // Other names for the same wires on the sheet: OP_CODE[5:0] = OP

  // Notes on the sheet:
  //   运算器控制器，根据指令生成运算器功能选择信号
  //   控制信号生成，产生数据通路需要的其他控制信号
endmodule

// 27+4条扩展指令生成
module \_27_4条指令扩展信号自动生成  (
  input  OP0,
  input  OP1,
  input  OP2,
  input  OP3,
  input  OP4,
  input  OP5,
  input  F0,
  input  F1,
  input  F2,
  input  F3,
  input  F4,
  input  F5,
  input  MFMT0,
  input  MFMT1,
  input  MFMT2,
  input  MFMT3,
  input  MFMT4,
  output MFC0,
  output MTC0,
  output ERET
);

  wire not_1_out, not_2_out, not_3_out, not_4_out, not_5_out, not_6_out, not_7_out, not_8_out, not_9_out,
       not_10_out, not_11_out, not_12_out, not_13_out, not_14_out, not_15_out, not_16_out, not_17_out,
       not_18_out, not_19_out, not_20_out, not_21_out, not_22_out, not_23_out, not_24_out, not_25_out,
       not_26_out, not_27_out, not_28_out;

  not not_1 (not_1_out, OP5);
  not not_2 (not_2_out, OP3);
  not not_3 (not_3_out, OP2);
  not not_4 (not_4_out, OP1);
  not not_5 (not_5_out, OP0);
  not not_6 (not_6_out, MFMT4);
  not not_7 (not_7_out, MFMT3);
  not not_8 (not_8_out, MFMT2);
  not not_9 (not_9_out, MFMT1);
  not not_10 (not_10_out, MFMT0);
  not not_11 (not_11_out, OP5);
  not not_12 (not_12_out, OP3);
  not not_13 (not_13_out, OP2);
  not not_14 (not_14_out, OP1);
  not not_15 (not_15_out, OP0);
  not not_16 (not_16_out, MFMT4);
  not not_17 (not_17_out, MFMT3);
  not not_18 (not_18_out, MFMT1);
  not not_19 (not_19_out, MFMT0);
  not not_20 (not_20_out, OP5);
  not not_21 (not_21_out, OP3);
  not not_22 (not_22_out, OP2);
  not not_23 (not_23_out, OP1);
  not not_24 (not_24_out, OP0);
  not not_25 (not_25_out, F5);
  not not_26 (not_26_out, F2);
  not not_27 (not_27_out, F1);
  not not_28 (not_28_out, F0);
  and and_1 (MFC0, not_1_out, OP4, not_2_out, not_3_out, not_4_out, not_5_out, not_6_out, not_7_out, not_8_out, not_9_out, not_10_out);
  and and_2 (MTC0, not_11_out, OP4, not_12_out, not_13_out, not_14_out, not_15_out, not_16_out, not_17_out, MFMT2, not_18_out, not_19_out);
  and and_3 (ERET, not_20_out, OP4, not_21_out, not_22_out, not_23_out, not_24_out, not_25_out, F4, F3, not_26_out, not_27_out, not_28_out);
endmodule

module \单周期MIPS_单级中断  (
  input  IR1,
  input  IR2,
  input  IR3,
  output RegWrite,
  output MemWrite,
  output [31:0] PC,
  output [31:0] IR,
  output [31:0] RDin,
  output [31:0] MDin,
  output [31:0] LedData
);

  wire and_1_out, and_2_out, and_3_out, and_4_out, and_5_out, CLK, comparator_1_eq, ERET, Go, IR1_t, IR2_t,
       IR3_t, IRA, IRB, IRC, IRenable, lbu, lui, MFC0, mips_alu_1_equal, MTC0, \n27_4条扩展指令控制器_1_alu_src ,
       \n27_4条扩展指令控制器_1_beq , \n27_4条扩展指令控制器_1_bgez , \n27_4条扩展指令控制器_1_bne , \n27_4条扩展指令控制器_1_jal ,
       \n27_4条扩展指令控制器_1_jmp , \n27_4条扩展指令控制器_1_jr , \n27_4条扩展指令控制器_1_memtoreg , \n27_4条扩展指令控制器_1_regdst ,
       not_1_out, not_3_out, not_4_out, or_1_out, or_2_out, or_6_out, PCok, register_2_q, RST, SignedExt,
       Syscall, W1, W2, W3;
  wire [3:0] \n27_4条扩展指令控制器_1_alu_op ;
  wire [4:0] multiplexer_6_out, multiplexer_7_out, multiplexer_8_out, multiplexer_9_out;
  wire [15:0] \总周期数 ;
  wire [31:0] adder_1_out, adder_2_out, bit_extender_1_out, bit_extender_2_out, bit_extender_3_out, EPC,
       IRaddr, mips_alu_1_result, multiplexer_5_out, multiplexer_10_out, multiplexer_11_out,
       multiplexer_13_out, multiplexer_14_out, multiplexer_15_out, multiplexer_16_out, PC1, PC2, PC3, PC4,
       R1, ram_1_data, shifter_1_out, shifter_2_out, shifter_3_out;

  Clock #(.highDuration(1), .lowDuration(1)) clock_1 (.out(CLK));
  Button _1 (.out(IRA));
  Button _2 (.out(IRB));
  Button _3 (.out(IRC));
  Button \u_总复位  (.out(RST));
  LED #(.active("true")) led_1 (.in(W1));
  LED #(.active("true")) led_2 (.in(W2));
  LED #(.active("true")) led_3 (.in(W3));
  Button \u_继续运行  (.out(Go));
  Multiplexer #(.select(1), .width(32), .disabled("Z"), .enable("false")) multiplexer_1 (
    .in0(adder_1_out), .in1(adder_2_out), .out(PC1), .sel(or_6_out));
  Multiplexer #(.select(1), .width(32), .disabled("Z"), .enable("false")) multiplexer_2 (
    .in0(PC1), .in1(shifter_3_out), .out(PC2), .sel(or_1_out));
  Multiplexer #(.select(1), .width(32), .disabled("Z"), .enable("false")) multiplexer_3 (
    .in0(PC2), .in1(R1), .out(PC3), .sel(\n27_4条扩展指令控制器_1_jr ));
  Multiplexer #(.select(1), .width(32), .disabled("Z"), .enable("false")) multiplexer_4 (
    .in0(PC3), .in1(IRaddr), .out(PC4), .sel(IRenable));
  Multiplexer #(.select(1), .width(32), .disabled("Z"), .enable("false")) multiplexer_5 (
    .in0(PC4), .in1(EPC), .out(multiplexer_5_out), .sel(ERET));
  Register #(.width(32), .trigger("rising"), .Select("low")) u_PC (
    .D(multiplexer_5_out), .en(PCok), .Q(PC), .clk(CLK), .clr(RST));
  Comparator #(.width(32), .mode("twosComplement")) comparator_1 (
    .a(MDin), .b(32'h22), .eq(comparator_1_eq));  // open: gt, lt
  not not_1 (not_1_out, comparator_1_eq);
  Hex_Digit_Display hex_digit_display_1 (.value(LedData[31:28]));  // open: dp
  Hex_Digit_Display hex_digit_display_2 (.value(LedData[27:24]));  // open: dp
  or or_1 (or_1_out, \n27_4条扩展指令控制器_1_jal , \n27_4条扩展指令控制器_1_jmp );
  and and_1 (and_1_out, comparator_1_eq, Syscall);
  and and_2 (and_2_out, not_1_out, Syscall);
  Hex_Digit_Display hex_digit_display_3 (.value(LedData[19:16]));  // open: dp
  Hex_Digit_Display hex_digit_display_4 (.value(LedData[23:20]));  // open: dp
  Adder #(.width(32)) adder_1 (.a(PC), .b(32'h4), .out(adder_1_out));  // open: cin, cout
  Register #(.width(32), .trigger("rising"), .Select("low")) register_1 (
    .D(R1), .en(and_1_out), .Q(LedData), .clk(CLK), .clr(RST));
  not not_2 (PCok, register_2_q);
  Register #(.width(1), .trigger("rising"), .Select("low")) register_2 (
    .D(Syscall), .en(and_2_out), .Q(register_2_q), .clk(CLK), .clr(or_2_out));
  or or_2 (or_2_out, Go, RST);
  Hex_Digit_Display hex_digit_display_5 (.value(LedData[11:8]));  // open: dp
  Hex_Digit_Display hex_digit_display_6 (.value(LedData[15:12]));  // open: dp
  Counter #(.width(16), .max('hffff), .ongoal("wrap"), .trigger("rising"), .behavior("old")) counter_1 (
    .count(PCok), .Q(\总周期数 ), .clk(CLK), .clr(RST));  // open: load, D, carry, preset
  ROM #(.addrWidth(10), .dataWidth(32), .Select("high")) rom_1 (.addr(PC[11:2]), .data(IR));
  Hex_Digit_Display hex_digit_display_7 (.value(LedData[7:4]));  // open: dp
  Hex_Digit_Display hex_digit_display_8 (.value(LedData[3:0]));  // open: dp
  // Probe on \总周期数 
  Multiplexer #(.select(1), .width(5), .disabled("Z"), .enable("false")) multiplexer_6 (
    .in0(IR[25:21]), .in1(5'b00100), .out(multiplexer_6_out), .sel(Syscall));
  Multiplexer #(.select(1), .width(5), .disabled("Z"), .enable("false")) multiplexer_7 (
    .in0(IR[20:16]), .in1(5'b00010), .out(multiplexer_7_out), .sel(Syscall));
  Multiplexer #(.select(1), .width(5), .disabled("Z"), .enable("false")) multiplexer_8 (
    .in0(IR[20:16]), .in1(IR[15:11]), .out(multiplexer_8_out), .sel(\n27_4条扩展指令控制器_1_regdst ));
  Multiplexer #(.select(1), .width(5), .disabled("Z"), .enable("false")) multiplexer_9 (
    .in0(multiplexer_8_out), .in1({5{1'b1}}), .out(multiplexer_9_out), .sel(\n27_4条扩展指令控制器_1_jal ));
  assign bit_extender_1_out = {{16{1'b0}}, IR[15:0]};  // Bit_Extender bit_extender_1
  assign bit_extender_2_out = {{16{IR[15]}}, IR[15:0]};  // Bit_Extender bit_extender_2
  assign bit_extender_3_out = {{6{IR[25]}}, IR[25:0]};  // Bit_Extender bit_extender_3
  or or_3 (IR1_t, IR1, IRA);
  \_27_4条扩展指令控制器  \u_27_4条扩展指令控制器_1  (
    .OP(IR[31:26]), .Func(IR[5:0]), .ALU_OP(\n27_4条扩展指令控制器_1_alu_op ), .MemToReg(\n27_4条扩展指令控制器_1_memtoreg ),
    .MemWrite(MemWrite), .ALU_SRC(\n27_4条扩展指令控制器_1_alu_src ), .SysCALL(Syscall), .SignedExt(SignedExt),
    .RegDst(\n27_4条扩展指令控制器_1_regdst ), .Beq(\n27_4条扩展指令控制器_1_beq ), .Bne(\n27_4条扩展指令控制器_1_bne ),
    .JR(\n27_4条扩展指令控制器_1_jr ), .JMP(\n27_4条扩展指令控制器_1_jmp ), .JAL(\n27_4条扩展指令控制器_1_jal ), .LUI(lui),
    .LBU(lbu), .BGEZ(\n27_4条扩展指令控制器_1_bgez ), .MTC0(MTC0), .MFMT(IR[25:21]), .ERET(ERET), .MFC0(MFC0),
    .RegWrite(RegWrite));
  MIPS_Regifile mips_regifile_1 (
    .Din(RDin), .Clk(CLK), .R1(R1), .R2(MDin), .WE(RegWrite), .W_num(multiplexer_9_out),
    .R1_num(multiplexer_6_out), .R2_num(multiplexer_7_out));
  Multiplexer #(.select(1), .width(32), .disabled("Z"), .enable("false")) multiplexer_10 (
    .in0(bit_extender_1_out), .in1(bit_extender_2_out), .out(multiplexer_10_out), .sel(SignedExt));
  // Probe on RDin
  or or_4 (IR2_t, IR2, IRB);
  Multiplexer #(.select(1), .width(32), .disabled("Z"), .enable("false")) multiplexer_11 (
    .in0(MDin), .in1(multiplexer_10_out), .out(multiplexer_11_out), .sel(\n27_4条扩展指令控制器_1_alu_src ));
  Multiplexer #(.select(1), .width(32), .disabled("Z"), .enable("false")) multiplexer_12 (
    .in0(multiplexer_14_out), .in1(adder_1_out), .out(RDin), .sel(\n27_4条扩展指令控制器_1_jal ));
  Shifter #(.width(32), .shift("ll")) shifter_1 (.in(multiplexer_10_out), .\dist (5'b00010), .out(shifter_1_out));
  Shifter #(.width(32), .shift("ll")) shifter_2 (.in(bit_extender_1_out), .\dist (5'b10000), .out(shifter_2_out));
  Shifter #(.width(32), .shift("ll")) shifter_3 (.in(bit_extender_3_out), .\dist (5'b00010), .out(shifter_3_out));
  or or_5 (IR3_t, IR3, IRC);
  Multiplexer #(.select(1), .width(32), .disabled("Z"), .enable("false")) multiplexer_13 (
    .in0(multiplexer_11_out), .in1({32{1'b0}}), .out(multiplexer_13_out), .sel(\n27_4条扩展指令控制器_1_bgez ));
  MIPS_ALU mips_alu_1 (
    .X(R1), .Y(multiplexer_13_out), .AluOP(\n27_4条扩展指令控制器_1_alu_op ), .Equal(mips_alu_1_equal),
    .Result(mips_alu_1_result), .shamt(IR[10:6]));  // open: Result_2
  not not_3 (not_3_out, mips_alu_1_result[0]);
  not not_4 (not_4_out, mips_alu_1_equal);
  Multiplexer #(.select(1), .width(32), .disabled("Z"), .enable("false")) multiplexer_14 (
    .in0(multiplexer_16_out), .in1(shifter_2_out), .out(multiplexer_14_out), .sel(lui));
  Adder #(.width(32)) adder_2 (.a(shifter_1_out), .b(adder_1_out), .out(adder_2_out));  // open: cin, cout
  and and_3 (and_3_out, not_3_out, \n27_4条扩展指令控制器_1_bgez );
  and and_4 (and_4_out, mips_alu_1_equal, \n27_4条扩展指令控制器_1_beq );
  and and_5 (and_5_out, not_4_out, \n27_4条扩展指令控制器_1_bne );
  RAM #(.addrWidth(10), .dataWidth(32), .bus("separate"), .Select("high")) ram_1 (
    .addr(mips_alu_1_result[11:2]), .din(MDin), .data(ram_1_data), .str(MemWrite), .clk(CLK), .clr(RST));  // open: sel, ld
  \单级中断发生器  \u_单级中断发生器_1  (
    .CLK(CLK), .ERET(ERET), .W1(W1), .IRaddr(IRaddr), .IR1(IR1_t), .W2(W2), .IR2(IR2_t), .W3(W3),
    .IR3(IR3_t), .PC3(PC3), .IRenable(IRenable), .EPC(EPC));
  or or_6 (or_6_out, and_3_out, and_4_out, and_5_out);
  Multiplexer #(.select(1), .width(32), .disabled("Z"), .enable("false")) multiplexer_15 (
    .in0(ram_1_data), .in1({{24{1'b0}}, ram_1_data[7:0]}), .out(multiplexer_15_out), .sel(lbu));
  Multiplexer #(.select(1), .width(32), .disabled("Z"), .enable("false")) multiplexer_16 (
    .in0(mips_alu_1_result), .in1(multiplexer_15_out), .out(multiplexer_16_out),
    .sel(\n27_4条扩展指令控制器_1_memtoreg ));

  // Other names for the same wires on the sheet: R2[31:0] = MDin

  // Notes on the sheet:
  //   中断源
  //   中断等待指示
  //   总复位信号应将除ROM以外所有存储组件全部清零
  //   数码管输出
  //   指令存储器
  //   数码管输出应该用寄存器锁存，否则显示数据只能一闪而过
  //   指令字
  //   contents of rom_1 (hex, n*v repeats v):
  //   201d07d0 20100001 109fc0 139fc3 8021 2012000c 24160008 26100001 3210000f 20080008 20090001 139900
  //   2709825 132020 20020022 c 1094022 1500fff9 22100001 2018000f 2188024 108700 20080008 20090001 139902
  //   2709825 132021 20020022 c 1094022 1500fff9 108702 2c9b022 12c00001 8000c07 4020 1084027 84400
  //   3508ffff 82021 20020022 c 8000c01 afa20000 23bd0004 afa40000 23bd0004 afb00000 23bd0004 afb30000
  //   23bd0004 afb40000 23bd0004 afb50000 23bd0004 afb60000 23bd0004 20160001 20140003 20150001 168020
  //   108100 2149825 132020 20020022 c 1600fffa 295a022 1680fff7 23bdfffc 8fb60000 23bdfffc 8fb50000
  //   23bdfffc 8fb40000 23bdfffc 8fb30000 23bdfffc 8fb00000 23bdfffc 8fa40000 23bdfffc 8fa20000 42000018
  //   afa20000 23bd0004 afa40000 23bd0004 afb00000 23bd0004 afb30000 23bd0004 afb40000 23bd0004 afb50000
  //   23bd0004 afb60000 23bd0004 20160002 20140003 20150001 168020 108100 2149825 132020 20020022 c
  //   1600fffa 295a022 1680fff7 23bdfffc 8fb60000 23bdfffc 8fb50000 23bdfffc 8fb40000 23bdfffc 8fb30000
  //   23bdfffc 8fb00000 23bdfffc 8fa40000 23bdfffc 8fa20000 42000018 afa20000 23bd0004 afa40000 23bd0004
  //   afb00000 23bd0004 afb30000 23bd0004 afb40000 23bd0004 afb50000 23bd0004 afb60000 23bd0004 20160003
  //   20140003 20150001 168020 108100 2149825 132020 20020022 c 1600fffa 295a022 1680fff7 23bdfffc
  //   8fb60000 23bdfffc 8fb50000 23bdfffc 8fb40000 23bdfffc 8fb30000 23bdfffc 8fb00000 23bdfffc 8fa40000
  //   23bdfffc 8fa20000 42000018
  //   Func
  //   OP
  //   Func
  //   MF/MT
  //   rs
  //   rt
  //   rd
  //   JMP
  //   JR
  //   OP
  //   MF/MT
  //   Syscall
  //   Beq
  //   Bgez
  //   Bne
  //   MemToReg
  //   MemWrite
  //   AluOP
  //   AluSrcB
  //   RegWrite
  //   JAL
  //   RegDst
  //   ERET
  //   为方便自动评测，需要输出PC，IR，寄存器堆写如数据RDin
  //   RAM写使能MemWrite、RAM写入数据MDin等信号
  //   数据存储器
endmodule

// 单级中断发生
module \单级中断发生器  (
  input  CLK,
  input  ERET,
  input  IR1,
  input  IR2,
  input  [31:0] PC3,
  input  IR3,
  output W1,
  output [31:0] IRaddr,
  output W2,
  output W3,
  output IRenable,
  output [31:0] EPC
);

  wire and_5_out, and_6_out, and_7_out, and_8_out, clear1, clear2, clear3, d_ff_1_q, d_ff_2_q, d_ff_3_q,
       decoder_1_out1, decoder_1_out2, decoder_1_out3, IE, IReady, not_1_out, or_1_out, or_5_out, or_6_out,
       or_7_out, priority_encoder_1_gs, Ready1, Ready2, Ready3, undriven;
  wire [1:0] IRnum, \中断号_q ;

  Priority_Encoder #(.select(2), .disabled("Z")) priority_encoder_1 (
    .in0(1'b0), .in1(Ready1), .in2(Ready2), .in3(Ready3), .out(IRnum), .gs(priority_encoder_1_gs));  // open: en_out, en_in
  Decoder #(.select(2), .tristate("false"), .disabled("Z"), .enable("false")) decoder_1 (
    .out1(decoder_1_out1), .out2(decoder_1_out2), .out3(decoder_1_out3), .sel(\中断号_q ));  // open: out0
  Register #(.width(2), .trigger("rising"), .Select("low")) \u_中断号  (
    .D(IRnum), .en(IRenable), .Q(\中断号_q ), .clk(CLK));  // open: clr
  not not_1 (not_1_out, IE);
  and and_1 (IRenable, priority_encoder_1_gs, not_1_out);
  and and_2 (clear1, decoder_1_out1, ERET);
  and and_3 (clear2, decoder_1_out2, ERET);
  and and_4 (clear3, decoder_1_out3, ERET);
  and and_5 (and_5_out, IReady, IRenable);
  or or_1 (or_1_out, IRenable, ERET);
  Multiplexer #(.select(2), .width(32), .disabled("Z"), .enable("false")) multiplexer_1 (
    .in1(32'h30ac), .in2(32'h3150), .in3(32'h31f4), .out(IRaddr), .sel(IRnum));  // open: in0
  Register #(.width(32), .trigger("rising"), .Select("low")) u_EPC (
    .D(PC3), .en(and_5_out), .Q(EPC), .clk(CLK));  // open: clr
  Register #(.width(1), .trigger("rising"), .Select("low")) u_IE (
    .D(IRenable), .en(or_1_out), .Q(IE), .clk(CLK));  // open: clr
  or or_2 (W1, Ready1, d_ff_1_q);
  or or_3 (W2, Ready2, d_ff_2_q);
  or or_4 (W3, Ready3, d_ff_3_q);
  D_Flip_Flop #(.trigger("rising"), .Pre_Clr_Positions("LEGACY"), .NegatePresetClear("false"), .enable("true"), .NewFFLayout("false")) d_ff_1 (
    .clk(IR1), .D(1'b1), .Q(d_ff_1_q), .reset(Ready1));  // open: Qn, preset, en
  D_Flip_Flop #(.trigger("rising"), .Pre_Clr_Positions("LEGACY"), .NegatePresetClear("false"), .enable("true"), .NewFFLayout("false")) d_ff_2 (
    .clk(IR2), .D(1'b1), .Q(d_ff_2_q), .reset(Ready2));  // open: Qn, preset, en
  D_Flip_Flop #(.trigger("rising"), .Pre_Clr_Positions("LEGACY"), .NegatePresetClear("false"), .enable("true"), .NewFFLayout("false")) d_ff_3 (
    .clk(IR3), .D(1'b1), .Q(d_ff_3_q), .reset(Ready3));  // open: Qn, preset, en
  or or_5 (or_5_out, d_ff_1_q, Ready1);
  or or_6 (or_6_out, d_ff_2_q, Ready2);
  or or_7 (or_7_out, d_ff_3_q, Ready3);
  and and_6 (and_6_out, or_5_out, ~clear1);  // AND_Gate
  and and_7 (and_7_out, or_6_out, ~clear2);  // AND_Gate
  and and_8 (and_8_out, or_7_out, ~clear3);  // AND_Gate
  D_Flip_Flop #(.trigger("rising"), .Pre_Clr_Positions("LEGACY"), .NegatePresetClear("false"), .enable("true"), .NewFFLayout("false")) u_IR1 (
    .clk(CLK), .D(and_6_out), .Q(Ready1));  // open: Qn, preset, en, reset
  D_Flip_Flop #(.trigger("rising"), .Pre_Clr_Positions("LEGACY"), .NegatePresetClear("false"), .enable("true"), .NewFFLayout("false")) u_IR2 (
    .clk(CLK), .D(and_7_out), .Q(Ready2));  // open: Qn, preset, en, reset
  D_Flip_Flop #(.trigger("rising"), .Pre_Clr_Positions("LEGACY"), .NegatePresetClear("false"), .enable("true"), .NewFFLayout("false")) u_IR3 (
    .clk(CLK), .D(and_8_out), .Q(Ready3), .en(undriven));  // open: Qn, preset, reset

  // Notes on the sheet:
  //   中断仲裁及信号生成
  //   中断返回逻辑
  //   中断识别（入口地址）
  //   CP0寄存组
  //   1号中断信号采样参考电路
  //   2号中断信号采样参考电路
  //   3号中断信号采样参考电路
  //   Reset 
  //   Reset 
  //   Reset 
endmodule

module \单周期MIPS_多级中断_屏蔽字版本  (
  input  IR1,
  input  IR2,
  input  IR3,
  output RegWrite,
  output MemWrite,
  output [31:0] PC,
  output [31:0] IR,
  output [31:0] RDin,
  output [31:0] MDin,
  output [31:0] LedData
);

  wire and_1_out, and_2_out, and_3_out, and_4_out, and_5_out, CLK, comparator_1_eq, ERET, Go, IR1_t, IR2_t,
       IR3_t, IRA, IRB, IRC, IRenable, lbu, lui, MFC0, mips_alu_1_equal, MTC0, \n27_4条扩展指令控制器_1_alu_src ,
       \n27_4条扩展指令控制器_1_beq , \n27_4条扩展指令控制器_1_bgez , \n27_4条扩展指令控制器_1_bne , \n27_4条扩展指令控制器_1_jal ,
       \n27_4条扩展指令控制器_1_jmp , \n27_4条扩展指令控制器_1_jr , \n27_4条扩展指令控制器_1_memtoreg , \n27_4条扩展指令控制器_1_regdst ,
       not_1_out, not_3_out, not_4_out, or_1_out, or_2_out, or_6_out, PCok, register_2_q, RST, SignedExt,
       Syscall, W1, W2, W3;
  wire [3:0] \n27_4条扩展指令控制器_1_alu_op ;
  wire [4:0] multiplexer_6_out, multiplexer_7_out, multiplexer_8_out, multiplexer_9_out;
  wire [15:0] \总周期数 ;
  wire [31:0] adder_1_out, adder_2_out, bit_extender_1_out, bit_extender_2_out, bit_extender_3_out, EPC,
       IRaddr, IRin, IRout, mips_alu_1_result, multiplexer_5_out, multiplexer_11_out, multiplexer_13_out,
       multiplexer_14_out, multiplexer_15_out, multiplexer_16_out, multiplexer_17_out, multiplexer_18_out,
       PC1, PC2, PC3, PC4, R1, ram_1_data, shifter_1_out, shifter_2_out, shifter_3_out;

  Clock #(.highDuration(1), .lowDuration(1)) clock_1 (.out(CLK));
  Button _1 (.out(IRA));
  Button _2 (.out(IRB));
  Button _3 (.out(IRC));
  Button \u_总复位  (.out(RST));
  Button \u_继续运行  (.out(Go));
  LED #(.active("true")) led_1 (.in(W1));
  LED #(.active("true")) led_2 (.in(W2));
  LED #(.active("true")) led_3 (.in(W3));
  Multiplexer #(.select(1), .width(32), .disabled("Z"), .enable("false")) multiplexer_1 (
    .in0(adder_1_out), .in1(adder_2_out), .out(PC1), .sel(or_6_out));
  Multiplexer #(.select(1), .width(32), .disabled("Z"), .enable("false")) multiplexer_2 (
    .in0(PC1), .in1(shifter_3_out), .out(PC2), .sel(or_1_out));
  Multiplexer #(.select(1), .width(32), .disabled("Z"), .enable("false")) multiplexer_3 (
    .in0(PC2), .in1(R1), .out(PC3), .sel(\n27_4条扩展指令控制器_1_jr ));
  Multiplexer #(.select(1), .width(32), .disabled("Z"), .enable("false")) multiplexer_4 (
    .in0(PC3), .in1(IRaddr), .out(PC4), .sel(IRenable));
  Multiplexer #(.select(1), .width(32), .disabled("Z"), .enable("false")) multiplexer_5 (
    .in0(PC4), .in1(EPC), .out(multiplexer_5_out), .sel(ERET));
  Comparator #(.width(32), .mode("twosComplement")) comparator_1 (
    .a(MDin), .b(32'h22), .eq(comparator_1_eq));  // open: gt, lt
  Hex_Digit_Display hex_digit_display_1 (.value(LedData[31:28]));  // open: dp
  Hex_Digit_Display hex_digit_display_2 (.value(LedData[27:24]));  // open: dp
  or or_1 (or_1_out, \n27_4条扩展指令控制器_1_jal , \n27_4条扩展指令控制器_1_jmp );
  Register #(.width(32), .trigger("rising"), .Select("low")) u_PC (
    .D(multiplexer_5_out), .en(PCok), .Q(PC), .clk(CLK), .clr(RST));
  and and_1 (and_1_out, comparator_1_eq, Syscall);
  not not_1 (not_1_out, comparator_1_eq);
  and and_2 (and_2_out, not_1_out, Syscall);
  Hex_Digit_Display hex_digit_display_3 (.value(LedData[23:20]));  // open: dp
  Hex_Digit_Display hex_digit_display_4 (.value(LedData[19:16]));  // open: dp
  Adder #(.width(32)) adder_1 (.a(PC), .b(32'h4), .out(adder_1_out));  // open: cin, cout
  Register #(.width(32), .trigger("rising"), .Select("low")) register_1 (
    .D(R1), .en(and_1_out), .Q(LedData), .clk(CLK), .clr(RST));
  not not_2 (PCok, register_2_q);
  Register #(.width(1), .trigger("rising"), .Select("low")) register_2 (
    .D(Syscall), .en(and_2_out), .Q(register_2_q), .clk(CLK), .clr(or_2_out));
  or or_2 (or_2_out, Go, RST);
  Hex_Digit_Display hex_digit_display_5 (.value(LedData[15:12]));  // open: dp
  Hex_Digit_Display hex_digit_display_6 (.value(LedData[11:8]));  // open: dp
  Counter #(.width(16), .max('hffff), .ongoal("wrap"), .trigger("rising"), .behavior("old")) counter_1 (
    .count(PCok), .Q(\总周期数 ), .clk(CLK), .clr(RST));  // open: load, D, carry, preset
  ROM #(.addrWidth(10), .dataWidth(32), .Select("high")) rom_1 (.addr(PC[11:2]), .data(IR));
  Hex_Digit_Display hex_digit_display_7 (.value(LedData[3:0]));  // open: dp
  Hex_Digit_Display hex_digit_display_8 (.value(LedData[7:4]));  // open: dp
  // Probe on \总周期数 
  // Probe on IR[31:26]
  Multiplexer #(.select(1), .width(5), .disabled("Z"), .enable("false")) multiplexer_6 (
    .in0(IR[25:21]), .in1(5'b00100), .out(multiplexer_6_out), .sel(Syscall));
  Multiplexer #(.select(1), .width(5), .disabled("Z"), .enable("false")) multiplexer_7 (
    .in0(IR[20:16]), .in1(5'b00010), .out(multiplexer_7_out), .sel(Syscall));
  Multiplexer #(.select(1), .width(5), .disabled("Z"), .enable("false")) multiplexer_8 (
    .in0(IR[20:16]), .in1(IR[15:11]), .out(multiplexer_8_out), .sel(\n27_4条扩展指令控制器_1_regdst ));
  Multiplexer #(.select(1), .width(5), .disabled("Z"), .enable("false")) multiplexer_9 (
    .in0(multiplexer_8_out), .in1({5{1'b1}}), .out(multiplexer_9_out), .sel(\n27_4条扩展指令控制器_1_jal ));
  assign bit_extender_1_out = {{16{1'b0}}, IR[15:0]};  // Bit_Extender bit_extender_1
  assign bit_extender_2_out = {{16{IR[15]}}, IR[15:0]};  // Bit_Extender bit_extender_2
  assign bit_extender_3_out = {{6{IR[25]}}, IR[25:0]};  // Bit_Extender bit_extender_3
  or or_3 (IR1_t, IR1, IRA);
  \_27_4条扩展指令控制器  \u_27_4条扩展指令控制器_1  (
    .OP(IR[31:26]), .Func(IR[5:0]), .ALU_OP(\n27_4条扩展指令控制器_1_alu_op ), .MemToReg(\n27_4条扩展指令控制器_1_memtoreg ),
    .MemWrite(MemWrite), .ALU_SRC(\n27_4条扩展指令控制器_1_alu_src ), .SysCALL(Syscall), .SignedExt(SignedExt),
    .RegDst(\n27_4条扩展指令控制器_1_regdst ), .Beq(\n27_4条扩展指令控制器_1_beq ), .Bne(\n27_4条扩展指令控制器_1_bne ),
    .JR(\n27_4条扩展指令控制器_1_jr ), .JMP(\n27_4条扩展指令控制器_1_jmp ), .JAL(\n27_4条扩展指令控制器_1_jal ), .LUI(lui),
    .LBU(lbu), .BGEZ(\n27_4条扩展指令控制器_1_bgez ), .MTC0(MTC0), .MFMT(IR[25:21]), .ERET(ERET), .MFC0(MFC0),
    .RegWrite(RegWrite));
  Multiplexer #(.select(1), .width(32), .disabled("Z"), .enable("false")) multiplexer_10 (
    .in0(multiplexer_14_out), .in1(IRin), .out(RDin), .sel(MFC0));
  Multiplexer #(.select(1), .width(32), .disabled("Z"), .enable("false")) multiplexer_11 (
    .in0(bit_extender_1_out), .in1(bit_extender_2_out), .out(multiplexer_11_out), .sel(SignedExt));
  MIPS_Regifile mips_regifile_1 (
    .Din(RDin), .Clk(CLK), .R1(R1), .R2(MDin), .WE(RegWrite), .W_num(multiplexer_9_out),
    .R1_num(multiplexer_6_out), .R2_num(multiplexer_7_out));
  or or_4 (IR2_t, IR2, IRB);
  Multiplexer #(.select(1), .width(32), .disabled("Z"), .enable("false")) multiplexer_12 (
    .in0({32{1'b0}}), .in1(MDin), .out(IRout), .sel(MTC0));
  Multiplexer #(.select(1), .width(32), .disabled("Z"), .enable("false")) multiplexer_13 (
    .in0(MDin), .in1(multiplexer_11_out), .out(multiplexer_13_out), .sel(\n27_4条扩展指令控制器_1_alu_src ));
  Multiplexer #(.select(1), .width(32), .disabled("Z"), .enable("false")) multiplexer_14 (
    .in0(multiplexer_16_out), .in1(adder_1_out), .out(multiplexer_14_out), .sel(\n27_4条扩展指令控制器_1_jal ));
  Shifter #(.width(32), .shift("ll")) shifter_1 (.in(multiplexer_11_out), .\dist (5'b00010), .out(shifter_1_out));
  Shifter #(.width(32), .shift("ll")) shifter_2 (.in(bit_extender_1_out), .\dist (5'b10000), .out(shifter_2_out));
  Shifter #(.width(32), .shift("ll")) shifter_3 (.in(bit_extender_3_out), .\dist (5'b00010), .out(shifter_3_out));
  or or_5 (IR3_t, IR3, IRC);
  Multiplexer #(.select(1), .width(32), .disabled("Z"), .enable("false")) multiplexer_15 (
    .in0(multiplexer_13_out), .in1({32{1'b0}}), .out(multiplexer_15_out), .sel(\n27_4条扩展指令控制器_1_bgez ));
  MIPS_ALU mips_alu_1 (
    .X(R1), .Y(multiplexer_15_out), .AluOP(\n27_4条扩展指令控制器_1_alu_op ), .Equal(mips_alu_1_equal),
    .Result(mips_alu_1_result), .shamt(IR[10:6]));  // open: Result_2
  not not_3 (not_3_out, mips_alu_1_result[0]);
  not not_4 (not_4_out, mips_alu_1_equal);
  Multiplexer #(.select(1), .width(32), .disabled("Z"), .enable("false")) multiplexer_16 (
    .in0(multiplexer_18_out), .in1(shifter_2_out), .out(multiplexer_16_out), .sel(lui));
  Adder #(.width(32)) adder_2 (.a(shifter_1_out), .b(adder_1_out), .out(adder_2_out));  // open: cin, cout
  and and_3 (and_3_out, not_3_out, \n27_4条扩展指令控制器_1_bgez );
  and and_4 (and_4_out, mips_alu_1_equal, \n27_4条扩展指令控制器_1_beq );
  and and_5 (and_5_out, not_4_out, \n27_4条扩展指令控制器_1_bne );
  RAM #(.addrWidth(10), .dataWidth(32), .bus("separate"), .Select("high")) ram_1 (
    .addr(mips_alu_1_result[11:2]), .din(MDin), .data(ram_1_data), .str(MemWrite), .clk(CLK), .clr(RST));  // open: sel, ld
  \多级中断_屏蔽字_发生器  \u_多级中断_屏蔽字_发生器_1  (
    .CLK(CLK), .RD(IR[15:11]), .W1(W1), .IR1(IR1_t), .W2(W2), .IRin(IRin), .PC3(PC3), .IR2(IR2_t), .W3(W3),
    .IR3(IR3_t), .IRaddr(IRaddr), .MTC0(MTC0), .IRout(IRout), .ERET(ERET), .IRenable(IRenable), .EPC(EPC));
  or or_6 (or_6_out, and_3_out, and_4_out, and_5_out);
  Multiplexer #(.select(1), .width(32), .disabled("Z"), .enable("false")) multiplexer_17 (
    .in0(ram_1_data), .in1({{24{1'b0}}, ram_1_data[7:0]}), .out(multiplexer_17_out), .sel(lbu));
  Multiplexer #(.select(1), .width(32), .disabled("Z"), .enable("false")) multiplexer_18 (
    .in0(mips_alu_1_result), .in1(multiplexer_17_out), .out(multiplexer_18_out),
    .sel(\n27_4条扩展指令控制器_1_memtoreg ));

  // Other names for the same wires on the sheet: RD[4:0] = IR[15:11]; R2[31:0] = MDin

  // Notes on the sheet:
  //   中断源
  //   总复位信号应将除ROM以外所有存储组件全部清零
  //   中断等待指示
  //   指令存储器
  //   数码管输出
  //   指令字
  //   contents of rom_1 (hex, n*v repeats v):
  //   201d07d0 20100001 109fc0 139fc3 8021 2012000c 24160008 26100001 3210000f 20080008 20090001 139900
  //   2709825 132020 20020022 c 1094022 1500fff9 22100001 2018000f 2188024 108700 20080008 20090001 139902
  //   2709825 132021 20020022 c 1094022 1500fff9 108702 2c9b022 12c00001 8100007 4020 1084027 84400
  //   3508ffff 82021 20020022 c 8100001 afa20000 23bd0004 afa40000 23bd0004 afb00000 23bd0004 afb30000
  //   23bd0004 afb40000 23bd0004 afb50000 23bd0004 afb60000 23bd0004 afb70000 23bd0004 40167000 40175000
  //   afb70000 23bd0004 afb60000 23bd0004 20170001 40975000 20160001 40966000 20160001 20140003 20150001
  //   168020 108100 2149825 132020 20020022 c 1600fffa 295a022 1680fff7 40806000 23bdfffc 8fb60000
  //   23bdfffc 8fb70000 40967000 40975000 23bdfffc 8fb70000 23bdfffc 8fb60000 23bdfffc 8fb50000 23bdfffc
  //   8fb40000 23bdfffc 8fb30000 23bdfffc 8fb00000 23bdfffc 8fa40000 23bdfffc 8fa20000 42000018 afa20000
  //   23bd0004 afa40000 23bd0004 afb00000 23bd0004 afb30000 23bd0004 afb40000 23bd0004 afb50000 23bd0004
  //   afb60000 23bd0004 afb70000 23bd0004 40167000 40175000 afb70000 23bd0004 afb60000 23bd0004 20170003
  //   40975000 20160001 40966000 20160002 20140003 20150001 168020 108100 2149825 132020 20020022 c
  //   1600fffa 295a022 1680fff7 40806000 23bdfffc 8fb60000 23bdfffc 8fb70000 40975000 40967000 23bdfffc
  //   8fb70000 23bdfffc 8fb60000 23bdfffc 8fb50000 23bdfffc 8fb40000 23bdfffc 8fb30000 23bdfffc 8fb00000
  //   23bdfffc 8fa40000 23bdfffc 8fa20000 42000018 afa20000 23bd0004 afa40000 23bd0004 afb00000 23bd0004
  //   afb30000 23bd0004 afb40000 23bd0004 afb50000 23bd0004 afb60000 23bd0004 afb70000 23bd0004 40167000
  //   40175000 afb70000 23bd0004 afb60000 23bd0004 20170007 40975000 20160001 40966000 20160003 20140003
  //   20150001 168020 108100 2149825 132020 20020022 c 1600fffa 295a022 1680fff7 40806000 23bdfffc
  //   8fb60000 23bdfffc 8fb70000 40975000 40967000 23bdfffc 8fb70000 23bdfffc 8fb60000 23bdfffc 8fb50000
  //   23bdfffc 8fb40000 23bdfffc 8fb30000 23bdfffc 8fb00000 23bdfffc 8fa40000 23bdfffc 8fa20000 42000018
  //   数码管输出应该用寄存器锁存，否则显示数据只能一闪而过
  //   OP
  //   Func
  //   MF/MT
  //   rs
  //   rt
  //   rd
  //   JMP
  //   JR
  //   OP
  //   Func
  //   MF/MT
  //   Syscall
  //   Beq
  //   Bgez
  //   Bne
  //   MemToReg
  //   MemWrite
  //   AluOP
  //   AluSrcB
  //   RegWrite
  //   JAL
  //   RegDst
  //   ERET
  //   为方便自动评测，需要输出PC，IR，寄存器堆写如数据RDin
  //   RAM写使能MemWrite、RAM写入数据MDin等信号
  //   数据存储器
endmodule

// 屏蔽字中断发生
module \多级中断_屏蔽字_发生器  (
  input  [4:0] RD,
  input  CLK,
  input  IR1,
  input  [31:0] PC3,
  input  IR2,
  input  IR3,
  input  MTC0,
  input  [31:0] IRout,
  input  ERET,
  output W1,
  output W2,
  output [31:0] IRin,
  output W3,
  output IRenable,
  output [31:0] IRaddr,
  output [31:0] EPC
);

  wire _10, _12, _14, and_1_out, and_2_out, and_3_out, and_4_out, and_5_out, and_6_out, and_7_out, and_8_out,
       and_9_out, clear1, clear2, clear3, d_ff_1_q, d_ff_2_q, d_ff_3_q, d_ff_4_qn, d_ff_5_qn, d_ff_6_qn,
       decoder_1_out1, decoder_1_out2, decoder_1_out3, IE, IE_forward, multiplexer_1_out, multiplexer_2_out,
       multiplexer_3_out, multiplexer_6_out, not_1_out, not_2_out, or_4_out, or_5_out, or_6_out, or_7_out,
       or_8_out, priority_encoder_1_gs, Ready1, Ready2, Ready3;
  wire [1:0] IRnum, select;
  wire [2:0] \优先嵌套字 ;
  wire [31:0] EPC_forward, multiplexer_5_out, \优先嵌套字out ;
  wire [31:1] demultiplexer_1_out3;

  or or_1 (W1, Ready1, d_ff_1_q);
  or or_2 (W2, Ready2, d_ff_2_q);
  or or_3 (W3, Ready3, d_ff_3_q);
  D_Flip_Flop #(.trigger("rising"), .Pre_Clr_Positions("LEGACY"), .NegatePresetClear("false"), .enable("true"), .NewFFLayout("false")) d_ff_1 (
    .clk(IR1), .D(1'b1), .Q(d_ff_1_q), .reset(Ready1));  // open: Qn, preset, en
  D_Flip_Flop #(.trigger("rising"), .Pre_Clr_Positions("LEGACY"), .NegatePresetClear("false"), .enable("true"), .NewFFLayout("false")) d_ff_2 (
    .clk(IR2), .D(1'b1), .Q(d_ff_2_q), .reset(Ready2));  // open: Qn, preset, en
  D_Flip_Flop #(.trigger("rising"), .Pre_Clr_Positions("LEGACY"), .NegatePresetClear("false"), .enable("true"), .NewFFLayout("false")) d_ff_3 (
    .clk(IR3), .D(1'b1), .Q(d_ff_3_q), .reset(Ready3));  // open: Qn, preset, en
  or or_4 (or_4_out, d_ff_1_q, Ready1);
  or or_5 (or_5_out, d_ff_2_q, Ready2);
  or or_6 (or_6_out, d_ff_3_q, Ready3);
  and and_1 (and_1_out, or_4_out, ~clear1);  // AND_Gate
  and and_2 (and_2_out, or_5_out, ~clear2);  // AND_Gate
  and and_3 (and_3_out, or_6_out, ~clear3);  // AND_Gate
  D_Flip_Flop #(.trigger("rising"), .Pre_Clr_Positions("LEGACY"), .NegatePresetClear("false"), .enable("true"), .NewFFLayout("false")) u_IR1 (
    .clk(CLK), .D(and_1_out), .Q(Ready1));  // open: Qn, preset, en, reset
  D_Flip_Flop #(.trigger("rising"), .Pre_Clr_Positions("LEGACY"), .NegatePresetClear("false"), .enable("true"), .NewFFLayout("false")) u_IR2 (
    .clk(CLK), .D(and_2_out), .Q(Ready2));  // open: Qn, preset, en, reset
  D_Flip_Flop #(.trigger("rising"), .Pre_Clr_Positions("LEGACY"), .NegatePresetClear("false"), .enable("true"), .NewFFLayout("false")) u_IR3 (
    .clk(CLK), .D(and_3_out), .Q(Ready3));  // open: Qn, preset, en, reset
  Comparator #(.width(5), .mode("twosComplement")) comparator_1 (.a(RD), .b(5'b01110), .eq(_14));  // open: gt, lt
  Comparator #(.width(5), .mode("twosComplement")) comparator_2 (.a(RD), .b(5'b01100), .eq(_12));  // open: gt, lt
  Comparator #(.width(5), .mode("twosComplement")) comparator_3 (.a(RD), .b(5'b01010), .eq(_10));  // open: gt, lt
  Pull_Resistor #(.pull(0)) pull_resistor_1 (.node(\优先嵌套字out ));
  and and_4 (and_4_out, _14, MTC0);
  Pull_Resistor #(.pull(0)) pull_resistor_2 (.node(IE_forward));
  and and_5 (and_5_out, _12, MTC0);
  and and_6 (and_6_out, MTC0, _10);
  Multiplexer #(.select(1), .width(1), .disabled("Z"), .enable("false")) multiplexer_1 (
    .in0(1'b0), .in1(\优先嵌套字out [0]), .out(multiplexer_1_out), .sel(and_6_out));
  Multiplexer #(.select(1), .width(1), .disabled("Z"), .enable("false")) multiplexer_2 (
    .in0(1'b0), .in1(\优先嵌套字out [1]), .out(multiplexer_2_out), .sel(and_6_out));
  Multiplexer #(.select(1), .width(1), .disabled("Z"), .enable("false")) multiplexer_3 (
    .in0(1'b0), .in1(\优先嵌套字out [2]), .out(multiplexer_3_out), .sel(and_6_out));
  Multiplexer #(.select(2), .width(32), .disabled("Z"), .enable("false")) multiplexer_4 (
    .in1(32'hac), .in2(32'h1a4), .in3(32'h29c), .out(IRaddr), .sel(IRnum));  // open: in0
  Multiplexer #(.select(1), .width(32), .disabled("Z"), .enable("false")) multiplexer_5 (
    .in0(PC3), .in1(EPC_forward), .out(multiplexer_5_out), .sel(and_4_out));
  or or_7 (or_7_out, IRenable, and_4_out);
  Multiplexer #(.select(1), .width(1), .disabled("Z"), .enable("false")) multiplexer_6 (
    .in0(IRenable), .in1(not_1_out), .out(multiplexer_6_out), .sel(and_5_out));
  not not_1 (not_1_out, IE_forward);
  or or_8 (or_8_out, IRenable, and_5_out, ERET);
  D_Flip_Flop #(.trigger("rising"), .Pre_Clr_Positions("LEGACY"), .NegatePresetClear("false"), .enable("true"), .NewFFLayout("false")) d_ff_4 (
    .clk(CLK), .D(multiplexer_1_out), .Q(\优先嵌套字 [0]), .Qn(d_ff_4_qn), .en(and_6_out));  // open: preset, reset
  D_Flip_Flop #(.trigger("rising"), .Pre_Clr_Positions("LEGACY"), .NegatePresetClear("false"), .enable("true"), .NewFFLayout("false")) d_ff_5 (
    .clk(CLK), .D(multiplexer_2_out), .Q(\优先嵌套字 [1]), .Qn(d_ff_5_qn), .en(and_6_out));  // open: preset, reset
  D_Flip_Flop #(.trigger("rising"), .Pre_Clr_Positions("LEGACY"), .NegatePresetClear("false"), .enable("true"), .NewFFLayout("false")) d_ff_6 (
    .clk(CLK), .D(multiplexer_3_out), .Q(\优先嵌套字 [2]), .Qn(d_ff_6_qn), .en(and_6_out));  // open: preset, reset
  Register #(.width(32), .trigger("rising"), .Select("low")) u_EPC (
    .D(multiplexer_5_out), .en(or_7_out), .Q(EPC), .clk(CLK));  // open: clr
  Register #(.width(1), .trigger("rising"), .Select("low")) u_IE (
    .D(multiplexer_6_out), .en(or_8_out), .Q(IE), .clk(CLK));  // open: clr
  Multiplexer #(.select(2), .width(32), .disabled("Z"), .enable("false")) multiplexer_7 (
    .in1({{29{1'b0}}, \优先嵌套字 }), .in2(EPC), .in3({{31{1'b0}}, IE}), .out(IRin), .sel(select));  // open: in0
  and and_7 (and_7_out, Ready1, d_ff_4_qn);
  and and_8 (and_8_out, Ready2, d_ff_5_qn);
  and and_9 (and_9_out, Ready3, d_ff_6_qn);
  Decoder #(.select(2), .tristate("false"), .disabled("Z"), .enable("false")) decoder_1 (
    .out1(decoder_1_out1), .out2(decoder_1_out2), .out3(decoder_1_out3), .sel(IRnum));  // open: out0
  Pull_Resistor #(.pull(0)) pull_resistor_3 (.node(IRnum));
  Priority_Encoder #(.select(2), .disabled("Z")) priority_encoder_1 (
    .in0(1'b0), .in1(and_7_out), .in2(and_8_out), .in3(and_9_out), .out(IRnum), .gs(priority_encoder_1_gs));  // open: en_out, en_in
  and and_10 (clear1, decoder_1_out1, ERET);
  and and_11 (clear2, decoder_1_out2, ERET);
  and and_12 (clear3, decoder_1_out3, ERET);
  Demultiplexer #(.select(2), .width(32), .tristate("false"), .disabled("Z"), .enable("false")) demultiplexer_1 (
    .out1(\优先嵌套字out ), .out2(EPC_forward), .out3({demultiplexer_1_out3, IE_forward}), .in(IRout), .sel(select));  // open: out0
  Priority_Encoder #(.select(2), .disabled("Z")) priority_encoder_2 (
    .in0(1'b0), .in1(_10), .in2(_14), .in3(_12), .out(select));  // open: gs, en_out, en_in
  and and_13 (IRenable, priority_encoder_1_gs, not_2_out);
  not not_2 (not_2_out, IE);

  // Notes on the sheet:
  //   Reset 
  //   Reset 
  //   Reset 
  //   1号中断信号采样参考电路
  //   2号中断信号采样参考电路
  //   3号中断信号采样参考电路
  //   中断识别（入口地址）
  //   CP0寄存组
  //   协寄存器组和通用寄存器组的数据交换
  //   中断返回逻辑
  //   中断仲裁及信号生成
endmodule

module \单周期MIPS_多级中断_内存堆栈版本  (
  input  IR1,
  input  IR2,
  input  IR3,
  output RegWrite,
  output MemWrite,
  output [31:0] PC,
  output [31:0] IR,
  output [31:0] RDin,
  output [31:0] MDin,
  output [31:0] LedData
);

  wire and_1_out, and_2_out, and_3_out, and_4_out, and_5_out, CLK, comparator_1_eq, ERET, Go, IR1_t, IR2_t,
       IR3_t, IRA, IRB, IRC, IRenable, lbu, lui, MFC0, mips_alu_1_equal, MTC0, \n27_4条扩展指令控制器_1_alu_src ,
       \n27_4条扩展指令控制器_1_beq , \n27_4条扩展指令控制器_1_bgez , \n27_4条扩展指令控制器_1_bne , \n27_4条扩展指令控制器_1_jal ,
       \n27_4条扩展指令控制器_1_jmp , \n27_4条扩展指令控制器_1_jr , \n27_4条扩展指令控制器_1_memtoreg , \n27_4条扩展指令控制器_1_regdst ,
       not_1_out, not_3_out, not_4_out, or_1_out, or_2_out, or_6_out, PCok, register_2_q, RST, SignedExt,
       Syscall, W1, W2, W3;
  wire [3:0] \n27_4条扩展指令控制器_1_alu_op ;
  wire [4:0] multiplexer_6_out, multiplexer_7_out, multiplexer_8_out, multiplexer_9_out;
  wire [15:0] \总周期数 ;
  wire [31:0] adder_1_out, adder_2_out, bit_extender_1_out, bit_extender_2_out, bit_extender_3_out, EPC,
       IRaddr, IRin, IRout, mips_alu_1_result, multiplexer_5_out, multiplexer_11_out, multiplexer_13_out,
       multiplexer_14_out, multiplexer_15_out, multiplexer_16_out, multiplexer_17_out, multiplexer_18_out,
       PC1, PC2, PC3, PC4, R1, ram_1_data, shifter_1_out, shifter_2_out, shifter_3_out;

  Clock #(.highDuration(1), .lowDuration(1)) clock_1 (.out(CLK));
  Button _1 (.out(IRA));
  Button _2 (.out(IRB));
  Button _3 (.out(IRC));
  Button \u_总复位  (.out(RST));
  LED #(.active("true")) led_1 (.in(W1));
  LED #(.active("true")) led_2 (.in(W2));
  LED #(.active("true")) led_3 (.in(W3));
  Button \u_继续运行  (.out(Go));
  Multiplexer #(.select(1), .width(32), .disabled("Z"), .enable("false")) multiplexer_1 (
    .in0(adder_1_out), .in1(adder_2_out), .out(PC1), .sel(or_6_out));
  Multiplexer #(.select(1), .width(32), .disabled("Z"), .enable("false")) multiplexer_2 (
    .in0(PC1), .in1(shifter_3_out), .out(PC2), .sel(or_1_out));
  Multiplexer #(.select(1), .width(32), .disabled("Z"), .enable("false")) multiplexer_3 (
    .in0(PC2), .in1(R1), .out(PC3), .sel(\n27_4条扩展指令控制器_1_jr ));
  Multiplexer #(.select(1), .width(32), .disabled("Z"), .enable("false")) multiplexer_4 (
    .in0(PC3), .in1(IRaddr), .out(PC4), .sel(IRenable));
  Multiplexer #(.select(1), .width(32), .disabled("Z"), .enable("false")) multiplexer_5 (
    .in0(PC4), .in1(EPC), .out(multiplexer_5_out), .sel(ERET));
  Comparator #(.width(32), .mode("twosComplement")) comparator_1 (
    .a(MDin), .b(32'h22), .eq(comparator_1_eq));  // open: gt, lt
  not not_1 (not_1_out, comparator_1_eq);
  Hex_Digit_Display hex_digit_display_1 (.value(LedData[27:24]));  // open: dp
  Hex_Digit_Display hex_digit_display_2 (.value(LedData[31:28]));  // open: dp
  or or_1 (or_1_out, \n27_4条扩展指令控制器_1_jal , \n27_4条扩展指令控制器_1_jmp );
  Register #(.width(32), .trigger("rising"), .Select("low")) u_PC (
    .D(multiplexer_5_out), .en(PCok), .Q(PC), .clk(CLK), .clr(RST));
  and and_1 (and_1_out, comparator_1_eq, Syscall);
  and and_2 (and_2_out, not_1_out, Syscall);
  Hex_Digit_Display hex_digit_display_3 (.value(LedData[19:16]));  // open: dp
  Hex_Digit_Display hex_digit_display_4 (.value(LedData[23:20]));  // open: dp
  Adder #(.width(32)) adder_1 (.a(PC), .b(32'h4), .out(adder_1_out));  // open: cin, cout
  Register #(.width(32), .trigger("rising"), .Select("low")) register_1 (
    .D(R1), .en(and_1_out), .Q(LedData), .clk(CLK), .clr(RST));
  Register #(.width(1), .trigger("rising"), .Select("low")) register_2 (
    .D(Syscall), .en(and_2_out), .Q(register_2_q), .clk(CLK), .clr(or_2_out));
  not not_2 (PCok, register_2_q);
  or or_2 (or_2_out, Go, RST);
  Hex_Digit_Display hex_digit_display_5 (.value(LedData[11:8]));  // open: dp
  Hex_Digit_Display hex_digit_display_6 (.value(LedData[15:12]));  // open: dp
  Counter #(.width(16), .max('hffff), .ongoal("wrap"), .trigger("rising"), .behavior("old")) counter_1 (
    .count(PCok), .Q(\总周期数 ), .clk(CLK), .clr(RST));  // open: load, D, carry, preset
  ROM #(.addrWidth(10), .dataWidth(32), .Select("high")) rom_1 (.addr(PC[11:2]), .data(IR));
  Hex_Digit_Display hex_digit_display_7 (.value(LedData[7:4]));  // open: dp
  Hex_Digit_Display hex_digit_display_8 (.value(LedData[3:0]));  // open: dp
  // Probe on \总周期数 
  Multiplexer #(.select(1), .width(5), .disabled("Z"), .enable("false")) multiplexer_6 (
    .in0(IR[25:21]), .in1(5'b00100), .out(multiplexer_6_out), .sel(Syscall));
  Multiplexer #(.select(1), .width(5), .disabled("Z"), .enable("false")) multiplexer_7 (
    .in0(IR[20:16]), .in1(5'b00010), .out(multiplexer_7_out), .sel(Syscall));
  Multiplexer #(.select(1), .width(5), .disabled("Z"), .enable("false")) multiplexer_8 (
    .in0(IR[20:16]), .in1(IR[15:11]), .out(multiplexer_8_out), .sel(\n27_4条扩展指令控制器_1_regdst ));
  Multiplexer #(.select(1), .width(5), .disabled("Z"), .enable("false")) multiplexer_9 (
    .in0(multiplexer_8_out), .in1({5{1'b1}}), .out(multiplexer_9_out), .sel(\n27_4条扩展指令控制器_1_jal ));
  assign bit_extender_1_out = {{16{1'b0}}, IR[15:0]};  // Bit_Extender bit_extender_1
  assign bit_extender_2_out = {{16{IR[15]}}, IR[15:0]};  // Bit_Extender bit_extender_2
  assign bit_extender_3_out = {{6{IR[25]}}, IR[25:0]};  // Bit_Extender bit_extender_3
  or or_3 (IR1_t, IR1, IRA);
  \_27_4条扩展指令控制器  \u_27_4条扩展指令控制器_1  (
    .OP(IR[31:26]), .Func(IR[5:0]), .ALU_OP(\n27_4条扩展指令控制器_1_alu_op ), .MemToReg(\n27_4条扩展指令控制器_1_memtoreg ),
    .MemWrite(MemWrite), .ALU_SRC(\n27_4条扩展指令控制器_1_alu_src ), .SysCALL(Syscall), .SignedExt(SignedExt),
    .RegDst(\n27_4条扩展指令控制器_1_regdst ), .Beq(\n27_4条扩展指令控制器_1_beq ), .Bne(\n27_4条扩展指令控制器_1_bne ),
    .JR(\n27_4条扩展指令控制器_1_jr ), .JMP(\n27_4条扩展指令控制器_1_jmp ), .JAL(\n27_4条扩展指令控制器_1_jal ), .LUI(lui),
    .LBU(lbu), .BGEZ(\n27_4条扩展指令控制器_1_bgez ), .MTC0(MTC0), .MFMT(IR[25:21]), .ERET(ERET), .MFC0(MFC0),
    .RegWrite(RegWrite));
  MIPS_Regifile mips_regifile_1 (
    .Din(RDin), .Clk(CLK), .R1(R1), .R2(MDin), .WE(RegWrite), .W_num(multiplexer_9_out),
    .R1_num(multiplexer_6_out), .R2_num(multiplexer_7_out));
  Multiplexer #(.select(1), .width(32), .disabled("Z"), .enable("false")) multiplexer_10 (
    .in0(multiplexer_13_out), .in1(IRin), .out(RDin), .sel(MFC0));
  Multiplexer #(.select(1), .width(32), .disabled("Z"), .enable("false")) multiplexer_11 (
    .in0(bit_extender_1_out), .in1(bit_extender_2_out), .out(multiplexer_11_out), .sel(SignedExt));
  Multiplexer #(.select(1), .width(32), .disabled("Z"), .enable("false")) multiplexer_12 (
    .in0({32{1'b0}}), .in1(MDin), .out(IRout), .sel(MTC0));
  or or_4 (IR2_t, IR2, IRB);
  Multiplexer #(.select(1), .width(32), .disabled("Z"), .enable("false")) multiplexer_13 (
    .in0(multiplexer_16_out), .in1(adder_1_out), .out(multiplexer_13_out), .sel(\n27_4条扩展指令控制器_1_jal ));
  Multiplexer #(.select(1), .width(32), .disabled("Z"), .enable("false")) multiplexer_14 (
    .in0(MDin), .in1(multiplexer_11_out), .out(multiplexer_14_out), .sel(\n27_4条扩展指令控制器_1_alu_src ));
  Shifter #(.width(32), .shift("ll")) shifter_1 (.in(multiplexer_11_out), .\dist (5'b00010), .out(shifter_1_out));
  Shifter #(.width(32), .shift("ll")) shifter_2 (.in(bit_extender_1_out), .\dist (5'b10000), .out(shifter_2_out));
  Shifter #(.width(32), .shift("ll")) shifter_3 (.in(bit_extender_3_out), .\dist (5'b00010), .out(shifter_3_out));
  or or_5 (IR3_t, IR3, IRC);
  Multiplexer #(.select(1), .width(32), .disabled("Z"), .enable("false")) multiplexer_15 (
    .in0(multiplexer_14_out), .in1({32{1'b0}}), .out(multiplexer_15_out), .sel(\n27_4条扩展指令控制器_1_bgez ));
  MIPS_ALU mips_alu_1 (
    .X(R1), .Y(multiplexer_15_out), .AluOP(\n27_4条扩展指令控制器_1_alu_op ), .Equal(mips_alu_1_equal),
    .Result(mips_alu_1_result), .shamt(IR[10:6]));  // open: Result_2
  Multiplexer #(.select(1), .width(32), .disabled("Z"), .enable("false")) multiplexer_16 (
    .in0(multiplexer_17_out), .in1(shifter_2_out), .out(multiplexer_16_out), .sel(lui));
  not not_3 (not_3_out, mips_alu_1_result[0]);
  not not_4 (not_4_out, mips_alu_1_equal);
  Adder #(.width(32)) adder_2 (.a(shifter_1_out), .b(adder_1_out), .out(adder_2_out));  // open: cin, cout
  and and_3 (and_3_out, not_3_out, \n27_4条扩展指令控制器_1_bgez );
  and and_4 (and_4_out, mips_alu_1_equal, \n27_4条扩展指令控制器_1_beq );
  and and_5 (and_5_out, not_4_out, \n27_4条扩展指令控制器_1_bne );
  RAM #(.addrWidth(10), .dataWidth(32), .bus("separate"), .Select("high")) ram_1 (
    .addr(mips_alu_1_result[11:2]), .din(MDin), .data(ram_1_data), .str(MemWrite), .clk(CLK), .clr(RST));  // open: sel, ld
  \多级中断_内存堆栈_发生器  \u_多级中断_内存堆栈_发生器_1  (
    .W1(W1), .CLK(CLK), .RD(IR[15:11]), .W2(W2), .IRin(IRin), .IR1(IR1_t), .W3(W3), .PC3(PC3), .IR2(IR2_t),
    .IRenable(IRenable), .IR3(IR3_t), .IRaddr(IRaddr), .MTC0(MTC0), .EPC(EPC), .IRout(IRout), .ERET(ERET));
  or or_6 (or_6_out, and_3_out, and_4_out, and_5_out);
  Multiplexer #(.select(1), .width(32), .disabled("Z"), .enable("false")) multiplexer_17 (
    .in0(mips_alu_1_result), .in1(multiplexer_18_out), .out(multiplexer_17_out),
    .sel(\n27_4条扩展指令控制器_1_memtoreg ));
  Multiplexer #(.select(1), .width(32), .disabled("Z"), .enable("false")) multiplexer_18 (
    .in0(ram_1_data), .in1({{24{1'b0}}, ram_1_data[7:0]}), .out(multiplexer_18_out), .sel(lbu));

  // Other names for the same wires on the sheet: RD[4:0] = IR[15:11]; R2[31:0] = MDin

  // Notes on the sheet:
  //   中断源
  //   中断等待指示
  //   总复位信号应将除ROM以外所有存储组件全部清零
  //   数码管输出
  //   指令存储器
  //   指令字
  //   contents of rom_1 (hex, n*v repeats v):
  //   201d07d0 20100001 109fc0 139fc3 8021 2012000c 24160008 26100001 3210000f 20080008 20090001 139900
  //   2709825 132020 20020022 c 1094022 1500fff9 22100001 2018000f 2188024 108700 20080008 20090001 139902
  //   2709825 132021 20020022 c 1094022 1500fff9 108702 2c9b022 12c00001 8000c07 4020 1084027 84400
  //   3508ffff 82021 20020022 c 8000c01 afa20000 23bd0004 afa40000 23bd0004 afb00000 23bd0004 afb30000
  //   23bd0004 afb40000 23bd0004 afb50000 23bd0004 afb60000 23bd0004 40167000 afb60000 23bd0004 40806000
  //   20160001 20140003 20150001 168020 108100 2149825 132020 20020022 c 1600fffa 295a022 1680fff7
  //   20160001 40966000 23bdfffc 8fb60000 40967000 23bdfffc 8fb60000 23bdfffc 8fb50000 23bdfffc 8fb40000
  //   23bdfffc 8fb30000 23bdfffc 8fb00000 23bdfffc 8fa40000 23bdfffc 8fa20000 42000018 afa20000 23bd0004
  //   afa40000 23bd0004 afb00000 23bd0004 afb30000 23bd0004 afb40000 23bd0004 afb50000 23bd0004 afb60000
  //   23bd0004 40167000 afb60000 23bd0004 40806000 20160002 20140003 20150001 168020 108100 2149825 132020
  //   20020022 c 1600fffa 295a022 1680fff7 20160001 40966000 23bdfffc 8fb60000 40967000 23bdfffc 8fb60000
  //   23bdfffc 8fb50000 23bdfffc 8fb40000 23bdfffc 8fb30000 23bdfffc 8fb00000 23bdfffc 8fa40000 23bdfffc
  //   8fa20000 42000018 afa20000 23bd0004 afa40000 23bd0004 afb00000 23bd0004 afb30000 23bd0004 afb40000
  //   23bd0004 afb50000 23bd0004 afb60000 23bd0004 40167000 afb60000 23bd0004 40806000 20160003 20140003
  //   20150001 168020 108100 2149825 132020 20020022 c 1600fffa 295a022 1680fff7 20160001 40966000
  //   23bdfffc 8fb60000 40967000 23bdfffc 8fb60000 23bdfffc 8fb50000 23bdfffc 8fb40000 23bdfffc 8fb30000
  //   23bdfffc 8fb00000 23bdfffc 8fa40000 23bdfffc 8fa20000 42000018
  //   数码管输出应该用寄存器锁存，否则显示数据只能一闪而过
  //   Func
  //   OP
  //   Func
  //   MF/MT
  //   rs
  //   rt
  //   rd
  //   JMP
  //   JR
  //   OP
  //   MF/MT
  //   Syscall
  //   Beq
  //   Bgez
  //   Bne
  //   MemToReg
  //   MemWrite
  //   AluOP
  //   AluSrcB
  //   RegWrite
  //   JAL
  //   RegDst
  //   ERET
  //   为方便自动评测，需要输出PC，IR，寄存器堆写如数据RDin
  //   RAM写使能MemWrite、RAM写入数据MDin等信号
  //   数据存储器
endmodule

// 内存堆栈中断发生
module \多级中断_内存堆栈_发生器  (
  input  CLK,
  input  [4:0] RD,
  input  IR1,
  input  [31:0] PC3,
  input  IR2,
  input  IR3,
  input  MTC0,
  input  [31:0] IRout,
  input  ERET,
  output W1,
  output W2,
  output [31:0] IRin,
  output W3,
  output IRenable,
  output [31:0] IRaddr,
  output [31:0] EPC
);

  wire _1, _12, _14, and_1_out, and_2_out, and_3_out, and_4_out, and_5_out, and_11_out, clear1, clear2,
       clear3, comparator_2_eq, d_ff_1_q, d_ff_2_q, d_ff_3_q, decoder_1_out1, decoder_1_out2, decoder_1_out3,
       IE, IE_q, multiplexer_6_out, or_4_out, or_5_out, or_6_out, or_7_out, or_8_out, priority_encoder_1_gs,
       priority_encoder_2_out, Ready1, Ready2, Ready3, xnor_1_out, \中断来临 ;
  wire [1:0] IRnum, multiplexer_4_out, priority_encoder_1_out, Renum, \嵌套1_q , \嵌套2_q ;
  wire [31:0] multiplexer_2_out;

  D_Flip_Flop #(.trigger("rising"), .Pre_Clr_Positions("LEGACY"), .NegatePresetClear("false"), .enable("true"), .NewFFLayout("false")) d_ff_1 (
    .clk(IR1), .D(1'b1), .Q(d_ff_1_q), .reset(Ready1));  // open: Qn, preset, en
  or or_1 (W1, Ready1, d_ff_1_q);
  D_Flip_Flop #(.trigger("rising"), .Pre_Clr_Positions("LEGACY"), .NegatePresetClear("false"), .enable("true"), .NewFFLayout("false")) d_ff_2 (
    .clk(IR2), .D(1'b1), .Q(d_ff_2_q), .reset(Ready2));  // open: Qn, preset, en
  or or_2 (W2, Ready2, d_ff_2_q);
  D_Flip_Flop #(.trigger("rising"), .Pre_Clr_Positions("LEGACY"), .NegatePresetClear("false"), .enable("true"), .NewFFLayout("false")) d_ff_3 (
    .clk(IR3), .D(1'b1), .Q(d_ff_3_q), .reset(Ready3));  // open: Qn, preset, en
  or or_3 (W3, Ready3, d_ff_3_q);
  or or_4 (or_4_out, d_ff_1_q, Ready1);
  or or_5 (or_5_out, d_ff_2_q, Ready2);
  or or_6 (or_6_out, d_ff_3_q, Ready3);
  and and_1 (and_1_out, or_4_out, ~clear1);  // AND_Gate
  and and_2 (and_2_out, or_5_out, ~clear2);  // AND_Gate
  and and_3 (and_3_out, or_6_out, ~clear3);  // AND_Gate
  D_Flip_Flop #(.trigger("rising"), .Pre_Clr_Positions("LEGACY"), .NegatePresetClear("false"), .enable("true"), .NewFFLayout("false")) u_IR1 (
    .clk(CLK), .D(and_1_out), .Q(Ready1));  // open: Qn, preset, en, reset
  D_Flip_Flop #(.trigger("rising"), .Pre_Clr_Positions("LEGACY"), .NegatePresetClear("false"), .enable("true"), .NewFFLayout("false")) u_IR2 (
    .clk(CLK), .D(and_2_out), .Q(Ready2));  // open: Qn, preset, en, reset
  D_Flip_Flop #(.trigger("rising"), .Pre_Clr_Positions("LEGACY"), .NegatePresetClear("false"), .enable("true"), .NewFFLayout("false")) u_IR3 (
    .clk(CLK), .D(and_3_out), .Q(Ready3));  // open: Qn, preset, en, reset
  Comparator #(.width(5), .mode("twosComplement")) comparator_1 (.a(RD), .b(5'b01110), .eq(_14));  // open: gt, lt
  and and_4 (and_4_out, _14, MTC0);
  Priority_Encoder #(.select(2), .disabled("Z")) priority_encoder_1 (
    .in0(1'b0), .in1(Ready1), .in2(Ready2), .in3(Ready3), .out(priority_encoder_1_out),
    .gs(priority_encoder_1_gs));  // open: en_out, en_in
  Multiplexer #(.select(2), .width(32), .disabled("Z"), .enable("false")) multiplexer_1 (
    .in1(32'h30ac), .in2(32'h3174), .in3(32'h323c), .out(IRaddr), .sel(IRnum));  // open: in0
  Multiplexer #(.select(1), .width(32), .disabled("Z"), .enable("false")) multiplexer_2 (
    .in0(PC3), .in1(IRout), .out(multiplexer_2_out), .sel(and_4_out));
  or or_7 (or_7_out, and_4_out, and_5_out);
  and and_5 (and_5_out, ~ERET, IRenable);  // AND_Gate
  Pull_Resistor #(.pull(0)) pull_resistor_1 (.node(priority_encoder_1_out));
  and and_6 (IRenable, \中断来临 , priority_encoder_1_gs, IE);
  Decoder #(.select(2), .tristate("false"), .disabled("Z"), .enable("false")) decoder_1 (
    .out1(decoder_1_out1), .out2(decoder_1_out2), .out3(decoder_1_out3), .sel(Renum));  // open: out0
  Register #(.width(32), .trigger("rising"), .Select("low")) u_EPC (
    .D(multiplexer_2_out), .en(or_7_out), .Q(EPC), .clk(CLK));  // open: clr
  Multiplexer #(.select(1), .width(2), .disabled("Z"), .enable("false")) multiplexer_3 (
    .in0(priority_encoder_1_out), .in1(\嵌套1_q ), .out(IRnum), .sel(ERET));
  and and_7 (clear1, ERET, decoder_1_out1);
  and and_8 (clear2, ERET, decoder_1_out2);
  and and_9 (clear3, ERET, decoder_1_out3);
  Register #(.width(2), .trigger("rising"), .Select("low")) \u_当前中断号  (
    .D(IRnum), .en(or_8_out), .Q(Renum), .clk(CLK));  // open: clr
  Multiplexer #(.select(1), .width(2), .disabled("Z"), .enable("false")) multiplexer_4 (
    .in0(Renum), .in1(\嵌套2_q ), .out(multiplexer_4_out), .sel(ERET));
  Comparator #(.width(2), .mode("twosComplement")) comparator_2 (
    .a(IRnum), .b(Renum), .eq(comparator_2_eq));  // open: gt, lt
  Comparator #(.width(5), .mode("twosComplement")) comparator_3 (.a(RD), .b(5'b01100), .eq(_12));  // open: gt, lt
  Register #(.width(2), .trigger("rising"), .Select("low")) \u_嵌套1  (
    .D(multiplexer_4_out), .en(or_8_out), .Q(\嵌套1_q ), .clk(CLK));  // open: clr
  not not_1 (\中断来临 , comparator_2_eq);
  Priority_Encoder #(.select(1), .disabled("Z")) priority_encoder_2 (
    .in0(_12), .in1(_14), .out(priority_encoder_2_out));  // open: gs, en_out, en_in
  and and_10 (_1, _12, MTC0);
  and and_11 (and_11_out, ~ERET, xnor_1_out);  // AND_Gate
  xnor xnor_1 (xnor_1_out, IRenable, IE);
  Register #(.width(2), .trigger("rising"), .Select("low")) \u_嵌套2  (
    .D(\嵌套1_q ), .en(or_8_out), .Q(\嵌套2_q ), .clk(CLK));  // open: clr
  or or_8 (or_8_out, IRenable, ERET);
  Multiplexer #(.select(1), .width(32), .disabled("Z"), .enable("false")) multiplexer_5 (
    .in0({{31{1'b0}}, IE}), .in1(EPC), .out(IRin), .sel(priority_encoder_2_out));
  Register #(.width(1), .trigger("rising"), .Select("low")) u_IE (
    .D(multiplexer_6_out), .Q(IE_q), .clk(CLK));  // open: en, clr
  Multiplexer #(.select(1), .width(1), .disabled("Z"), .enable("false")) multiplexer_6 (
    .in0(and_11_out), .in1(IRout[0]), .out(multiplexer_6_out), .sel(_1));
  not not_2 (IE, IE_q);

  // Other names for the same wires on the sheet: EPC_forward[31:0] = IRout; IE_forward = IRout[0]

  // Notes on the sheet:
  //   Reset 
  //   1号中断信号采样参考电路
  //   Reset 
  //   Reset 
  //   2号中断信号采样参考电路
  //   3号中断信号采样参考电路
  //   中断识别（入口地址）
  //   EPC寄存器
  //   中断仲裁和中断生成逻辑
  //   中断返回逻辑
  //   MFC0送入
  //   IE寄存器
  //   MTC0读回
endmodule

module \单周期MIPS_多级中断  (
  input  IR1,
  input  IR2,
  input  IR3,
  output RegWrite,
  output MemWrite,
  output [31:0] PC,
  output [31:0] IR,
  output [31:0] RDin,
  output [31:0] MDin,
  output [31:0] LedData
);

  wire and_1_out, and_2_out, and_3_out, and_4_out, and_5_out, CLK, comparator_1_eq, ERET, Go, IR1_t, IR2_t,
       IR3_t, IRA, IRB, IRC, IRenable, lbu, lui, MFC0, mips_alu_1_equal, MTC0, \n27_4条扩展指令控制器_1_alu_src ,
       \n27_4条扩展指令控制器_1_beq , \n27_4条扩展指令控制器_1_bgez , \n27_4条扩展指令控制器_1_bne , \n27_4条扩展指令控制器_1_jal ,
       \n27_4条扩展指令控制器_1_jmp , \n27_4条扩展指令控制器_1_jr , \n27_4条扩展指令控制器_1_memtoreg , \n27_4条扩展指令控制器_1_regdst ,
       not_1_out, not_3_out, not_4_out, or_1_out, or_2_out, or_6_out, PCok, register_2_q, RST, SignedExt,
       Syscall, W1, W2, W3;
  wire [3:0] \n27_4条扩展指令控制器_1_alu_op ;
  wire [4:0] multiplexer_6_out, multiplexer_7_out, multiplexer_8_out, multiplexer_9_out;
  wire [15:0] \总周期数 ;
  wire [31:0] adder_1_out, adder_2_out, bit_extender_1_out, bit_extender_2_out, bit_extender_3_out, EPC,
       IRaddr, mips_alu_1_result, multiplexer_5_out, multiplexer_10_out, multiplexer_11_out,
       multiplexer_13_out, multiplexer_14_out, multiplexer_15_out, multiplexer_16_out, PC1, PC2, PC3, PC4,
       R1, ram_1_data, shifter_1_out, shifter_2_out, shifter_3_out;

  Clock #(.highDuration(1), .lowDuration(1)) clock_1 (.out(CLK));
  Button _1 (.out(IRA));
  Button _2 (.out(IRB));
  Button _3 (.out(IRC));
  Button \u_总复位  (.out(RST));
  LED #(.active("true")) led_1 (.in(W1));
  LED #(.active("true")) led_2 (.in(W2));
  LED #(.active("true")) led_3 (.in(W3));
  Button \u_继续运行  (.out(Go));
  Multiplexer #(.select(1), .width(32), .disabled("Z"), .enable("false")) multiplexer_1 (
    .in0(adder_1_out), .in1(adder_2_out), .out(PC1), .sel(or_6_out));
  Multiplexer #(.select(1), .width(32), .disabled("Z"), .enable("false")) multiplexer_2 (
    .in0(PC1), .in1(shifter_3_out), .out(PC2), .sel(or_1_out));
  Multiplexer #(.select(1), .width(32), .disabled("Z"), .enable("false")) multiplexer_3 (
    .in0(PC2), .in1(R1), .out(PC3), .sel(\n27_4条扩展指令控制器_1_jr ));
  Multiplexer #(.select(1), .width(32), .disabled("Z"), .enable("false")) multiplexer_4 (
    .in0(PC3), .in1(IRaddr), .out(PC4), .sel(IRenable));
  Multiplexer #(.select(1), .width(32), .disabled("Z"), .enable("false")) multiplexer_5 (
    .in0(PC4), .in1(EPC), .out(multiplexer_5_out), .sel(ERET));
  Comparator #(.width(32), .mode("twosComplement")) comparator_1 (
    .a(MDin), .b(32'h22), .eq(comparator_1_eq));  // open: gt, lt
  not not_1 (not_1_out, comparator_1_eq);
  Hex_Digit_Display hex_digit_display_1 (.value(LedData[27:24]));  // open: dp
  Hex_Digit_Display hex_digit_display_2 (.value(LedData[31:28]));  // open: dp
  or or_1 (or_1_out, \n27_4条扩展指令控制器_1_jal , \n27_4条扩展指令控制器_1_jmp );
  Register #(.width(32), .trigger("rising"), .Select("low")) u_PC (
    .D(multiplexer_5_out), .en(PCok), .Q(PC), .clk(CLK), .clr(RST));
  and and_1 (and_1_out, comparator_1_eq, Syscall);
  and and_2 (and_2_out, not_1_out, Syscall);
  Hex_Digit_Display hex_digit_display_3 (.value(LedData[23:20]));  // open: dp
  Hex_Digit_Display hex_digit_display_4 (.value(LedData[19:16]));  // open: dp
  Adder #(.width(32)) adder_1 (.a(PC), .b(32'h4), .out(adder_1_out));  // open: cin, cout
  Register #(.width(32), .trigger("rising"), .Select("low")) register_1 (
    .D(R1), .en(and_1_out), .Q(LedData), .clk(CLK), .clr(RST));
  Register #(.width(1), .trigger("rising"), .Select("low")) register_2 (
    .D(Syscall), .en(and_2_out), .Q(register_2_q), .clk(CLK), .clr(or_2_out));
  not not_2 (PCok, register_2_q);
  or or_2 (or_2_out, Go, RST);
  Hex_Digit_Display hex_digit_display_5 (.value(LedData[15:12]));  // open: dp
  Hex_Digit_Display hex_digit_display_6 (.value(LedData[11:8]));  // open: dp
  Counter #(.width(16), .max('hffff), .ongoal("wrap"), .trigger("rising"), .behavior("old")) counter_1 (
    .count(PCok), .Q(\总周期数 ), .clk(CLK), .clr(RST));  // open: load, D, carry, preset
  ROM #(.addrWidth(10), .dataWidth(32), .Select("high")) rom_1 (.addr(PC[11:2]), .data(IR));
  Hex_Digit_Display hex_digit_display_7 (.value(LedData[7:4]));  // open: dp
  Hex_Digit_Display hex_digit_display_8 (.value(LedData[3:0]));  // open: dp
  // Probe on \总周期数 
  Multiplexer #(.select(1), .width(5), .disabled("Z"), .enable("false")) multiplexer_6 (
    .in0(IR[25:21]), .in1(5'b00100), .out(multiplexer_6_out), .sel(Syscall));
  Multiplexer #(.select(1), .width(5), .disabled("Z"), .enable("false")) multiplexer_7 (
    .in0(IR[20:16]), .in1(5'b00010), .out(multiplexer_7_out), .sel(Syscall));
  Multiplexer #(.select(1), .width(5), .disabled("Z"), .enable("false")) multiplexer_8 (
    .in0(IR[20:16]), .in1(IR[15:11]), .out(multiplexer_8_out), .sel(\n27_4条扩展指令控制器_1_regdst ));
  Multiplexer #(.select(1), .width(5), .disabled("Z"), .enable("false")) multiplexer_9 (
    .in0(multiplexer_8_out), .in1({5{1'b1}}), .out(multiplexer_9_out), .sel(\n27_4条扩展指令控制器_1_jal ));
  assign bit_extender_1_out = {{16{1'b0}}, IR[15:0]};  // Bit_Extender bit_extender_1
  assign bit_extender_2_out = {{16{IR[15]}}, IR[15:0]};  // Bit_Extender bit_extender_2
  assign bit_extender_3_out = {{6{IR[25]}}, IR[25:0]};  // Bit_Extender bit_extender_3
  or or_3 (IR1_t, IR1, IRA);
  \_27_4条扩展指令控制器  \u_27_4条扩展指令控制器_1  (
    .OP(IR[31:26]), .Func(IR[5:0]), .ALU_OP(\n27_4条扩展指令控制器_1_alu_op ), .MemToReg(\n27_4条扩展指令控制器_1_memtoreg ),
    .MemWrite(MemWrite), .ALU_SRC(\n27_4条扩展指令控制器_1_alu_src ), .SysCALL(Syscall), .SignedExt(SignedExt),
    .RegDst(\n27_4条扩展指令控制器_1_regdst ), .Beq(\n27_4条扩展指令控制器_1_beq ), .Bne(\n27_4条扩展指令控制器_1_bne ),
    .JR(\n27_4条扩展指令控制器_1_jr ), .JMP(\n27_4条扩展指令控制器_1_jmp ), .JAL(\n27_4条扩展指令控制器_1_jal ), .LUI(lui),
    .LBU(lbu), .BGEZ(\n27_4条扩展指令控制器_1_bgez ), .MTC0(MTC0), .MFMT(IR[25:21]), .ERET(ERET), .MFC0(MFC0),
    .RegWrite(RegWrite));
  MIPS_Regifile mips_regifile_1 (
    .Din(RDin), .Clk(CLK), .R1(R1), .R2(MDin), .WE(RegWrite), .W_num(multiplexer_9_out),
    .R1_num(multiplexer_6_out), .R2_num(multiplexer_7_out));
  Multiplexer #(.select(1), .width(32), .disabled("Z"), .enable("false")) multiplexer_10 (
    .in0(bit_extender_1_out), .in1(bit_extender_2_out), .out(multiplexer_10_out), .sel(SignedExt));
  or or_4 (IR2_t, IR2, IRB);
  Multiplexer #(.select(1), .width(32), .disabled("Z"), .enable("false")) multiplexer_11 (
    .in0(MDin), .in1(multiplexer_10_out), .out(multiplexer_11_out), .sel(\n27_4条扩展指令控制器_1_alu_src ));
  Multiplexer #(.select(1), .width(32), .disabled("Z"), .enable("false")) multiplexer_12 (
    .in0(multiplexer_14_out), .in1(adder_1_out), .out(RDin), .sel(\n27_4条扩展指令控制器_1_jal ));
  Shifter #(.width(32), .shift("ll")) shifter_1 (.in(multiplexer_10_out), .\dist (5'b00010), .out(shifter_1_out));
  Shifter #(.width(32), .shift("ll")) shifter_2 (.in(bit_extender_1_out), .\dist (5'b10000), .out(shifter_2_out));
  Shifter #(.width(32), .shift("ll")) shifter_3 (.in(bit_extender_3_out), .\dist (5'b00010), .out(shifter_3_out));
  Multiplexer #(.select(1), .width(32), .disabled("Z"), .enable("false")) multiplexer_13 (
    .in0(multiplexer_11_out), .in1({32{1'b0}}), .out(multiplexer_13_out), .sel(\n27_4条扩展指令控制器_1_bgez ));
  or or_5 (IR3_t, IR3, IRC);
  MIPS_ALU mips_alu_1 (
    .X(R1), .Y(multiplexer_13_out), .AluOP(\n27_4条扩展指令控制器_1_alu_op ), .Equal(mips_alu_1_equal),
    .Result(mips_alu_1_result), .shamt(IR[10:6]));  // open: Result_2
  not not_3 (not_3_out, mips_alu_1_result[0]);
  not not_4 (not_4_out, mips_alu_1_equal);
  Multiplexer #(.select(1), .width(32), .disabled("Z"), .enable("false")) multiplexer_14 (
    .in0(multiplexer_16_out), .in1(shifter_2_out), .out(multiplexer_14_out), .sel(lui));
  Adder #(.width(32)) adder_2 (.a(shifter_1_out), .b(adder_1_out), .out(adder_2_out));  // open: cin, cout
  and and_3 (and_3_out, not_3_out, \n27_4条扩展指令控制器_1_bgez );
  and and_4 (and_4_out, mips_alu_1_equal, \n27_4条扩展指令控制器_1_beq );
  and and_5 (and_5_out, not_4_out, \n27_4条扩展指令控制器_1_bne );
  RAM #(.addrWidth(10), .dataWidth(32), .bus("separate"), .Select("high")) ram_1 (
    .addr(mips_alu_1_result[11:2]), .din(MDin), .data(ram_1_data), .str(MemWrite), .clk(CLK), .clr(RST));  // open: sel, ld
  \多级中断_硬件保护_发生器  \u_多级中断_硬件保护_发生器_1  (
    .CLK(CLK), .RD(IR[15:11]), .W1(W1), .IR1(IR1_t), .EPC(EPC), .MFC0(MFC0), .W2(W2), .IR2(IR2_t), .W3(W3),
    .IR3(IR3_t), .PC3(PC3), .IRaddr(IRaddr), .MTC0(MTC0), .IRenable(IRenable), .ERET(ERET));
  or or_6 (or_6_out, and_3_out, and_4_out, and_5_out);
  Multiplexer #(.select(1), .width(32), .disabled("Z"), .enable("false")) multiplexer_15 (
    .in0(ram_1_data), .in1({{24{1'b0}}, ram_1_data[7:0]}), .out(multiplexer_15_out), .sel(lbu));
  Multiplexer #(.select(1), .width(32), .disabled("Z"), .enable("false")) multiplexer_16 (
    .in0(mips_alu_1_result), .in1(multiplexer_15_out), .out(multiplexer_16_out),
    .sel(\n27_4条扩展指令控制器_1_memtoreg ));

  // Other names for the same wires on the sheet: RD[4:0] = IR[15:11]; R2[31:0] = MDin

  // Notes on the sheet:
  //   中断源
  //   中断等待指示
  //   总复位信号应将除ROM以外所有存储组件全部清零
  //   数码管输出
  //   指令存储器
  //   指令字
  //   contents of rom_1 (hex, n*v repeats v):
  //   201d07d0 20100001 109fc0 139fc3 8021 2012000c 24160008 26100001 3210000f 20080008 20090001 139900
  //   2709825 132020 20020022 c 1094022 1500fff9 22100001 2018000f 2188024 108700 20080008 20090001 139902
  //   2709825 132021 20020022 c 1094022 1500fff9 108702 2c9b022 12c00001 8000c07 4020 1084027 84400
  //   3508ffff 82021 20020022 c 8000c01 afa20000 23bd0004 afa40000 23bd0004 afb00000 23bd0004 afb30000
  //   23bd0004 afb40000 23bd0004 afb50000 23bd0004 afb60000 23bd0004 40000000 20160001 20140003 20150001
  //   168020 108100 2149825 132020 20020022 c 1600fffa 295a022 1680fff7 40800000 23bdfffc 8fb60000
  //   23bdfffc 8fb50000 23bdfffc 8fb40000 23bdfffc 8fb30000 23bdfffc 8fb00000 23bdfffc 8fa40000 23bdfffc
  //   8fa20000 42000018 afa20000 23bd0004 afa40000 23bd0004 afb00000 23bd0004 afb30000 23bd0004 afb40000
  //   23bd0004 afb50000 23bd0004 afb60000 23bd0004 40000000 20160002 20140003 20150001 168020 108100
  //   2149825 132020 20020022 c 1600fffa 295a022 1680fff7 40800000 23bdfffc 8fb60000 23bdfffc 8fb50000
  //   23bdfffc 8fb40000 23bdfffc 8fb30000 23bdfffc 8fb00000 23bdfffc 8fa40000 23bdfffc 8fa20000 42000018
  //   afa20000 23bd0004 afa40000 23bd0004 afb00000 23bd0004 afb30000 23bd0004 afb40000 23bd0004 afb50000
  //   23bd0004 afb60000 23bd0004 40000000 20160003 20140003 20150001 168020 108100 2149825 132020 20020022
  //   c 1600fffa 295a022 1680fff7 40800000 23bdfffc 8fb60000 23bdfffc 8fb50000 23bdfffc 8fb40000 23bdfffc
  //   8fb30000 23bdfffc 8fb00000 23bdfffc 8fa40000 23bdfffc 8fa20000 42000018
  //   Func
  //   OP
  //   Func
  //   MF/MT
  //   rs
  //   rt
  //   rd
  //   JMP
  //   JR
  //   OP
  //   MF/MT
  //   Syscall
  //   Beq
  //   Bgez
  //   Bne
  //   MemToReg
  //   MemWrite
  //   AluOP
  //   AluSrcB
  //   RegWrite
  //   JAL
  //   RegDst
  //   ERET
  //   数据存储器
  //   为方便自动评测，需要输出PC，IR，寄存器堆写如数据RDin
  //   RAM写使能MemWrite、RAM写入数据MDin等信号
endmodule

// 硬件中断中断发生
module \多级中断_硬件保护_发生器  (
  input  CLK,
  input  [4:0] RD,
  input  IR1,
  input  MFC0,
  input  IR2,
  input  IR3,
  input  [31:0] PC3,
  input  MTC0,
  input  ERET,
  output W1,
  output [31:0] EPC,
  output W2,
  output W3,
  output [31:0] IRaddr,
  output IRenable
);

  wire and_1_out, and_2_out, and_3_out, and_5_out, and_6_out, clear1, clear2, clear3, comparator_1_eq,
       d_ff_1_q, d_ff_2_q, d_ff_3_q, decoder_1_out1, decoder_1_out2, decoder_1_out3, IE, IE_q, not_2_out,
       or_4_out, or_5_out, or_6_out, or_7_out, or_8_out, or_9_out, priority_encoder_1_gs, Ready1, Ready2,
       Ready3, xnor_1_out, \中断来临 ;
  wire [1:0] IRnum, multiplexer_5_out, priority_encoder_1_out, Renum, \嵌套1_q , \嵌套2_q ;
  wire [31:0] EPC2_q, EPC3_q, multiplexer_1_out, multiplexer_2_out;

  or or_1 (W1, Ready1, d_ff_1_q);
  or or_2 (W2, Ready2, d_ff_2_q);
  or or_3 (W3, Ready3, d_ff_3_q);
  D_Flip_Flop #(.trigger("rising"), .Pre_Clr_Positions("LEGACY"), .NegatePresetClear("false"), .enable("true"), .NewFFLayout("false")) d_ff_1 (
    .clk(IR1), .D(1'b1), .Q(d_ff_1_q), .reset(Ready1));  // open: Qn, preset, en
  D_Flip_Flop #(.trigger("rising"), .Pre_Clr_Positions("LEGACY"), .NegatePresetClear("false"), .enable("true"), .NewFFLayout("false")) d_ff_2 (
    .clk(IR2), .D(1'b1), .Q(d_ff_2_q), .reset(Ready2));  // open: Qn, preset, en
  D_Flip_Flop #(.trigger("rising"), .Pre_Clr_Positions("LEGACY"), .NegatePresetClear("false"), .enable("true"), .NewFFLayout("false")) d_ff_3 (
    .clk(IR3), .D(1'b1), .Q(d_ff_3_q), .reset(Ready3));  // open: Qn, preset, en
  or or_4 (or_4_out, d_ff_1_q, Ready1);
  or or_5 (or_5_out, d_ff_2_q, Ready2);
  or or_6 (or_6_out, d_ff_3_q, Ready3);
  and and_1 (and_1_out, or_4_out, ~clear1);  // AND_Gate
  and and_2 (and_2_out, or_5_out, ~clear2);  // AND_Gate
  and and_3 (and_3_out, or_6_out, ~clear3);  // AND_Gate
  D_Flip_Flop #(.trigger("rising"), .Pre_Clr_Positions("LEGACY"), .NegatePresetClear("false"), .enable("true"), .NewFFLayout("false")) u_IR1 (
    .clk(CLK), .D(and_1_out), .Q(Ready1));  // open: Qn, preset, en, reset
  D_Flip_Flop #(.trigger("rising"), .Pre_Clr_Positions("LEGACY"), .NegatePresetClear("false"), .enable("true"), .NewFFLayout("false")) u_IR2 (
    .clk(CLK), .D(and_2_out), .Q(Ready2));  // open: Qn, preset, en, reset
  D_Flip_Flop #(.trigger("rising"), .Pre_Clr_Positions("LEGACY"), .NegatePresetClear("false"), .enable("true"), .NewFFLayout("false")) u_IR3 (
    .clk(CLK), .D(and_3_out), .Q(Ready3));  // open: Qn, preset, en, reset
  Multiplexer #(.select(1), .width(32), .disabled("Z"), .enable("false")) multiplexer_1 (
    .in0(PC3), .in1(EPC2_q), .out(multiplexer_1_out), .sel(ERET));
  Register #(.width(32), .trigger("rising"), .Select("low")) EPC1 (
    .D(multiplexer_1_out), .en(or_7_out), .Q(EPC), .clk(CLK));  // open: clr
  Multiplexer #(.select(1), .width(32), .disabled("Z"), .enable("false")) multiplexer_2 (
    .in0(EPC), .in1(EPC3_q), .out(multiplexer_2_out), .sel(ERET));
  Priority_Encoder #(.select(2), .disabled("Z")) priority_encoder_1 (
    .in0(1'b0), .in1(Ready1), .in2(Ready2), .in3(Ready3), .out(priority_encoder_1_out),
    .gs(priority_encoder_1_gs));  // open: en_out, en_in
  Pull_Resistor #(.pull(0)) pull_resistor_1 (.node(priority_encoder_1_out));
  and and_4 (IRenable, \中断来临 , priority_encoder_1_gs, IE);
  Multiplexer #(.select(2), .width(32), .disabled("Z"), .enable("false")) multiplexer_3 (
    .in1(32'h30ac), .in2(32'h3158), .in3(32'h3204), .out(IRaddr), .sel(IRnum));  // open: in0
  Register #(.width(32), .trigger("rising"), .Select("low")) EPC2 (
    .D(multiplexer_2_out), .en(or_7_out), .Q(EPC2_q), .clk(CLK));  // open: clr
  or or_7 (or_7_out, IRenable, ERET);
  Multiplexer #(.select(1), .width(2), .disabled("Z"), .enable("false")) multiplexer_4 (
    .in0(priority_encoder_1_out), .in1(\嵌套1_q ), .out(IRnum), .sel(ERET));
  Register #(.width(32), .trigger("rising"), .Select("low")) EPC3 (
    .D(EPC2_q), .en(or_7_out), .Q(EPC3_q), .clk(CLK));  // open: clr
  Register #(.width(2), .trigger("rising"), .Select("low")) \u_当前中断号  (
    .D(IRnum), .en(or_9_out), .Q(Renum), .clk(CLK));  // open: clr
  Multiplexer #(.select(1), .width(2), .disabled("Z"), .enable("false")) multiplexer_5 (
    .in0(Renum), .in1(\嵌套2_q ), .out(multiplexer_5_out), .sel(ERET));
  Register #(.width(2), .trigger("rising"), .Select("low")) \u_嵌套1  (
    .D(multiplexer_5_out), .en(or_9_out), .Q(\嵌套1_q ), .clk(CLK));  // open: clr
  not not_1 (\中断来临 , comparator_1_eq);
  Comparator #(.width(2), .mode("twosComplement")) comparator_1 (
    .a(IRnum), .b(Renum), .eq(comparator_1_eq));  // open: gt, lt
  xnor xnor_1 (xnor_1_out, IRenable, IE);
  Register #(.width(2), .trigger("rising"), .Select("low")) \u_嵌套2  (
    .D(\嵌套1_q ), .en(or_9_out), .Q(\嵌套2_q ), .clk(CLK));  // open: clr
  Decoder #(.select(2), .tristate("false"), .disabled("Z"), .enable("false")) decoder_1 (
    .out1(decoder_1_out1), .out2(decoder_1_out2), .out3(decoder_1_out3), .sel(Renum));  // open: out0
  not not_2 (not_2_out, MFC0);
  and and_5 (and_5_out, not_2_out, or_8_out);
  or or_8 (or_8_out, MTC0, and_6_out);
  and and_6 (and_6_out, ~ERET, xnor_1_out);  // AND_Gate
  or or_9 (or_9_out, IRenable, ERET);
  and and_7 (clear1, ERET, decoder_1_out1);
  and and_8 (clear2, ERET, decoder_1_out2);
  and and_9 (clear3, ERET, decoder_1_out3);
  not not_3 (IE, IE_q);
  Register #(.width(1), .trigger("rising"), .Select("low")) u_IE (.D(and_5_out), .Q(IE_q), .clk(CLK));  // open: en, clr

  // Notes on the sheet:
  //   Reset 
  //   Reset 
  //   Reset 
  //   1号中断信号采样参考电路
  //   2号中断信号采样参考电路
  //   3号中断信号采样参考电路
  //   中断识别（入口地址）
  //   EPC寄存器
  //   中断仲裁和中断生成逻辑
  //   IE寄存器
  //   中断返回逻辑
endmodule

module \理想流水线  (
  output RegWrite,
  output MemWrite,
  output [31:0] IF_PC,
  output [31:0] ID_PC,
  output [31:0] EX_PC,
  output [31:0] M_PC,
  output [31:0] WB_PC,
  output [31:0] RDin,
  output [31:0] MDin,
  output [31:0] LedData
);

  wire and_1_out, and_2_out, and_3_out, and_4_out, and_5_out, CLK, comparator_1_eq, ex_mem_1_eret_2,
       ex_mem_1_ifshow_2, ex_mem_1_jal_2, ex_mem_1_lbu_2, ex_mem_1_lui_2, ex_mem_1_memtoreg_2,
       ex_mem_1_mfc0_2, ex_mem_1_regwrite_3, ex_mem_1_syscall_2, \ex_mem_1_传输状态out_表明当前传输数据有效 , Go,
       id_ex_1_p31, id_ex_1_p32, id_ex_1_p33, id_ex_1_p34, id_ex_1_p35, id_ex_1_p36, id_ex_1_p37,
       id_ex_1_p38, id_ex_1_p39, id_ex_1_p40, id_ex_1_p42, id_ex_1_p43, id_ex_1_p44, id_ex_1_p45,
       id_ex_1_p46, id_ex_1_p47, id_ex_1_p58, \if_id_1_传输状态out_表明当前传输数据有效 , IR1, IR2, IR3, mem_wb_1_ifshow_2,
       mem_wb_1_jal_2, mem_wb_1_lbu_2, mem_wb_1_lui_2, mem_wb_1_memtoreg_2, mem_wb_1_syscall_2,
       mips_alu_1_equal, \n27_4条扩展指令控制器_1_alu_src , \n27_4条扩展指令控制器_1_beq , \n27_4条扩展指令控制器_1_bgez ,
       \n27_4条扩展指令控制器_1_bne , \n27_4条扩展指令控制器_1_eret , \n27_4条扩展指令控制器_1_jal , \n27_4条扩展指令控制器_1_jmp ,
       \n27_4条扩展指令控制器_1_jr , \n27_4条扩展指令控制器_1_lbu , \n27_4条扩展指令控制器_1_lui , \n27_4条扩展指令控制器_1_memtoreg ,
       \n27_4条扩展指令控制器_1_memwrite , \n27_4条扩展指令控制器_1_mfc0 , \n27_4条扩展指令控制器_1_mtc0 , \n27_4条扩展指令控制器_1_regdst ,
       \n27_4条扩展指令控制器_1_regwrite , \n27_4条扩展指令控制器_1_signedext , \n27_4条扩展指令控制器_1_syscall , not_1_out,
       not_2_out, not_3_out, not_4_out, or_1_out, or_2_out, or_3_out, or_4_out, register_1_q, RST, W1, W2, W3;
  wire [3:0] id_ex_1_p41, \n27_4条扩展指令控制器_1_alu_op ;
  wire [4:0] ex_mem_1_regwrite_4, id_ex_1_p53_2, id_ex_1_p54, mem_wb_1_regwrite_4, multiplexer_2_out,
       multiplexer_3_out, multiplexer_4_out, multiplexer_5_out;
  wire [15:0] \LoadUse次数 , \总周期数 , \插入气泡数 , \无条件分支数 , \条件分支成功数 ;
  wire [31:0] adder_1_out, adder_2_out, bit_extender_1_out, bit_extender_2_out, bit_extender_3_out,
       ex_mem_1_alu_2, ex_mem_1_immzeroext16shift_2, ex_mem_1_ir_2, ex_mem_1_leadata, ex_mem_1_pc_4_2,
       id_ex_1_p48, id_ex_1_p49, id_ex_1_p50, id_ex_1_p51, id_ex_1_p52, id_ex_1_p53, id_ex_1_p57,
       if_id_1_ir_2, if_id_1_pc_4_2, mem_wb_1_alu_2, mem_wb_1_immzeroext16shift_2, mem_wb_1_md_2,
       mem_wb_1_pc_4_2, mips_alu_1_result, mips_regifile_1_r1, mips_regifile_1_r2, multiplexer_1_out,
       multiplexer_6_out, multiplexer_7_out, multiplexer_8_out, multiplexer_9_out, multiplexer_10_out,
       multiplexer_11_out, multiplexer_12_out, multiplexer_13_out, multiplexer_14_out, ram_1_data,
       register_2_q, rom_1_data, shifter_1_out, shifter_2_out, shifter_3_out;

  Button \u_总复位  (.out(RST));
  Button _1 (.out(IR1));
  Button _2 (.out(IR2));
  Button _3 (.out(IR3));
  Button \u_继续运行  (.out(Go));
  LED #(.active("true")) led_1 (.in(W1));
  LED #(.active("true")) led_2 (.in(W2));
  LED #(.active("true")) led_3 (.in(W3));
  Register #(.width(32), .trigger("rising"), .Select("low")) PC (
    .D(multiplexer_1_out), .en(not_1_out), .Q(IF_PC), .clk(CLK), .clr(RST));
  Multiplexer #(.select(1), .width(32), .disabled("Z"), .enable("false")) multiplexer_1 (
    .in0(adder_1_out), .in1(multiplexer_11_out), .out(multiplexer_1_out), .sel(or_4_out));
  Hex_Digit_Display hex_digit_display_1 (.value(LedData[31:28]));  // open: dp
  Adder #(.width(32)) adder_1 (.a(IF_PC), .b(32'h4), .out(adder_1_out));  // open: cin, cout
  not not_1 (not_1_out, register_1_q);
  Register #(.width(1), .trigger("rising"), .Select("low")) register_1 (
    .D(mem_wb_1_syscall_2), .en(and_1_out), .Q(register_1_q), .clk(CLK), .clr(or_1_out));
  or or_1 (or_1_out, RST, Go);
  Counter #(.width(16), .max('hffff), .ongoal("wrap"), .trigger("rising"), .behavior("old")) counter_1 (
    .count(not_1_out), .Q(\总周期数 ), .clk(CLK), .clr(RST));  // open: load, D, carry, preset
  and and_1 (and_1_out, not_2_out, mem_wb_1_syscall_2);
  Hex_Digit_Display hex_digit_display_2 (.value(LedData[23:20]));  // open: dp
  Hex_Digit_Display hex_digit_display_3 (.value(LedData[27:24]));  // open: dp
  ROM #(.addrWidth(10), .dataWidth(32), .Select("high")) rom_1 (.addr(IF_PC[11:2]), .data(rom_1_data));
  not not_2 (not_2_out, mem_wb_1_ifshow_2);
  Hex_Digit_Display hex_digit_display_4 (.value(LedData[15:12]));  // open: dp
  Hex_Digit_Display hex_digit_display_5 (.value(LedData[19:16]));  // open: dp
  Hex_Digit_Display hex_digit_display_6 (.value(LedData[11:8]));  // open: dp
  Hex_Digit_Display hex_digit_display_7 (.value(LedData[7:4]));  // open: dp
  Clock #(.highDuration(1), .lowDuration(1)) clock_1 (.out(CLK));
  IF_ID if_id_1 (
    .IR(rom_1_data), .PC_4(adder_1_out), .\传输状态In_表明当前传输数据有效 (1'b1), .CLK(CLK), .IR_2(if_id_1_ir_2),
    .PC_4_2(if_id_1_pc_4_2), .\传输状态Out_表明当前传输数据有效 (\if_id_1_传输状态out_表明当前传输数据有效 ), .\同步清零_气泡_高电平有效 (1'b0),
    .\使能端_低电平有效_stall_高电平有效 (1'b0), .PC(IF_PC), .PC_2(ID_PC));  // open: DesAddr, DesAddr_2, Miss, Miss_2, Hit, Hit_2, Prediction_2, Prediction
  Hex_Digit_Display hex_digit_display_8 (.value(LedData[3:0]));  // open: dp
  // Probe on \总周期数 
  Multiplexer #(.select(1), .width(5), .disabled("Z"), .enable("false")) multiplexer_2 (
    .in0(if_id_1_ir_2[25:21]), .in1(5'b00100), .out(multiplexer_2_out), .sel(\n27_4条扩展指令控制器_1_syscall ));
  Multiplexer #(.select(1), .width(5), .disabled("Z"), .enable("false")) multiplexer_3 (
    .in0(if_id_1_ir_2[20:16]), .in1(5'b00010), .out(multiplexer_3_out), .sel(\n27_4条扩展指令控制器_1_syscall ));
  Multiplexer #(.select(1), .width(5), .disabled("Z"), .enable("false")) multiplexer_4 (
    .in0(if_id_1_ir_2[20:16]), .in1(if_id_1_ir_2[15:11]), .out(multiplexer_4_out),
    .sel(\n27_4条扩展指令控制器_1_regdst ));
  assign bit_extender_1_out = {{16{1'b0}}, if_id_1_ir_2[15:0]};  // Bit_Extender bit_extender_1
  assign bit_extender_2_out = {{16{if_id_1_ir_2[15]}}, if_id_1_ir_2[15:0]};  // Bit_Extender bit_extender_2
  assign bit_extender_3_out = {{6{if_id_1_ir_2[25]}}, if_id_1_ir_2[25:0]};  // Bit_Extender bit_extender_3
  // Probe on \总周期数 
  // Probe on \无条件分支数 
  // Probe on \条件分支成功数 
  // Probe on \插入气泡数 
  // Probe on \LoadUse次数 
  \_27_4条扩展指令控制器  \u_27_4条扩展指令控制器_1  (
    .OP(if_id_1_ir_2[31:26]), .Func(if_id_1_ir_2[5:0]), .ALU_OP(\n27_4条扩展指令控制器_1_alu_op ),
    .MemToReg(\n27_4条扩展指令控制器_1_memtoreg ), .MemWrite(\n27_4条扩展指令控制器_1_memwrite ),
    .ALU_SRC(\n27_4条扩展指令控制器_1_alu_src ), .SysCALL(\n27_4条扩展指令控制器_1_syscall ),
    .SignedExt(\n27_4条扩展指令控制器_1_signedext ), .RegDst(\n27_4条扩展指令控制器_1_regdst ), .Beq(\n27_4条扩展指令控制器_1_beq ),
    .Bne(\n27_4条扩展指令控制器_1_bne ), .JR(\n27_4条扩展指令控制器_1_jr ), .JMP(\n27_4条扩展指令控制器_1_jmp ),
    .JAL(\n27_4条扩展指令控制器_1_jal ), .LUI(\n27_4条扩展指令控制器_1_lui ), .LBU(\n27_4条扩展指令控制器_1_lbu ),
    .BGEZ(\n27_4条扩展指令控制器_1_bgez ), .MTC0(\n27_4条扩展指令控制器_1_mtc0 ), .MFMT(if_id_1_ir_2[25:21]),
    .ERET(\n27_4条扩展指令控制器_1_eret ), .MFC0(\n27_4条扩展指令控制器_1_mfc0 ), .RegWrite(\n27_4条扩展指令控制器_1_regwrite ));
  Multiplexer #(.select(1), .width(5), .disabled("Z"), .enable("false")) multiplexer_5 (
    .in0(multiplexer_4_out), .in1({5{1'b1}}), .out(multiplexer_5_out), .sel(\n27_4条扩展指令控制器_1_jal ));
  // Probe on IF_PC[11:0]
  Multiplexer #(.select(1), .width(32), .disabled("Z"), .enable("false")) multiplexer_6 (
    .in0(bit_extender_1_out), .in1(bit_extender_2_out), .out(multiplexer_6_out),
    .sel(\n27_4条扩展指令控制器_1_signedext ));
  // Probe on ID_PC[11:0]
  // Probe on EX_PC[11:0]
  MIPS_Regifile mips_regifile_1 (
    .Din(RDin), .Clk(CLK), .R1(mips_regifile_1_r1), .R2(mips_regifile_1_r2), .WE(RegWrite),
    .W_num(mem_wb_1_regwrite_4), .R1_num(multiplexer_2_out), .R2_num(multiplexer_3_out));
  // Probe on M_PC[11:0]
  // Probe on WB_PC[11:0]
  // ID_EX id_ex_1: pin names not known; wires that end beside it: \n27_4条扩展指令控制器_1_regwrite , \n27_4条扩展指令控制器_1_eret , \n27_4条扩展指令控制器_1_syscall , \n27_4条扩展指令控制器_1_memtoreg , \n27_4条扩展指令控制器_1_lui , \n27_4条扩展指令控制器_1_mfc0 , \n27_4条扩展指令控制器_1_jal , \n27_4条扩展指令控制器_1_lbu , \n27_4条扩展指令控制器_1_memwrite , \n27_4条扩展指令控制器_1_alu_op , \n27_4条扩展指令控制器_1_alu_src , \n27_4条扩展指令控制器_1_mtc0 , \n27_4条扩展指令控制器_1_beq , \n27_4条扩展指令控制器_1_bgez , \n27_4条扩展指令控制器_1_bne , \n27_4条扩展指令控制器_1_jmp , \n27_4条扩展指令控制器_1_jr , mips_regifile_1_r1, mips_regifile_1_r2, multiplexer_6_out, bit_extender_1_out, bit_extender_3_out, if_id_1_ir_2, multiplexer_5_out, ID_PC, if_id_1_pc_4_2, \if_id_1_传输状态out_表明当前传输数据有效 , 1'b0, 1'b0, CLK, id_ex_1_p31, id_ex_1_p32, id_ex_1_p33, id_ex_1_p34, id_ex_1_p35, id_ex_1_p36, id_ex_1_p37, id_ex_1_p38, id_ex_1_p39, id_ex_1_p40, id_ex_1_p41, id_ex_1_p42, id_ex_1_p43, id_ex_1_p44, id_ex_1_p45, id_ex_1_p46, id_ex_1_p47, id_ex_1_p48, id_ex_1_p49, id_ex_1_p50, id_ex_1_p51, id_ex_1_p52, {id_ex_1_p53[31:11], id_ex_1_p53_2, id_ex_1_p53[5:0]}, id_ex_1_p54, EX_PC, id_ex_1_p31, id_ex_1_p57, id_ex_1_p58, 32'h22
  Comparator #(.width(32), .mode("twosComplement")) comparator_1 (
    .a(32'h22), .b(id_ex_1_p49), .eq(comparator_1_eq));  // open: gt, lt
  and and_2 (and_2_out, id_ex_1_p34, comparator_1_eq);
  Multiplexer #(.select(1), .width(32), .disabled("Z"), .enable("false")) multiplexer_7 (
    .in0(id_ex_1_p49), .in1(id_ex_1_p50), .out(multiplexer_7_out), .sel(id_ex_1_p42));
  Shifter #(.width(32), .shift("ll")) shifter_1 (.in(id_ex_1_p50), .\dist (5'b00010), .out(shifter_1_out));
  Shifter #(.width(32), .shift("ll")) shifter_2 (.in(id_ex_1_p51), .\dist (5'b10000), .out(shifter_2_out));
  Shifter #(.width(32), .shift("ll")) shifter_3 (.in(id_ex_1_p52), .\dist (5'b00010), .out(shifter_3_out));
  Multiplexer #(.select(1), .width(32), .disabled("Z"), .enable("false")) multiplexer_8 (
    .in0(multiplexer_7_out), .in1({32{1'b0}}), .out(multiplexer_8_out), .sel(id_ex_1_p44));
  not not_3 (not_3_out, mips_alu_1_equal);
  not not_4 (not_4_out, mips_alu_1_result[0]);
  MIPS_ALU mips_alu_1 (
    .X(id_ex_1_p48), .Y(multiplexer_8_out), .AluOP(id_ex_1_p41), .Equal(mips_alu_1_equal),
    .Result(mips_alu_1_result), .shamt(id_ex_1_p53_2));  // open: Result_2
  Adder #(.width(32)) adder_2 (.a(shifter_1_out), .b(id_ex_1_p57), .out(adder_2_out));  // open: cin, cout
  and and_3 (and_3_out, not_3_out, id_ex_1_p45);
  and and_4 (and_4_out, not_4_out, id_ex_1_p44);
  and and_5 (and_5_out, id_ex_1_p43, mips_alu_1_equal);
  Register #(.width(32), .trigger("rising"), .Select("low")) register_2 (
    .D(id_ex_1_p48), .en(and_2_out), .Q(register_2_q), .clk(CLK), .clr(RST));
  or or_2 (or_2_out, id_ex_1_p38, id_ex_1_p46);
  or or_3 (or_3_out, and_3_out, and_4_out, and_5_out);
  Multiplexer #(.select(1), .width(32), .disabled("Z"), .enable("false")) multiplexer_9 (
    .in0(id_ex_1_p57), .in1(adder_2_out), .out(multiplexer_9_out), .sel(or_3_out));
  Multiplexer #(.select(1), .width(32), .disabled("Z"), .enable("false")) multiplexer_10 (
    .in0(multiplexer_9_out), .in1(shifter_3_out), .out(multiplexer_10_out), .sel(or_2_out));
  Multiplexer #(.select(1), .width(32), .disabled("Z"), .enable("false")) multiplexer_11 (
    .in0(multiplexer_10_out), .in1(id_ex_1_p48), .out(multiplexer_11_out), .sel(id_ex_1_p47));
  or or_4 (or_4_out, or_3_out, id_ex_1_p47, or_2_out);
  EX_MEM ex_mem_1 (
    .ERET(id_ex_1_p33), .Syscall(id_ex_1_p34), .MemToReg(id_ex_1_p35), .MFC0(id_ex_1_p37), .JAL(id_ex_1_p38),
    .LBU(id_ex_1_p39), .B(id_ex_1_p49), .ALU(mips_alu_1_result),
    .IR({id_ex_1_p53[31:11], id_ex_1_p53_2, id_ex_1_p53[5:0]}), .PC(EX_PC),
    .\传输状态In_表明当前传输数据有效 (id_ex_1_p58), .CLK(CLK), .ERET_2(ex_mem_1_eret_2), .Syscall_2(ex_mem_1_syscall_2),
    .MemToReg_2(ex_mem_1_memtoreg_2), .LUI_2(ex_mem_1_lui_2), .MFC0_2(ex_mem_1_mfc0_2),
    .JAL_2(ex_mem_1_jal_2), .LBU_2(ex_mem_1_lbu_2), .B_2(MDin), .ALU_2(ex_mem_1_alu_2), .IR_2(ex_mem_1_ir_2),
    .PC_2(M_PC), .\传输状态Out_表明当前传输数据有效 (\ex_mem_1_传输状态out_表明当前传输数据有效 ), .\同步清零_气泡_高电平有效 (1'b0),
    .\使能端_低电平有效_stall_高电平有效 (1'b0), .PC_4(id_ex_1_p57), .PC_4_2(ex_mem_1_pc_4_2), .MemWrite(id_ex_1_p40),
    .MemWrite_2(MemWrite), .RegWrite_2(id_ex_1_p54), .RegWrite_4(ex_mem_1_regwrite_4),
    .RegWrite(id_ex_1_p32), .RegWrite_3(ex_mem_1_regwrite_3), .ImmZeroExt16Shift(shifter_2_out),
    .ImmZeroExt16Shift_2(ex_mem_1_immzeroext16shift_2), .ifshow(comparator_1_eq),
    .ifshow_2(ex_mem_1_ifshow_2), .LedData(register_2_q), .LeaData(ex_mem_1_leadata), .LUI(id_ex_1_p36));  // open: rd, rd_2, MTC0, MTC0_2, IRout, IRout_2
  RAM #(.addrWidth(10), .dataWidth(32), .bus("separate"), .Select("high")) ram_1 (
    .addr(ex_mem_1_alu_2[11:2]), .din(MDin), .data(ram_1_data), .str(MemWrite), .clk(CLK), .clr(RST));  // open: sel, ld
  MEM_WB mem_wb_1 (
    .ERET(ex_mem_1_eret_2), .Syscall(ex_mem_1_syscall_2), .MemToReg(ex_mem_1_memtoreg_2),
    .LUI(ex_mem_1_lui_2), .MFC0(ex_mem_1_mfc0_2), .JAL(ex_mem_1_jal_2), .ALU(ex_mem_1_alu_2),
    .MD(ram_1_data), .IR(ex_mem_1_ir_2), .PC(M_PC), .PC_4(ex_mem_1_pc_4_2),
    .\传输状态In_表明当前传输数据有效 (\ex_mem_1_传输状态out_表明当前传输数据有效 ), .CLK(CLK), .Syscall_2(mem_wb_1_syscall_2),
    .MemToReg_2(mem_wb_1_memtoreg_2), .JAL_2(mem_wb_1_jal_2), .ALU_2(mem_wb_1_alu_2), .MD_2(mem_wb_1_md_2),
    .PC_2(WB_PC), .PC_4_2(mem_wb_1_pc_4_2), .\同步清零_气泡_高电平有效 (1'b0), .\使能端_低电平有效_stall_高电平有效 (1'b0),
    .LBU(ex_mem_1_lbu_2), .LBU_2(mem_wb_1_lbu_2), .ImmZeroExt16Shift(ex_mem_1_immzeroext16shift_2),
    .ImmZeroExt16Shift_2(mem_wb_1_immzeroext16shift_2), .RegWrite(ex_mem_1_regwrite_3),
    .RegWrite_3(RegWrite), .RegWrite_2(ex_mem_1_regwrite_4), .RegWrite_4(mem_wb_1_regwrite_4),
    .ifshow_2(mem_wb_1_ifshow_2), .ifshow(ex_mem_1_ifshow_2), .LedData(ex_mem_1_leadata),
    .LedData_2(LedData), .LUI_2(mem_wb_1_lui_2));  // open: ERET_2, MFC0_2, IR_2, 传输状态Out_表明当前传输数据有效, rd, rd_2, MTC0, MTC0_2, IRout, IRout_2
  Multiplexer #(.select(1), .width(32), .disabled("Z"), .enable("false")) multiplexer_12 (
    .in0(mem_wb_1_alu_2), .in1(multiplexer_13_out), .out(multiplexer_12_out), .sel(mem_wb_1_memtoreg_2));
  Multiplexer #(.select(1), .width(32), .disabled("Z"), .enable("false")) multiplexer_13 (
    .in0(mem_wb_1_md_2), .in1({{24{1'b0}}, mem_wb_1_md_2[7:0]}), .out(multiplexer_13_out),
    .sel(mem_wb_1_lbu_2));
  Multiplexer #(.select(1), .width(32), .disabled("Z"), .enable("false")) multiplexer_14 (
    .in0(multiplexer_12_out), .in1(mem_wb_1_immzeroext16shift_2), .out(multiplexer_14_out),
    .sel(mem_wb_1_lui_2));
  Multiplexer #(.select(1), .width(32), .disabled("Z"), .enable("false")) multiplexer_15 (
    .in0(multiplexer_14_out), .in1(mem_wb_1_pc_4_2), .out(RDin), .sel(mem_wb_1_jal_2));

  // Other names for the same wires on the sheet: MEM_PC[31:0] = M_PC

  // Notes on the sheet:
  //   中断源
  //   中断等待指示
  //   指令存储器
  //   contents of rom_1 (hex, n*v repeats v):
  //   20100000 20110000 20120000 20130000 36100000 36310001 36520002 36730003 ae100000 ae110004 ae120008
  //   ae13000c 2002000a 20110000 20120000 20130000 c
  //   数码管输出
  //   指令字
  //   OP
  //   Func
  //   MF/MT
  //   rs
  //   rt
  //   rd
  //   JMP
  //   JR
  //   SignedExt
  //   LUI
  //   LBU
  //   MFC0
  //   MTC0
  //   OP
  //   Func
  //   MF/MT
  //   Syscall
  //   Beq
  //   Bgez
  //   Bne
  //   MemToReg
  //   MemWrite
  //   AluOP
  //   AluSrcB
  //   RegWrite
  //   JAL
  //   RegDst
  //   ERET
  //   流水调试日志用
  //   为方便自动评测，需要输出流水线各段保存的PC值，注意是PC不是PC+4，另外ID段寄存器写入信息，Mem段内存写入信息也要输出
  //   数据存储器
endmodule
module \流水分支电路  (
  output RegWrite,
  output MemWrite,
  output [31:0] IF_PC,
  output [31:0] ID_PC,
  output [31:0] EX_PC,
  output [31:0] M_PC,
  output [31:0] WB_PC,
  output [31:0] RDin,
  output [31:0] MDin,
  output [31:0] LedData
);

  wire and_1_out, and_2_out, and_3_out, and_4_out, and_5_out, Clear, CLK, comparator_1_eq, ex_mem_1_eret_2,
       ex_mem_1_ifshow_2, ex_mem_1_jal_2, ex_mem_1_lbu_2, ex_mem_1_lui_2, ex_mem_1_memtoreg_2,
       ex_mem_1_mfc0_2, ex_mem_1_regwrite_3, ex_mem_1_syscall_2, \ex_mem_1_传输状态out_表明当前传输数据有效 , Go,
       id_ex_1_p31, id_ex_1_p32, id_ex_1_p33, id_ex_1_p34, id_ex_1_p35, id_ex_1_p36, id_ex_1_p37,
       id_ex_1_p38, id_ex_1_p39, id_ex_1_p40, id_ex_1_p42, id_ex_1_p43, id_ex_1_p44, id_ex_1_p45,
       id_ex_1_p46, id_ex_1_p47, id_ex_1_p58, \if_id_1_传输状态out_表明当前传输数据有效 , IR1, IR2, IR3, mem_wb_1_ifshow_2,
       mem_wb_1_jal_2, mem_wb_1_lbu_2, mem_wb_1_lui_2, mem_wb_1_memtoreg_2, mem_wb_1_syscall_2,
       mips_alu_1_equal, \n27_4条扩展指令控制器_1_alu_src , \n27_4条扩展指令控制器_1_beq , \n27_4条扩展指令控制器_1_bgez ,
       \n27_4条扩展指令控制器_1_bne , \n27_4条扩展指令控制器_1_eret , \n27_4条扩展指令控制器_1_jal , \n27_4条扩展指令控制器_1_jmp ,
       \n27_4条扩展指令控制器_1_jr , \n27_4条扩展指令控制器_1_lbu , \n27_4条扩展指令控制器_1_lui , \n27_4条扩展指令控制器_1_memtoreg ,
       \n27_4条扩展指令控制器_1_memwrite , \n27_4条扩展指令控制器_1_mfc0 , \n27_4条扩展指令控制器_1_mtc0 , \n27_4条扩展指令控制器_1_regdst ,
       \n27_4条扩展指令控制器_1_regwrite , \n27_4条扩展指令控制器_1_signedext , \n27_4条扩展指令控制器_1_syscall , not_1_out,
       not_2_out, not_3_out, not_4_out, or_1_out, or_2_out, or_3_out, register_1_q, RST, W1, W2, W3;
  wire [3:0] id_ex_1_p41, \n27_4条扩展指令控制器_1_alu_op ;
  wire [4:0] ex_mem_1_regwrite_4, id_ex_1_p53_2, id_ex_1_p54, mem_wb_1_regwrite_4, multiplexer_2_out,
       multiplexer_3_out, multiplexer_4_out, multiplexer_5_out;
  wire [15:0] \LoadUse次数 , \总周期数 , \插入气泡数 , \无条件分支数 , \条件分支成功数 ;
  wire [31:0] adder_1_out, adder_2_out, bit_extender_1_out, bit_extender_2_out, bit_extender_3_out,
       ex_mem_1_alu_2, ex_mem_1_immzeroext16shift_2, ex_mem_1_ir_2, ex_mem_1_leadata, ex_mem_1_pc_4_2,
       id_ex_1_p48, id_ex_1_p49, id_ex_1_p50, id_ex_1_p51, id_ex_1_p52, id_ex_1_p53, id_ex_1_p57,
       if_id_1_ir_2, if_id_1_pc_4_2, mem_wb_1_alu_2, mem_wb_1_immzeroext16shift_2, mem_wb_1_md_2,
       mem_wb_1_pc_4_2, mips_alu_1_result, mips_regifile_1_r1, mips_regifile_1_r2, multiplexer_1_out,
       multiplexer_6_out, multiplexer_7_out, multiplexer_8_out, multiplexer_9_out, multiplexer_10_out,
       multiplexer_11_out, multiplexer_12_out, multiplexer_13_out, multiplexer_14_out, ram_1_data,
       register_2_q, rom_1_data, shifter_1_out, shifter_2_out, shifter_3_out;

  Button \u_总复位  (.out(RST));
  Button _1 (.out(IR1));
  Button _2 (.out(IR2));
  Button _3 (.out(IR3));
  Button \u_继续运行  (.out(Go));
  LED #(.active("true")) led_1 (.in(W1));
  LED #(.active("true")) led_2 (.in(W2));
  LED #(.active("true")) led_3 (.in(W3));
  Register #(.width(32), .trigger("rising"), .Select("low")) PC (
    .D(multiplexer_1_out), .en(not_1_out), .Q(IF_PC), .clk(CLK), .clr(RST));
  Multiplexer #(.select(1), .width(32), .disabled("Z"), .enable("false")) multiplexer_1 (
    .in0(adder_1_out), .in1(multiplexer_11_out), .out(multiplexer_1_out), .sel(Clear));
  Hex_Digit_Display hex_digit_display_1 (.value(LedData[31:28]));  // open: dp
  Adder #(.width(32)) adder_1 (.a(IF_PC), .b(32'h4), .out(adder_1_out));  // open: cin, cout
  not not_1 (not_1_out, register_1_q);
  Register #(.width(1), .trigger("rising"), .Select("low")) register_1 (
    .D(mem_wb_1_syscall_2), .en(and_1_out), .Q(register_1_q), .clk(CLK), .clr(or_1_out));
  or or_1 (or_1_out, RST, Go);
  Counter #(.width(16), .max('hffff), .ongoal("wrap"), .trigger("rising"), .behavior("old")) counter_1 (
    .count(not_1_out), .Q(\总周期数 ), .clk(CLK), .clr(RST));  // open: load, D, carry, preset
  and and_1 (and_1_out, not_2_out, mem_wb_1_syscall_2);
  Hex_Digit_Display hex_digit_display_2 (.value(LedData[23:20]));  // open: dp
  Hex_Digit_Display hex_digit_display_3 (.value(LedData[27:24]));  // open: dp
  ROM #(.addrWidth(10), .dataWidth(32), .Select("high")) rom_1 (.addr(IF_PC[11:2]), .data(rom_1_data));
  not not_2 (not_2_out, mem_wb_1_ifshow_2);
  Hex_Digit_Display hex_digit_display_4 (.value(LedData[15:12]));  // open: dp
  Hex_Digit_Display hex_digit_display_5 (.value(LedData[19:16]));  // open: dp
  Hex_Digit_Display hex_digit_display_6 (.value(LedData[7:4]));  // open: dp
  Hex_Digit_Display hex_digit_display_7 (.value(LedData[11:8]));  // open: dp
  Clock #(.highDuration(1), .lowDuration(1)) clock_1 (.out(CLK));
  IF_ID if_id_1 (
    .IR(rom_1_data), .PC_4(adder_1_out), .\传输状态In_表明当前传输数据有效 (1'b1), .CLK(CLK), .IR_2(if_id_1_ir_2),
    .PC_4_2(if_id_1_pc_4_2), .\传输状态Out_表明当前传输数据有效 (\if_id_1_传输状态out_表明当前传输数据有效 ), .\同步清零_气泡_高电平有效 (Clear),
    .\使能端_低电平有效_stall_高电平有效 (1'b0), .PC(IF_PC), .PC_2(ID_PC));  // open: DesAddr, DesAddr_2, Miss, Miss_2, Hit, Hit_2, Prediction_2, Prediction
  Hex_Digit_Display hex_digit_display_8 (.value(LedData[3:0]));  // open: dp
  // Probe on \总周期数 
  Multiplexer #(.select(1), .width(5), .disabled("Z"), .enable("false")) multiplexer_2 (
    .in0(if_id_1_ir_2[25:21]), .in1(5'b00100), .out(multiplexer_2_out), .sel(\n27_4条扩展指令控制器_1_syscall ));
  Multiplexer #(.select(1), .width(5), .disabled("Z"), .enable("false")) multiplexer_3 (
    .in0(if_id_1_ir_2[20:16]), .in1(5'b00010), .out(multiplexer_3_out), .sel(\n27_4条扩展指令控制器_1_syscall ));
  Multiplexer #(.select(1), .width(5), .disabled("Z"), .enable("false")) multiplexer_4 (
    .in0(if_id_1_ir_2[20:16]), .in1(if_id_1_ir_2[15:11]), .out(multiplexer_4_out),
    .sel(\n27_4条扩展指令控制器_1_regdst ));
  assign bit_extender_1_out = {{16{1'b0}}, if_id_1_ir_2[15:0]};  // Bit_Extender bit_extender_1
  assign bit_extender_2_out = {{16{if_id_1_ir_2[15]}}, if_id_1_ir_2[15:0]};  // Bit_Extender bit_extender_2
  assign bit_extender_3_out = {{6{if_id_1_ir_2[25]}}, if_id_1_ir_2[25:0]};  // Bit_Extender bit_extender_3
  // Probe on \总周期数 
  // Probe on \无条件分支数 
  // Probe on \条件分支成功数 
  // Probe on \插入气泡数 
  // Probe on \LoadUse次数 
  \_27_4条扩展指令控制器  \u_27_4条扩展指令控制器_1  (
    .OP(if_id_1_ir_2[31:26]), .Func(if_id_1_ir_2[5:0]), .ALU_OP(\n27_4条扩展指令控制器_1_alu_op ),
    .MemToReg(\n27_4条扩展指令控制器_1_memtoreg ), .MemWrite(\n27_4条扩展指令控制器_1_memwrite ),
    .ALU_SRC(\n27_4条扩展指令控制器_1_alu_src ), .SysCALL(\n27_4条扩展指令控制器_1_syscall ),
    .SignedExt(\n27_4条扩展指令控制器_1_signedext ), .RegDst(\n27_4条扩展指令控制器_1_regdst ), .Beq(\n27_4条扩展指令控制器_1_beq ),
    .Bne(\n27_4条扩展指令控制器_1_bne ), .JR(\n27_4条扩展指令控制器_1_jr ), .JMP(\n27_4条扩展指令控制器_1_jmp ),
    .JAL(\n27_4条扩展指令控制器_1_jal ), .LUI(\n27_4条扩展指令控制器_1_lui ), .LBU(\n27_4条扩展指令控制器_1_lbu ),
    .BGEZ(\n27_4条扩展指令控制器_1_bgez ), .MTC0(\n27_4条扩展指令控制器_1_mtc0 ), .MFMT(if_id_1_ir_2[25:21]),
    .ERET(\n27_4条扩展指令控制器_1_eret ), .MFC0(\n27_4条扩展指令控制器_1_mfc0 ), .RegWrite(\n27_4条扩展指令控制器_1_regwrite ));
  Multiplexer #(.select(1), .width(5), .disabled("Z"), .enable("false")) multiplexer_5 (
    .in0(multiplexer_4_out), .in1({5{1'b1}}), .out(multiplexer_5_out), .sel(\n27_4条扩展指令控制器_1_jal ));
  // Probe on IF_PC[11:0]
  Multiplexer #(.select(1), .width(32), .disabled("Z"), .enable("false")) multiplexer_6 (
    .in0(bit_extender_1_out), .in1(bit_extender_2_out), .out(multiplexer_6_out),
    .sel(\n27_4条扩展指令控制器_1_signedext ));
  // Probe on EX_PC[11:0]
  // Probe on ID_PC[11:0]
  MIPS_Regifile mips_regifile_1 (
    .Din(RDin), .Clk(CLK), .R1(mips_regifile_1_r1), .R2(mips_regifile_1_r2), .WE(RegWrite),
    .W_num(mem_wb_1_regwrite_4), .R1_num(multiplexer_2_out), .R2_num(multiplexer_3_out));
  // Probe on M_PC[11:0]
  // Probe on WB_PC[11:0]
  // ID_EX id_ex_1: pin names not known; wires that end beside it: \n27_4条扩展指令控制器_1_regwrite , \n27_4条扩展指令控制器_1_eret , \n27_4条扩展指令控制器_1_syscall , \n27_4条扩展指令控制器_1_memtoreg , \n27_4条扩展指令控制器_1_lui , \n27_4条扩展指令控制器_1_mfc0 , \n27_4条扩展指令控制器_1_jal , \n27_4条扩展指令控制器_1_lbu , \n27_4条扩展指令控制器_1_memwrite , \n27_4条扩展指令控制器_1_alu_op , \n27_4条扩展指令控制器_1_alu_src , \n27_4条扩展指令控制器_1_mtc0 , \n27_4条扩展指令控制器_1_beq , \n27_4条扩展指令控制器_1_bgez , \n27_4条扩展指令控制器_1_bne , \n27_4条扩展指令控制器_1_jmp , \n27_4条扩展指令控制器_1_jr , mips_regifile_1_r1, mips_regifile_1_r2, multiplexer_6_out, bit_extender_1_out, bit_extender_3_out, if_id_1_ir_2, multiplexer_5_out, ID_PC, if_id_1_pc_4_2, \if_id_1_传输状态out_表明当前传输数据有效 , 1'b0, Clear, CLK, id_ex_1_p31, id_ex_1_p32, id_ex_1_p33, id_ex_1_p34, id_ex_1_p35, id_ex_1_p36, id_ex_1_p37, id_ex_1_p38, id_ex_1_p39, id_ex_1_p40, id_ex_1_p41, id_ex_1_p42, id_ex_1_p43, id_ex_1_p44, id_ex_1_p45, id_ex_1_p46, id_ex_1_p47, id_ex_1_p48, id_ex_1_p49, id_ex_1_p50, id_ex_1_p51, id_ex_1_p52, {id_ex_1_p53[31:11], id_ex_1_p53_2, id_ex_1_p53[5:0]}, id_ex_1_p54, EX_PC, id_ex_1_p31, id_ex_1_p57, id_ex_1_p58
  Comparator #(.width(32), .mode("twosComplement")) comparator_1 (
    .a(32'h22), .b(id_ex_1_p49), .eq(comparator_1_eq));  // open: gt, lt
  and and_2 (and_2_out, id_ex_1_p34, comparator_1_eq);
  Multiplexer #(.select(1), .width(32), .disabled("Z"), .enable("false")) multiplexer_7 (
    .in0(id_ex_1_p49), .in1(id_ex_1_p50), .out(multiplexer_7_out), .sel(id_ex_1_p42));
  Shifter #(.width(32), .shift("ll")) shifter_1 (.in(id_ex_1_p50), .\dist (5'b00010), .out(shifter_1_out));
  Shifter #(.width(32), .shift("ll")) shifter_2 (.in(id_ex_1_p51), .\dist (5'b10000), .out(shifter_2_out));
  Shifter #(.width(32), .shift("ll")) shifter_3 (.in(id_ex_1_p52), .\dist (5'b00010), .out(shifter_3_out));
  Multiplexer #(.select(1), .width(32), .disabled("Z"), .enable("false")) multiplexer_8 (
    .in0(multiplexer_7_out), .in1({32{1'b0}}), .out(multiplexer_8_out), .sel(id_ex_1_p44));
  not not_3 (not_3_out, mips_alu_1_equal);
  not not_4 (not_4_out, mips_alu_1_result[0]);
  MIPS_ALU mips_alu_1 (
    .X(id_ex_1_p48), .Y(multiplexer_8_out), .AluOP(id_ex_1_p41), .Equal(mips_alu_1_equal),
    .Result(mips_alu_1_result), .shamt(id_ex_1_p53_2));  // open: Result_2
  Adder #(.width(32)) adder_2 (.a(shifter_1_out), .b(id_ex_1_p57), .out(adder_2_out));  // open: cin, cout
  and and_3 (and_3_out, not_3_out, id_ex_1_p45);
  and and_4 (and_4_out, not_4_out, id_ex_1_p44);
  and and_5 (and_5_out, id_ex_1_p43, mips_alu_1_equal);
  Register #(.width(32), .trigger("rising"), .Select("low")) register_2 (
    .D(id_ex_1_p48), .en(and_2_out), .Q(register_2_q), .clk(CLK), .clr(RST));
  or or_2 (or_2_out, id_ex_1_p38, id_ex_1_p46);
  or or_3 (or_3_out, and_3_out, and_4_out, and_5_out);
  Multiplexer #(.select(1), .width(32), .disabled("Z"), .enable("false")) multiplexer_9 (
    .in0(id_ex_1_p57), .in1(adder_2_out), .out(multiplexer_9_out), .sel(or_3_out));
  Multiplexer #(.select(1), .width(32), .disabled("Z"), .enable("false")) multiplexer_10 (
    .in0(multiplexer_9_out), .in1(shifter_3_out), .out(multiplexer_10_out), .sel(or_2_out));
  Multiplexer #(.select(1), .width(32), .disabled("Z"), .enable("false")) multiplexer_11 (
    .in0(multiplexer_10_out), .in1(id_ex_1_p48), .out(multiplexer_11_out), .sel(id_ex_1_p47));
  or or_4 (Clear, or_3_out, id_ex_1_p47, or_2_out);
  EX_MEM ex_mem_1 (
    .ERET(id_ex_1_p33), .Syscall(id_ex_1_p34), .MemToReg(id_ex_1_p35), .MFC0(id_ex_1_p37), .JAL(id_ex_1_p38),
    .LBU(id_ex_1_p39), .B(id_ex_1_p49), .ALU(mips_alu_1_result),
    .IR({id_ex_1_p53[31:11], id_ex_1_p53_2, id_ex_1_p53[5:0]}), .PC(EX_PC),
    .\传输状态In_表明当前传输数据有效 (id_ex_1_p58), .CLK(CLK), .ERET_2(ex_mem_1_eret_2), .Syscall_2(ex_mem_1_syscall_2),
    .MemToReg_2(ex_mem_1_memtoreg_2), .LUI_2(ex_mem_1_lui_2), .MFC0_2(ex_mem_1_mfc0_2),
    .JAL_2(ex_mem_1_jal_2), .LBU_2(ex_mem_1_lbu_2), .B_2(MDin), .ALU_2(ex_mem_1_alu_2), .IR_2(ex_mem_1_ir_2),
    .PC_2(M_PC), .\传输状态Out_表明当前传输数据有效 (\ex_mem_1_传输状态out_表明当前传输数据有效 ), .\同步清零_气泡_高电平有效 (1'b0),
    .\使能端_低电平有效_stall_高电平有效 (1'b0), .PC_4(id_ex_1_p57), .PC_4_2(ex_mem_1_pc_4_2), .MemWrite(id_ex_1_p40),
    .MemWrite_2(MemWrite), .RegWrite_2(id_ex_1_p54), .RegWrite_4(ex_mem_1_regwrite_4),
    .RegWrite(id_ex_1_p32), .RegWrite_3(ex_mem_1_regwrite_3), .ImmZeroExt16Shift(shifter_2_out),
    .ImmZeroExt16Shift_2(ex_mem_1_immzeroext16shift_2), .ifshow(comparator_1_eq),
    .ifshow_2(ex_mem_1_ifshow_2), .LedData(register_2_q), .LeaData(ex_mem_1_leadata), .LUI(id_ex_1_p36));  // open: rd, rd_2, MTC0, MTC0_2, IRout, IRout_2
  RAM #(.addrWidth(10), .dataWidth(32), .bus("separate"), .Select("high")) ram_1 (
    .addr(ex_mem_1_alu_2[11:2]), .din(MDin), .data(ram_1_data), .str(MemWrite), .clk(CLK), .clr(RST));  // open: sel, ld
  MEM_WB mem_wb_1 (
    .ERET(ex_mem_1_eret_2), .Syscall(ex_mem_1_syscall_2), .MemToReg(ex_mem_1_memtoreg_2),
    .LUI(ex_mem_1_lui_2), .MFC0(ex_mem_1_mfc0_2), .JAL(ex_mem_1_jal_2), .ALU(ex_mem_1_alu_2),
    .MD(ram_1_data), .IR(ex_mem_1_ir_2), .PC(M_PC), .PC_4(ex_mem_1_pc_4_2),
    .\传输状态In_表明当前传输数据有效 (\ex_mem_1_传输状态out_表明当前传输数据有效 ), .CLK(CLK), .Syscall_2(mem_wb_1_syscall_2),
    .MemToReg_2(mem_wb_1_memtoreg_2), .JAL_2(mem_wb_1_jal_2), .ALU_2(mem_wb_1_alu_2), .MD_2(mem_wb_1_md_2),
    .PC_2(WB_PC), .PC_4_2(mem_wb_1_pc_4_2), .\同步清零_气泡_高电平有效 (1'b0), .\使能端_低电平有效_stall_高电平有效 (1'b0),
    .LBU(ex_mem_1_lbu_2), .LBU_2(mem_wb_1_lbu_2), .ImmZeroExt16Shift(ex_mem_1_immzeroext16shift_2),
    .ImmZeroExt16Shift_2(mem_wb_1_immzeroext16shift_2), .RegWrite(ex_mem_1_regwrite_3),
    .RegWrite_3(RegWrite), .RegWrite_2(ex_mem_1_regwrite_4), .RegWrite_4(mem_wb_1_regwrite_4),
    .ifshow_2(mem_wb_1_ifshow_2), .ifshow(ex_mem_1_ifshow_2), .LedData(ex_mem_1_leadata),
    .LedData_2(LedData), .LUI_2(mem_wb_1_lui_2));  // open: ERET_2, MFC0_2, IR_2, 传输状态Out_表明当前传输数据有效, rd, rd_2, MTC0, MTC0_2, IRout, IRout_2
  Multiplexer #(.select(1), .width(32), .disabled("Z"), .enable("false")) multiplexer_12 (
    .in0(mem_wb_1_alu_2), .in1(multiplexer_13_out), .out(multiplexer_12_out), .sel(mem_wb_1_memtoreg_2));
  Multiplexer #(.select(1), .width(32), .disabled("Z"), .enable("false")) multiplexer_13 (
    .in0(mem_wb_1_md_2), .in1({{24{1'b0}}, mem_wb_1_md_2[7:0]}), .out(multiplexer_13_out),
    .sel(mem_wb_1_lbu_2));
  Multiplexer #(.select(1), .width(32), .disabled("Z"), .enable("false")) multiplexer_14 (
    .in0(multiplexer_12_out), .in1(mem_wb_1_immzeroext16shift_2), .out(multiplexer_14_out),
    .sel(mem_wb_1_lui_2));
  Multiplexer #(.select(1), .width(32), .disabled("Z"), .enable("false")) multiplexer_15 (
    .in0(multiplexer_14_out), .in1(mem_wb_1_pc_4_2), .out(RDin), .sel(mem_wb_1_jal_2));

  // Other names for the same wires on the sheet: MEM_PC[31:0] = M_PC

  // Notes on the sheet:
  //   中断源
  //   中断等待指示
  //   指令存储器
  //   contents of rom_1 (hex, n*v repeats v):
  //   20110100 20020022 8000006 20110004 20120005 20130006 10000003 20110007 20120008 20130009 14110003
  //   2011000a 2012000b 2013000c c000014 2002000a 0 0 0 c 2231ffff 0 0 0 112020 0 0 0 c 1620fff6 3e00008
  //   数码管输出
  //   指令字
  //   OP
  //   Func
  //   MF/MT
  //   rs
  //   rt
  //   rd
  //   JMP
  //   JR
  //   SignedExt
  //   LUI
  //   LBU
  //   MFC0
  //   MTC0
  //   OP
  //   Func
  //   MF/MT
  //   Syscall
  //   Beq
  //   Bgez
  //   Bne
  //   MemToReg
  //   MemWrite
  //   AluOP
  //   AluSrcB
  //   RegWrite
  //   JAL
  //   RegDst
  //   ERET
  //   流水调试日志用
  //   为方便自动评测，需要输出流水线各段保存的PC值，注意是PC不是PC+4，另外ID段寄存器写入信息，Mem段内存写入信息也要输出
  //   数据存储器
endmodule

module \气泡流水线  (
  output RegWrite,
  output MemWrite,
  output [31:0] IF_PC,
  output [31:0] ID_PC,
  output [31:0] EX_PC,
  output [31:0] M_PC,
  output [31:0] WB_PC,
  output [31:0] RDin,
  output [31:0] MDin,
  output [31:0] LedData
);

  wire and_1_out, and_2_out, and_3_out, and_4_out, and_5_out, and_6_out, and_7_out, and_8_out, and_9_out,
       Clear, CLK, comparator_1_eq, ex_mem_1_eret_2, ex_mem_1_ifshow_2, ex_mem_1_jal_2, ex_mem_1_lbu_2,
       ex_mem_1_lui_2, ex_mem_1_memtoreg_2, ex_mem_1_mfc0_2, ex_mem_1_regwrite_3, ex_mem_1_syscall_2,
       \ex_mem_1_传输状态out_表明当前传输数据有效 , ExNotStop, Go, id_ex_1_alusrc_2, id_ex_1_beq_2, id_ex_1_bgez_2,
       id_ex_1_bne_2, id_ex_1_eret_2, id_ex_1_jal_2, id_ex_1_jmp_2, id_ex_1_jr_2, id_ex_1_lbu_2,
       id_ex_1_lui_2, id_ex_1_memtoreg_2, id_ex_1_memwrite_2, id_ex_1_mfc0_2, id_ex_1_regwrite_3,
       id_ex_1_syscall_2, \id_ex_1_传输状态out_表明当前传输数据有效 , \if_id_1_传输状态out_表明当前传输数据有效 , ifjump, IR1, IR2, IR3,
       mem_wb_1_ifshow_2, mem_wb_1_jal_2, mem_wb_1_lbu_2, mem_wb_1_lui_2, mem_wb_1_memtoreg_2,
       mem_wb_1_syscall_2, MemNotStop, mips_alu_1_equal, \n27_4条扩展指令控制器_1_alu_src , \n27_4条扩展指令控制器_1_beq ,
       \n27_4条扩展指令控制器_1_bgez , \n27_4条扩展指令控制器_1_bne , \n27_4条扩展指令控制器_1_eret , \n27_4条扩展指令控制器_1_jal ,
       \n27_4条扩展指令控制器_1_jmp , \n27_4条扩展指令控制器_1_jr , \n27_4条扩展指令控制器_1_lbu , \n27_4条扩展指令控制器_1_lui ,
       \n27_4条扩展指令控制器_1_memtoreg , \n27_4条扩展指令控制器_1_memwrite , \n27_4条扩展指令控制器_1_mfc0 ,
       \n27_4条扩展指令控制器_1_mtc0 , \n27_4条扩展指令控制器_1_regdst , \n27_4条扩展指令控制器_1_regwrite ,
       \n27_4条扩展指令控制器_1_signedext , \n27_4条扩展指令控制器_1_syscall , nifjump, not_1_out, not_2_out, not_3_out,
       not_5_out, not_6_out, not_7_out, not_8_out, or_1_out, or_2_out, or_3_out, register_1_q, RST, W1, W2,
       W3, \数据相关检测 , \源寄存器使用情况_1_r1_used , \源寄存器使用情况_1_r2_used ;
  wire [3:0] id_ex_1_aluop_2, \n27_4条扩展指令控制器_1_alu_op ;
  wire [4:0] ex_mem_1_regwrite_4, id_ex_1_ir_2_2, id_ex_1_regwrite_4, mem_wb_1_regwrite_4, multiplexer_2_out,
       multiplexer_3_out, multiplexer_4_out, multiplexer_5_out;
  wire [11:0] if_id_1_ir_2;
  wire [15:0] \LoadUse次数 , \总周期数 , \插入气泡数 , \无条件分支数 , \条件分支成功数 ;
  wire [25:6] if_id_1_ir_2_2;
  wire [31:0] adder_1_out, adder_2_out, bit_extender_1_out, bit_extender_2_out, bit_extender_3_out,
       ex_mem_1_alu_2, ex_mem_1_immzeroext16shift_2, ex_mem_1_ir_2, ex_mem_1_leadata, ex_mem_1_pc_4_2,
       id_ex_1_a_2, id_ex_1_b_2, id_ex_1_immext16_2, id_ex_1_immsignedext26_2,
       \id_ex_1_immzeroext16_用于lui指令_2 , id_ex_1_ir_2, id_ex_1_pc_4_2, if_id_1_pc_4_2, mem_wb_1_alu_2,
       mem_wb_1_immzeroext16shift_2, mem_wb_1_md_2, mem_wb_1_pc_4_2, mips_alu_1_result, mips_regifile_1_r1,
       mips_regifile_1_r2, multiplexer_1_out, multiplexer_6_out, multiplexer_7_out, multiplexer_8_out,
       multiplexer_9_out, multiplexer_10_out, multiplexer_11_out, multiplexer_12_out, multiplexer_13_out,
       multiplexer_14_out, ram_1_data, register_2_q, rom_1_data, shifter_1_out, shifter_2_out, shifter_3_out;

  Button \u_总复位  (.out(RST));
  Button _1 (.out(IR1));
  Button _2 (.out(IR2));
  Button _3 (.out(IR3));
  Button \u_继续运行  (.out(Go));
  LED #(.active("true")) led_1 (.in(W1));
  LED #(.active("true")) led_2 (.in(W2));
  LED #(.active("true")) led_3 (.in(W3));
  Register #(.width(32), .trigger("rising"), .Select("low")) PC (
    .D(multiplexer_1_out), .en(and_2_out), .Q(IF_PC), .clk(CLK), .clr(RST));
  Hex_Digit_Display hex_digit_display_1 (.value(LedData[31:28]));  // open: dp
  and and_1 (and_1_out, \数据相关检测 , ExNotStop, MemNotStop, not_1_out);
  and and_2 (and_2_out, not_3_out, not_1_out);
  Register #(.width(1), .trigger("rising"), .Select("low")) register_1 (
    .D(mem_wb_1_syscall_2), .en(and_3_out), .Q(register_1_q), .clk(CLK), .clr(or_1_out));
  or or_1 (or_1_out, RST, Go);
  Counter #(.width(16), .max('hffff), .ongoal("wrap"), .trigger("rising"), .behavior("old")) counter_1 (
    .count(not_1_out), .Q(\总周期数 ), .clk(CLK), .clr(RST));  // open: load, D, carry, preset
  Multiplexer #(.select(1), .width(32), .disabled("Z"), .enable("false")) multiplexer_1 (
    .in0(adder_1_out), .in1(multiplexer_11_out), .out(multiplexer_1_out), .sel(Clear));
  and and_3 (and_3_out, not_2_out, mem_wb_1_syscall_2);
  Hex_Digit_Display hex_digit_display_2 (.value(LedData[23:20]));  // open: dp
  Hex_Digit_Display hex_digit_display_3 (.value(LedData[27:24]));  // open: dp
  Counter #(.width(16), .max('hffff), .ongoal("wrap"), .trigger("rising"), .behavior("old")) counter_2 (
    .count(ifjump), .Q(\条件分支成功数 ), .clk(CLK), .clr(RST));  // open: load, D, carry, preset
  Counter #(.width(16), .max('hffff), .ongoal("wrap"), .trigger("rising"), .behavior("old")) counter_3 (
    .count(nifjump), .Q(\无条件分支数 ), .clk(CLK), .clr(RST));  // open: load, D, carry, preset
  Counter #(.width(16), .max('hffff), .ongoal("wrap"), .trigger("rising"), .behavior("old")) counter_4 (
    .count(and_1_out), .Q(\插入气泡数 ), .clk(CLK), .clr(RST));  // open: load, D, carry, preset
  Adder #(.width(32)) adder_1 (.a(IF_PC), .b(32'h4), .out(adder_1_out));  // open: cin, cout
  not not_1 (not_1_out, register_1_q);
  not not_2 (not_2_out, mem_wb_1_ifshow_2);
  Hex_Digit_Display hex_digit_display_4 (.value(LedData[19:16]));  // open: dp
  Hex_Digit_Display hex_digit_display_5 (.value(LedData[15:12]));  // open: dp
  ROM #(.addrWidth(10), .dataWidth(32), .Select("high")) rom_1 (.addr(IF_PC[11:2]), .data(rom_1_data));
  not not_3 (not_3_out, \数据相关检测 );
  Hex_Digit_Display hex_digit_display_6 (.value(LedData[11:8]));  // open: dp
  Hex_Digit_Display hex_digit_display_7 (.value(LedData[7:4]));  // open: dp
  Clock #(.highDuration(1), .lowDuration(1)) clock_1 (.out(CLK));
  IF_ID if_id_1 (
    .IR(rom_1_data), .PC_4(adder_1_out), .\传输状态In_表明当前传输数据有效 (1'b1), .CLK(CLK),
    .IR_2({if_id_1_ir_2[5:0], if_id_1_ir_2_2, if_id_1_ir_2[11:6]}), .PC_4_2(if_id_1_pc_4_2),
    .\传输状态Out_表明当前传输数据有效 (\if_id_1_传输状态out_表明当前传输数据有效 ), .\同步清零_气泡_高电平有效 (Clear),
    .\使能端_低电平有效_stall_高电平有效 (\数据相关检测 ), .PC(IF_PC), .PC_2(ID_PC));  // open: DesAddr, DesAddr_2, Miss, Miss_2, Hit, Hit_2, Prediction_2, Prediction
  Hex_Digit_Display hex_digit_display_8 (.value(LedData[3:0]));  // open: dp
  \源寄存器使用情况  \u_源寄存器使用情况_1  (
    .OP0(if_id_1_ir_2[0]), .OP1(if_id_1_ir_2[1]), .OP2(if_id_1_ir_2[2]), .OP3(if_id_1_ir_2[3]),
    .OP4(if_id_1_ir_2[4]), .OP5(if_id_1_ir_2[5]), .F0(if_id_1_ir_2[6]), .F1(if_id_1_ir_2[7]),
    .F2(if_id_1_ir_2[8]), .F3(if_id_1_ir_2[9]), .F4(if_id_1_ir_2[10]), .F5(if_id_1_ir_2[11]),
    .R1_Used(\源寄存器使用情况_1_r1_used ), .R2_Used(\源寄存器使用情况_1_r2_used ));
  // Probe on \总周期数 
  \数据相关检测  \u_数据相关检测_1  (
    .R1_Used(\源寄存器使用情况_1_r1_used ), .R2_Used(\源寄存器使用情况_1_r2_used ), .ID_R1_num(multiplexer_2_out),
    .ID_R2_num(multiplexer_3_out), .EX_WriteReg_num(id_ex_1_regwrite_4),
    .MEM_WriteReg_num(ex_mem_1_regwrite_4), .EX_RegWrite(id_ex_1_regwrite_3),
    .MEM__RegWrite(ex_mem_1_regwrite_3), .\数据相关 (\数据相关检测 ));  // open: EX_MemToReg, MEM_MemToReg, Forward1, Forward2, Load_Use
  // Probe on \总周期数 
  // Probe on \无条件分支数 
  // Probe on \条件分支成功数 
  // Probe on \插入气泡数 
  // Probe on \LoadUse次数 
  Multiplexer #(.select(1), .width(5), .disabled("Z"), .enable("false")) multiplexer_2 (
    .in0(if_id_1_ir_2_2[25:21]), .in1(5'b00100), .out(multiplexer_2_out), .sel(\n27_4条扩展指令控制器_1_syscall ));
  Multiplexer #(.select(1), .width(5), .disabled("Z"), .enable("false")) multiplexer_3 (
    .in0(if_id_1_ir_2_2[20:16]), .in1(5'b00010), .out(multiplexer_3_out), .sel(\n27_4条扩展指令控制器_1_syscall ));
  Multiplexer #(.select(1), .width(5), .disabled("Z"), .enable("false")) multiplexer_4 (
    .in0(if_id_1_ir_2_2[20:16]), .in1(if_id_1_ir_2_2[15:11]), .out(multiplexer_4_out),
    .sel(\n27_4条扩展指令控制器_1_regdst ));
  assign bit_extender_1_out = {{16{1'b0}}, {if_id_1_ir_2_2[15:6], if_id_1_ir_2[11:6]}};  // Bit_Extender bit_extender_1
  assign bit_extender_2_out = {{16{if_id_1_ir_2_2[15]}}, {if_id_1_ir_2_2[15:6], if_id_1_ir_2[11:6]}};  // Bit_Extender bit_extender_2
  assign bit_extender_3_out = {{6{if_id_1_ir_2_2[25]}}, {if_id_1_ir_2_2, if_id_1_ir_2[11:6]}};  // Bit_Extender bit_extender_3
  // Probe on IF_PC[11:0]
  \_27_4条扩展指令控制器  \u_27_4条扩展指令控制器_1  (
    .OP(if_id_1_ir_2[5:0]), .Func(if_id_1_ir_2[11:6]), .ALU_OP(\n27_4条扩展指令控制器_1_alu_op ),
    .MemToReg(\n27_4条扩展指令控制器_1_memtoreg ), .MemWrite(\n27_4条扩展指令控制器_1_memwrite ),
    .ALU_SRC(\n27_4条扩展指令控制器_1_alu_src ), .SysCALL(\n27_4条扩展指令控制器_1_syscall ),
    .SignedExt(\n27_4条扩展指令控制器_1_signedext ), .RegDst(\n27_4条扩展指令控制器_1_regdst ), .Beq(\n27_4条扩展指令控制器_1_beq ),
    .Bne(\n27_4条扩展指令控制器_1_bne ), .JR(\n27_4条扩展指令控制器_1_jr ), .JMP(\n27_4条扩展指令控制器_1_jmp ),
    .JAL(\n27_4条扩展指令控制器_1_jal ), .LUI(\n27_4条扩展指令控制器_1_lui ), .LBU(\n27_4条扩展指令控制器_1_lbu ),
    .BGEZ(\n27_4条扩展指令控制器_1_bgez ), .MTC0(\n27_4条扩展指令控制器_1_mtc0 ), .MFMT(if_id_1_ir_2_2[25:21]),
    .ERET(\n27_4条扩展指令控制器_1_eret ), .MFC0(\n27_4条扩展指令控制器_1_mfc0 ), .RegWrite(\n27_4条扩展指令控制器_1_regwrite ));
  Multiplexer #(.select(1), .width(5), .disabled("Z"), .enable("false")) multiplexer_5 (
    .in0(multiplexer_4_out), .in1({5{1'b1}}), .out(multiplexer_5_out), .sel(\n27_4条扩展指令控制器_1_jal ));
  // Probe on EX_PC[11:0]
  // Probe on ID_PC[11:0]
  Multiplexer #(.select(1), .width(32), .disabled("Z"), .enable("false")) multiplexer_6 (
    .in0(bit_extender_1_out), .in1(bit_extender_2_out), .out(multiplexer_6_out),
    .sel(\n27_4条扩展指令控制器_1_signedext ));
  // Probe on M_PC[11:0]
  MIPS_Regifile mips_regifile_1 (
    .Din(RDin), .Clk(CLK), .R1(mips_regifile_1_r1), .R2(mips_regifile_1_r2), .WE(RegWrite),
    .W_num(mem_wb_1_regwrite_4), .R1_num(multiplexer_2_out), .R2_num(multiplexer_3_out));
  // Probe on WB_PC[11:0]
  or or_2 (or_2_out, Clear, \数据相关检测 );
  ID_EX id_ex_1 (
    .MemToReg(\n27_4条扩展指令控制器_1_memtoreg ), .LUI(\n27_4条扩展指令控制器_1_lui ), .MFC0(\n27_4条扩展指令控制器_1_mfc0 ),
    .LBU(\n27_4条扩展指令控制器_1_lbu ), .MemWrite(\n27_4条扩展指令控制器_1_memwrite ), .AluOP(\n27_4条扩展指令控制器_1_alu_op ),
    .MTC0(\n27_4条扩展指令控制器_1_mtc0 ), .Beq(\n27_4条扩展指令控制器_1_beq ), .Bgez(\n27_4条扩展指令控制器_1_bgez ),
    .Bne(\n27_4条扩展指令控制器_1_bne ), .JMP(\n27_4条扩展指令控制器_1_jmp ), .A(mips_regifile_1_r1), .B(mips_regifile_1_r2),
    .ImmExt16(multiplexer_6_out), .\ImmZeroExt16_用于LUI指令 (bit_extender_1_out),
    .ImmSignedExt26(bit_extender_3_out), .IR({if_id_1_ir_2[5:0], if_id_1_ir_2_2, if_id_1_ir_2[11:6]}),
    .\传输状态In_表明当前传输数据有效 (\if_id_1_传输状态out_表明当前传输数据有效 ), .CLK(CLK), .MemToReg_2(id_ex_1_memtoreg_2),
    .LUI_2(id_ex_1_lui_2), .MFC0_2(id_ex_1_mfc0_2), .JAL_2(id_ex_1_jal_2), .LBU_2(id_ex_1_lbu_2),
    .MemWrite_2(id_ex_1_memwrite_2), .AluOP_2(id_ex_1_aluop_2), .AluSrc_2(id_ex_1_alusrc_2),
    .Beq_2(id_ex_1_beq_2), .Bgez_2(id_ex_1_bgez_2), .Bne_2(id_ex_1_bne_2), .JMP_2(id_ex_1_jmp_2),
    .A_2(id_ex_1_a_2), .B_2(id_ex_1_b_2), .ImmExt16_2(id_ex_1_immext16_2),
    .\ImmZeroExt16_用于LUI指令_2 (\id_ex_1_immzeroext16_用于lui指令_2 ), .ImmSignedExt26_2(id_ex_1_immsignedext26_2),
    .IR_2({id_ex_1_ir_2[31:11], id_ex_1_ir_2_2, id_ex_1_ir_2[5:0]}),
    .\传输状态Out_表明当前传输数据有效 (\id_ex_1_传输状态out_表明当前传输数据有效 ), .\同步清零_气泡_高电平有效 (or_2_out),
    .\使能端_低电平有效_stall_高电平有效 (1'b0), .ERET(\n27_4条扩展指令控制器_1_eret ), .ERET_2(id_ex_1_eret_2),
    .Syscall(\n27_4条扩展指令控制器_1_syscall ), .Syscall_2(id_ex_1_syscall_2), .PC(ID_PC), .PC_2(EX_PC),
    .PC_4_2(id_ex_1_pc_4_2), .PC_4(if_id_1_pc_4_2), .RegWrite_3(id_ex_1_regwrite_3),
    .RegWrite_2(multiplexer_5_out), .RegWrite_4(id_ex_1_regwrite_4), .AluSrc(\n27_4条扩展指令控制器_1_alu_src ),
    .RegWrite(\n27_4条扩展指令控制器_1_regwrite ), .JAL(\n27_4条扩展指令控制器_1_jal ), .JR(\n27_4条扩展指令控制器_1_jr ),
    .JR_2(id_ex_1_jr_2));  // open: MTC0_2, forwar1, forward1, forward2, forward2_2, rd, rd_2, prediction, prediction_2, Miss, Miss_2, Hit, Hit_2, DesAddr, DesAddr_2
  and and_4 (and_4_out, id_ex_1_syscall_2, not_5_out);
  not not_4 (ExNotStop, and_4_out);
  not not_5 (not_5_out, comparator_1_eq);
  and and_5 (and_5_out, id_ex_1_syscall_2, comparator_1_eq);
  Comparator #(.width(32), .mode("twosComplement")) comparator_1 (
    .a(32'h22), .b(id_ex_1_b_2), .eq(comparator_1_eq));  // open: gt, lt
  Multiplexer #(.select(1), .width(32), .disabled("Z"), .enable("false")) multiplexer_7 (
    .in0(id_ex_1_b_2), .in1(id_ex_1_immext16_2), .out(multiplexer_7_out), .sel(id_ex_1_alusrc_2));
  Multiplexer #(.select(1), .width(32), .disabled("Z"), .enable("false")) multiplexer_8 (
    .in0(multiplexer_7_out), .in1({32{1'b0}}), .out(multiplexer_8_out), .sel(id_ex_1_bgez_2));
  Shifter #(.width(32), .shift("ll")) shifter_1 (.in(id_ex_1_immext16_2), .\dist (5'b00010), .out(shifter_1_out));
  Shifter #(.width(32), .shift("ll")) shifter_2 (
    .in(\id_ex_1_immzeroext16_用于lui指令_2 ), .\dist (5'b10000), .out(shifter_2_out));
  Shifter #(.width(32), .shift("ll")) shifter_3 (.in(id_ex_1_immsignedext26_2), .\dist (5'b00010), .out(shifter_3_out));
  MIPS_ALU mips_alu_1 (
    .X(id_ex_1_a_2), .Y(multiplexer_8_out), .AluOP(id_ex_1_aluop_2), .Equal(mips_alu_1_equal),
    .Result(mips_alu_1_result), .shamt(id_ex_1_ir_2_2));  // open: Result_2
  not not_6 (not_6_out, mips_alu_1_equal);
  not not_7 (not_7_out, mips_alu_1_result[0]);
  Adder #(.width(32)) adder_2 (.a(shifter_1_out), .b(id_ex_1_pc_4_2), .out(adder_2_out));  // open: cin, cout
  and and_6 (and_6_out, not_6_out, id_ex_1_bne_2);
  and and_7 (and_7_out, not_7_out, id_ex_1_bgez_2);
  and and_8 (and_8_out, id_ex_1_beq_2, mips_alu_1_equal);
  Register #(.width(32), .trigger("rising"), .Select("low")) register_2 (
    .D(id_ex_1_a_2), .en(and_5_out), .Q(register_2_q), .clk(CLK), .clr(RST));
  or or_3 (or_3_out, id_ex_1_jal_2, id_ex_1_jmp_2);
  or or_4 (ifjump, and_6_out, and_7_out, and_8_out);
  Multiplexer #(.select(1), .width(32), .disabled("Z"), .enable("false")) multiplexer_9 (
    .in0(id_ex_1_pc_4_2), .in1(adder_2_out), .out(multiplexer_9_out), .sel(ifjump));
  Multiplexer #(.select(1), .width(32), .disabled("Z"), .enable("false")) multiplexer_10 (
    .in0(multiplexer_9_out), .in1(shifter_3_out), .out(multiplexer_10_out), .sel(or_3_out));
  Multiplexer #(.select(1), .width(32), .disabled("Z"), .enable("false")) multiplexer_11 (
    .in0(multiplexer_10_out), .in1(id_ex_1_a_2), .out(multiplexer_11_out), .sel(id_ex_1_jr_2));
  or or_5 (Clear, ifjump, id_ex_1_jr_2, or_3_out);
  or or_6 (nifjump, or_3_out, id_ex_1_jr_2);
  EX_MEM ex_mem_1 (
    .ERET(id_ex_1_eret_2), .Syscall(id_ex_1_syscall_2), .MemToReg(id_ex_1_memtoreg_2), .MFC0(id_ex_1_mfc0_2),
    .JAL(id_ex_1_jal_2), .LBU(id_ex_1_lbu_2), .B(id_ex_1_b_2), .ALU(mips_alu_1_result),
    .IR({id_ex_1_ir_2[31:11], id_ex_1_ir_2_2, id_ex_1_ir_2[5:0]}), .PC(EX_PC),
    .\传输状态In_表明当前传输数据有效 (\id_ex_1_传输状态out_表明当前传输数据有效 ), .CLK(CLK), .ERET_2(ex_mem_1_eret_2),
    .Syscall_2(ex_mem_1_syscall_2), .MemToReg_2(ex_mem_1_memtoreg_2), .LUI_2(ex_mem_1_lui_2),
    .MFC0_2(ex_mem_1_mfc0_2), .JAL_2(ex_mem_1_jal_2), .LBU_2(ex_mem_1_lbu_2), .B_2(MDin),
    .ALU_2(ex_mem_1_alu_2), .IR_2(ex_mem_1_ir_2), .PC_2(M_PC),
    .\传输状态Out_表明当前传输数据有效 (\ex_mem_1_传输状态out_表明当前传输数据有效 ), .\同步清零_气泡_高电平有效 (1'b0),
    .\使能端_低电平有效_stall_高电平有效 (1'b0), .PC_4(id_ex_1_pc_4_2), .PC_4_2(ex_mem_1_pc_4_2),
    .MemWrite(id_ex_1_memwrite_2), .MemWrite_2(MemWrite), .RegWrite_2(id_ex_1_regwrite_4),
    .RegWrite_4(ex_mem_1_regwrite_4), .RegWrite(id_ex_1_regwrite_3), .RegWrite_3(ex_mem_1_regwrite_3),
    .ImmZeroExt16Shift(shifter_2_out), .ImmZeroExt16Shift_2(ex_mem_1_immzeroext16shift_2),
    .ifshow(comparator_1_eq), .ifshow_2(ex_mem_1_ifshow_2), .LedData(register_2_q),
    .LeaData(ex_mem_1_leadata), .LUI(id_ex_1_lui_2));  // open: rd, rd_2, MTC0, MTC0_2, IRout, IRout_2
  not not_8 (not_8_out, ex_mem_1_ifshow_2);
  not not_9 (MemNotStop, and_9_out);
  and and_9 (and_9_out, ex_mem_1_syscall_2, not_8_out);
  RAM #(.addrWidth(10), .dataWidth(32), .bus("separate"), .Select("high")) ram_1 (
    .addr(ex_mem_1_alu_2[11:2]), .din(MDin), .data(ram_1_data), .str(MemWrite), .clk(CLK), .clr(RST));  // open: sel, ld
  MEM_WB mem_wb_1 (
    .ERET(ex_mem_1_eret_2), .Syscall(ex_mem_1_syscall_2), .MemToReg(ex_mem_1_memtoreg_2),
    .LUI(ex_mem_1_lui_2), .MFC0(ex_mem_1_mfc0_2), .JAL(ex_mem_1_jal_2), .ALU(ex_mem_1_alu_2),
    .MD(ram_1_data), .IR(ex_mem_1_ir_2), .PC(M_PC), .PC_4(ex_mem_1_pc_4_2),
    .\传输状态In_表明当前传输数据有效 (\ex_mem_1_传输状态out_表明当前传输数据有效 ), .CLK(CLK), .Syscall_2(mem_wb_1_syscall_2),
    .MemToReg_2(mem_wb_1_memtoreg_2), .JAL_2(mem_wb_1_jal_2), .ALU_2(mem_wb_1_alu_2), .MD_2(mem_wb_1_md_2),
    .PC_2(WB_PC), .PC_4_2(mem_wb_1_pc_4_2), .\同步清零_气泡_高电平有效 (1'b0), .\使能端_低电平有效_stall_高电平有效 (1'b0),
    .LBU(ex_mem_1_lbu_2), .LBU_2(mem_wb_1_lbu_2), .ImmZeroExt16Shift(ex_mem_1_immzeroext16shift_2),
    .ImmZeroExt16Shift_2(mem_wb_1_immzeroext16shift_2), .RegWrite(ex_mem_1_regwrite_3),
    .RegWrite_3(RegWrite), .RegWrite_2(ex_mem_1_regwrite_4), .RegWrite_4(mem_wb_1_regwrite_4),
    .ifshow_2(mem_wb_1_ifshow_2), .ifshow(ex_mem_1_ifshow_2), .LedData(ex_mem_1_leadata),
    .LedData_2(LedData), .LUI_2(mem_wb_1_lui_2));  // open: ERET_2, MFC0_2, IR_2, 传输状态Out_表明当前传输数据有效, rd, rd_2, MTC0, MTC0_2, IRout, IRout_2
  Multiplexer #(.select(1), .width(32), .disabled("Z"), .enable("false")) multiplexer_12 (
    .in0(mem_wb_1_md_2), .in1({{24{1'b0}}, mem_wb_1_md_2[7:0]}), .out(multiplexer_12_out),
    .sel(mem_wb_1_lbu_2));
  Multiplexer #(.select(1), .width(32), .disabled("Z"), .enable("false")) multiplexer_13 (
    .in0(mem_wb_1_alu_2), .in1(multiplexer_12_out), .out(multiplexer_13_out), .sel(mem_wb_1_memtoreg_2));
  Multiplexer #(.select(1), .width(32), .disabled("Z"), .enable("false")) multiplexer_14 (
    .in0(multiplexer_13_out), .in1(mem_wb_1_immzeroext16shift_2), .out(multiplexer_14_out),
    .sel(mem_wb_1_lui_2));
  Multiplexer #(.select(1), .width(32), .disabled("Z"), .enable("false")) multiplexer_15 (
    .in0(multiplexer_14_out), .in1(mem_wb_1_pc_4_2), .out(RDin), .sel(mem_wb_1_jal_2));

  // Other names for the same wires on the sheet: MEM_PC[31:0] = M_PC

  // Notes on the sheet:
  //   中断源
  //   中断等待指示
  //   指令存储器
  //   数码管输出
  //   指令字
  //   contents of rom_1 (hex, n*v repeats v):
  //   20110001 8100005 20110001 20120002 20130003 8100009 20110001 20120002 20130003 810000d 20110001
  //   20120002 20130003 8100011 20110001 20120002 20130003 c1000fc 20100001 20110001 118fc0 112020
  //   20020022 c 118882 12200001 8100015 112020 20020022 c 20110001 118880 112020 20020022 c 12200001
  //   810001f 20110001 118fc0 112020 20020022 c 1188c3 112020 20020022 c 118903 112020 20020022 c 118903
  //   112020 20020022 c 118903 112020 20020022 c 118903 112020 20020022 c 118903 112020 20020022 c 118903
  //   112020 20020022 c 118903 112020 20020022 c 20100001 109fc0 139fc3 8021 2012000c 24160003 26100001
  //   3210000f 20080008 20090001 139900 2709825 132020 20020022 c 1094022 1500fff9 22100001 2018000f
  //   2188024 108700 20080008 20090001 139902 2709825 132021 20020022 c 1094022 1500fff9 108702 2c9b022
  //   12c00001 8100050 4020 1084027 84400 3508ffff 82021 20020022 c 2010ffff 20110000 ae300000 22100001
  //   22310004 ae300000 22100001 22310004 ae300000 22100001 22310004 ae300000 22100001 22310004 ae300000
  //   22100001 22310004 ae300000 22100001 22310004 ae300000 22100001 22310004 ae300000 22100001 22310004
  //   ae300000 22100001 22310004 ae300000 22100001 22310004 ae300000 22100001 22310004 ae300000 22100001
  //   22310004 ae300000 22100001 22310004 ae300000 22100001 22310004 ae300000 22100001 22310004 ae300000
  //   22100001 22310004 22100001 8020 2011003c 8e130000 8e340000 274402a 11000002 ae330000 ae140000
  //   2231fffc 1611fff8 102020 20020022 c 22100004 2011003c 1611fff2 20020032 c 20080001 20110010 112020
  //   20020022 c 200b0020 2288823 112020 20020022 c 216bffff 1560fffa 2002000a c 200b0008 3c11fedc
  //   3631ffff 112020 20020022 c 3c11ba98 112020 c 3c117654 112020 c 3c113210 112020 c 216bffff 1560fff0
  //   2002000a c 20090000 200b0020 34118483 20120401 118c00 129400 36318281 22520401 ad310000 2328820
  //   21290004 216bffff 1560fffb 20020022 200b0020 20090000 91310000 112020 20020022 c 21290004 216bffff
  //   1560fff9 2002000a c 2011000f 112020 20020022 c 2231ffff 621fffb 2002000a c 2002000a c 20100000
  //   22100001 102020 20020022 c 22100002 102020 20020022 c 22100003 102020 20020022 c 22100004 102020
  //   20020022 c 22100005 102020 20020022 c 22100006 102020 20020022 c 22100007 102020 20020022 c 22100008
  //   102020 20020022 20020022 c 3e00008
  //   OP
  //   Func
  //   rs
  //   rt
  //   rd
  //   MF/MT
  //   JMP
  //   JR
  //   SignedExt
  //   LUI
  //   LBU
  //   MFC0
  //   MTC0
  //   OP
  //   Func
  //   MF/MT
  //   Syscall
  //   Beq
  //   Bgez
  //   Bne
  //   MemToReg
  //   MemWrite
  //   AluOP
  //   AluSrcB
  //   RegWrite
  //   JAL
  //   RegDst
  //   ERET
  //   流水调试日志用
  //   为方便自动评测，需要输出流水线各段保存的PC值，注意是PC不是PC+4，另外ID段寄存器写入信息，Mem段内存写入信息也要输出
  //   数据存储器
endmodule

module \重定向流水线  (
  output RegWrite,
  output MemWrite,
  output [31:0] IF_PC,
  output [31:0] ID_PC,
  output [31:0] EX_PC,
  output [31:0] M_PC,
  output [31:0] WB_PC,
  output [31:0] RDin,
  output [31:0] MDin,
  output [31:0] LedData
);

  wire and_1_out, and_2_out, and_3_out, and_4_out, and_5_out, and_6_out, and_7_out, and_8_out, and_9_out,
       Clear, CLK, comparator_1_eq, ex_mem_1_eret_2, ex_mem_1_ifshow_2, ex_mem_1_jal_2, ex_mem_1_lbu_2,
       ex_mem_1_lui_2, ex_mem_1_memtoreg_2, ex_mem_1_mfc0_2, ex_mem_1_regwrite_3, ex_mem_1_syscall_2,
       \ex_mem_1_传输状态out_表明当前传输数据有效 , ExNotStop, Go, id_ex_1_alusrc_2, id_ex_1_beq_2, id_ex_1_bgez_2,
       id_ex_1_bne_2, id_ex_1_eret_2, id_ex_1_jal_2, id_ex_1_jmp_2, id_ex_1_jr_2, id_ex_1_lbu_2,
       id_ex_1_lui_2, id_ex_1_memtoreg_2, id_ex_1_memwrite_2, id_ex_1_mfc0_2, id_ex_1_regwrite_3,
       id_ex_1_syscall_2, \id_ex_1_传输状态out_表明当前传输数据有效 , \if_id_1_传输状态out_表明当前传输数据有效 , ifjump, IR1, IR2, IR3,
       Load_Use, mem_wb_1_ifshow_2, mem_wb_1_jal_2, mem_wb_1_lbu_2, mem_wb_1_lui_2, mem_wb_1_memtoreg_2,
       mem_wb_1_syscall_2, MemNotStop, mips_alu_1_equal, \n27_4条扩展指令控制器_1_alu_src , \n27_4条扩展指令控制器_1_beq ,
       \n27_4条扩展指令控制器_1_bgez , \n27_4条扩展指令控制器_1_bne , \n27_4条扩展指令控制器_1_eret , \n27_4条扩展指令控制器_1_jal ,
       \n27_4条扩展指令控制器_1_jmp , \n27_4条扩展指令控制器_1_jr , \n27_4条扩展指令控制器_1_lbu , \n27_4条扩展指令控制器_1_lui ,
       \n27_4条扩展指令控制器_1_memtoreg , \n27_4条扩展指令控制器_1_memwrite , \n27_4条扩展指令控制器_1_mfc0 ,
       \n27_4条扩展指令控制器_1_mtc0 , \n27_4条扩展指令控制器_1_regdst , \n27_4条扩展指令控制器_1_regwrite ,
       \n27_4条扩展指令控制器_1_signedext , \n27_4条扩展指令控制器_1_syscall , nifjump, not_1_out, not_2_out, not_3_out,
       not_5_out, not_6_out, not_7_out, not_8_out, or_1_out, or_2_out, or_3_out, or_4_out, register_1_q, RST,
       W1, W2, W3, \源寄存器使用情况_1_r1_used , \源寄存器使用情况_1_r2_used ;
  wire [1:0] id_ex_1_forward1, id_ex_1_forward2_2, \数据相关检测_1_forward1 , \数据相关检测_1_forward2 ;
  wire [3:0] id_ex_1_aluop_2, \n27_4条扩展指令控制器_1_alu_op ;
  wire [4:0] ex_mem_1_regwrite_4, id_ex_1_regwrite_4, mem_wb_1_regwrite_4, multiplexer_2_out,
       multiplexer_3_out, multiplexer_4_out, multiplexer_5_out;
  wire [11:0] if_id_1_ir_2;
  wire [15:0] \LoadUse次数 , \总周期数 , \无条件分支数 , \条件分支成功数 ;
  wire [25:6] if_id_1_ir_2_2;
  wire [31:0] adder_1_out, adder_2_out, bit_extender_1_out, bit_extender_2_out, bit_extender_3_out,
       ex_mem_1_alu_2, ex_mem_1_immzeroext16shift_2, ex_mem_1_ir_2, ex_mem_1_leadata, ex_mem_1_pc_4_2,
       id_ex_1_a_2, id_ex_1_b_2, id_ex_1_immext16_2, id_ex_1_immsignedext26_2,
       \id_ex_1_immzeroext16_用于lui指令_2 , id_ex_1_ir_2, id_ex_1_pc_4_2, if_id_1_pc_4_2, mem_wb_1_alu_2,
       mem_wb_1_immzeroext16shift_2, mem_wb_1_md_2, mem_wb_1_pc_4_2, mips_alu_1_result, mips_regifile_1_r1,
       mips_regifile_1_r2, multiplexer_1_out, multiplexer_6_out, multiplexer_7_out, multiplexer_8_out,
       multiplexer_9_out, multiplexer_10_out, multiplexer_11_out, multiplexer_12_out, multiplexer_13_out,
       multiplexer_14_out, multiplexer_15_out, multiplexer_16_out, multiplexer_17_out, ram_1_data,
       register_2_q, rom_1_data, shifter_1_out, shifter_2_out, shifter_3_out;

  Button \u_总复位  (.out(RST));
  Button _1 (.out(IR1));
  Button _2 (.out(IR2));
  Button _3 (.out(IR3));
  Button \u_继续运行  (.out(Go));
  LED #(.active("true")) led_1 (.in(W1));
  LED #(.active("true")) led_2 (.in(W2));
  LED #(.active("true")) led_3 (.in(W3));
  Register #(.width(32), .trigger("rising"), .Select("low")) PC (
    .D(multiplexer_1_out), .en(and_2_out), .Q(IF_PC), .clk(CLK), .clr(RST));
  Hex_Digit_Display hex_digit_display_1 (.value(LedData[31:28]));  // open: dp
  and and_1 (and_1_out, MemNotStop, ExNotStop, Load_Use, not_1_out);
  and and_2 (and_2_out, not_3_out, not_1_out);
  Register #(.width(1), .trigger("rising"), .Select("low")) register_1 (
    .D(mem_wb_1_syscall_2), .en(and_3_out), .Q(register_1_q), .clk(CLK), .clr(or_1_out));
  or or_1 (or_1_out, RST, Go);
  Counter #(.width(16), .max('hffff), .ongoal("wrap"), .trigger("rising"), .behavior("old")) counter_1 (
    .count(not_1_out), .Q(\总周期数 ), .clk(CLK), .clr(RST));  // open: load, D, carry, preset
  Multiplexer #(.select(1), .width(32), .disabled("Z"), .enable("false")) multiplexer_1 (
    .in0(adder_1_out), .in1(multiplexer_13_out), .out(multiplexer_1_out), .sel(Clear));
  and and_3 (and_3_out, not_2_out, mem_wb_1_syscall_2);
  Hex_Digit_Display hex_digit_display_2 (.value(LedData[23:20]));  // open: dp
  Hex_Digit_Display hex_digit_display_3 (.value(LedData[27:24]));  // open: dp
  Counter #(.width(16), .max('hffff), .ongoal("wrap"), .trigger("rising"), .behavior("old")) counter_2 (
    .count(ifjump), .Q(\条件分支成功数 ), .clk(CLK), .clr(RST));  // open: load, D, carry, preset
  Counter #(.width(16), .max('hffff), .ongoal("wrap"), .trigger("rising"), .behavior("old")) counter_3 (
    .count(nifjump), .Q(\无条件分支数 ), .clk(CLK), .clr(RST));  // open: load, D, carry, preset
  Counter #(.width(16), .max('hffff), .ongoal("wrap"), .trigger("rising"), .behavior("old")) counter_4 (
    .count(and_1_out), .Q(\LoadUse次数 ), .clk(CLK), .clr(RST));  // open: load, D, carry, preset
  Adder #(.width(32)) adder_1 (.a(IF_PC), .b(32'h4), .out(adder_1_out));  // open: cin, cout
  not not_1 (not_1_out, register_1_q);
  not not_2 (not_2_out, mem_wb_1_ifshow_2);
  Hex_Digit_Display hex_digit_display_4 (.value(LedData[19:16]));  // open: dp
  Hex_Digit_Display hex_digit_display_5 (.value(LedData[15:12]));  // open: dp
  ROM #(.addrWidth(10), .dataWidth(32), .Select("high")) rom_1 (.addr(IF_PC[11:2]), .data(rom_1_data));
  not not_3 (not_3_out, Load_Use);
  Hex_Digit_Display hex_digit_display_6 (.value(LedData[11:8]));  // open: dp
  Hex_Digit_Display hex_digit_display_7 (.value(LedData[7:4]));  // open: dp
  Clock #(.highDuration(1), .lowDuration(1)) clock_1 (.out(CLK));
  IF_ID if_id_1 (
    .IR(rom_1_data), .PC_4(adder_1_out), .\传输状态In_表明当前传输数据有效 (1'b1), .CLK(CLK),
    .IR_2({if_id_1_ir_2[5:0], if_id_1_ir_2_2, if_id_1_ir_2[11:6]}), .PC_4_2(if_id_1_pc_4_2),
    .\传输状态Out_表明当前传输数据有效 (\if_id_1_传输状态out_表明当前传输数据有效 ), .\同步清零_气泡_高电平有效 (Clear),
    .\使能端_低电平有效_stall_高电平有效 (or_2_out), .PC(IF_PC), .PC_2(ID_PC));  // open: DesAddr, DesAddr_2, Miss, Miss_2, Hit, Hit_2, Prediction_2, Prediction
  or or_2 (or_2_out, Load_Use, register_1_q);
  Hex_Digit_Display hex_digit_display_8 (.value(LedData[3:0]));  // open: dp
  \源寄存器使用情况  \u_源寄存器使用情况_1  (
    .OP0(if_id_1_ir_2[0]), .OP1(if_id_1_ir_2[1]), .OP2(if_id_1_ir_2[2]), .OP3(if_id_1_ir_2[3]),
    .OP4(if_id_1_ir_2[4]), .OP5(if_id_1_ir_2[5]), .F0(if_id_1_ir_2[6]), .F1(if_id_1_ir_2[7]),
    .F2(if_id_1_ir_2[8]), .F3(if_id_1_ir_2[9]), .F4(if_id_1_ir_2[10]), .F5(if_id_1_ir_2[11]),
    .R1_Used(\源寄存器使用情况_1_r1_used ), .R2_Used(\源寄存器使用情况_1_r2_used ));
  // Probe on \总周期数 
  \数据相关检测  \u_数据相关检测_1  (
    .R1_Used(\源寄存器使用情况_1_r1_used ), .R2_Used(\源寄存器使用情况_1_r2_used ), .ID_R1_num(multiplexer_2_out),
    .ID_R2_num(multiplexer_3_out), .EX_WriteReg_num(id_ex_1_regwrite_4),
    .MEM_WriteReg_num(ex_mem_1_regwrite_4), .EX_RegWrite(id_ex_1_regwrite_3),
    .MEM__RegWrite(ex_mem_1_regwrite_3), .EX_MemToReg(id_ex_1_memtoreg_2),
    .MEM_MemToReg(ex_mem_1_memtoreg_2), .Forward1(\数据相关检测_1_forward1 ), .Forward2(\数据相关检测_1_forward2 ),
    .Load_Use(Load_Use));  // open: 数据相关
  or or_3 (or_3_out, Load_Use, Clear);
  // Probe on \总周期数 
  // Probe on \无条件分支数 
  // Probe on \条件分支成功数 
  // Probe on \LoadUse次数 
  // Probe on \LoadUse次数 
  Multiplexer #(.select(1), .width(5), .disabled("Z"), .enable("false")) multiplexer_2 (
    .in0(if_id_1_ir_2_2[25:21]), .in1(5'b00100), .out(multiplexer_2_out), .sel(\n27_4条扩展指令控制器_1_syscall ));
  Multiplexer #(.select(1), .width(5), .disabled("Z"), .enable("false")) multiplexer_3 (
    .in0(if_id_1_ir_2_2[20:16]), .in1(5'b00010), .out(multiplexer_3_out), .sel(\n27_4条扩展指令控制器_1_syscall ));
  Multiplexer #(.select(1), .width(5), .disabled("Z"), .enable("false")) multiplexer_4 (
    .in0(if_id_1_ir_2_2[20:16]), .in1(if_id_1_ir_2_2[15:11]), .out(multiplexer_4_out),
    .sel(\n27_4条扩展指令控制器_1_regdst ));
  assign bit_extender_1_out = {{16{1'b0}}, {if_id_1_ir_2_2[15:6], if_id_1_ir_2[11:6]}};  // Bit_Extender bit_extender_1
  assign bit_extender_2_out = {{16{if_id_1_ir_2_2[15]}}, {if_id_1_ir_2_2[15:6], if_id_1_ir_2[11:6]}};  // Bit_Extender bit_extender_2
  assign bit_extender_3_out = {{6{if_id_1_ir_2_2[25]}}, {if_id_1_ir_2_2, if_id_1_ir_2[11:6]}};  // Bit_Extender bit_extender_3
  // Probe on IF_PC[11:0]
  \_27_4条扩展指令控制器  \u_27_4条扩展指令控制器_1  (
    .OP(if_id_1_ir_2[5:0]), .Func(if_id_1_ir_2[11:6]), .ALU_OP(\n27_4条扩展指令控制器_1_alu_op ),
    .MemToReg(\n27_4条扩展指令控制器_1_memtoreg ), .MemWrite(\n27_4条扩展指令控制器_1_memwrite ),
    .ALU_SRC(\n27_4条扩展指令控制器_1_alu_src ), .SysCALL(\n27_4条扩展指令控制器_1_syscall ),
    .SignedExt(\n27_4条扩展指令控制器_1_signedext ), .RegDst(\n27_4条扩展指令控制器_1_regdst ), .Beq(\n27_4条扩展指令控制器_1_beq ),
    .Bne(\n27_4条扩展指令控制器_1_bne ), .JR(\n27_4条扩展指令控制器_1_jr ), .JMP(\n27_4条扩展指令控制器_1_jmp ),
    .JAL(\n27_4条扩展指令控制器_1_jal ), .LUI(\n27_4条扩展指令控制器_1_lui ), .LBU(\n27_4条扩展指令控制器_1_lbu ),
    .BGEZ(\n27_4条扩展指令控制器_1_bgez ), .MTC0(\n27_4条扩展指令控制器_1_mtc0 ), .MFMT(if_id_1_ir_2_2[25:21]),
    .ERET(\n27_4条扩展指令控制器_1_eret ), .MFC0(\n27_4条扩展指令控制器_1_mfc0 ), .RegWrite(\n27_4条扩展指令控制器_1_regwrite ));
  // Probe on multiplexer_2_out
  // Probe on multiplexer_3_out
  Multiplexer #(.select(1), .width(5), .disabled("Z"), .enable("false")) multiplexer_5 (
    .in0(multiplexer_4_out), .in1({5{1'b1}}), .out(multiplexer_5_out), .sel(\n27_4条扩展指令控制器_1_jal ));
  // Probe on EX_PC[11:0]
  // Probe on ID_PC[11:0]
  Multiplexer #(.select(1), .width(32), .disabled("Z"), .enable("false")) multiplexer_6 (
    .in0(bit_extender_1_out), .in1(bit_extender_2_out), .out(multiplexer_6_out),
    .sel(\n27_4条扩展指令控制器_1_signedext ));
  // Probe on M_PC[11:0]
  MIPS_Regifile mips_regifile_1 (
    .Din(RDin), .Clk(CLK), .R1(mips_regifile_1_r1), .R2(mips_regifile_1_r2), .WE(RegWrite),
    .W_num(mem_wb_1_regwrite_4), .R1_num(multiplexer_2_out), .R2_num(multiplexer_3_out));
  // Probe on WB_PC[11:0]
  ID_EX id_ex_1 (
    .MemToReg(\n27_4条扩展指令控制器_1_memtoreg ), .LUI(\n27_4条扩展指令控制器_1_lui ), .MFC0(\n27_4条扩展指令控制器_1_mfc0 ),
    .LBU(\n27_4条扩展指令控制器_1_lbu ), .MemWrite(\n27_4条扩展指令控制器_1_memwrite ), .AluOP(\n27_4条扩展指令控制器_1_alu_op ),
    .MTC0(\n27_4条扩展指令控制器_1_mtc0 ), .Beq(\n27_4条扩展指令控制器_1_beq ), .Bgez(\n27_4条扩展指令控制器_1_bgez ),
    .Bne(\n27_4条扩展指令控制器_1_bne ), .JMP(\n27_4条扩展指令控制器_1_jmp ), .A(mips_regifile_1_r1), .B(mips_regifile_1_r2),
    .ImmExt16(multiplexer_6_out), .\ImmZeroExt16_用于LUI指令 (bit_extender_1_out),
    .ImmSignedExt26(bit_extender_3_out), .IR({if_id_1_ir_2[5:0], if_id_1_ir_2_2, if_id_1_ir_2[11:6]}),
    .\传输状态In_表明当前传输数据有效 (\if_id_1_传输状态out_表明当前传输数据有效 ), .CLK(CLK), .MemToReg_2(id_ex_1_memtoreg_2),
    .LUI_2(id_ex_1_lui_2), .MFC0_2(id_ex_1_mfc0_2), .JAL_2(id_ex_1_jal_2), .LBU_2(id_ex_1_lbu_2),
    .MemWrite_2(id_ex_1_memwrite_2), .AluOP_2(id_ex_1_aluop_2), .AluSrc_2(id_ex_1_alusrc_2),
    .Beq_2(id_ex_1_beq_2), .Bgez_2(id_ex_1_bgez_2), .Bne_2(id_ex_1_bne_2), .JMP_2(id_ex_1_jmp_2),
    .A_2(id_ex_1_a_2), .B_2(id_ex_1_b_2), .ImmExt16_2(id_ex_1_immext16_2),
    .\ImmZeroExt16_用于LUI指令_2 (\id_ex_1_immzeroext16_用于lui指令_2 ), .ImmSignedExt26_2(id_ex_1_immsignedext26_2),
    .IR_2(id_ex_1_ir_2), .\传输状态Out_表明当前传输数据有效 (\id_ex_1_传输状态out_表明当前传输数据有效 ), .\同步清零_气泡_高电平有效 (or_3_out),
    .\使能端_低电平有效_stall_高电平有效 (register_1_q), .ERET(\n27_4条扩展指令控制器_1_eret ), .ERET_2(id_ex_1_eret_2),
    .Syscall(\n27_4条扩展指令控制器_1_syscall ), .Syscall_2(id_ex_1_syscall_2), .PC(ID_PC), .PC_2(EX_PC),
    .PC_4_2(id_ex_1_pc_4_2), .PC_4(if_id_1_pc_4_2), .RegWrite_3(id_ex_1_regwrite_3),
    .RegWrite_2(multiplexer_5_out), .RegWrite_4(id_ex_1_regwrite_4), .AluSrc(\n27_4条扩展指令控制器_1_alu_src ),
    .RegWrite(\n27_4条扩展指令控制器_1_regwrite ), .JAL(\n27_4条扩展指令控制器_1_jal ), .JR(\n27_4条扩展指令控制器_1_jr ),
    .JR_2(id_ex_1_jr_2), .forwar1(\数据相关检测_1_forward1 ), .forward1(id_ex_1_forward1),
    .forward2(\数据相关检测_1_forward2 ), .forward2_2(id_ex_1_forward2_2));  // open: MTC0_2, rd, rd_2, prediction, prediction_2, Miss, Miss_2, Hit, Hit_2, DesAddr, DesAddr_2
  not not_4 (ExNotStop, and_4_out);
  and and_4 (and_4_out, id_ex_1_syscall_2, not_5_out);
  Comparator #(.width(32), .mode("twosComplement")) comparator_1 (
    .a(32'h22), .b(multiplexer_8_out), .eq(comparator_1_eq));  // open: gt, lt
  not not_5 (not_5_out, comparator_1_eq);
  and and_5 (and_5_out, id_ex_1_syscall_2, comparator_1_eq);
  Multiplexer #(.select(2), .width(32), .disabled("Z"), .enable("false")) multiplexer_7 (
    .in0(id_ex_1_a_2), .in1(multiplexer_14_out), .in2(mem_wb_1_alu_2), .in3(multiplexer_16_out),
    .out(multiplexer_7_out), .sel(id_ex_1_forward1));
  Multiplexer #(.select(2), .width(32), .disabled("Z"), .enable("false")) multiplexer_8 (
    .in0(id_ex_1_b_2), .in1(multiplexer_14_out), .in2(mem_wb_1_alu_2), .in3(multiplexer_16_out),
    .out(multiplexer_8_out), .sel(id_ex_1_forward2_2));
  Multiplexer #(.select(1), .width(32), .disabled("Z"), .enable("false")) multiplexer_9 (
    .in0(multiplexer_8_out), .in1(id_ex_1_immext16_2), .out(multiplexer_9_out), .sel(id_ex_1_alusrc_2));
  Multiplexer #(.select(1), .width(32), .disabled("Z"), .enable("false")) multiplexer_10 (
    .in0(multiplexer_9_out), .in1({32{1'b0}}), .out(multiplexer_10_out), .sel(id_ex_1_bgez_2));
  Shifter #(.width(32), .shift("ll")) shifter_1 (.in(id_ex_1_immext16_2), .\dist (5'b00010), .out(shifter_1_out));
  Shifter #(.width(32), .shift("ll")) shifter_2 (
    .in(\id_ex_1_immzeroext16_用于lui指令_2 ), .\dist (5'b10000), .out(shifter_2_out));
  Shifter #(.width(32), .shift("ll")) shifter_3 (.in(id_ex_1_immsignedext26_2), .\dist (5'b00010), .out(shifter_3_out));
  not not_6 (not_6_out, mips_alu_1_equal);
  not not_7 (not_7_out, mips_alu_1_result[0]);
  MIPS_ALU mips_alu_1 (
    .X(multiplexer_7_out), .Y(multiplexer_10_out), .AluOP(id_ex_1_aluop_2), .Equal(mips_alu_1_equal),
    .Result(mips_alu_1_result), .shamt(id_ex_1_ir_2[10:6]));  // open: Result_2
  Adder #(.width(32)) adder_2 (.a(shifter_1_out), .b(id_ex_1_pc_4_2), .out(adder_2_out));  // open: cin, cout
  and and_6 (and_6_out, not_6_out, id_ex_1_bne_2);
  and and_7 (and_7_out, not_7_out, id_ex_1_bgez_2);
  and and_8 (and_8_out, id_ex_1_beq_2, mips_alu_1_equal);
  Register #(.width(32), .trigger("rising"), .Select("low")) register_2 (
    .D(multiplexer_7_out), .en(and_5_out), .Q(register_2_q), .clk(CLK), .clr(RST));
  or or_4 (or_4_out, id_ex_1_jal_2, id_ex_1_jmp_2);
  or or_5 (ifjump, and_6_out, and_7_out, and_8_out);
  Multiplexer #(.select(1), .width(32), .disabled("Z"), .enable("false")) multiplexer_11 (
    .in0(id_ex_1_pc_4_2), .in1(adder_2_out), .out(multiplexer_11_out), .sel(ifjump));
  Multiplexer #(.select(1), .width(32), .disabled("Z"), .enable("false")) multiplexer_12 (
    .in0(multiplexer_11_out), .in1(shifter_3_out), .out(multiplexer_12_out), .sel(or_4_out));
  Multiplexer #(.select(1), .width(32), .disabled("Z"), .enable("false")) multiplexer_13 (
    .in0(multiplexer_12_out), .in1(multiplexer_7_out), .out(multiplexer_13_out), .sel(id_ex_1_jr_2));
  or or_6 (Clear, ifjump, id_ex_1_jr_2, or_4_out);
  or or_7 (nifjump, or_4_out, id_ex_1_jr_2);
  EX_MEM ex_mem_1 (
    .ERET(id_ex_1_eret_2), .Syscall(id_ex_1_syscall_2), .MemToReg(id_ex_1_memtoreg_2), .MFC0(id_ex_1_mfc0_2),
    .JAL(id_ex_1_jal_2), .LBU(id_ex_1_lbu_2), .B(multiplexer_8_out), .ALU(mips_alu_1_result),
    .IR(id_ex_1_ir_2), .PC(EX_PC), .\传输状态In_表明当前传输数据有效 (\id_ex_1_传输状态out_表明当前传输数据有效 ), .CLK(CLK),
    .ERET_2(ex_mem_1_eret_2), .Syscall_2(ex_mem_1_syscall_2), .MemToReg_2(ex_mem_1_memtoreg_2),
    .LUI_2(ex_mem_1_lui_2), .MFC0_2(ex_mem_1_mfc0_2), .JAL_2(ex_mem_1_jal_2), .LBU_2(ex_mem_1_lbu_2),
    .B_2(MDin), .ALU_2(ex_mem_1_alu_2), .IR_2(ex_mem_1_ir_2), .PC_2(M_PC),
    .\传输状态Out_表明当前传输数据有效 (\ex_mem_1_传输状态out_表明当前传输数据有效 ), .\同步清零_气泡_高电平有效 (1'b0),
    .\使能端_低电平有效_stall_高电平有效 (register_1_q), .PC_4(id_ex_1_pc_4_2), .PC_4_2(ex_mem_1_pc_4_2),
    .MemWrite(id_ex_1_memwrite_2), .MemWrite_2(MemWrite), .RegWrite_2(id_ex_1_regwrite_4),
    .RegWrite_4(ex_mem_1_regwrite_4), .RegWrite(id_ex_1_regwrite_3), .RegWrite_3(ex_mem_1_regwrite_3),
    .ImmZeroExt16Shift(shifter_2_out), .ImmZeroExt16Shift_2(ex_mem_1_immzeroext16shift_2),
    .ifshow(comparator_1_eq), .ifshow_2(ex_mem_1_ifshow_2), .LedData(register_2_q),
    .LeaData(ex_mem_1_leadata), .LUI(id_ex_1_lui_2));  // open: rd, rd_2, MTC0, MTC0_2, IRout, IRout_2
  not not_8 (not_8_out, ex_mem_1_ifshow_2);
  not not_9 (MemNotStop, and_9_out);
  and and_9 (and_9_out, ex_mem_1_syscall_2, not_8_out);
  Multiplexer #(.select(1), .width(32), .disabled("Z"), .enable("false")) multiplexer_14 (
    .in0(ex_mem_1_alu_2), .in1(ex_mem_1_immzeroext16shift_2), .out(multiplexer_14_out), .sel(ex_mem_1_lui_2));
  RAM #(.addrWidth(10), .dataWidth(32), .bus("separate"), .Select("high")) ram_1 (
    .addr(ex_mem_1_alu_2[11:2]), .din(MDin), .data(ram_1_data), .str(MemWrite), .clk(CLK), .clr(RST));  // open: sel, ld
  MEM_WB mem_wb_1 (
    .ERET(ex_mem_1_eret_2), .Syscall(ex_mem_1_syscall_2), .MemToReg(ex_mem_1_memtoreg_2),
    .LUI(ex_mem_1_lui_2), .MFC0(ex_mem_1_mfc0_2), .JAL(ex_mem_1_jal_2), .ALU(ex_mem_1_alu_2),
    .MD(ram_1_data), .IR(ex_mem_1_ir_2), .PC(M_PC), .PC_4(ex_mem_1_pc_4_2),
    .\传输状态In_表明当前传输数据有效 (\ex_mem_1_传输状态out_表明当前传输数据有效 ), .CLK(CLK), .Syscall_2(mem_wb_1_syscall_2),
    .MemToReg_2(mem_wb_1_memtoreg_2), .JAL_2(mem_wb_1_jal_2), .ALU_2(mem_wb_1_alu_2), .MD_2(mem_wb_1_md_2),
    .PC_2(WB_PC), .PC_4_2(mem_wb_1_pc_4_2), .\同步清零_气泡_高电平有效 (1'b0), .\使能端_低电平有效_stall_高电平有效 (register_1_q),
    .LBU(ex_mem_1_lbu_2), .LBU_2(mem_wb_1_lbu_2), .ImmZeroExt16Shift(ex_mem_1_immzeroext16shift_2),
    .ImmZeroExt16Shift_2(mem_wb_1_immzeroext16shift_2), .RegWrite(ex_mem_1_regwrite_3),
    .RegWrite_3(RegWrite), .RegWrite_2(ex_mem_1_regwrite_4), .RegWrite_4(mem_wb_1_regwrite_4),
    .ifshow_2(mem_wb_1_ifshow_2), .ifshow(ex_mem_1_ifshow_2), .LedData(ex_mem_1_leadata),
    .LedData_2(LedData), .LUI_2(mem_wb_1_lui_2));  // open: ERET_2, MFC0_2, IR_2, 传输状态Out_表明当前传输数据有效, rd, rd_2, MTC0, MTC0_2, IRout, IRout_2
  Multiplexer #(.select(1), .width(32), .disabled("Z"), .enable("false")) multiplexer_15 (
    .in0(mem_wb_1_alu_2), .in1(multiplexer_16_out), .out(multiplexer_15_out), .sel(mem_wb_1_memtoreg_2));
  Multiplexer #(.select(1), .width(32), .disabled("Z"), .enable("false")) multiplexer_16 (
    .in0(mem_wb_1_md_2), .in1({{24{1'b0}}, mem_wb_1_md_2[7:0]}), .out(multiplexer_16_out),
    .sel(mem_wb_1_lbu_2));
  Multiplexer #(.select(1), .width(32), .disabled("Z"), .enable("false")) multiplexer_17 (
    .in0(multiplexer_15_out), .in1(mem_wb_1_immzeroext16shift_2), .out(multiplexer_17_out),
    .sel(mem_wb_1_lui_2));
  Multiplexer #(.select(1), .width(32), .disabled("Z"), .enable("false")) multiplexer_18 (
    .in0(multiplexer_17_out), .in1(mem_wb_1_pc_4_2), .out(RDin), .sel(mem_wb_1_jal_2));

  // Other names for the same wires on the sheet: MEM_PC[31:0] = M_PC; 插入气泡数[15:0] = \LoadUse次数 

  // Notes on the sheet:
  //   中断源
  //   中断等待指示
  //   指令存储器
  //   数码管输出
  //   指令字
  //   contents of rom_1 (hex, n*v repeats v):
  //   20110001 8100005 20110001 20120002 20130003 8100009 20110001 20120002 20130003 810000d 20110001
  //   20120002 20130003 8100011 20110001 20120002 20130003 c1000fc 20100001 20110001 118fc0 112020
  //   20020022 c 118882 12200001 8100015 112020 20020022 c 20110001 118880 112020 20020022 c 12200001
  //   810001f 20110001 118fc0 112020 20020022 c 1188c3 112020 20020022 c 118903 112020 20020022 c 118903
  //   112020 20020022 c 118903 112020 20020022 c 118903 112020 20020022 c 118903 112020 20020022 c 118903
  //   112020 20020022 c 118903 112020 20020022 c 20100001 109fc0 139fc3 8021 2012000c 24160003 26100001
  //   3210000f 20080008 20090001 139900 2709825 132020 20020022 c 1094022 1500fff9 22100001 2018000f
  //   2188024 108700 20080008 20090001 139902 2709825 132021 20020022 c 1094022 1500fff9 108702 2c9b022
  //   12c00001 8100050 4020 1084027 84400 3508ffff 82021 20020022 c 2010ffff 20110000 ae300000 22100001
  //   22310004 ae300000 22100001 22310004 ae300000 22100001 22310004 ae300000 22100001 22310004 ae300000
  //   22100001 22310004 ae300000 22100001 22310004 ae300000 22100001 22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
  //   OP
  //   Func
  //   rs
  //   rt
  //   rd
  //   MF/MT
  //   JMP
  //   JR
  //   SignedExt
  //   LUI
  //   LBU
  //   MFC0
  //   MTC0
  //   OP
  //   Func
  //   MF/MT
  //   Syscall
  //   Beq
  //   Bgez
  //   Bne
  //   MemToReg
  //   MemWrite
  //   AluOP
  //   AluSrcB
  //   RegWrite
  //   JAL
  //   RegDst
  //   ERET
  //   流水调试日志用
  //   为方便自动评测，需要输出流水线各段保存的PC值，注意是PC不是PC+4，另外ID段寄存器写入信息，Mem段内存写入信息也要输出
  //   数据存储器
endmodule

module \动态分支预测  (
  output RegWrite,
  output MemWrite,
  output [31:0] IF_PC,
  output [31:0] ID_PC,
  output [31:0] EX_PC,
  output [31:0] M_PC,
  output [31:0] WB_PC,
  output [31:0] RDin,
  output [31:0] MDin,
  output [31:0] LedData
);

  wire and_2_out, and_3_out, and_4_out, and_5_out, and_6_out, and_7_out, and_8_out, and_9_out, and_10_out,
       and_11_out, Clear, CLK, comparator_1_eq, ex_mem_1_eret_2, ex_mem_1_ifshow_2, ex_mem_1_jal_2,
       ex_mem_1_lbu_2, ex_mem_1_lui_2, ex_mem_1_memtoreg_2, ex_mem_1_mfc0_2, ex_mem_1_regwrite_3,
       ex_mem_1_syscall_2, \ex_mem_1_传输状态out_表明当前传输数据有效 , ExNotStop, fail, Go, hit, id_ex_1_alusrc_2,
       id_ex_1_beq_2, id_ex_1_bgez_2, id_ex_1_bne_2, id_ex_1_eret_2, id_ex_1_jal_2, id_ex_1_jmp_2,
       id_ex_1_jr_2, id_ex_1_lbu_2, id_ex_1_lui_2, id_ex_1_memtoreg_2, id_ex_1_memwrite_2, id_ex_1_mfc0_2,
       id_ex_1_miss_2, id_ex_1_regwrite_3, id_ex_1_syscall_2, \id_ex_1_传输状态out_表明当前传输数据有效 , if_id_1_hit_2,
       if_id_1_miss_2, \if_id_1_传输状态out_表明当前传输数据有效 , ifjump, IR1, IR2, IR3, jfail, Load_Use,
       mem_wb_1_ifshow_2, mem_wb_1_jal_2, mem_wb_1_lbu_2, mem_wb_1_lui_2, mem_wb_1_memtoreg_2,
       mem_wb_1_syscall_2, MemNotStop, mips_alu_1_equal, \n27_4条扩展指令控制器_1_alu_src , \n27_4条扩展指令控制器_1_beq ,
       \n27_4条扩展指令控制器_1_bgez , \n27_4条扩展指令控制器_1_bne , \n27_4条扩展指令控制器_1_eret , \n27_4条扩展指令控制器_1_jal ,
       \n27_4条扩展指令控制器_1_jmp , \n27_4条扩展指令控制器_1_jr , \n27_4条扩展指令控制器_1_lbu , \n27_4条扩展指令控制器_1_lui ,
       \n27_4条扩展指令控制器_1_memtoreg , \n27_4条扩展指令控制器_1_memwrite , \n27_4条扩展指令控制器_1_mfc0 ,
       \n27_4条扩展指令控制器_1_mtc0 , \n27_4条扩展指令控制器_1_regdst , \n27_4条扩展指令控制器_1_regwrite ,
       \n27_4条扩展指令控制器_1_signedext , \n27_4条扩展指令控制器_1_syscall , nifjump, not_1_out, not_2_out, not_3_out,
       not_4_out, not_6_out, not_7_out, not_8_out, not_9_out, or_1_out, or_2_out, or_3_out, or_4_out,
       register_1_q, RST, W1, W2, W3, \全相联bht_1_miss , \全相联bht_1_predictjmp , \源寄存器使用情况_1_r1_used ,
       \源寄存器使用情况_1_r2_used ;
  wire [1:0] id_ex_1_forward1, id_ex_1_forward2_2, id_ex_1_prediction_2, if_id_1_prediction_2,
       multiplexer_4_out, \全相联bht_1_predata , \数据相关检测_1_forward1 , \数据相关检测_1_forward2 ,
       \预测状态逻辑转换_1_afterstatus0 ;
  wire [3:0] id_ex_1_aluop_2, \n27_4条扩展指令控制器_1_alu_op ;
  wire [4:0] ex_mem_1_regwrite_4, id_ex_1_ir_2_2, id_ex_1_regwrite_4, mem_wb_1_regwrite_4, multiplexer_5_out,
       multiplexer_6_out, multiplexer_7_out, multiplexer_8_out;
  wire [11:0] if_id_1_ir_2;
  wire [15:0] counter_3_q, \LoadUse次数 , \总周期数 , \无条件分支数 , \条件分支成功数 , \预测失败次数 , \预测成功次数 ;
  wire [25:6] if_id_1_ir_2_2;
  wire [31:0] adder_1_out, adder_2_out, bit_extender_1_out, bit_extender_2_out, bit_extender_3_out,
       ex_mem_1_alu_2, ex_mem_1_immzeroext16shift_2, ex_mem_1_ir_2, ex_mem_1_leadata, ex_mem_1_pc_4_2,
       id_ex_1_a_2, id_ex_1_b_2, id_ex_1_desaddr_2, id_ex_1_immext16_2, id_ex_1_immsignedext26_2,
       \id_ex_1_immzeroext16_用于lui指令_2 , id_ex_1_ir_2, id_ex_1_pc_4_2, if_id_1_desaddr_2, if_id_1_pc_4_2,
       mem_wb_1_alu_2, mem_wb_1_immzeroext16shift_2, mem_wb_1_md_2, mem_wb_1_pc_4_2, mips_alu_1_result,
       mips_regifile_1_r1, mips_regifile_1_r2, multiplexer_1_out, multiplexer_2_out, multiplexer_3_out,
       multiplexer_9_out, multiplexer_10_out, multiplexer_11_out, multiplexer_12_out, multiplexer_13_out,
       multiplexer_14_out, multiplexer_15_out, multiplexer_16_out, multiplexer_17_out, multiplexer_18_out,
       multiplexer_19_out, multiplexer_20_out, multiplexer_21_out, ram_1_data, register_2_q, rom_1_data,
       shifter_1_out, shifter_2_out, shifter_3_out, \全相联bht_1_desdata ;

  Button \u_总复位  (.out(RST));
  Button _1 (.out(IR1));
  Button _2 (.out(IR2));
  Button _3 (.out(IR3));
  Button \u_继续运行  (.out(Go));
  LED #(.active("true")) led_1 (.in(W1));
  LED #(.active("true")) led_2 (.in(W2));
  LED #(.active("true")) led_3 (.in(W3));
  Hex_Digit_Display hex_digit_display_1 (.value(LedData[31:28]));  // open: dp
  Counter #(.width(16), .max('hffff), .ongoal("wrap"), .trigger("rising"), .behavior("old")) counter_1 (
    .count(jfail), .Q(\预测失败次数 ), .clk(CLK), .clr(RST));  // open: load, D, carry, preset
  Counter #(.width(16), .max('hffff), .ongoal("wrap"), .trigger("rising"), .behavior("old")) counter_2 (
    .count(nifjump), .Q(\无条件分支数 ), .clk(CLK), .clr(RST));  // open: load, D, carry, preset
  and and_1 (jfail, hit, fail);
  Multiplexer #(.select(1), .width(32), .disabled("Z"), .enable("false")) multiplexer_1 (
    .in0(multiplexer_2_out), .in1(multiplexer_3_out), .out(multiplexer_1_out), .sel(fail));
  Hex_Digit_Display hex_digit_display_2 (.value(LedData[23:20]));  // open: dp
  Hex_Digit_Display hex_digit_display_3 (.value(LedData[27:24]));  // open: dp
  \全相联BHT  \u_全相联bht_1  (
    .PRE(\预测状态逻辑转换_1_afterstatus0 ), .update(and_7_out), .IF_PC(IF_PC), .EX_PC(EX_PC),
    .DES(multiplexer_17_out), .CLK(CLK), .ex_hit(hit), .Miss(\全相联bht_1_miss ), .DesData(\全相联bht_1_desdata ),
    .PreData(\全相联bht_1_predata ), .PredictJmp(\全相联bht_1_predictjmp ));
  and and_2 (and_2_out, MemNotStop, ExNotStop, Load_Use, not_1_out);
  Register #(.width(32), .trigger("rising"), .Select("low")) PC (
    .D(multiplexer_1_out), .en(and_3_out), .Q(IF_PC), .clk(CLK), .clr(RST));
  Multiplexer #(.select(1), .width(32), .disabled("Z"), .enable("false")) multiplexer_2 (
    .in0(adder_1_out), .in1(\全相联bht_1_desdata ), .out(multiplexer_2_out), .sel(\全相联bht_1_predictjmp ));
  Hex_Digit_Display hex_digit_display_4 (.value(LedData[19:16]));  // open: dp
  Hex_Digit_Display hex_digit_display_5 (.value(LedData[15:12]));  // open: dp
  \预测状态逻辑转换  \u_预测状态逻辑转换_1  (
    .jmp(Clear), .AfterStatus1(\预测状态逻辑转换_1_afterstatus0 [1]), .PreStatus1(id_ex_1_prediction_2[1]),
    .PreStatus0(id_ex_1_prediction_2[0]), .AfterStatus0(\预测状态逻辑转换_1_afterstatus0 [0]), .fail(fail));
  Counter #(.width(16), .max('hffff), .ongoal("wrap"), .trigger("rising"), .behavior("old")) counter_3 (
    .count(hit), .Q(counter_3_q), .clk(CLK), .clr(RST));  // open: load, D, carry, preset
  Counter #(.width(16), .max('hffff), .ongoal("wrap"), .trigger("rising"), .behavior("old")) counter_4 (
    .count(and_2_out), .Q(\LoadUse次数 ), .clk(CLK), .clr(RST));  // open: load, D, carry, preset
  Adder #(.width(32)) adder_1 (.a(IF_PC), .b(32'h4), .out(adder_1_out));  // open: cin, cout
  and and_3 (and_3_out, not_3_out, not_1_out);
  Register #(.width(1), .trigger("rising"), .Select("low")) register_1 (
    .D(mem_wb_1_syscall_2), .en(and_4_out), .Q(register_1_q), .clk(CLK), .clr(or_1_out));
  not not_1 (not_1_out, register_1_q);
  or or_1 (or_1_out, RST, Go);
  Counter #(.width(16), .max('hffff), .ongoal("wrap"), .trigger("rising"), .behavior("old")) counter_5 (
    .count(not_1_out), .Q(\总周期数 ), .clk(CLK), .clr(RST));  // open: load, D, carry, preset
  Multiplexer #(.select(1), .width(32), .disabled("Z"), .enable("false")) multiplexer_3 (
    .in0(id_ex_1_pc_4_2), .in1(multiplexer_17_out), .out(multiplexer_3_out), .sel(Clear));
  not not_2 (not_2_out, mem_wb_1_ifshow_2);
  and and_4 (and_4_out, not_2_out, mem_wb_1_syscall_2);
  Hex_Digit_Display hex_digit_display_6 (.value(LedData[11:8]));  // open: dp
  Hex_Digit_Display hex_digit_display_7 (.value(LedData[7:4]));  // open: dp
  Clock #(.highDuration(1), .lowDuration(1)) clock_1 (.out(CLK));
  Subtractor #(.width(16)) subtractor_1 (.a(counter_3_q), .b(\预测失败次数 ), .out(\预测成功次数 ));  // open: bin, bout
  Counter #(.width(16), .max('hffff), .ongoal("wrap"), .trigger("rising"), .behavior("old")) counter_6 (
    .count(ifjump), .Q(\条件分支成功数 ), .clk(CLK), .clr(RST));  // open: load, D, carry, preset
  ROM #(.addrWidth(10), .dataWidth(32), .Select("high")) rom_1 (.addr(IF_PC[11:2]), .data(rom_1_data));
  Hex_Digit_Display hex_digit_display_8 (.value(LedData[3:0]));  // open: dp
  not not_3 (not_3_out, Load_Use);
  or or_2 (or_2_out, Load_Use, register_1_q);
  // Probe on \总周期数 
  Multiplexer #(.select(1), .width(2), .disabled("Z"), .enable("false")) multiplexer_4 (
    .in0(\全相联bht_1_predata ), .in1(2'b01), .out(multiplexer_4_out), .sel(\全相联bht_1_miss ));
  not not_4 (not_4_out, \全相联bht_1_miss );
  // Probe on \总周期数 
  // Probe on \无条件分支数 
  // Probe on \条件分支成功数 
  // Probe on \LoadUse次数 
  // Probe on \LoadUse次数 
  // Probe on \预测成功次数 
  // Probe on \预测失败次数 
  \源寄存器使用情况  \u_源寄存器使用情况_1  (
    .OP0(if_id_1_ir_2[0]), .OP1(if_id_1_ir_2[1]), .OP2(if_id_1_ir_2[2]), .OP3(if_id_1_ir_2[3]),
    .OP4(if_id_1_ir_2[4]), .OP5(if_id_1_ir_2[5]), .F0(if_id_1_ir_2[6]), .F1(if_id_1_ir_2[7]),
    .F2(if_id_1_ir_2[8]), .F3(if_id_1_ir_2[9]), .F4(if_id_1_ir_2[10]), .F5(if_id_1_ir_2[11]),
    .R1_Used(\源寄存器使用情况_1_r1_used ), .R2_Used(\源寄存器使用情况_1_r2_used ));
  IF_ID if_id_1 (
    .IR(rom_1_data), .PC_4(adder_1_out), .\传输状态In_表明当前传输数据有效 (1'b1), .CLK(CLK),
    .IR_2({if_id_1_ir_2[5:0], if_id_1_ir_2_2, if_id_1_ir_2[11:6]}), .PC_4_2(if_id_1_pc_4_2),
    .\传输状态Out_表明当前传输数据有效 (\if_id_1_传输状态out_表明当前传输数据有效 ), .\同步清零_气泡_高电平有效 (fail),
    .\使能端_低电平有效_stall_高电平有效 (or_2_out), .PC(IF_PC), .PC_2(ID_PC), .DesAddr(\全相联bht_1_desdata ),
    .DesAddr_2(if_id_1_desaddr_2), .Miss(\全相联bht_1_miss ), .Miss_2(if_id_1_miss_2), .Hit(not_4_out),
    .Hit_2(if_id_1_hit_2), .Prediction_2(if_id_1_prediction_2), .Prediction(multiplexer_4_out));
  // Probe on IF_PC[11:0]
  \数据相关检测  \u_数据相关检测_1  (
    .R1_Used(\源寄存器使用情况_1_r1_used ), .R2_Used(\源寄存器使用情况_1_r2_used ), .ID_R1_num(multiplexer_5_out),
    .ID_R2_num(multiplexer_6_out), .EX_WriteReg_num(id_ex_1_regwrite_4),
    .MEM_WriteReg_num(ex_mem_1_regwrite_4), .EX_RegWrite(id_ex_1_regwrite_3),
    .MEM__RegWrite(ex_mem_1_regwrite_3), .EX_MemToReg(id_ex_1_memtoreg_2),
    .MEM_MemToReg(ex_mem_1_memtoreg_2), .Forward1(\数据相关检测_1_forward1 ), .Forward2(\数据相关检测_1_forward2 ),
    .Load_Use(Load_Use));  // open: 数据相关
  // Probe on ID_PC[11:0]
  // Probe on EX_PC[11:0]
  or or_3 (or_3_out, Load_Use, fail);
  Multiplexer #(.select(1), .width(5), .disabled("Z"), .enable("false")) multiplexer_5 (
    .in0(if_id_1_ir_2_2[25:21]), .in1(5'b00100), .out(multiplexer_5_out), .sel(\n27_4条扩展指令控制器_1_syscall ));
  Multiplexer #(.select(1), .width(5), .disabled("Z"), .enable("false")) multiplexer_6 (
    .in0(if_id_1_ir_2_2[20:16]), .in1(5'b00010), .out(multiplexer_6_out), .sel(\n27_4条扩展指令控制器_1_syscall ));
  Multiplexer #(.select(1), .width(5), .disabled("Z"), .enable("false")) multiplexer_7 (
    .in0(if_id_1_ir_2_2[20:16]), .in1(if_id_1_ir_2_2[15:11]), .out(multiplexer_7_out),
    .sel(\n27_4条扩展指令控制器_1_regdst ));
  assign bit_extender_1_out = {{16{1'b0}}, {if_id_1_ir_2_2[15:6], if_id_1_ir_2[11:6]}};  // Bit_Extender bit_extender_1
  assign bit_extender_2_out = {{16{if_id_1_ir_2_2[15]}}, {if_id_1_ir_2_2[15:6], if_id_1_ir_2[11:6]}};  // Bit_Extender bit_extender_2
  assign bit_extender_3_out = {{6{if_id_1_ir_2_2[25]}}, {if_id_1_ir_2_2, if_id_1_ir_2[11:6]}};  // Bit_Extender bit_extender_3
  // Probe on M_PC[11:0]
  \_27_4条扩展指令控制器  \u_27_4条扩展指令控制器_1  (
    .OP(if_id_1_ir_2[5:0]), .Func(if_id_1_ir_2[11:6]), .ALU_OP(\n27_4条扩展指令控制器_1_alu_op ),
    .MemToReg(\n27_4条扩展指令控制器_1_memtoreg ), .MemWrite(\n27_4条扩展指令控制器_1_memwrite ),
    .ALU_SRC(\n27_4条扩展指令控制器_1_alu_src ), .SysCALL(\n27_4条扩展指令控制器_1_syscall ),
    .SignedExt(\n27_4条扩展指令控制器_1_signedext ), .RegDst(\n27_4条扩展指令控制器_1_regdst ), .Beq(\n27_4条扩展指令控制器_1_beq ),
    .Bne(\n27_4条扩展指令控制器_1_bne ), .JR(\n27_4条扩展指令控制器_1_jr ), .JMP(\n27_4条扩展指令控制器_1_jmp ),
    .JAL(\n27_4条扩展指令控制器_1_jal ), .LUI(\n27_4条扩展指令控制器_1_lui ), .LBU(\n27_4条扩展指令控制器_1_lbu ),
    .BGEZ(\n27_4条扩展指令控制器_1_bgez ), .MTC0(\n27_4条扩展指令控制器_1_mtc0 ), .MFMT(if_id_1_ir_2_2[25:21]),
    .ERET(\n27_4条扩展指令控制器_1_eret ), .MFC0(\n27_4条扩展指令控制器_1_mfc0 ), .RegWrite(\n27_4条扩展指令控制器_1_regwrite ));
  Multiplexer #(.select(1), .width(5), .disabled("Z"), .enable("false")) multiplexer_8 (
    .in0(multiplexer_7_out), .in1({5{1'b1}}), .out(multiplexer_8_out), .sel(\n27_4条扩展指令控制器_1_jal ));
  // Probe on WB_PC[11:0]
  Multiplexer #(.select(1), .width(32), .disabled("Z"), .enable("false")) multiplexer_9 (
    .in0(bit_extender_1_out), .in1(bit_extender_2_out), .out(multiplexer_9_out),
    .sel(\n27_4条扩展指令控制器_1_signedext ));
  MIPS_Regifile mips_regifile_1 (
    .Din(RDin), .Clk(CLK), .R1(mips_regifile_1_r1), .R2(mips_regifile_1_r2), .WE(RegWrite),
    .W_num(mem_wb_1_regwrite_4), .R1_num(multiplexer_5_out), .R2_num(multiplexer_6_out));
  ID_EX id_ex_1 (
    .MemToReg(\n27_4条扩展指令控制器_1_memtoreg ), .LUI(\n27_4条扩展指令控制器_1_lui ), .MFC0(\n27_4条扩展指令控制器_1_mfc0 ),
    .LBU(\n27_4条扩展指令控制器_1_lbu ), .MemWrite(\n27_4条扩展指令控制器_1_memwrite ), .AluOP(\n27_4条扩展指令控制器_1_alu_op ),
    .MTC0(\n27_4条扩展指令控制器_1_mtc0 ), .Beq(\n27_4条扩展指令控制器_1_beq ), .Bgez(\n27_4条扩展指令控制器_1_bgez ),
    .Bne(\n27_4条扩展指令控制器_1_bne ), .JMP(\n27_4条扩展指令控制器_1_jmp ), .A(mips_regifile_1_r1), .B(mips_regifile_1_r2),
    .ImmExt16(multiplexer_9_out), .\ImmZeroExt16_用于LUI指令 (bit_extender_1_out),
    .ImmSignedExt26(bit_extender_3_out), .IR({if_id_1_ir_2[5:0], if_id_1_ir_2_2, if_id_1_ir_2[11:6]}),
    .\传输状态In_表明当前传输数据有效 (\if_id_1_传输状态out_表明当前传输数据有效 ), .CLK(CLK), .MemToReg_2(id_ex_1_memtoreg_2),
    .LUI_2(id_ex_1_lui_2), .MFC0_2(id_ex_1_mfc0_2), .JAL_2(id_ex_1_jal_2), .LBU_2(id_ex_1_lbu_2),
    .MemWrite_2(id_ex_1_memwrite_2), .AluOP_2(id_ex_1_aluop_2), .AluSrc_2(id_ex_1_alusrc_2),
    .Beq_2(id_ex_1_beq_2), .Bgez_2(id_ex_1_bgez_2), .Bne_2(id_ex_1_bne_2), .JMP_2(id_ex_1_jmp_2),
    .A_2(id_ex_1_a_2), .B_2(id_ex_1_b_2), .ImmExt16_2(id_ex_1_immext16_2),
    .\ImmZeroExt16_用于LUI指令_2 (\id_ex_1_immzeroext16_用于lui指令_2 ), .ImmSignedExt26_2(id_ex_1_immsignedext26_2),
    .IR_2({id_ex_1_ir_2[31:11], id_ex_1_ir_2_2, id_ex_1_ir_2[5:0]}),
    .\传输状态Out_表明当前传输数据有效 (\id_ex_1_传输状态out_表明当前传输数据有效 ), .\同步清零_气泡_高电平有效 (or_3_out),
    .\使能端_低电平有效_stall_高电平有效 (register_1_q), .ERET(\n27_4条扩展指令控制器_1_eret ), .ERET_2(id_ex_1_eret_2),
    .Syscall(\n27_4条扩展指令控制器_1_syscall ), .Syscall_2(id_ex_1_syscall_2), .PC(ID_PC), .PC_2(EX_PC),
    .PC_4_2(id_ex_1_pc_4_2), .PC_4(if_id_1_pc_4_2), .RegWrite_3(id_ex_1_regwrite_3),
    .RegWrite_2(multiplexer_8_out), .RegWrite_4(id_ex_1_regwrite_4), .AluSrc(\n27_4条扩展指令控制器_1_alu_src ),
    .RegWrite(\n27_4条扩展指令控制器_1_regwrite ), .JAL(\n27_4条扩展指令控制器_1_jal ), .JR(\n27_4条扩展指令控制器_1_jr ),
    .JR_2(id_ex_1_jr_2), .forwar1(\数据相关检测_1_forward1 ), .forward1(id_ex_1_forward1),
    .forward2(\数据相关检测_1_forward2 ), .forward2_2(id_ex_1_forward2_2), .prediction(if_id_1_prediction_2),
    .prediction_2(id_ex_1_prediction_2), .Miss(if_id_1_miss_2), .Miss_2(id_ex_1_miss_2), .Hit(if_id_1_hit_2),
    .Hit_2(hit), .DesAddr(if_id_1_desaddr_2), .DesAddr_2(id_ex_1_desaddr_2));  // open: MTC0_2, rd, rd_2
  and and_5 (and_5_out, id_ex_1_syscall_2, not_6_out);
  not not_5 (ExNotStop, and_5_out);
  not not_6 (not_6_out, comparator_1_eq);
  Comparator #(.width(32), .mode("twosComplement")) comparator_1 (
    .a(32'h22), .b(multiplexer_12_out), .eq(comparator_1_eq));  // open: gt, lt
  and and_6 (and_6_out, id_ex_1_syscall_2, comparator_1_eq);
  Multiplexer #(.select(2), .width(32), .disabled("Z"), .enable("false")) multiplexer_10 (
    .in0(id_ex_1_a_2), .in1(multiplexer_18_out), .in2(mem_wb_1_alu_2), .in3(multiplexer_19_out),
    .out(multiplexer_10_out), .sel(id_ex_1_forward1));
  Multiplexer #(.select(1), .width(32), .disabled("Z"), .enable("false")) multiplexer_11 (
    .in0(multiplexer_12_out), .in1(id_ex_1_immext16_2), .out(multiplexer_11_out), .sel(id_ex_1_alusrc_2));
  Multiplexer #(.select(2), .width(32), .disabled("Z"), .enable("false")) multiplexer_12 (
    .in0(id_ex_1_b_2), .in1(multiplexer_18_out), .in2(mem_wb_1_alu_2), .in3(multiplexer_19_out),
    .out(multiplexer_12_out), .sel(id_ex_1_forward2_2));
  Multiplexer #(.select(1), .width(32), .disabled("Z"), .enable("false")) multiplexer_13 (
    .in0(multiplexer_11_out), .in1({32{1'b0}}), .out(multiplexer_13_out), .sel(id_ex_1_bgez_2));
  Shifter #(.width(32), .shift("ll")) shifter_1 (.in(id_ex_1_immext16_2), .\dist (5'b00010), .out(shifter_1_out));
  Shifter #(.width(32), .shift("ll")) shifter_2 (
    .in(\id_ex_1_immzeroext16_用于lui指令_2 ), .\dist (5'b10000), .out(shifter_2_out));
  Shifter #(.width(32), .shift("ll")) shifter_3 (.in(id_ex_1_immsignedext26_2), .\dist (5'b00010), .out(shifter_3_out));
  and and_7 (and_7_out, id_ex_1_miss_2, Clear);
  MIPS_ALU mips_alu_1 (
    .X(multiplexer_10_out), .Y(multiplexer_13_out), .AluOP(id_ex_1_aluop_2), .Equal(mips_alu_1_equal),
    .Result(mips_alu_1_result), .shamt(id_ex_1_ir_2_2));  // open: Result_2
  not not_7 (not_7_out, mips_alu_1_equal);
  and and_8 (and_8_out, not_7_out, id_ex_1_bne_2);
  not not_8 (not_8_out, mips_alu_1_result[0]);
  and and_9 (and_9_out, not_8_out, id_ex_1_bgez_2);
  and and_10 (and_10_out, id_ex_1_beq_2, mips_alu_1_equal);
  Adder #(.width(32)) adder_2 (.a(shifter_1_out), .b(id_ex_1_pc_4_2), .out(adder_2_out));  // open: cin, cout
  Multiplexer #(.select(1), .width(32), .disabled("Z"), .enable("false")) multiplexer_14 (
    .in0(multiplexer_16_out), .in1(shifter_3_out), .out(multiplexer_14_out), .sel(or_4_out));
  or or_4 (or_4_out, id_ex_1_jal_2, id_ex_1_jmp_2);
  or or_5 (ifjump, and_8_out, and_9_out, and_10_out);
  Register #(.width(32), .trigger("rising"), .Select("low")) register_2 (
    .D(multiplexer_10_out), .en(and_6_out), .Q(register_2_q), .clk(CLK), .clr(RST));
  Multiplexer #(.select(1), .width(32), .disabled("Z"), .enable("false")) multiplexer_15 (
    .in0(multiplexer_14_out), .in1(multiplexer_10_out), .out(multiplexer_15_out), .sel(id_ex_1_jr_2));
  or or_6 (Clear, ifjump, id_ex_1_jr_2, or_4_out);
  or or_7 (nifjump, or_4_out, id_ex_1_jr_2);
  Multiplexer #(.select(1), .width(32), .disabled("Z"), .enable("false")) multiplexer_16 (
    .in0(id_ex_1_pc_4_2), .in1(adder_2_out), .out(multiplexer_16_out), .sel(ifjump));
  Multiplexer #(.select(1), .width(32), .disabled("Z"), .enable("false")) multiplexer_17 (
    .in0(id_ex_1_desaddr_2), .in1(multiplexer_15_out), .out(multiplexer_17_out), .sel(fail));
  EX_MEM ex_mem_1 (
    .ERET(id_ex_1_eret_2), .Syscall(id_ex_1_syscall_2), .MemToReg(id_ex_1_memtoreg_2), .MFC0(id_ex_1_mfc0_2),
    .JAL(id_ex_1_jal_2), .LBU(id_ex_1_lbu_2), .B(multiplexer_12_out), .ALU(mips_alu_1_result),
    .IR({id_ex_1_ir_2[31:11], id_ex_1_ir_2_2, id_ex_1_ir_2[5:0]}), .PC(EX_PC),
    .\传输状态In_表明当前传输数据有效 (\id_ex_1_传输状态out_表明当前传输数据有效 ), .CLK(CLK), .ERET_2(ex_mem_1_eret_2),
    .Syscall_2(ex_mem_1_syscall_2), .MemToReg_2(ex_mem_1_memtoreg_2), .LUI_2(ex_mem_1_lui_2),
    .MFC0_2(ex_mem_1_mfc0_2), .JAL_2(ex_mem_1_jal_2), .LBU_2(ex_mem_1_lbu_2), .B_2(MDin),
    .ALU_2(ex_mem_1_alu_2), .IR_2(ex_mem_1_ir_2), .PC_2(M_PC),
    .\传输状态Out_表明当前传输数据有效 (\ex_mem_1_传输状态out_表明当前传输数据有效 ), .\同步清零_气泡_高电平有效 (1'b0),
    .\使能端_低电平有效_stall_高电平有效 (register_1_q), .PC_4(id_ex_1_pc_4_2), .PC_4_2(ex_mem_1_pc_4_2),
    .MemWrite(id_ex_1_memwrite_2), .MemWrite_2(MemWrite), .RegWrite_2(id_ex_1_regwrite_4),
    .RegWrite_4(ex_mem_1_regwrite_4), .RegWrite(id_ex_1_regwrite_3), .RegWrite_3(ex_mem_1_regwrite_3),
    .ImmZeroExt16Shift(shifter_2_out), .ImmZeroExt16Shift_2(ex_mem_1_immzeroext16shift_2),
    .ifshow(comparator_1_eq), .ifshow_2(ex_mem_1_ifshow_2), .LedData(register_2_q),
    .LeaData(ex_mem_1_leadata), .LUI(id_ex_1_lui_2));  // open: rd, rd_2, MTC0, MTC0_2, IRout, IRout_2
  and and_11 (and_11_out, ex_mem_1_syscall_2, not_9_out);
  not not_9 (not_9_out, ex_mem_1_ifshow_2);
  Multiplexer #(.select(1), .width(32), .disabled("Z"), .enable("false")) multiplexer_18 (
    .in0(ex_mem_1_alu_2), .in1(ex_mem_1_immzeroext16shift_2), .out(multiplexer_18_out), .sel(ex_mem_1_lui_2));
  not not_10 (MemNotStop, and_11_out);
  RAM #(.addrWidth(10), .dataWidth(32), .bus("separate"), .Select("high")) ram_1 (
    .addr(ex_mem_1_alu_2[11:2]), .din(MDin), .data(ram_1_data), .str(MemWrite), .clk(CLK), .clr(RST));  // open: sel, ld
  MEM_WB mem_wb_1 (
    .ERET(ex_mem_1_eret_2), .Syscall(ex_mem_1_syscall_2), .MemToReg(ex_mem_1_memtoreg_2),
    .LUI(ex_mem_1_lui_2), .MFC0(ex_mem_1_mfc0_2), .JAL(ex_mem_1_jal_2), .ALU(ex_mem_1_alu_2),
    .MD(ram_1_data), .IR(ex_mem_1_ir_2), .PC(M_PC), .PC_4(ex_mem_1_pc_4_2),
    .\传输状态In_表明当前传输数据有效 (\ex_mem_1_传输状态out_表明当前传输数据有效 ), .CLK(CLK), .Syscall_2(mem_wb_1_syscall_2),
    .MemToReg_2(mem_wb_1_memtoreg_2), .JAL_2(mem_wb_1_jal_2), .ALU_2(mem_wb_1_alu_2), .MD_2(mem_wb_1_md_2),
    .PC_2(WB_PC), .PC_4_2(mem_wb_1_pc_4_2), .\同步清零_气泡_高电平有效 (1'b0), .\使能端_低电平有效_stall_高电平有效 (register_1_q),
    .LBU(ex_mem_1_lbu_2), .LBU_2(mem_wb_1_lbu_2), .ImmZeroExt16Shift(ex_mem_1_immzeroext16shift_2),
    .ImmZeroExt16Shift_2(mem_wb_1_immzeroext16shift_2), .RegWrite(ex_mem_1_regwrite_3),
    .RegWrite_3(RegWrite), .RegWrite_2(ex_mem_1_regwrite_4), .RegWrite_4(mem_wb_1_regwrite_4),
    .ifshow_2(mem_wb_1_ifshow_2), .ifshow(ex_mem_1_ifshow_2), .LedData(ex_mem_1_leadata),
    .LedData_2(LedData), .LUI_2(mem_wb_1_lui_2));  // open: ERET_2, MFC0_2, IR_2, 传输状态Out_表明当前传输数据有效, rd, rd_2, MTC0, MTC0_2, IRout, IRout_2
  Multiplexer #(.select(1), .width(32), .disabled("Z"), .enable("false")) multiplexer_19 (
    .in0(mem_wb_1_md_2), .in1({{24{1'b0}}, mem_wb_1_md_2[7:0]}), .out(multiplexer_19_out),
    .sel(mem_wb_1_lbu_2));
  Multiplexer #(.select(1), .width(32), .disabled("Z"), .enable("false")) multiplexer_20 (
    .in0(mem_wb_1_alu_2), .in1(multiplexer_19_out), .out(multiplexer_20_out), .sel(mem_wb_1_memtoreg_2));
  Multiplexer #(.select(1), .width(32), .disabled("Z"), .enable("false")) multiplexer_21 (
    .in0(multiplexer_20_out), .in1(mem_wb_1_immzeroext16shift_2), .out(multiplexer_21_out),
    .sel(mem_wb_1_lui_2));
  Multiplexer #(.select(1), .width(32), .disabled("Z"), .enable("false")) multiplexer_22 (
    .in0(multiplexer_21_out), .in1(mem_wb_1_pc_4_2), .out(RDin), .sel(mem_wb_1_jal_2));

  // Other names for the same wires on the sheet: MEM_PC[31:0] = M_PC; 插入气泡数[15:0] = \LoadUse次数 

  // Notes on the sheet:
  //   中断源
  //   中断等待指示
  //   数码管输出
  //   指令存储器
  //   指令字
  //   contents of rom_1 (hex, n*v repeats v):
  //   20110001 8100005 20110001 20120002 20130003 8100009 20110001 20120002 20130003 810000d 20110001
  //   20120002 20130003 8100011 20110001 20120002 20130003 c1000fc 20100001 20110001 118fc0 112020
  //   20020022 c 118882 12200001 8100015 112020 20020022 c 20110001 118880 112020 20020022 c 12200001
  //   810001f 2011000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
  //   OP
  //   Func
  //   MF/MT
  //   rs
  //   rt
  //   rd
  //   SignedExt
  //   LUI
  //   MFC0
  //   MTC0
  //   Func
  //   MF/MT
  //   流水调试日志用
  //   Beq
  //   JMP
  //   JR
  //   Bgez
  //   Bne
  //   LBU
  //   AluOP
  //   OP
  //   JAL
  //   ERET
  //   Syscall
  //   MemToReg
  //   MemWrite
  //   AluSrcB
  //   RegWrite
  //   RegDst
  //   为方便自动评测，需要输出流水线各段保存的PC值，注意是PC不是PC+4，另外ID段寄存器写入信息，Mem段内存写入信息也要输出
  //   数据存储器
endmodule
module \最终版cpu24_五段流水_动态分支预测_流水多级中断  (
  output RegWrite,
  output MemWrite,
  output [31:0] IF_PC,
  output [31:0] ID_PC,
  output [31:0] EX_PC,
  output [31:0] M_PC,
  output [31:0] WB_PC,
  output [31:0] RDin,
  output [31:0] MDin,
  output [31:0] LedData
);

  wire and_1_out, and_2_out, and_4_out, and_5_out, and_6_out, and_7_out, and_8_out, and_9_out, and_10_out,
       and_11_out, Clear, CLK, comparator_1_eq, comparator_2_eq, ERET, ex_mem_1_eret_2, ex_mem_1_ifshow_2,
       ex_mem_1_jal_2, ex_mem_1_lbu_2, ex_mem_1_lui_2, ex_mem_1_memtoreg_2, ex_mem_1_mfc0_2, ex_mem_1_mtc0_2,
       ex_mem_1_regwrite_3, ex_mem_1_syscall_2, \ex_mem_1_传输状态out_表明当前传输数据有效 , ExNotStop, fail, Go, hit,
       id_ex_1_alusrc_2, id_ex_1_beq_2, id_ex_1_bgez_2, id_ex_1_bne_2, id_ex_1_eret_2, id_ex_1_jal_2,
       id_ex_1_jmp_2, id_ex_1_jr_2, id_ex_1_lbu_2, id_ex_1_lui_2, id_ex_1_memtoreg_2, id_ex_1_memwrite_2,
       id_ex_1_mfc0_2, id_ex_1_miss_2, id_ex_1_mtc0_2, id_ex_1_regwrite_3, id_ex_1_syscall_2,
       \id_ex_1_传输状态out_表明当前传输数据有效 , if_id_1_hit_2, if_id_1_miss_2, \if_id_1_传输状态out_表明当前传输数据有效 , ifjump,
       IR1, IR2, IR3, IRenable, IRready, jfail, Load_Use, mem_wb_1_ifshow_2, mem_wb_1_jal_2, mem_wb_1_lbu_2,
       mem_wb_1_lui_2, mem_wb_1_memtoreg_2, mem_wb_1_syscall_2, MemNotStop, MFC0, mips_alu_1_equal, MTC0,
       \n27_4条扩展指令控制器_1_alu_src , \n27_4条扩展指令控制器_1_beq , \n27_4条扩展指令控制器_1_bgez , \n27_4条扩展指令控制器_1_bne ,
       \n27_4条扩展指令控制器_1_eret , \n27_4条扩展指令控制器_1_jal , \n27_4条扩展指令控制器_1_jmp , \n27_4条扩展指令控制器_1_jr ,
       \n27_4条扩展指令控制器_1_lbu , \n27_4条扩展指令控制器_1_lui , \n27_4条扩展指令控制器_1_memtoreg , \n27_4条扩展指令控制器_1_memwrite ,
       \n27_4条扩展指令控制器_1_mfc0 , \n27_4条扩展指令控制器_1_mtc0 , \n27_4条扩展指令控制器_1_regdst , \n27_4条扩展指令控制器_1_regwrite ,
       \n27_4条扩展指令控制器_1_signedext , \n27_4条扩展指令控制器_1_syscall , nifjump, not_1_out, not_2_out, not_3_out,
       not_4_out, not_6_out, not_7_out, not_8_out, not_10_out, or_1_out, or_2_out, or_3_out, or_4_out,
       or_5_out, or_9_out, register_1_q, RST, W1, W2, W3, \全相联bht_1_miss , \全相联bht_1_predictjmp ,
       \源寄存器使用情况_1_r1_used , \源寄存器使用情况_1_r2_used ;
  wire [1:0] id_ex_1_forward1, id_ex_1_forward2_2, id_ex_1_prediction_2, if_id_1_prediction_2,
       multiplexer_6_out, \全相联bht_1_predata , \数据相关检测_1_forward1 , \数据相关检测_1_forward2 ,
       \预测状态逻辑转换_1_afterstatus0 ;
  wire [3:0] id_ex_1_aluop_2, \n27_4条扩展指令控制器_1_alu_op ;
  wire [4:0] ex_mem_1_rd_2, ex_mem_1_regwrite_4, id_ex_1_rd_2, id_ex_1_regwrite_4, mem_wb_1_regwrite_4,
       multiplexer_7_out, multiplexer_8_out, multiplexer_9_out, multiplexer_10_out, RD;
  wire [15:0] counter_5_q, \LoadUse次数 , \总周期数 , \无条件分支数 , \条件分支成功数 , \预测失败次数 , \预测成功次数 ;
  wire [31:0] adder_1_out, adder_2_out, bit_extender_1_out, bit_extender_2_out, bit_extender_3_out, EPC,
       ex_mem_1_alu_2, ex_mem_1_immzeroext16shift_2, ex_mem_1_ir_2, ex_mem_1_leadata, ex_mem_1_pc_4_2,
       id_ex_1_a_2, id_ex_1_b_2, id_ex_1_desaddr_2, id_ex_1_immext16_2, id_ex_1_immsignedext26_2,
       \id_ex_1_immzeroext16_用于lui指令_2 , id_ex_1_ir_2, id_ex_1_pc_4_2, if_id_1_desaddr_2, if_id_1_ir_2,
       if_id_1_pc_4_2, IRaddr, mem_wb_1_alu_2, mem_wb_1_immzeroext16shift_2, mem_wb_1_md_2, mem_wb_1_pc_4_2,
       mips_alu_1_result, mips_regifile_1_r1, mips_regifile_1_r2, multiplexer_1_out, multiplexer_2_out,
       multiplexer_3_out, multiplexer_4_out, multiplexer_5_out, multiplexer_11_out, multiplexer_12_out,
       multiplexer_13_out, multiplexer_14_out, multiplexer_15_out, multiplexer_16_out, multiplexer_17_out,
       multiplexer_18_out, multiplexer_19_out, multiplexer_20_out, multiplexer_21_out, multiplexer_22_out,
       multiplexer_23_out, ram_1_data, register_2_q, rom_1_data, shifter_1_out, shifter_2_out, shifter_3_out,
       \全相联bht_1_desdata ;

  Button \u_总复位  (.out(RST));
  Button _1 (.out(IR1));
  Button _2 (.out(IR2));
  Button _3 (.out(IR3));
  Button \u_继续运行  (.out(Go));
  LED #(.active("true")) led_1 (.in(W1));
  LED #(.active("true")) led_2 (.in(W2));
  LED #(.active("true")) led_3 (.in(W3));
  Hex_Digit_Display hex_digit_display_1 (.value(LedData[31:28]));  // open: dp
  Hex_Digit_Display hex_digit_display_2 (.value(LedData[27:24]));  // open: dp
  Hex_Digit_Display hex_digit_display_3 (.value(LedData[23:20]));  // open: dp
  \最终版电路中断发生器_硬件实现  \u_最终版电路中断发生器_硬件实现_1  (
    .CLK(CLK), .RD(RD), .W1(W1), .IR1(IR1), .MFC0(MFC0), .EPC(EPC), .W2(W2), .IR2(IR2), .PC3(M_PC), .W3(W3),
    .IR3(IR3), .IRaddr(IRaddr), .MTC0(MTC0), .IRenable(IRenable), .ERET(ERET));
  Counter #(.width(16), .max('hffff), .ongoal("wrap"), .trigger("rising"), .behavior("old")) counter_1 (
    .count(jfail), .Q(\预测失败次数 ), .clk(CLK), .clr(RST));  // open: load, D, carry, preset
  Hex_Digit_Display hex_digit_display_4 (.value(LedData[15:12]));  // open: dp
  Hex_Digit_Display hex_digit_display_5 (.value(LedData[19:16]));  // open: dp
  Counter #(.width(16), .max('hffff), .ongoal("wrap"), .trigger("rising"), .behavior("old")) counter_2 (
    .count(nifjump), .Q(\无条件分支数 ), .clk(CLK), .clr(RST));  // open: load, D, carry, preset
  Register #(.width(32), .trigger("rising"), .Select("low")) PC (
    .D(multiplexer_2_out), .en(and_2_out), .Q(IF_PC), .clk(CLK), .clr(RST));
  Multiplexer #(.select(1), .width(32), .disabled("Z"), .enable("false")) multiplexer_1 (
    .in0(multiplexer_4_out), .in1(IRaddr), .out(multiplexer_1_out), .sel(IRenable));
  Multiplexer #(.select(1), .width(32), .disabled("Z"), .enable("false")) multiplexer_2 (
    .in0(multiplexer_1_out), .in1(EPC), .out(multiplexer_2_out), .sel(ERET));
  Hex_Digit_Display hex_digit_display_6 (.value(LedData[11:8]));  // open: dp
  Hex_Digit_Display hex_digit_display_7 (.value(LedData[7:4]));  // open: dp
  Clock #(.highDuration(1), .lowDuration(1)) clock_1 (.out(CLK));
  \全相联BHT  \u_全相联bht_1  (
    .PRE(\预测状态逻辑转换_1_afterstatus0 ), .update(and_7_out), .IF_PC(IF_PC), .EX_PC(EX_PC),
    .DES(multiplexer_19_out), .CLK(CLK), .ex_hit(hit), .Miss(\全相联bht_1_miss ), .DesData(\全相联bht_1_desdata ),
    .PreData(\全相联bht_1_predata ), .PredictJmp(\全相联bht_1_predictjmp ));
  Counter #(.width(16), .max('hffff), .ongoal("wrap"), .trigger("rising"), .behavior("old")) counter_3 (
    .count(and_1_out), .Q(\LoadUse次数 ), .clk(CLK), .clr(RST));  // open: load, D, carry, preset
  and and_1 (and_1_out, MemNotStop, ExNotStop, Load_Use, not_2_out);
  not not_1 (not_1_out, Load_Use);
  and and_2 (and_2_out, not_1_out, not_2_out);
  Register #(.width(1), .trigger("rising"), .Select("low")) register_1 (
    .D(mem_wb_1_syscall_2), .en(and_4_out), .Q(register_1_q), .clk(CLK), .clr(or_1_out));
  not not_2 (not_2_out, register_1_q);
  or or_1 (or_1_out, RST, Go);
  Counter #(.width(16), .max('hffff), .ongoal("wrap"), .trigger("rising"), .behavior("old")) counter_4 (
    .count(not_2_out), .Q(\总周期数 ), .clk(CLK), .clr(RST));  // open: load, D, carry, preset
  and and_3 (jfail, hit, fail);
  Multiplexer #(.select(1), .width(32), .disabled("Z"), .enable("false")) multiplexer_3 (
    .in0(adder_1_out), .in1(\全相联bht_1_desdata ), .out(multiplexer_3_out), .sel(\全相联bht_1_predictjmp ));
  Multiplexer #(.select(1), .width(32), .disabled("Z"), .enable("false")) multiplexer_4 (
    .in0(multiplexer_3_out), .in1(multiplexer_5_out), .out(multiplexer_4_out), .sel(fail));
  Hex_Digit_Display hex_digit_display_8 (.value(LedData[3:0]));  // open: dp
  \预测状态逻辑转换  \u_预测状态逻辑转换_1  (
    .jmp(Clear), .AfterStatus1(\预测状态逻辑转换_1_afterstatus0 [1]), .PreStatus1(id_ex_1_prediction_2[1]),
    .PreStatus0(id_ex_1_prediction_2[0]), .AfterStatus0(\预测状态逻辑转换_1_afterstatus0 [0]), .fail(fail));
  Counter #(.width(16), .max('hffff), .ongoal("wrap"), .trigger("rising"), .behavior("old")) counter_5 (
    .count(hit), .Q(counter_5_q), .clk(CLK), .clr(RST));  // open: load, D, carry, preset
  Subtractor #(.width(16)) subtractor_1 (.a(counter_5_q), .b(\预测失败次数 ), .out(\预测成功次数 ));  // open: bin, bout
  Counter #(.width(16), .max('hffff), .ongoal("wrap"), .trigger("rising"), .behavior("old")) counter_6 (
    .count(ifjump), .Q(\条件分支成功数 ), .clk(CLK), .clr(RST));  // open: load, D, carry, preset
  Adder #(.width(32)) adder_1 (.a(IF_PC), .b(32'h4), .out(adder_1_out));  // open: cin, cout
  Multiplexer #(.select(1), .width(32), .disabled("Z"), .enable("false")) multiplexer_5 (
    .in0(id_ex_1_pc_4_2), .in1(multiplexer_19_out), .out(multiplexer_5_out), .sel(Clear));
  and and_4 (and_4_out, not_3_out, mem_wb_1_syscall_2);
  // Probe on \总周期数 
  ROM #(.addrWidth(10), .dataWidth(32), .Select("high")) rom_1 (.addr(IF_PC[11:2]), .data(rom_1_data));
  not not_3 (not_3_out, mem_wb_1_ifshow_2);
  // Probe on \总周期数 
  // Probe on \无条件分支数 
  // Probe on \条件分支成功数 
  // Probe on \LoadUse次数 
  // Probe on \LoadUse次数 
  // Probe on \预测成功次数 
  // Probe on \预测失败次数 
  or or_2 (or_2_out, Load_Use, register_1_q);
  // Probe on IF_PC[11:0]
  or or_3 (or_3_out, fail, ERET, IRenable);
  IF_ID if_id_1 (
    .IR(rom_1_data), .PC_4(adder_1_out), .\传输状态In_表明当前传输数据有效 (1'b1), .CLK(CLK), .IR_2(if_id_1_ir_2),
    .PC_4_2(if_id_1_pc_4_2), .\传输状态Out_表明当前传输数据有效 (\if_id_1_传输状态out_表明当前传输数据有效 ), .\同步清零_气泡_高电平有效 (or_3_out),
    .\使能端_低电平有效_stall_高电平有效 (or_2_out), .PC(IF_PC), .PC_2(ID_PC), .DesAddr(\全相联bht_1_desdata ),
    .DesAddr_2(if_id_1_desaddr_2), .Miss(\全相联bht_1_miss ), .Miss_2(if_id_1_miss_2), .Hit(not_4_out),
    .Hit_2(if_id_1_hit_2), .Prediction_2(if_id_1_prediction_2), .Prediction(multiplexer_6_out));
  Multiplexer #(.select(1), .width(2), .disabled("Z"), .enable("false")) multiplexer_6 (
    .in0(\全相联bht_1_predata ), .in1(2'b01), .out(multiplexer_6_out), .sel(\全相联bht_1_miss ));
  not not_4 (not_4_out, \全相联bht_1_miss );
  // Probe on ID_PC[11:0]
  // Probe on EX_PC[11:0]
  \源寄存器使用情况  \u_源寄存器使用情况_1  (
    .OP0(if_id_1_ir_2[26]), .OP1(if_id_1_ir_2[27]), .OP2(if_id_1_ir_2[28]), .OP3(if_id_1_ir_2[29]),
    .OP4(if_id_1_ir_2[30]), .OP5(if_id_1_ir_2[31]), .F0(if_id_1_ir_2[0]), .F1(if_id_1_ir_2[1]),
    .F2(if_id_1_ir_2[2]), .F3(if_id_1_ir_2[3]), .F4(if_id_1_ir_2[4]), .F5(if_id_1_ir_2[5]),
    .R1_Used(\源寄存器使用情况_1_r1_used ), .R2_Used(\源寄存器使用情况_1_r2_used ));
  // Probe on M_PC[11:0]
  \数据相关检测  \u_数据相关检测_1  (
    .R1_Used(\源寄存器使用情况_1_r1_used ), .R2_Used(\源寄存器使用情况_1_r2_used ), .ID_R1_num(multiplexer_7_out),
    .ID_R2_num(multiplexer_8_out), .EX_WriteReg_num(id_ex_1_regwrite_4),
    .MEM_WriteReg_num(ex_mem_1_regwrite_4), .EX_RegWrite(id_ex_1_regwrite_3),
    .MEM__RegWrite(ex_mem_1_regwrite_3), .EX_MemToReg(id_ex_1_memtoreg_2),
    .MEM_MemToReg(ex_mem_1_memtoreg_2), .Forward1(\数据相关检测_1_forward1 ), .Forward2(\数据相关检测_1_forward2 ),
    .Load_Use(Load_Use));  // open: 数据相关
  or or_4 (or_4_out, Load_Use, or_3_out);
  // Probe on WB_PC[11:0]
  Multiplexer #(.select(1), .width(5), .disabled("Z"), .enable("false")) multiplexer_7 (
    .in0(if_id_1_ir_2[25:21]), .in1(5'b00100), .out(multiplexer_7_out), .sel(\n27_4条扩展指令控制器_1_syscall ));
  Multiplexer #(.select(1), .width(5), .disabled("Z"), .enable("false")) multiplexer_8 (
    .in0(if_id_1_ir_2[20:16]), .in1(5'b00010), .out(multiplexer_8_out), .sel(\n27_4条扩展指令控制器_1_syscall ));
  Multiplexer #(.select(1), .width(5), .disabled("Z"), .enable("false")) multiplexer_9 (
    .in0(if_id_1_ir_2[20:16]), .in1(if_id_1_ir_2[15:11]), .out(multiplexer_9_out),
    .sel(\n27_4条扩展指令控制器_1_regdst ));
  assign bit_extender_1_out = {{16{1'b0}}, if_id_1_ir_2[15:0]};  // Bit_Extender bit_extender_1
  assign bit_extender_2_out = {{16{if_id_1_ir_2[15]}}, if_id_1_ir_2[15:0]};  // Bit_Extender bit_extender_2
  assign bit_extender_3_out = {{6{if_id_1_ir_2[25]}}, if_id_1_ir_2[25:0]};  // Bit_Extender bit_extender_3
  \_27_4条扩展指令控制器  \u_27_4条扩展指令控制器_1  (
    .OP(if_id_1_ir_2[31:26]), .Func(if_id_1_ir_2[5:0]), .ALU_OP(\n27_4条扩展指令控制器_1_alu_op ),
    .MemToReg(\n27_4条扩展指令控制器_1_memtoreg ), .MemWrite(\n27_4条扩展指令控制器_1_memwrite ),
    .ALU_SRC(\n27_4条扩展指令控制器_1_alu_src ), .SysCALL(\n27_4条扩展指令控制器_1_syscall ),
    .SignedExt(\n27_4条扩展指令控制器_1_signedext ), .RegDst(\n27_4条扩展指令控制器_1_regdst ), .Beq(\n27_4条扩展指令控制器_1_beq ),
    .Bne(\n27_4条扩展指令控制器_1_bne ), .JR(\n27_4条扩展指令控制器_1_jr ), .JMP(\n27_4条扩展指令控制器_1_jmp ),
    .JAL(\n27_4条扩展指令控制器_1_jal ), .LUI(\n27_4条扩展指令控制器_1_lui ), .LBU(\n27_4条扩展指令控制器_1_lbu ),
    .BGEZ(\n27_4条扩展指令控制器_1_bgez ), .MTC0(\n27_4条扩展指令控制器_1_mtc0 ), .MFMT(if_id_1_ir_2[25:21]),
    .ERET(\n27_4条扩展指令控制器_1_eret ), .MFC0(\n27_4条扩展指令控制器_1_mfc0 ), .RegWrite(\n27_4条扩展指令控制器_1_regwrite ));
  Multiplexer #(.select(1), .width(5), .disabled("Z"), .enable("false")) multiplexer_10 (
    .in0(multiplexer_9_out), .in1({5{1'b1}}), .out(multiplexer_10_out), .sel(\n27_4条扩展指令控制器_1_jal ));
  Multiplexer #(.select(1), .width(32), .disabled("Z"), .enable("false")) multiplexer_11 (
    .in0(bit_extender_1_out), .in1(bit_extender_2_out), .out(multiplexer_11_out),
    .sel(\n27_4条扩展指令控制器_1_signedext ));
  MIPS_Regifile mips_regifile_1 (
    .Din(RDin), .Clk(CLK), .R1(mips_regifile_1_r1), .R2(mips_regifile_1_r2), .WE(RegWrite),
    .W_num(mem_wb_1_regwrite_4), .R1_num(multiplexer_7_out), .R2_num(multiplexer_8_out));
  ID_EX id_ex_1 (
    .MemToReg(\n27_4条扩展指令控制器_1_memtoreg ), .LUI(\n27_4条扩展指令控制器_1_lui ), .MFC0(\n27_4条扩展指令控制器_1_mfc0 ),
    .LBU(\n27_4条扩展指令控制器_1_lbu ), .MemWrite(\n27_4条扩展指令控制器_1_memwrite ), .AluOP(\n27_4条扩展指令控制器_1_alu_op ),
    .MTC0(\n27_4条扩展指令控制器_1_mtc0 ), .Beq(\n27_4条扩展指令控制器_1_beq ), .Bgez(\n27_4条扩展指令控制器_1_bgez ),
    .Bne(\n27_4条扩展指令控制器_1_bne ), .JMP(\n27_4条扩展指令控制器_1_jmp ), .A(mips_regifile_1_r1), .B(mips_regifile_1_r2),
    .ImmExt16(multiplexer_11_out), .\ImmZeroExt16_用于LUI指令 (bit_extender_1_out),
    .ImmSignedExt26(bit_extender_3_out), .IR(if_id_1_ir_2),
    .\传输状态In_表明当前传输数据有效 (\if_id_1_传输状态out_表明当前传输数据有效 ), .CLK(CLK), .MemToReg_2(id_ex_1_memtoreg_2),
    .LUI_2(id_ex_1_lui_2), .MFC0_2(id_ex_1_mfc0_2), .JAL_2(id_ex_1_jal_2), .LBU_2(id_ex_1_lbu_2),
    .MemWrite_2(id_ex_1_memwrite_2), .AluOP_2(id_ex_1_aluop_2), .AluSrc_2(id_ex_1_alusrc_2),
    .MTC0_2(id_ex_1_mtc0_2), .Beq_2(id_ex_1_beq_2), .Bgez_2(id_ex_1_bgez_2), .Bne_2(id_ex_1_bne_2),
    .JMP_2(id_ex_1_jmp_2), .A_2(id_ex_1_a_2), .B_2(id_ex_1_b_2), .ImmExt16_2(id_ex_1_immext16_2),
    .\ImmZeroExt16_用于LUI指令_2 (\id_ex_1_immzeroext16_用于lui指令_2 ), .ImmSignedExt26_2(id_ex_1_immsignedext26_2),
    .IR_2(id_ex_1_ir_2), .\传输状态Out_表明当前传输数据有效 (\id_ex_1_传输状态out_表明当前传输数据有效 ), .\同步清零_气泡_高电平有效 (or_4_out),
    .\使能端_低电平有效_stall_高电平有效 (register_1_q), .ERET(\n27_4条扩展指令控制器_1_eret ), .ERET_2(id_ex_1_eret_2),
    .Syscall(\n27_4条扩展指令控制器_1_syscall ), .Syscall_2(id_ex_1_syscall_2), .PC(ID_PC), .PC_2(EX_PC),
    .PC_4_2(id_ex_1_pc_4_2), .PC_4(if_id_1_pc_4_2), .RegWrite_3(id_ex_1_regwrite_3),
    .RegWrite_2(multiplexer_10_out), .RegWrite_4(id_ex_1_regwrite_4), .AluSrc(\n27_4条扩展指令控制器_1_alu_src ),
    .RegWrite(\n27_4条扩展指令控制器_1_regwrite ), .JAL(\n27_4条扩展指令控制器_1_jal ), .JR(\n27_4条扩展指令控制器_1_jr ),
    .JR_2(id_ex_1_jr_2), .forwar1(\数据相关检测_1_forward1 ), .forward1(id_ex_1_forward1),
    .forward2(\数据相关检测_1_forward2 ), .forward2_2(id_ex_1_forward2_2), .rd(if_id_1_ir_2[15:11]),
    .rd_2(id_ex_1_rd_2), .prediction(if_id_1_prediction_2), .prediction_2(id_ex_1_prediction_2),
    .Miss(if_id_1_miss_2), .Miss_2(id_ex_1_miss_2), .Hit(if_id_1_hit_2), .Hit_2(hit),
    .DesAddr(if_id_1_desaddr_2), .DesAddr_2(id_ex_1_desaddr_2));
  and and_5 (and_5_out, id_ex_1_syscall_2, not_6_out);
  Comparator #(.width(32), .mode("twosComplement")) comparator_1 (
    .a(32'h22), .b(multiplexer_13_out), .eq(comparator_1_eq));  // open: gt, lt
  not not_5 (ExNotStop, and_5_out);
  not not_6 (not_6_out, comparator_1_eq);
  and and_6 (and_6_out, id_ex_1_syscall_2, comparator_1_eq);
  Multiplexer #(.select(2), .width(32), .disabled("Z"), .enable("false")) multiplexer_12 (
    .in0(id_ex_1_a_2), .in1(multiplexer_20_out), .in2(mem_wb_1_alu_2), .in3(multiplexer_22_out),
    .out(multiplexer_12_out), .sel(id_ex_1_forward1));
  Multiplexer #(.select(2), .width(32), .disabled("Z"), .enable("false")) multiplexer_13 (
    .in0(id_ex_1_b_2), .in1(multiplexer_20_out), .in2(mem_wb_1_alu_2), .in3(multiplexer_22_out),
    .out(multiplexer_13_out), .sel(id_ex_1_forward2_2));
  Multiplexer #(.select(1), .width(32), .disabled("Z"), .enable("false")) multiplexer_14 (
    .in0(multiplexer_13_out), .in1(id_ex_1_immext16_2), .out(multiplexer_14_out), .sel(id_ex_1_alusrc_2));
  Shifter #(.width(32), .shift("ll")) shifter_1 (.in(id_ex_1_immext16_2), .\dist (5'b00010), .out(shifter_1_out));
  Shifter #(.width(32), .shift("ll")) shifter_2 (
    .in(\id_ex_1_immzeroext16_用于lui指令_2 ), .\dist (5'b10000), .out(shifter_2_out));
  Shifter #(.width(32), .shift("ll")) shifter_3 (.in(id_ex_1_immsignedext26_2), .\dist (5'b00010), .out(shifter_3_out));
  Multiplexer #(.select(1), .width(32), .disabled("Z"), .enable("false")) multiplexer_15 (
    .in0(multiplexer_14_out), .in1({32{1'b0}}), .out(multiplexer_15_out), .sel(id_ex_1_bgez_2));
  and and_7 (and_7_out, id_ex_1_miss_2, Clear);
  not not_7 (not_7_out, mips_alu_1_equal);
  not not_8 (not_8_out, mips_alu_1_result[0]);
  MIPS_ALU mips_alu_1 (
    .X(multiplexer_12_out), .Y(multiplexer_15_out), .AluOP(id_ex_1_aluop_2), .Equal(mips_alu_1_equal),
    .Result(mips_alu_1_result), .shamt(id_ex_1_ir_2[10:6]));  // open: Result_2
  and and_8 (and_8_out, not_7_out, id_ex_1_bne_2);
  and and_9 (and_9_out, not_8_out, id_ex_1_bgez_2);
  and and_10 (and_10_out, id_ex_1_beq_2, mips_alu_1_equal);
  Register #(.width(32), .trigger("rising"), .Select("low")) register_2 (
    .D(multiplexer_12_out), .en(and_6_out), .Q(register_2_q), .clk(CLK), .clr(RST));
  Adder #(.width(32)) adder_2 (.a(shifter_1_out), .b(id_ex_1_pc_4_2), .out(adder_2_out));  // open: cin, cout
  Multiplexer #(.select(1), .width(32), .disabled("Z"), .enable("false")) multiplexer_16 (
    .in0(multiplexer_17_out), .in1(shifter_3_out), .out(multiplexer_16_out), .sel(or_5_out));
  or or_5 (or_5_out, id_ex_1_jal_2, id_ex_1_jmp_2);
  or or_6 (ifjump, and_8_out, and_9_out, and_10_out);
  Multiplexer #(.select(1), .width(32), .disabled("Z"), .enable("false")) multiplexer_17 (
    .in0(id_ex_1_pc_4_2), .in1(adder_2_out), .out(multiplexer_17_out), .sel(ifjump));
  Multiplexer #(.select(1), .width(32), .disabled("Z"), .enable("false")) multiplexer_18 (
    .in0(multiplexer_16_out), .in1(multiplexer_12_out), .out(multiplexer_18_out), .sel(id_ex_1_jr_2));
  not not_9 (IRready, comparator_2_eq);
  Comparator #(.width(32), .mode("twosComplement")) comparator_2 (
    .a(EX_PC), .b({32{1'b0}}), .eq(comparator_2_eq));  // open: gt, lt
  or or_7 (Clear, ifjump, id_ex_1_jr_2, or_5_out);
  or or_8 (nifjump, or_5_out, id_ex_1_jr_2);
  Multiplexer #(.select(1), .width(32), .disabled("Z"), .enable("false")) multiplexer_19 (
    .in0(id_ex_1_desaddr_2), .in1(multiplexer_18_out), .out(multiplexer_19_out), .sel(fail));
  EX_MEM ex_mem_1 (
    .ERET(id_ex_1_eret_2), .Syscall(id_ex_1_syscall_2), .MemToReg(id_ex_1_memtoreg_2), .MFC0(id_ex_1_mfc0_2),
    .JAL(id_ex_1_jal_2), .LBU(id_ex_1_lbu_2), .B(multiplexer_13_out), .ALU(mips_alu_1_result),
    .IR(id_ex_1_ir_2), .PC(EX_PC), .\传输状态In_表明当前传输数据有效 (\id_ex_1_传输状态out_表明当前传输数据有效 ), .CLK(CLK),
    .ERET_2(ex_mem_1_eret_2), .Syscall_2(ex_mem_1_syscall_2), .MemToReg_2(ex_mem_1_memtoreg_2),
    .LUI_2(ex_mem_1_lui_2), .MFC0_2(ex_mem_1_mfc0_2), .JAL_2(ex_mem_1_jal_2), .LBU_2(ex_mem_1_lbu_2),
    .B_2(MDin), .ALU_2(ex_mem_1_alu_2), .IR_2(ex_mem_1_ir_2), .PC_2(M_PC),
    .\传输状态Out_表明当前传输数据有效 (\ex_mem_1_传输状态out_表明当前传输数据有效 ), .\同步清零_气泡_高电平有效 (or_9_out),
    .\使能端_低电平有效_stall_高电平有效 (register_1_q), .PC_4(id_ex_1_pc_4_2), .PC_4_2(ex_mem_1_pc_4_2),
    .MemWrite(id_ex_1_memwrite_2), .MemWrite_2(MemWrite), .RegWrite_2(id_ex_1_regwrite_4),
    .RegWrite_4(ex_mem_1_regwrite_4), .RegWrite(id_ex_1_regwrite_3), .RegWrite_3(ex_mem_1_regwrite_3),
    .ImmZeroExt16Shift(shifter_2_out), .ImmZeroExt16Shift_2(ex_mem_1_immzeroext16shift_2),
    .ifshow(comparator_1_eq), .ifshow_2(ex_mem_1_ifshow_2), .LedData(register_2_q),
    .LeaData(ex_mem_1_leadata), .LUI(id_ex_1_lui_2), .rd(id_ex_1_rd_2), .rd_2(ex_mem_1_rd_2),
    .MTC0(id_ex_1_mtc0_2), .MTC0_2(ex_mem_1_mtc0_2));  // open: IRout, IRout_2
  not not_10 (not_10_out, ex_mem_1_ifshow_2);
  and and_11 (and_11_out, ex_mem_1_syscall_2, not_10_out);
  not not_11 (MemNotStop, and_11_out);
  Multiplexer #(.select(1), .width(32), .disabled("Z"), .enable("false")) multiplexer_20 (
    .in0(ex_mem_1_alu_2), .in1(ex_mem_1_immzeroext16shift_2), .out(multiplexer_20_out), .sel(ex_mem_1_lui_2));
  or or_9 (or_9_out, IRenable, ERET);
  RAM #(.addrWidth(10), .dataWidth(32), .bus("separate"), .Select("high")) ram_1 (
    .addr(ex_mem_1_alu_2[11:2]), .din(MDin), .data(ram_1_data), .str(MemWrite), .clk(CLK), .clr(RST));  // open: sel, ld
  MEM_WB mem_wb_1 (
    .ERET(ex_mem_1_eret_2), .Syscall(ex_mem_1_syscall_2), .MemToReg(ex_mem_1_memtoreg_2),
    .LUI(ex_mem_1_lui_2), .MFC0(ex_mem_1_mfc0_2), .JAL(ex_mem_1_jal_2), .ALU(ex_mem_1_alu_2),
    .MD(ram_1_data), .IR(ex_mem_1_ir_2), .PC(M_PC), .PC_4(ex_mem_1_pc_4_2),
    .\传输状态In_表明当前传输数据有效 (\ex_mem_1_传输状态out_表明当前传输数据有效 ), .CLK(CLK), .ERET_2(ERET),
    .Syscall_2(mem_wb_1_syscall_2), .MemToReg_2(mem_wb_1_memtoreg_2), .MFC0_2(MFC0), .JAL_2(mem_wb_1_jal_2),
    .ALU_2(mem_wb_1_alu_2), .MD_2(mem_wb_1_md_2), .PC_2(WB_PC), .PC_4_2(mem_wb_1_pc_4_2),
    .\同步清零_气泡_高电平有效 (ERET), .\使能端_低电平有效_stall_高电平有效 (register_1_q), .LBU(ex_mem_1_lbu_2),
    .LBU_2(mem_wb_1_lbu_2), .ImmZeroExt16Shift(ex_mem_1_immzeroext16shift_2),
    .ImmZeroExt16Shift_2(mem_wb_1_immzeroext16shift_2), .RegWrite(ex_mem_1_regwrite_3),
    .RegWrite_3(RegWrite), .RegWrite_2(ex_mem_1_regwrite_4), .RegWrite_4(mem_wb_1_regwrite_4),
    .ifshow_2(mem_wb_1_ifshow_2), .ifshow(ex_mem_1_ifshow_2), .LedData(ex_mem_1_leadata),
    .LedData_2(LedData), .LUI_2(mem_wb_1_lui_2), .rd(ex_mem_1_rd_2), .rd_2(RD), .MTC0(ex_mem_1_mtc0_2),
    .MTC0_2(MTC0));  // open: IR_2, 传输状态Out_表明当前传输数据有效, IRout, IRout_2
  Multiplexer #(.select(1), .width(32), .disabled("Z"), .enable("false")) multiplexer_21 (
    .in0(mem_wb_1_alu_2), .in1(multiplexer_22_out), .out(multiplexer_21_out), .sel(mem_wb_1_memtoreg_2));
  Multiplexer #(.select(1), .width(32), .disabled("Z"), .enable("false")) multiplexer_22 (
    .in0(mem_wb_1_md_2), .in1({{24{1'b0}}, mem_wb_1_md_2[7:0]}), .out(multiplexer_22_out),
    .sel(mem_wb_1_lbu_2));
  Multiplexer #(.select(1), .width(32), .disabled("Z"), .enable("false")) multiplexer_23 (
    .in0(multiplexer_21_out), .in1(mem_wb_1_immzeroext16shift_2), .out(multiplexer_23_out),
    .sel(mem_wb_1_lui_2));
  Multiplexer #(.select(1), .width(32), .disabled("Z"), .enable("false")) multiplexer_24 (
    .in0(multiplexer_23_out), .in1(mem_wb_1_pc_4_2), .out(RDin), .sel(mem_wb_1_jal_2));

  // Other names for the same wires on the sheet: MEM_PC[31:0] = M_PC; 插入气泡数[15:0] = \LoadUse次数 

  // Notes on the sheet:
  //   中断源
  //   中断等待指示
  //   数码管输出
  //   指令存储器
  //   指令字
  //   contents of rom_1 (hex, n*v repeats v):
  //   20110001 8100005 20110001 20120002 20130003 8100009 20110001 20120002 20130003 810000d 20110001
  //   20120002 20130003 8100011 20110001 20120002 20130003 c1000fc 20100001 20110001 118fc0 112020
  //   20020022 c 118882 12200001 8100015 112020 20020022 c 20110001 118880 112020 20020022 c 12200001
  //   810001f 2011000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
  //   流水调试日志用
  //   OP
  //   Func
  //   MF/MT
  //   rs
  //   rt
  //   rd
  //   JMP
  //   JR
  //   SignedExt
  //   LUI
  //   LBU
  //   MFC0
  //   MTC0
  //   OP
  //   Func
  //   MF/MT
  //   Syscall
  //   Beq
  //   Bgez
  //   Bne
  //   MemToReg
  //   MemWrite
  //   AluOP
  //   AluSrcB
  //   RegWrite
  //   JAL
  //   RegDst
  //   ERET
  //   为方便自动评测，需要输出流水线各段保存的PC值，注意是PC不是PC+4，另外ID段寄存器写入信息，Mem段内存写入信息也要输出
  //   数据存储器
endmodule

// 多级中断器
module \最终版电路中断发生器_硬件实现  (
  input  CLK,
  input  [4:0] RD,
  input  IR1,
  input  MFC0,
  input  IR2,
  input  IR3,
  input  [31:0] PC3,
  input  MTC0,
  input  ERET,
  output W1,
  output [31:0] EPC,
  output W2,
  output W3,
  output [31:0] IRaddr,
  output IRenable
);

  wire and_1_out, and_2_out, and_3_out, and_5_out, and_6_out, clear1, clear2, clear3, comparator_1_eq,
       d_ff_1_q, d_ff_2_q, d_ff_3_q, decoder_1_out1, decoder_1_out2, decoder_1_out3, IE, IE_q, not_2_out,
       or_4_out, or_5_out, or_6_out, or_7_out, or_8_out, or_9_out, priority_encoder_1_gs, Ready1, Ready2,
       Ready3, xnor_1_out, \中断来临 ;
  wire [1:0] IRnum, multiplexer_5_out, pull_resistor_1_node, Renum, \嵌套1_q , \嵌套2_q ;
  wire [31:0] EPC2_q, EPC3_q, multiplexer_1_out, multiplexer_2_out;

  or or_1 (W1, Ready1, d_ff_1_q);
  or or_2 (W2, Ready2, d_ff_2_q);
  or or_3 (W3, Ready3, d_ff_3_q);
  D_Flip_Flop #(.trigger("rising"), .Pre_Clr_Positions("LEGACY"), .NegatePresetClear("false"), .enable("true"), .NewFFLayout("false")) d_ff_1 (
    .clk(IR1), .D(1'b1), .Q(d_ff_1_q), .reset(Ready1));  // open: Qn, preset, en
  D_Flip_Flop #(.trigger("rising"), .Pre_Clr_Positions("LEGACY"), .NegatePresetClear("false"), .enable("true"), .NewFFLayout("false")) d_ff_2 (
    .clk(IR2), .D(1'b1), .Q(d_ff_2_q), .reset(Ready2));  // open: Qn, preset, en
  D_Flip_Flop #(.trigger("rising"), .Pre_Clr_Positions("LEGACY"), .NegatePresetClear("false"), .enable("true"), .NewFFLayout("false")) d_ff_3 (
    .clk(IR3), .D(1'b1), .Q(d_ff_3_q), .reset(Ready3));  // open: Qn, preset, en
  or or_4 (or_4_out, d_ff_1_q, Ready1);
  or or_5 (or_5_out, d_ff_2_q, Ready2);
  or or_6 (or_6_out, d_ff_3_q, Ready3);
  and and_1 (and_1_out, or_4_out, ~clear1);  // AND_Gate
  and and_2 (and_2_out, or_5_out, ~clear2);  // AND_Gate
  and and_3 (and_3_out, or_6_out, ~clear3);  // AND_Gate
  D_Flip_Flop #(.trigger("rising"), .Pre_Clr_Positions("LEGACY"), .NegatePresetClear("false"), .enable("true"), .NewFFLayout("false")) u_IR1 (
    .clk(CLK), .D(and_1_out), .Q(Ready1));  // open: Qn, preset, en, reset
  D_Flip_Flop #(.trigger("rising"), .Pre_Clr_Positions("LEGACY"), .NegatePresetClear("false"), .enable("true"), .NewFFLayout("false")) u_IR2 (
    .clk(CLK), .D(and_2_out), .Q(Ready2));  // open: Qn, preset, en, reset
  D_Flip_Flop #(.trigger("rising"), .Pre_Clr_Positions("LEGACY"), .NegatePresetClear("false"), .enable("true"), .NewFFLayout("false")) u_IR3 (
    .clk(CLK), .D(and_3_out), .Q(Ready3));  // open: Qn, preset, en, reset
  Multiplexer #(.select(1), .width(32), .disabled("Z"), .enable("false")) multiplexer_1 (
    .in0(PC3), .in1(EPC2_q), .out(multiplexer_1_out), .sel(ERET));
  Register #(.width(32), .trigger("rising"), .Select("low")) EPC1 (
    .D(multiplexer_1_out), .en(or_7_out), .Q(EPC), .clk(CLK));  // open: clr
  Multiplexer #(.select(1), .width(32), .disabled("Z"), .enable("false")) multiplexer_2 (
    .in0(EPC), .in1(EPC3_q), .out(multiplexer_2_out), .sel(ERET));
  Pull_Resistor #(.pull(0)) pull_resistor_1 (.node(pull_resistor_1_node));
  Priority_Encoder #(.select(2), .disabled("Z")) priority_encoder_1 (
    .in0(1'b0), .in1(Ready1), .in2(Ready2), .in3(Ready3), .out(pull_resistor_1_node),
    .gs(priority_encoder_1_gs));  // open: en_out, en_in
  and and_4 (IRenable, \中断来临 , priority_encoder_1_gs, IE);
  Multiplexer #(.select(2), .width(32), .disabled("Z"), .enable("false")) multiplexer_3 (
    .in1(32'h47c), .in2(32'h3528), .in3(32'h35d4), .out(IRaddr), .sel(IRnum));  // open: in0
  Register #(.width(32), .trigger("rising"), .Select("low")) EPC2 (
    .D(multiplexer_2_out), .en(or_7_out), .Q(EPC2_q), .clk(CLK));  // open: clr
  or or_7 (or_7_out, IRenable, ERET);
  Multiplexer #(.select(1), .width(2), .disabled("Z"), .enable("false")) multiplexer_4 (
    .in0(pull_resistor_1_node), .in1(\嵌套1_q ), .out(IRnum), .sel(ERET));
  Register #(.width(32), .trigger("rising"), .Select("low")) EPC3 (
    .D(EPC2_q), .en(or_7_out), .Q(EPC3_q), .clk(CLK));  // open: clr
  Register #(.width(2), .trigger("rising"), .Select("low")) \u_当前中断号  (
    .D(IRnum), .en(or_9_out), .Q(Renum), .clk(CLK));  // open: clr
  Register #(.width(2), .trigger("rising"), .Select("low")) \u_嵌套1  (
    .D(multiplexer_5_out), .en(or_9_out), .Q(\嵌套1_q ), .clk(CLK));  // open: clr
  Multiplexer #(.select(1), .width(2), .disabled("Z"), .enable("false")) multiplexer_5 (
    .in0(Renum), .in1(\嵌套2_q ), .out(multiplexer_5_out), .sel(ERET));
  Comparator #(.width(2), .mode("twosComplement")) comparator_1 (
    .a(IRnum), .b(Renum), .eq(comparator_1_eq));  // open: gt, lt
  not not_1 (\中断来临 , comparator_1_eq);
  xnor xnor_1 (xnor_1_out, IRenable, IE);
  Register #(.width(2), .trigger("rising"), .Select("low")) \u_嵌套2  (
    .D(\嵌套1_q ), .en(or_9_out), .Q(\嵌套2_q ), .clk(CLK));  // open: clr
  Decoder #(.select(2), .tristate("false"), .disabled("Z"), .enable("false")) decoder_1 (
    .out1(decoder_1_out1), .out2(decoder_1_out2), .out3(decoder_1_out3), .sel(Renum));  // open: out0
  not not_2 (not_2_out, MFC0);
  and and_5 (and_5_out, not_2_out, or_8_out);
  or or_8 (or_8_out, MTC0, and_6_out);
  and and_6 (and_6_out, ~ERET, xnor_1_out);  // AND_Gate
  or or_9 (or_9_out, IRenable, ERET);
  and and_7 (clear1, ERET, decoder_1_out1);
  and and_8 (clear2, ERET, decoder_1_out2);
  and and_9 (clear3, ERET, decoder_1_out3);
  not not_3 (IE, IE_q);
  Register #(.width(1), .trigger("rising"), .Select("low")) u_IE (.D(and_5_out), .Q(IE_q), .clk(CLK));  // open: en, clr

  // Notes on the sheet:
  //   Reset 
  //   Reset 
  //   Reset 
  //   1号中断信号采样参考电路
  //   2号中断信号采样参考电路
  //   3号中断信号采样参考电路
  //   中断识别（入口地址）
  //   EPC寄存器
  //   中断仲裁和中断生成逻辑
  //   IE寄存器
  //   中断返回逻辑
endmodule

module IF_ID (
  input  Miss,
  input  Hit,
  input  [1:0] Prediction,
  input  [31:0] IR,
  input  [31:0] PC,
  input  [31:0] PC_4,
  input  [31:0] DesAddr,
  input  \传输状态In_表明当前传输数据有效 ,
  input  CLK,
  input  \同步清零_气泡_高电平有效 ,
  input  \使能端_低电平有效_stall_高电平有效 ,
  output Miss_2,
  output Hit_2,
  output [1:0] Prediction_2,
  output [31:0] IR_2,
  output [31:0] PC_2,
  output [31:0] PC_4_2,
  output [31:0] DesAddr_2,
  output \传输状态Out_表明当前传输数据有效 
);

  wire multiplexer_1_out, multiplexer_2_out, multiplexer_8_out, pull_resistor_2_node;
  wire [1:0] multiplexer_3_out;
  wire [31:0] multiplexer_4_out, multiplexer_5_out, multiplexer_6_out, multiplexer_7_out;

  Multiplexer #(.select(1), .width(1), .disabled("Z"), .enable("false")) multiplexer_1 (
    .in0(Miss), .in1(1'b0), .out(multiplexer_1_out), .sel(\同步清零_气泡_高电平有效 ));
  Multiplexer #(.select(1), .width(1), .disabled("Z"), .enable("false")) multiplexer_2 (
    .in0(Hit), .in1(1'b0), .out(multiplexer_2_out), .sel(\同步清零_气泡_高电平有效 ));
  Multiplexer #(.select(1), .width(2), .disabled("Z"), .enable("false")) multiplexer_3 (
    .in0(Prediction), .in1(2'b00), .out(multiplexer_3_out), .sel(\同步清零_气泡_高电平有效 ));
  Multiplexer #(.select(1), .width(32), .disabled("Z"), .enable("false")) multiplexer_4 (
    .in0(IR), .in1({32{1'b0}}), .out(multiplexer_4_out), .sel(\同步清零_气泡_高电平有效 ));
  Multiplexer #(.select(1), .width(32), .disabled("Z"), .enable("false")) multiplexer_5 (
    .in0(PC), .in1({32{1'b0}}), .out(multiplexer_5_out), .sel(\同步清零_气泡_高电平有效 ));
  Multiplexer #(.select(1), .width(32), .disabled("Z"), .enable("false")) multiplexer_6 (
    .in0(PC_4), .in1({32{1'b0}}), .out(multiplexer_6_out), .sel(\同步清零_气泡_高电平有效 ));
  Multiplexer #(.select(1), .width(32), .disabled("Z"), .enable("false")) multiplexer_7 (
    .in0(DesAddr), .in1({32{1'b0}}), .out(multiplexer_7_out), .sel(\同步清零_气泡_高电平有效 ));
  Multiplexer #(.select(1), .width(1), .disabled("Z"), .enable("false")) multiplexer_8 (
    .in0(\传输状态In_表明当前传输数据有效 ), .in1(1'b0), .out(multiplexer_8_out), .sel(\同步清零_气泡_高电平有效 ));
  Pull_Resistor #(.pull(0)) pull_resistor_1 (.node(\同步清零_气泡_高电平有效 ));
  Register #(.width(1), .trigger("rising"), .Select("low")) register_1 (
    .D(multiplexer_1_out), .en(pull_resistor_2_node), .Q(Miss_2), .clk(CLK));  // open: clr
  Register #(.width(1), .trigger("rising"), .Select("low")) register_2 (
    .D(multiplexer_2_out), .en(pull_resistor_2_node), .Q(Hit_2), .clk(CLK));  // open: clr
  Register #(.width(2), .trigger("rising"), .Select("low")) register_3 (
    .D(multiplexer_3_out), .en(pull_resistor_2_node), .Q(Prediction_2), .clk(CLK));  // open: clr
  Register #(.width(32), .trigger("rising"), .Select("low")) register_4 (
    .D(multiplexer_4_out), .en(pull_resistor_2_node), .Q(IR_2), .clk(CLK));  // open: clr
  Register #(.width(32), .trigger("rising"), .Select("low")) register_5 (
    .D(multiplexer_5_out), .en(pull_resistor_2_node), .Q(PC_2), .clk(CLK));  // open: clr
  Register #(.width(32), .trigger("rising"), .Select("low")) register_6 (
    .D(multiplexer_6_out), .en(pull_resistor_2_node), .Q(PC_4_2), .clk(CLK));  // open: clr
  Register #(.width(32), .trigger("rising"), .Select("low")) register_7 (
    .D(multiplexer_7_out), .en(pull_resistor_2_node), .Q(DesAddr_2), .clk(CLK));  // open: clr
  Pull_Resistor #(.pull(0)) pull_resistor_2 (.node(pull_resistor_2_node));
  not not_1 (pull_resistor_2_node, \使能端_低电平有效_stall_高电平有效 );
  Register #(.width(1), .trigger("rising"), .Select("low")) register_8 (
    .D(multiplexer_8_out), .en(pull_resistor_2_node), .Q(\传输状态Out_表明当前传输数据有效 ), .clk(CLK));  // open: clr

  // Notes on the sheet:
  //   使能端_低电平有效_stall_高电平有效: pull=down
  //   同步清零_气泡_高电平有效: pull=down
endmodule

module ID_EX (
  input  RegWrite,
  input  ERET,
  input  Syscall,
  input  MemToReg,
  input  LUI,
  input  MFC0,
  input  JAL,
  input  LBU,
  input  MemWrite,
  input  [3:0] AluOP,
  input  AluSrc,
  input  MTC0,
  input  Beq,
  input  Bgez,
  input  Bne,
  input  JMP,
  input  JR,
  input  [1:0] forwar1,
  input  [1:0] forward2,
  input  [1:0] prediction,
  input  [4:0] rd,
  input  [31:0] A,
  input  [31:0] B,
  input  [31:0] ImmExt16,
  input  [31:0] \ImmZeroExt16_用于LUI指令 ,
  input  [31:0] ImmSignedExt26,
  input  [31:0] IR,
  input  [4:0] RegWrite_2,
  input  [31:0] PC,
  input  [31:0] PC_4,
  input  [31:0] DesAddr,
  input  Miss,
  input  Hit,
  input  \传输状态In_表明当前传输数据有效 ,
  input  CLK,
  input  \同步清零_气泡_高电平有效 ,
  input  \使能端_低电平有效_stall_高电平有效 ,
  output RegWrite_3,
  output ERET_2,
  output Syscall_2,
  output MemToReg_2,
  output LUI_2,
  output MFC0_2,
  output JAL_2,
  output LBU_2,
  output MemWrite_2,
  output [3:0] AluOP_2,
  output AluSrc_2,
  output MTC0_2,
  output Beq_2,
  output Bgez_2,
  output Bne_2,
  output JMP_2,
  output JR_2,
  output [1:0] forward1,
  output [1:0] forward2_2,
  output [1:0] prediction_2,
  output [4:0] rd_2,
  output [31:0] A_2,
  output [31:0] B_2,
  output [31:0] ImmExt16_2,
  output [31:0] \ImmZeroExt16_用于LUI指令_2 ,
  output [31:0] ImmSignedExt26_2,
  output [31:0] IR_2,
  output [4:0] RegWrite_4,
  output [31:0] PC_2,
  output [31:0] PC_4_2,
  output [31:0] DesAddr_2,
  output Miss_2,
  output Hit_2,
  output \传输状态Out_表明当前传输数据有效 
);

  wire multiplexer_1_out, multiplexer_2_out, multiplexer_3_out, multiplexer_4_out, multiplexer_5_out,
       multiplexer_6_out, multiplexer_7_out, multiplexer_8_out, multiplexer_9_out, multiplexer_11_out,
       multiplexer_12_out, multiplexer_13_out, multiplexer_14_out, multiplexer_15_out, multiplexer_16_out,
       multiplexer_17_out, multiplexer_32_out, multiplexer_33_out, multiplexer_34_out, pull_resistor_2_node;
  wire [1:0] multiplexer_18_out, multiplexer_19_out, multiplexer_20_out;
  wire [3:0] multiplexer_10_out;
  wire [4:0] multiplexer_21_out, multiplexer_28_out;
  wire [31:0] multiplexer_22_out, multiplexer_23_out, multiplexer_24_out, multiplexer_25_out,
       multiplexer_26_out, multiplexer_27_out, multiplexer_29_out, multiplexer_30_out, multiplexer_31_out;

  Multiplexer #(.select(1), .width(1), .disabled("Z"), .enable("false")) multiplexer_1 (
    .in0(RegWrite), .in1(1'b0), .out(multiplexer_1_out), .sel(\同步清零_气泡_高电平有效 ));
  Multiplexer #(.select(1), .width(1), .disabled("Z"), .enable("false")) multiplexer_2 (
    .in0(ERET), .in1(1'b0), .out(multiplexer_2_out), .sel(\同步清零_气泡_高电平有效 ));
  Multiplexer #(.select(1), .width(1), .disabled("Z"), .enable("false")) multiplexer_3 (
    .in0(Syscall), .in1(1'b0), .out(multiplexer_3_out), .sel(\同步清零_气泡_高电平有效 ));
  Multiplexer #(.select(1), .width(1), .disabled("Z"), .enable("false")) multiplexer_4 (
    .in0(MemToReg), .in1(1'b0), .out(multiplexer_4_out), .sel(\同步清零_气泡_高电平有效 ));
  Multiplexer #(.select(1), .width(1), .disabled("Z"), .enable("false")) multiplexer_5 (
    .in0(LUI), .in1(1'b0), .out(multiplexer_5_out), .sel(\同步清零_气泡_高电平有效 ));
  Multiplexer #(.select(1), .width(1), .disabled("Z"), .enable("false")) multiplexer_6 (
    .in0(MFC0), .in1(1'b0), .out(multiplexer_6_out), .sel(\同步清零_气泡_高电平有效 ));
  Multiplexer #(.select(1), .width(1), .disabled("Z"), .enable("false")) multiplexer_7 (
    .in0(JAL), .in1(1'b0), .out(multiplexer_7_out), .sel(\同步清零_气泡_高电平有效 ));
  Multiplexer #(.select(1), .width(1), .disabled("Z"), .enable("false")) multiplexer_8 (
    .in0(LBU), .in1(1'b0), .out(multiplexer_8_out), .sel(\同步清零_气泡_高电平有效 ));
  Multiplexer #(.select(1), .width(1), .disabled("Z"), .enable("false")) multiplexer_9 (
    .in0(MemWrite), .in1(1'b0), .out(multiplexer_9_out), .sel(\同步清零_气泡_高电平有效 ));
  Multiplexer #(.select(1), .width(4), .disabled("Z"), .enable("false")) multiplexer_10 (
    .in0(AluOP), .in1(4'b0000), .out(multiplexer_10_out), .sel(\同步清零_气泡_高电平有效 ));
  Multiplexer #(.select(1), .width(1), .disabled("Z"), .enable("false")) multiplexer_11 (
    .in0(AluSrc), .in1(1'b0), .out(multiplexer_11_out), .sel(\同步清零_气泡_高电平有效 ));
  Multiplexer #(.select(1), .width(1), .disabled("Z"), .enable("false")) multiplexer_12 (
    .in0(MTC0), .in1(1'b0), .out(multiplexer_12_out), .sel(\同步清零_气泡_高电平有效 ));
  Multiplexer #(.select(1), .width(1), .disabled("Z"), .enable("false")) multiplexer_13 (
    .in0(Beq), .in1(1'b0), .out(multiplexer_13_out), .sel(\同步清零_气泡_高电平有效 ));
  Multiplexer #(.select(1), .width(1), .disabled("Z"), .enable("false")) multiplexer_14 (
    .in0(Bgez), .in1(1'b0), .out(multiplexer_14_out), .sel(\同步清零_气泡_高电平有效 ));
  Multiplexer #(.select(1), .width(1), .disabled("Z"), .enable("false")) multiplexer_15 (
    .in0(Bne), .in1(1'b0), .out(multiplexer_15_out), .sel(\同步清零_气泡_高电平有效 ));
  Multiplexer #(.select(1), .width(1), .disabled("Z"), .enable("false")) multiplexer_16 (
    .in0(JMP), .in1(1'b0), .out(multiplexer_16_out), .sel(\同步清零_气泡_高电平有效 ));
  Multiplexer #(.select(1), .width(1), .disabled("Z"), .enable("false")) multiplexer_17 (
    .in0(JR), .in1(1'b0), .out(multiplexer_17_out), .sel(\同步清零_气泡_高电平有效 ));
  Multiplexer #(.select(1), .width(2), .disabled("Z"), .enable("false")) multiplexer_18 (
    .in0(forwar1), .in1(2'b00), .out(multiplexer_18_out), .sel(\同步清零_气泡_高电平有效 ));
  Multiplexer #(.select(1), .width(2), .disabled("Z"), .enable("false")) multiplexer_19 (
    .in0(forward2), .in1(2'b00), .out(multiplexer_19_out), .sel(\同步清零_气泡_高电平有效 ));
  Multiplexer #(.select(1), .width(2), .disabled("Z"), .enable("false")) multiplexer_20 (
    .in0(prediction), .in1(2'b00), .out(multiplexer_20_out), .sel(\同步清零_气泡_高电平有效 ));
  Multiplexer #(.select(1), .width(5), .disabled("Z"), .enable("false")) multiplexer_21 (
    .in0(rd), .in1({5{1'b0}}), .out(multiplexer_21_out), .sel(\同步清零_气泡_高电平有效 ));
  Multiplexer #(.select(1), .width(32), .disabled("Z"), .enable("false")) multiplexer_22 (
    .in0(A), .in1({32{1'b0}}), .out(multiplexer_22_out), .sel(\同步清零_气泡_高电平有效 ));
  Multiplexer #(.select(1), .width(32), .disabled("Z"), .enable("false")) multiplexer_23 (
    .in0(B), .in1({32{1'b0}}), .out(multiplexer_23_out), .sel(\同步清零_气泡_高电平有效 ));
  Multiplexer #(.select(1), .width(32), .disabled("Z"), .enable("false")) multiplexer_24 (
    .in0(ImmExt16), .in1({32{1'b0}}), .out(multiplexer_24_out), .sel(\同步清零_气泡_高电平有效 ));
  Multiplexer #(.select(1), .width(32), .disabled("Z"), .enable("false")) multiplexer_25 (
    .in0(\ImmZeroExt16_用于LUI指令 ), .in1({32{1'b0}}), .out(multiplexer_25_out), .sel(\同步清零_气泡_高电平有效 ));
  Multiplexer #(.select(1), .width(32), .disabled("Z"), .enable("false")) multiplexer_26 (
    .in0(ImmSignedExt26), .in1({32{1'b0}}), .out(multiplexer_26_out), .sel(\同步清零_气泡_高电平有效 ));
  Multiplexer #(.select(1), .width(32), .disabled("Z"), .enable("false")) multiplexer_27 (
    .in0(IR), .in1({32{1'b0}}), .out(multiplexer_27_out), .sel(\同步清零_气泡_高电平有效 ));
  Multiplexer #(.select(1), .width(5), .disabled("Z"), .enable("false")) multiplexer_28 (
    .in0(RegWrite_2), .in1({5{1'b0}}), .out(multiplexer_28_out), .sel(\同步清零_气泡_高电平有效 ));
  Multiplexer #(.select(1), .width(32), .disabled("Z"), .enable("false")) multiplexer_29 (
    .in0(PC), .in1({32{1'b0}}), .out(multiplexer_29_out), .sel(\同步清零_气泡_高电平有效 ));
  Multiplexer #(.select(1), .width(32), .disabled("Z"), .enable("false")) multiplexer_30 (
    .in0(PC_4), .in1({32{1'b0}}), .out(multiplexer_30_out), .sel(\同步清零_气泡_高电平有效 ));
  Multiplexer #(.select(1), .width(32), .disabled("Z"), .enable("false")) multiplexer_31 (
    .in0(DesAddr), .in1({32{1'b0}}), .out(multiplexer_31_out), .sel(\同步清零_气泡_高电平有效 ));
  Multiplexer #(.select(1), .width(1), .disabled("Z"), .enable("false")) multiplexer_32 (
    .in0(Miss), .in1(1'b0), .out(multiplexer_32_out), .sel(\同步清零_气泡_高电平有效 ));
  Multiplexer #(.select(1), .width(1), .disabled("Z"), .enable("false")) multiplexer_33 (
    .in0(Hit), .in1(1'b0), .out(multiplexer_33_out), .sel(\同步清零_气泡_高电平有效 ));
  Multiplexer #(.select(1), .width(1), .disabled("Z"), .enable("false")) multiplexer_34 (
    .in0(\传输状态In_表明当前传输数据有效 ), .in1(1'b0), .out(multiplexer_34_out), .sel(\同步清零_气泡_高电平有效 ));
  Pull_Resistor #(.pull(0)) pull_resistor_1 (.node(\同步清零_气泡_高电平有效 ));
  Pull_Resistor #(.pull(0)) pull_resistor_2 (.node(pull_resistor_2_node));
  not not_1 (pull_resistor_2_node, \使能端_低电平有效_stall_高电平有效 );
  Register #(.width(1), .trigger("rising"), .Select("low")) register_1 (
    .D(multiplexer_1_out), .en(pull_resistor_2_node), .Q(RegWrite_3), .clk(CLK));  // open: clr
  Register #(.width(1), .trigger("rising"), .Select("low")) register_2 (
    .D(multiplexer_2_out), .en(pull_resistor_2_node), .Q(ERET_2), .clk(CLK));  // open: clr
  Register #(.width(1), .trigger("rising"), .Select("low")) register_3 (
    .D(multiplexer_3_out), .en(pull_resistor_2_node), .Q(Syscall_2), .clk(CLK));  // open: clr
  Register #(.width(1), .trigger("rising"), .Select("low")) register_4 (
    .D(multiplexer_4_out), .en(pull_resistor_2_node), .Q(MemToReg_2), .clk(CLK));  // open: clr
  Register #(.width(1), .trigger("rising"), .Select("low")) register_5 (
    .D(multiplexer_5_out), .en(pull_resistor_2_node), .Q(LUI_2), .clk(CLK));  // open: clr
  Register #(.width(1), .trigger("rising"), .Select("low")) register_6 (
    .D(multiplexer_6_out), .en(pull_resistor_2_node), .Q(MFC0_2), .clk(CLK));  // open: clr
  Register #(.width(1), .trigger("rising"), .Select("low")) register_7 (
    .D(multiplexer_7_out), .en(pull_resistor_2_node), .Q(JAL_2), .clk(CLK));  // open: clr
  Register #(.width(1), .trigger("rising"), .Select("low")) register_8 (
    .D(multiplexer_8_out), .en(pull_resistor_2_node), .Q(LBU_2), .clk(CLK));  // open: clr
  Register #(.width(1), .trigger("rising"), .Select("low")) register_9 (
    .D(multiplexer_9_out), .en(pull_resistor_2_node), .Q(MemWrite_2), .clk(CLK));  // open: clr
  Register #(.width(4), .trigger("rising"), .Select("low")) register_10 (
    .D(multiplexer_10_out), .en(pull_resistor_2_node), .Q(AluOP_2), .clk(CLK));  // open: clr
  Register #(.width(1), .trigger("rising"), .Select("low")) register_11 (
    .D(multiplexer_11_out), .en(pull_resistor_2_node), .Q(AluSrc_2), .clk(CLK));  // open: clr
  Register #(.width(1), .trigger("rising"), .Select("low")) register_12 (
    .D(multiplexer_12_out), .en(pull_resistor_2_node), .Q(MTC0_2), .clk(CLK));  // open: clr
  Register #(.width(1), .trigger("rising"), .Select("low")) register_13 (
    .D(multiplexer_13_out), .en(pull_resistor_2_node), .Q(Beq_2), .clk(CLK));  // open: clr
  Register #(.width(1), .trigger("rising"), .Select("low")) register_14 (
    .D(multiplexer_14_out), .en(pull_resistor_2_node), .Q(Bgez_2), .clk(CLK));  // open: clr
  Register #(.width(1), .trigger("rising"), .Select("low")) register_15 (
    .D(multiplexer_15_out), .en(pull_resistor_2_node), .Q(Bne_2), .clk(CLK));  // open: clr
  Register #(.width(1), .trigger("rising"), .Select("low")) register_16 (
    .D(multiplexer_16_out), .en(pull_resistor_2_node), .Q(JMP_2), .clk(CLK));  // open: clr
  Register #(.width(1), .trigger("rising"), .Select("low")) register_17 (
    .D(multiplexer_17_out), .en(pull_resistor_2_node), .Q(JR_2), .clk(CLK));  // open: clr
  Register #(.width(2), .trigger("rising"), .Select("low")) register_18 (
    .D(multiplexer_18_out), .en(pull_resistor_2_node), .Q(forward1), .clk(CLK));  // open: clr
  Register #(.width(2), .trigger("rising"), .Select("low")) register_19 (
    .D(multiplexer_19_out), .en(pull_resistor_2_node), .Q(forward2_2), .clk(CLK));  // open: clr
  Register #(.width(2), .trigger("rising"), .Select("low")) register_20 (
    .D(multiplexer_20_out), .en(pull_resistor_2_node), .Q(prediction_2), .clk(CLK));  // open: clr
  Register #(.width(5), .trigger("rising"), .Select("low")) register_21 (
    .D(multiplexer_21_out), .en(pull_resistor_2_node), .Q(rd_2), .clk(CLK));  // open: clr
  Register #(.width(32), .trigger("rising"), .Select("low")) register_22 (
    .D(multiplexer_22_out), .en(pull_resistor_2_node), .Q(A_2), .clk(CLK));  // open: clr
  Register #(.width(32), .trigger("rising"), .Select("low")) register_23 (
    .D(multiplexer_23_out), .en(pull_resistor_2_node), .Q(B_2), .clk(CLK));  // open: clr
  Register #(.width(32), .trigger("rising"), .Select("low")) register_24 (
    .D(multiplexer_24_out), .en(pull_resistor_2_node), .Q(ImmExt16_2), .clk(CLK));  // open: clr
  Register #(.width(32), .trigger("rising"), .Select("low")) register_25 (
    .D(multiplexer_25_out), .en(pull_resistor_2_node), .Q(\ImmZeroExt16_用于LUI指令_2 ), .clk(CLK));  // open: clr
  Register #(.width(32), .trigger("rising"), .Select("low")) register_26 (
    .D(multiplexer_26_out), .en(pull_resistor_2_node), .Q(ImmSignedExt26_2), .clk(CLK));  // open: clr
  Register #(.width(32), .trigger("rising"), .Select("low")) register_27 (
    .D(multiplexer_27_out), .en(pull_resistor_2_node), .Q(IR_2), .clk(CLK));  // open: clr
  Register #(.width(5), .trigger("rising"), .Select("low")) register_28 (
    .D(multiplexer_28_out), .en(pull_resistor_2_node), .Q(RegWrite_4), .clk(CLK));  // open: clr
  Register #(.width(32), .trigger("rising"), .Select("low")) register_29 (
    .D(multiplexer_29_out), .en(pull_resistor_2_node), .Q(PC_2), .clk(CLK));  // open: clr
  Register #(.width(32), .trigger("rising"), .Select("low")) register_30 (
    .D(multiplexer_30_out), .en(pull_resistor_2_node), .Q(PC_4_2), .clk(CLK));  // open: clr
  Register #(.width(32), .trigger("rising"), .Select("low")) register_31 (
    .D(multiplexer_31_out), .en(pull_resistor_2_node), .Q(DesAddr_2), .clk(CLK));  // open: clr
  Register #(.width(1), .trigger("rising"), .Select("low")) register_32 (
    .D(multiplexer_32_out), .en(pull_resistor_2_node), .Q(Miss_2), .clk(CLK));  // open: clr
  Register #(.width(1), .trigger("rising"), .Select("low")) register_33 (
    .D(multiplexer_33_out), .en(pull_resistor_2_node), .Q(Hit_2), .clk(CLK));  // open: clr
  Register #(.width(1), .trigger("rising"), .Select("low")) register_34 (
    .D(multiplexer_34_out), .en(pull_resistor_2_node), .Q(\传输状态Out_表明当前传输数据有效 ), .clk(CLK));  // open: clr

  // Notes on the sheet:
  //   同步清零_气泡_高电平有效: pull=down
  //   使能端_低电平有效_stall_高电平有效: pull=down
endmodule

module EX_MEM (
  input  RegWrite,
  input  ERET,
  input  Syscall,
  input  MemToReg,
  input  LUI,
  input  MFC0,
  input  JAL,
  input  LBU,
  input  MemWrite,
  input  ifshow,
  input  [4:0] rd,
  input  MTC0,
  input  [31:0] LedData,
  input  [31:0] B,
  input  [31:0] ALU,
  input  [31:0] IR,
  input  [4:0] RegWrite_2,
  input  [31:0] ImmZeroExt16Shift,
  input  [31:0] PC,
  input  [31:0] PC_4,
  input  [31:0] IRout,
  input  \传输状态In_表明当前传输数据有效 ,
  input  CLK,
  input  \同步清零_气泡_高电平有效 ,
  input  \使能端_低电平有效_stall_高电平有效 ,
  output RegWrite_3,
  output ERET_2,
  output Syscall_2,
  output MemToReg_2,
  output LUI_2,
  output MFC0_2,
  output JAL_2,
  output LBU_2,
  output MemWrite_2,
  output ifshow_2,
  output [4:0] rd_2,
  output MTC0_2,
  output [31:0] LeaData,
  output [31:0] B_2,
  output [31:0] ALU_2,
  output [31:0] IR_2,
  output [4:0] RegWrite_4,
  output [31:0] ImmZeroExt16Shift_2,
  output [31:0] PC_2,
  output [31:0] PC_4_2,
  output [31:0] IRout_2,
  output \传输状态Out_表明当前传输数据有效 
);

  wire multiplexer_1_out, multiplexer_2_out, multiplexer_3_out, multiplexer_4_out, multiplexer_5_out,
       multiplexer_6_out, multiplexer_7_out, multiplexer_8_out, multiplexer_9_out, multiplexer_10_out,
       multiplexer_12_out, multiplexer_22_out, pull_resistor_2_node;
  wire [4:0] multiplexer_11_out, multiplexer_17_out;
  wire [31:0] multiplexer_13_out, multiplexer_14_out, multiplexer_15_out, multiplexer_16_out,
       multiplexer_18_out, multiplexer_19_out, multiplexer_20_out, multiplexer_21_out;

  Multiplexer #(.select(1), .width(1), .disabled("Z"), .enable("false")) multiplexer_1 (
    .in0(RegWrite), .in1(1'b0), .out(multiplexer_1_out), .sel(\同步清零_气泡_高电平有效 ));
  Multiplexer #(.select(1), .width(1), .disabled("Z"), .enable("false")) multiplexer_2 (
    .in0(ERET), .in1(1'b0), .out(multiplexer_2_out), .sel(\同步清零_气泡_高电平有效 ));
  Multiplexer #(.select(1), .width(1), .disabled("Z"), .enable("false")) multiplexer_3 (
    .in0(Syscall), .in1(1'b0), .out(multiplexer_3_out), .sel(\同步清零_气泡_高电平有效 ));
  Multiplexer #(.select(1), .width(1), .disabled("Z"), .enable("false")) multiplexer_4 (
    .in0(MemToReg), .in1(1'b0), .out(multiplexer_4_out), .sel(\同步清零_气泡_高电平有效 ));
  Multiplexer #(.select(1), .width(1), .disabled("Z"), .enable("false")) multiplexer_5 (
    .in0(LUI), .in1(1'b0), .out(multiplexer_5_out), .sel(\同步清零_气泡_高电平有效 ));
  Multiplexer #(.select(1), .width(1), .disabled("Z"), .enable("false")) multiplexer_6 (
    .in0(MFC0), .in1(1'b0), .out(multiplexer_6_out), .sel(\同步清零_气泡_高电平有效 ));
  Multiplexer #(.select(1), .width(1), .disabled("Z"), .enable("false")) multiplexer_7 (
    .in0(JAL), .in1(1'b0), .out(multiplexer_7_out), .sel(\同步清零_气泡_高电平有效 ));
  Multiplexer #(.select(1), .width(1), .disabled("Z"), .enable("false")) multiplexer_8 (
    .in0(LBU), .in1(1'b0), .out(multiplexer_8_out), .sel(\同步清零_气泡_高电平有效 ));
  Multiplexer #(.select(1), .width(1), .disabled("Z"), .enable("false")) multiplexer_9 (
    .in0(MemWrite), .in1(1'b0), .out(multiplexer_9_out), .sel(\同步清零_气泡_高电平有效 ));
  Multiplexer #(.select(1), .width(1), .disabled("Z"), .enable("false")) multiplexer_10 (
    .in0(ifshow), .in1(1'b0), .out(multiplexer_10_out), .sel(\同步清零_气泡_高电平有效 ));
  Multiplexer #(.select(1), .width(5), .disabled("Z"), .enable("false")) multiplexer_11 (
    .in0(rd), .in1({5{1'b0}}), .out(multiplexer_11_out), .sel(\同步清零_气泡_高电平有效 ));
  Multiplexer #(.select(1), .width(1), .disabled("Z"), .enable("false")) multiplexer_12 (
    .in0(MTC0), .in1(1'b0), .out(multiplexer_12_out), .sel(\同步清零_气泡_高电平有效 ));
  Multiplexer #(.select(1), .width(32), .disabled("Z"), .enable("false")) multiplexer_13 (
    .in0(LedData), .in1({32{1'b0}}), .out(multiplexer_13_out), .sel(\同步清零_气泡_高电平有效 ));
  Multiplexer #(.select(1), .width(32), .disabled("Z"), .enable("false")) multiplexer_14 (
    .in0(B), .in1({32{1'b0}}), .out(multiplexer_14_out), .sel(\同步清零_气泡_高电平有效 ));
  Multiplexer #(.select(1), .width(32), .disabled("Z"), .enable("false")) multiplexer_15 (
    .in0(ALU), .in1({32{1'b0}}), .out(multiplexer_15_out), .sel(\同步清零_气泡_高电平有效 ));
  Multiplexer #(.select(1), .width(32), .disabled("Z"), .enable("false")) multiplexer_16 (
    .in0(IR), .in1({32{1'b0}}), .out(multiplexer_16_out), .sel(\同步清零_气泡_高电平有效 ));
  Multiplexer #(.select(1), .width(5), .disabled("Z"), .enable("false")) multiplexer_17 (
    .in0(RegWrite_2), .in1({5{1'b0}}), .out(multiplexer_17_out), .sel(\同步清零_气泡_高电平有效 ));
  Multiplexer #(.select(1), .width(32), .disabled("Z"), .enable("false")) multiplexer_18 (
    .in0(ImmZeroExt16Shift), .in1({32{1'b0}}), .out(multiplexer_18_out), .sel(\同步清零_气泡_高电平有效 ));
  Multiplexer #(.select(1), .width(32), .disabled("Z"), .enable("false")) multiplexer_19 (
    .in0(PC), .in1({32{1'b0}}), .out(multiplexer_19_out), .sel(\同步清零_气泡_高电平有效 ));
  Multiplexer #(.select(1), .width(32), .disabled("Z"), .enable("false")) multiplexer_20 (
    .in0(PC_4), .in1({32{1'b0}}), .out(multiplexer_20_out), .sel(\同步清零_气泡_高电平有效 ));
  Multiplexer #(.select(1), .width(32), .disabled("Z"), .enable("false")) multiplexer_21 (
    .in0(IRout), .in1({32{1'b0}}), .out(multiplexer_21_out), .sel(\同步清零_气泡_高电平有效 ));
  Multiplexer #(.select(1), .width(1), .disabled("Z"), .enable("false")) multiplexer_22 (
    .in0(\传输状态In_表明当前传输数据有效 ), .in1(1'b0), .out(multiplexer_22_out), .sel(\同步清零_气泡_高电平有效 ));
  Pull_Resistor #(.pull(0)) pull_resistor_1 (.node(\同步清零_气泡_高电平有效 ));
  Register #(.width(1), .trigger("rising"), .Select("low")) register_1 (
    .D(multiplexer_1_out), .en(pull_resistor_2_node), .Q(RegWrite_3), .clk(CLK));  // open: clr
  Register #(.width(1), .trigger("rising"), .Select("low")) register_2 (
    .D(multiplexer_2_out), .en(pull_resistor_2_node), .Q(ERET_2), .clk(CLK));  // open: clr
  Register #(.width(1), .trigger("rising"), .Select("low")) register_3 (
    .D(multiplexer_3_out), .en(pull_resistor_2_node), .Q(Syscall_2), .clk(CLK));  // open: clr
  Register #(.width(1), .trigger("rising"), .Select("low")) register_4 (
    .D(multiplexer_4_out), .en(pull_resistor_2_node), .Q(MemToReg_2), .clk(CLK));  // open: clr
  Register #(.width(1), .trigger("rising"), .Select("low")) register_5 (
    .D(multiplexer_5_out), .en(pull_resistor_2_node), .Q(LUI_2), .clk(CLK));  // open: clr
  Register #(.width(1), .trigger("rising"), .Select("low")) register_6 (
    .D(multiplexer_6_out), .en(pull_resistor_2_node), .Q(MFC0_2), .clk(CLK));  // open: clr
  Register #(.width(1), .trigger("rising"), .Select("low")) register_7 (
    .D(multiplexer_7_out), .en(pull_resistor_2_node), .Q(JAL_2), .clk(CLK));  // open: clr
  Register #(.width(1), .trigger("rising"), .Select("low")) register_8 (
    .D(multiplexer_8_out), .en(pull_resistor_2_node), .Q(LBU_2), .clk(CLK));  // open: clr
  Register #(.width(1), .trigger("rising"), .Select("low")) register_9 (
    .D(multiplexer_9_out), .en(pull_resistor_2_node), .Q(MemWrite_2), .clk(CLK));  // open: clr
  Register #(.width(1), .trigger("rising"), .Select("low")) register_10 (
    .D(multiplexer_10_out), .en(pull_resistor_2_node), .Q(ifshow_2), .clk(CLK));  // open: clr
  Register #(.width(5), .trigger("rising"), .Select("low")) register_11 (
    .D(multiplexer_11_out), .en(pull_resistor_2_node), .Q(rd_2), .clk(CLK));  // open: clr
  Register #(.width(1), .trigger("rising"), .Select("low")) register_12 (
    .D(multiplexer_12_out), .en(pull_resistor_2_node), .Q(MTC0_2), .clk(CLK));  // open: clr
  Register #(.width(32), .trigger("rising"), .Select("low")) register_13 (
    .D(multiplexer_13_out), .en(pull_resistor_2_node), .Q(LeaData), .clk(CLK));  // open: clr
  Register #(.width(32), .trigger("rising"), .Select("low")) register_14 (
    .D(multiplexer_14_out), .en(pull_resistor_2_node), .Q(B_2), .clk(CLK));  // open: clr
  Register #(.width(32), .trigger("rising"), .Select("low")) register_15 (
    .D(multiplexer_15_out), .en(pull_resistor_2_node), .Q(ALU_2), .clk(CLK));  // open: clr
  Register #(.width(32), .trigger("rising"), .Select("low")) register_16 (
    .D(multiplexer_16_out), .en(pull_resistor_2_node), .Q(IR_2), .clk(CLK));  // open: clr
  Register #(.width(5), .trigger("rising"), .Select("low")) register_17 (
    .D(multiplexer_17_out), .en(pull_resistor_2_node), .Q(RegWrite_4), .clk(CLK));  // open: clr
  Register #(.width(32), .trigger("rising"), .Select("low")) register_18 (
    .D(multiplexer_18_out), .en(pull_resistor_2_node), .Q(ImmZeroExt16Shift_2), .clk(CLK));  // open: clr
  Register #(.width(32), .trigger("rising"), .Select("low")) register_19 (
    .D(multiplexer_19_out), .en(pull_resistor_2_node), .Q(PC_2), .clk(CLK));  // open: clr
  Register #(.width(32), .trigger("rising"), .Select("low")) register_20 (
    .D(multiplexer_20_out), .en(pull_resistor_2_node), .Q(PC_4_2), .clk(CLK));  // open: clr
  Register #(.width(32), .trigger("rising"), .Select("low")) register_21 (
    .D(multiplexer_21_out), .en(pull_resistor_2_node), .Q(IRout_2), .clk(CLK));  // open: clr
  Pull_Resistor #(.pull(0)) pull_resistor_2 (.node(pull_resistor_2_node));
  not not_1 (pull_resistor_2_node, \使能端_低电平有效_stall_高电平有效 );
  Register #(.width(1), .trigger("rising"), .Select("low")) register_22 (
    .D(multiplexer_22_out), .en(pull_resistor_2_node), .Q(\传输状态Out_表明当前传输数据有效 ), .clk(CLK));  // open: clr

  // Notes on the sheet:
  //   使能端_低电平有效_stall_高电平有效: pull=down
  //   同步清零_气泡_高电平有效: pull=down
endmodule

module MEM_WB (
  input  RegWrite,
  input  ERET,
  input  Syscall,
  input  MemToReg,
  input  LUI,
  input  MFC0,
  input  JAL,
  input  LBU,
  input  ifshow,
  input  [4:0] rd,
  input  MTC0,
  input  [31:0] LedData,
  input  [31:0] ImmZeroExt16Shift,
  input  [31:0] ALU,
  input  [31:0] MD,
  input  [31:0] IR,
  input  [4:0] RegWrite_2,
  input  [31:0] PC,
  input  [31:0] PC_4,
  input  [31:0] IRout,
  input  \传输状态In_表明当前传输数据有效 ,
  input  CLK,
  input  \同步清零_气泡_高电平有效 ,
  input  \使能端_低电平有效_stall_高电平有效 ,
  output RegWrite_3,
  output ERET_2,
  output Syscall_2,
  output MemToReg_2,
  output LUI_2,
  output MFC0_2,
  output JAL_2,
  output LBU_2,
  output ifshow_2,
  output [4:0] rd_2,
  output MTC0_2,
  output [31:0] LedData_2,
  output [31:0] ImmZeroExt16Shift_2,
  output [31:0] ALU_2,
  output [31:0] MD_2,
  output [31:0] IR_2,
  output [4:0] RegWrite_4,
  output [31:0] PC_2,
  output [31:0] PC_4_2,
  output [31:0] IRout_2,
  output \传输状态Out_表明当前传输数据有效 
);

  wire multiplexer_1_out, multiplexer_2_out, multiplexer_3_out, multiplexer_4_out, multiplexer_5_out,
       multiplexer_6_out, multiplexer_7_out, multiplexer_8_out, multiplexer_9_out, multiplexer_11_out,
       multiplexer_21_out, pull_resistor_2_node;
  wire [4:0] multiplexer_10_out, multiplexer_17_out;
  wire [31:0] multiplexer_12_out, multiplexer_13_out, multiplexer_14_out, multiplexer_15_out,
       multiplexer_16_out, multiplexer_18_out, multiplexer_19_out, multiplexer_20_out;

  Multiplexer #(.select(1), .width(1), .disabled("Z"), .enable("false")) multiplexer_1 (
    .in0(RegWrite), .in1(1'b0), .out(multiplexer_1_out), .sel(\同步清零_气泡_高电平有效 ));
  Multiplexer #(.select(1), .width(1), .disabled("Z"), .enable("false")) multiplexer_2 (
    .in0(ERET), .in1(1'b0), .out(multiplexer_2_out), .sel(\同步清零_气泡_高电平有效 ));
  Multiplexer #(.select(1), .width(1), .disabled("Z"), .enable("false")) multiplexer_3 (
    .in0(Syscall), .in1(1'b0), .out(multiplexer_3_out), .sel(\同步清零_气泡_高电平有效 ));
  Multiplexer #(.select(1), .width(1), .disabled("Z"), .enable("false")) multiplexer_4 (
    .in0(MemToReg), .in1(1'b0), .out(multiplexer_4_out), .sel(\同步清零_气泡_高电平有效 ));
  Multiplexer #(.select(1), .width(1), .disabled("Z"), .enable("false")) multiplexer_5 (
    .in0(LUI), .in1(1'b0), .out(multiplexer_5_out), .sel(\同步清零_气泡_高电平有效 ));
  Multiplexer #(.select(1), .width(1), .disabled("Z"), .enable("false")) multiplexer_6 (
    .in0(MFC0), .in1(1'b0), .out(multiplexer_6_out), .sel(\同步清零_气泡_高电平有效 ));
  Multiplexer #(.select(1), .width(1), .disabled("Z"), .enable("false")) multiplexer_7 (
    .in0(JAL), .in1(1'b0), .out(multiplexer_7_out), .sel(\同步清零_气泡_高电平有效 ));
  Multiplexer #(.select(1), .width(1), .disabled("Z"), .enable("false")) multiplexer_8 (
    .in0(LBU), .in1(1'b0), .out(multiplexer_8_out), .sel(\同步清零_气泡_高电平有效 ));
  Multiplexer #(.select(1), .width(1), .disabled("Z"), .enable("false")) multiplexer_9 (
    .in0(ifshow), .in1(1'b0), .out(multiplexer_9_out), .sel(\同步清零_气泡_高电平有效 ));
  Multiplexer #(.select(1), .width(5), .disabled("Z"), .enable("false")) multiplexer_10 (
    .in0(rd), .in1({5{1'b0}}), .out(multiplexer_10_out), .sel(\同步清零_气泡_高电平有效 ));
  Multiplexer #(.select(1), .width(1), .disabled("Z"), .enable("false")) multiplexer_11 (
    .in0(MTC0), .in1(1'b0), .out(multiplexer_11_out), .sel(\同步清零_气泡_高电平有效 ));
  Multiplexer #(.select(1), .width(32), .disabled("Z"), .enable("false")) multiplexer_12 (
    .in0(LedData), .in1({32{1'b0}}), .out(multiplexer_12_out), .sel(\同步清零_气泡_高电平有效 ));
  Multiplexer #(.select(1), .width(32), .disabled("Z"), .enable("false")) multiplexer_13 (
    .in0(ImmZeroExt16Shift), .in1({32{1'b0}}), .out(multiplexer_13_out), .sel(\同步清零_气泡_高电平有效 ));
  Multiplexer #(.select(1), .width(32), .disabled("Z"), .enable("false")) multiplexer_14 (
    .in0(ALU), .in1({32{1'b0}}), .out(multiplexer_14_out), .sel(\同步清零_气泡_高电平有效 ));
  Multiplexer #(.select(1), .width(32), .disabled("Z"), .enable("false")) multiplexer_15 (
    .in0(MD), .in1({32{1'b0}}), .out(multiplexer_15_out), .sel(\同步清零_气泡_高电平有效 ));
  Multiplexer #(.select(1), .width(32), .disabled("Z"), .enable("false")) multiplexer_16 (
    .in0(IR), .in1({32{1'b0}}), .out(multiplexer_16_out), .sel(\同步清零_气泡_高电平有效 ));
  Multiplexer #(.select(1), .width(5), .disabled("Z"), .enable("false")) multiplexer_17 (
    .in0(RegWrite_2), .in1({5{1'b0}}), .out(multiplexer_17_out), .sel(\同步清零_气泡_高电平有效 ));
  Multiplexer #(.select(1), .width(32), .disabled("Z"), .enable("false")) multiplexer_18 (
    .in0(PC), .in1({32{1'b0}}), .out(multiplexer_18_out), .sel(\同步清零_气泡_高电平有效 ));
  Multiplexer #(.select(1), .width(32), .disabled("Z"), .enable("false")) multiplexer_19 (
    .in0(PC_4), .in1({32{1'b0}}), .out(multiplexer_19_out), .sel(\同步清零_气泡_高电平有效 ));
  Multiplexer #(.select(1), .width(32), .disabled("Z"), .enable("false")) multiplexer_20 (
    .in0(IRout), .in1({32{1'b0}}), .out(multiplexer_20_out), .sel(\同步清零_气泡_高电平有效 ));
  Multiplexer #(.select(1), .width(1), .disabled("Z"), .enable("false")) multiplexer_21 (
    .in0(\传输状态In_表明当前传输数据有效 ), .in1(1'b0), .out(multiplexer_21_out), .sel(\同步清零_气泡_高电平有效 ));
  Pull_Resistor #(.pull(0)) pull_resistor_1 (.node(\同步清零_气泡_高电平有效 ));
  Register #(.width(1), .trigger("rising"), .Select("low")) register_1 (
    .D(multiplexer_1_out), .en(pull_resistor_2_node), .Q(RegWrite_3), .clk(CLK));  // open: clr
  Register #(.width(1), .trigger("rising"), .Select("low")) register_2 (
    .D(multiplexer_2_out), .en(pull_resistor_2_node), .Q(ERET_2), .clk(CLK));  // open: clr
  Register #(.width(1), .trigger("rising"), .Select("low")) register_3 (
    .D(multiplexer_3_out), .en(pull_resistor_2_node), .Q(Syscall_2), .clk(CLK));  // open: clr
  Register #(.width(1), .trigger("rising"), .Select("low")) register_4 (
    .D(multiplexer_4_out), .en(pull_resistor_2_node), .Q(MemToReg_2), .clk(CLK));  // open: clr
  Register #(.width(1), .trigger("rising"), .Select("low")) register_5 (
    .D(multiplexer_5_out), .en(pull_resistor_2_node), .Q(LUI_2), .clk(CLK));  // open: clr
  Register #(.width(1), .trigger("rising"), .Select("low")) register_6 (
    .D(multiplexer_6_out), .en(pull_resistor_2_node), .Q(MFC0_2), .clk(CLK));  // open: clr
  Register #(.width(1), .trigger("rising"), .Select("low")) register_7 (
    .D(multiplexer_7_out), .en(pull_resistor_2_node), .Q(JAL_2), .clk(CLK));  // open: clr
  Register #(.width(1), .trigger("rising"), .Select("low")) register_8 (
    .D(multiplexer_8_out), .en(pull_resistor_2_node), .Q(LBU_2), .clk(CLK));  // open: clr
  Register #(.width(1), .trigger("rising"), .Select("low")) register_9 (
    .D(multiplexer_9_out), .en(pull_resistor_2_node), .Q(ifshow_2), .clk(CLK));  // open: clr
  Register #(.width(5), .trigger("rising"), .Select("low")) register_10 (
    .D(multiplexer_10_out), .en(pull_resistor_2_node), .Q(rd_2), .clk(CLK));  // open: clr
  Register #(.width(1), .trigger("rising"), .Select("low")) register_11 (
    .D(multiplexer_11_out), .en(pull_resistor_2_node), .Q(MTC0_2), .clk(CLK));  // open: clr
  Register #(.width(32), .trigger("rising"), .Select("low")) register_12 (
    .D(multiplexer_12_out), .en(pull_resistor_2_node), .Q(LedData_2), .clk(CLK));  // open: clr
  Register #(.width(32), .trigger("rising"), .Select("low")) register_13 (
    .D(multiplexer_13_out), .en(pull_resistor_2_node), .Q(ImmZeroExt16Shift_2), .clk(CLK));  // open: clr
  Register #(.width(32), .trigger("rising"), .Select("low")) register_14 (
    .D(multiplexer_14_out), .en(pull_resistor_2_node), .Q(ALU_2), .clk(CLK));  // open: clr
  Register #(.width(32), .trigger("rising"), .Select("low")) register_15 (
    .D(multiplexer_15_out), .en(pull_resistor_2_node), .Q(MD_2), .clk(CLK));  // open: clr
  Register #(.width(32), .trigger("rising"), .Select("low")) register_16 (
    .D(multiplexer_16_out), .en(pull_resistor_2_node), .Q(IR_2), .clk(CLK));  // open: clr
  Register #(.width(5), .trigger("rising"), .Select("low")) register_17 (
    .D(multiplexer_17_out), .en(pull_resistor_2_node), .Q(RegWrite_4), .clk(CLK));  // open: clr
  Register #(.width(32), .trigger("rising"), .Select("low")) register_18 (
    .D(multiplexer_18_out), .en(pull_resistor_2_node), .Q(PC_2), .clk(CLK));  // open: clr
  Register #(.width(32), .trigger("rising"), .Select("low")) register_19 (
    .D(multiplexer_19_out), .en(pull_resistor_2_node), .Q(PC_4_2), .clk(CLK));  // open: clr
  Register #(.width(32), .trigger("rising"), .Select("low")) register_20 (
    .D(multiplexer_20_out), .en(pull_resistor_2_node), .Q(IRout_2), .clk(CLK));  // open: clr
  Pull_Resistor #(.pull(0)) pull_resistor_2 (.node(pull_resistor_2_node));
  not not_1 (pull_resistor_2_node, \使能端_低电平有效_stall_高电平有效 );
  Register #(.width(1), .trigger("rising"), .Select("low")) register_21 (
    .D(multiplexer_21_out), .en(pull_resistor_2_node), .Q(\传输状态Out_表明当前传输数据有效 ), .clk(CLK));  // open: clr

  // Notes on the sheet:
  //   同步清零_气泡_高电平有效: pull=down
  //   使能端_低电平有效_stall_高电平有效: pull=down
endmodule

// 源寄存器使用情况
module \源寄存器使用情况  (
  input  OP0,
  input  OP1,
  input  OP2,
  input  OP3,
  input  OP4,
  input  OP5,
  input  F0,
  input  F1,
  input  F2,
  input  F3,
  input  F4,
  input  F5,
  output R1_Used,
  output R2_Used
);

  wire and_1_out, and_2_out, and_3_out, and_4_out, and_5_out, and_6_out, and_7_out, and_8_out, and_9_out,
       and_10_out, and_11_out, and_12_out, and_13_out, and_14_out, and_15_out, and_16_out, and_17_out,
       and_18_out, and_19_out, and_20_out, and_21_out, and_22_out, and_23_out, and_24_out, and_25_out,
       and_26_out, and_27_out, and_28_out, and_29_out, and_30_out, and_31_out, and_32_out, and_33_out,
       and_34_out, and_35_out, and_36_out, and_37_out, and_38_out, and_39_out, and_40_out, and_41_out,
       and_42_out, and_43_out, and_44_out, not_1_out, not_2_out, not_3_out, not_4_out, not_5_out, not_6_out,
       not_7_out, not_8_out, not_9_out, not_10_out, not_11_out, not_12_out, not_13_out, not_14_out,
       not_15_out, not_16_out, not_17_out, not_18_out, not_19_out, not_20_out, not_21_out, not_22_out,
       not_23_out, not_24_out, not_25_out, not_26_out, not_27_out, not_28_out, not_29_out, not_30_out,
       not_31_out, not_32_out, not_33_out, not_34_out, not_35_out, not_36_out, not_37_out, not_38_out,
       not_39_out, not_40_out, not_41_out, not_42_out, not_43_out, not_44_out, not_45_out, not_46_out,
       not_47_out, not_48_out, not_49_out, not_50_out, not_51_out, not_52_out, not_53_out, not_54_out,
       not_55_out, not_56_out, not_57_out, not_58_out, not_59_out, not_60_out, not_61_out, not_62_out,
       not_63_out, not_64_out, not_65_out, not_66_out, not_67_out, not_68_out, not_69_out, not_70_out,
       not_71_out, not_72_out, not_73_out, not_74_out, not_75_out, not_76_out, not_77_out, not_78_out,
       not_79_out, not_80_out, not_81_out, not_82_out, not_83_out, not_84_out, not_85_out, not_86_out,
       not_87_out, not_88_out, not_89_out, not_90_out, not_91_out, not_92_out, not_93_out, not_94_out,
       not_95_out, not_96_out, not_97_out, not_98_out, not_99_out, not_100_out, not_101_out, not_102_out,
       not_103_out, not_104_out, not_105_out, not_106_out, not_107_out, not_108_out, not_109_out,
       not_110_out, not_111_out, not_112_out, not_113_out, not_114_out, not_115_out, not_116_out,
       not_117_out, not_118_out, not_119_out, not_120_out, not_121_out, not_122_out, not_123_out,
       not_124_out, not_125_out, not_126_out, not_127_out, not_128_out, not_129_out, not_130_out,
       not_131_out, not_132_out, not_133_out, not_134_out, not_135_out, not_136_out, not_137_out,
       not_138_out, not_139_out, not_140_out, not_141_out, not_142_out, not_143_out, not_144_out,
       not_145_out, not_146_out, not_147_out, not_148_out, not_149_out, not_150_out, not_151_out,
       not_152_out, not_153_out, not_154_out, not_155_out, not_156_out, not_157_out, not_158_out,
       not_159_out, not_160_out, not_161_out, not_162_out, not_163_out, not_164_out, not_165_out,
       not_166_out, not_167_out, not_168_out, not_169_out, not_170_out, not_171_out, not_172_out,
       not_173_out, not_174_out, not_175_out, not_176_out, not_177_out, not_178_out, not_179_out,
       not_180_out, not_181_out, not_182_out, not_183_out, not_184_out, not_185_out, not_186_out,
       not_187_out, not_188_out, not_189_out, not_190_out, not_191_out, not_192_out, not_193_out,
       not_194_out, not_195_out, not_196_out, not_197_out, not_198_out, not_199_out, not_200_out,
       not_201_out, not_202_out, not_203_out, not_204_out, not_205_out, not_206_out, not_207_out,
       not_208_out, not_209_out, not_210_out, not_211_out, not_212_out, not_213_out, not_214_out,
       not_215_out, not_216_out, not_217_out, not_218_out, not_219_out, not_220_out, not_221_out,
       not_222_out, not_223_out, not_224_out, not_225_out, not_226_out, not_227_out, not_228_out,
       not_229_out, not_230_out, not_231_out, not_232_out, not_233_out, not_234_out, not_235_out,
       not_236_out, not_237_out, not_238_out, not_239_out, not_240_out, not_241_out, not_242_out,
       not_243_out, not_244_out, not_245_out, not_246_out, not_247_out, not_248_out, not_249_out,
       not_250_out, not_251_out, not_252_out, not_253_out, not_254_out, not_255_out, not_256_out,
       not_257_out, not_258_out, not_259_out, not_260_out, not_261_out, not_262_out, not_263_out,
       not_264_out, not_265_out, not_266_out, not_267_out, not_268_out, not_269_out, not_270_out,
       not_271_out, not_272_out, not_273_out, not_274_out, not_275_out, not_276_out, not_277_out,
       not_278_out, not_279_out, not_280_out, not_281_out, not_282_out, not_283_out, not_284_out,
       not_285_out, not_286_out, not_287_out, not_288_out, not_289_out, not_290_out, not_291_out,
       not_292_out, not_293_out, not_294_out, not_295_out, not_296_out, not_297_out, not_298_out,
       not_299_out, not_300_out, not_301_out, not_302_out, not_303_out, not_304_out, not_305_out,
       not_306_out, not_307_out, not_308_out, not_309_out, not_310_out, not_311_out, not_312_out,
       not_313_out, not_314_out, not_315_out, not_316_out, not_317_out, not_318_out, not_319_out,
       not_320_out, not_321_out, not_322_out, not_323_out, not_324_out, not_325_out, not_326_out,
       not_327_out, not_328_out, not_329_out, not_330_out, not_331_out;

  not not_1 (not_1_out, OP5);
  not not_2 (not_2_out, OP4);
  not not_3 (not_3_out, OP3);
  not not_4 (not_4_out, OP2);
  not not_5 (not_5_out, OP1);
  not not_6 (not_6_out, OP0);
  not not_7 (not_7_out, F5);
  not not_8 (not_8_out, F4);
  not not_9 (not_9_out, F3);
  not not_10 (not_10_out, F2);
  not not_11 (not_11_out, F1);
  not not_12 (not_12_out, F0);
  not not_13 (not_13_out, OP5);
  not not_14 (not_14_out, OP4);
  not not_15 (not_15_out, OP3);
  not not_16 (not_16_out, OP2);
  not not_17 (not_17_out, OP1);
  not not_18 (not_18_out, OP0);
  not not_19 (not_19_out, F5);
  not not_20 (not_20_out, F4);
  not not_21 (not_21_out, F3);
  not not_22 (not_22_out, F2);
  not not_23 (not_23_out, OP5);
  not not_24 (not_24_out, OP4);
  not not_25 (not_25_out, OP3);
  not not_26 (not_26_out, OP2);
  not not_27 (not_27_out, OP1);
  not not_28 (not_28_out, OP0);
  not not_29 (not_29_out, F5);
  not not_30 (not_30_out, F4);
  not not_31 (not_31_out, F3);
  not not_32 (not_32_out, F2);
  not not_33 (not_33_out, F0);
  not not_34 (not_34_out, OP5);
  not not_35 (not_35_out, OP4);
  not not_36 (not_36_out, OP3);
  not not_37 (not_37_out, OP2);
  not not_38 (not_38_out, OP1);
  not not_39 (not_39_out, OP0);
  not not_40 (not_40_out, F4);
  not not_41 (not_41_out, F3);
  not not_42 (not_42_out, F2);
  not not_43 (not_43_out, F1);
  not not_44 (not_44_out, F0);
  not not_45 (not_45_out, OP5);
  not not_46 (not_46_out, OP4);
  not not_47 (not_47_out, OP3);
  not not_48 (not_48_out, OP2);
  not not_49 (not_49_out, OP1);
  not not_50 (not_50_out, OP0);
  not not_51 (not_51_out, F4);
  not not_52 (not_52_out, F3);
  not not_53 (not_53_out, F2);
  not not_54 (not_54_out, F1);
  not not_55 (not_55_out, OP5);
  not not_56 (not_56_out, OP4);
  not not_57 (not_57_out, OP3);
  not not_58 (not_58_out, OP2);
  not not_59 (not_59_out, OP1);
  not not_60 (not_60_out, OP0);
  not not_61 (not_61_out, F4);
  not not_62 (not_62_out, F3);
  not not_63 (not_63_out, F2);
  not not_64 (not_64_out, F0);
  not not_65 (not_65_out, OP5);
  not not_66 (not_66_out, OP4);
  not not_67 (not_67_out, OP3);
  not not_68 (not_68_out, OP2);
  not not_69 (not_69_out, OP1);
  not not_70 (not_70_out, OP0);
  not not_71 (not_71_out, F4);
  not not_72 (not_72_out, F3);
  not not_73 (not_73_out, F1);
  not not_74 (not_74_out, F0);
  not not_75 (not_75_out, OP5);
  not not_76 (not_76_out, OP4);
  not not_77 (not_77_out, OP3);
  not not_78 (not_78_out, OP2);
  not not_79 (not_79_out, OP1);
  not not_80 (not_80_out, OP0);
  not not_81 (not_81_out, F4);
  not not_82 (not_82_out, F3);
  not not_83 (not_83_out, F1);
  not not_84 (not_84_out, OP5);
  not not_85 (not_85_out, OP4);
  not not_86 (not_86_out, OP3);
  not not_87 (not_87_out, OP2);
  not not_88 (not_88_out, OP1);
  not not_89 (not_89_out, OP0);
  not not_90 (not_90_out, F4);
  not not_91 (not_91_out, F3);
  not not_92 (not_92_out, OP5);
  not not_93 (not_93_out, OP4);
  not not_94 (not_94_out, OP3);
  not not_95 (not_95_out, OP2);
  not not_96 (not_96_out, OP1);
  not not_97 (not_97_out, OP0);
  not not_98 (not_98_out, F4);
  not not_99 (not_99_out, F2);
  not not_100 (not_100_out, F0);
  not not_101 (not_101_out, OP5);
  not not_102 (not_102_out, OP4);
  not not_103 (not_103_out, OP3);
  not not_104 (not_104_out, OP2);
  not not_105 (not_105_out, OP1);
  not not_106 (not_106_out, OP0);
  not not_107 (not_107_out, F4);
  not not_108 (not_108_out, F2);
  not not_109 (not_109_out, OP5);
  not not_110 (not_110_out, OP4);
  not not_111 (not_111_out, OP3);
  not not_112 (not_112_out, OP2);
  not not_113 (not_113_out, OP1);
  not not_114 (not_114_out, OP0);
  not not_115 (not_115_out, F5);
  not not_116 (not_116_out, F4);
  not not_117 (not_117_out, F2);
  not not_118 (not_118_out, F1);
  not not_119 (not_119_out, F0);
  not not_120 (not_120_out, OP5);
  not not_121 (not_121_out, OP4);
  not not_122 (not_122_out, OP3);
  not not_123 (not_123_out, OP2);
  not not_124 (not_124_out, OP1);
  not not_125 (not_125_out, OP0);
  not not_126 (not_126_out, F5);
  not not_127 (not_127_out, F4);
  not not_128 (not_128_out, F1);
  not not_129 (not_129_out, F0);
  not not_130 (not_130_out, OP5);
  not not_131 (not_131_out, OP4);
  not not_132 (not_132_out, OP3);
  not not_133 (not_133_out, OP1);
  not not_134 (not_134_out, OP0);
  not not_135 (not_135_out, OP5);
  not not_136 (not_136_out, OP4);
  not not_137 (not_137_out, OP3);
  not not_138 (not_138_out, OP1);
  not not_139 (not_139_out, OP5);
  not not_140 (not_140_out, OP4);
  not not_141 (not_141_out, OP2);
  not not_142 (not_142_out, OP1);
  not not_143 (not_143_out, OP0);
  not not_144 (not_144_out, OP5);
  not not_145 (not_145_out, OP4);
  not not_146 (not_146_out, OP1);
  not not_147 (not_147_out, OP0);
  not not_148 (not_148_out, OP5);
  not not_149 (not_149_out, OP4);
  not not_150 (not_150_out, OP2);
  not not_151 (not_151_out, OP1);
  not not_152 (not_152_out, OP5);
  not not_153 (not_153_out, OP4);
  not not_154 (not_154_out, OP2);
  not not_155 (not_155_out, OP0);
  not not_156 (not_156_out, OP5);
  not not_157 (not_157_out, OP4);
  not not_158 (not_158_out, OP1);
  not not_159 (not_159_out, OP4);
  not not_160 (not_160_out, OP3);
  not not_161 (not_161_out, OP2);
  not not_162 (not_162_out, OP4);
  not not_163 (not_163_out, OP2);
  not not_164 (not_164_out, OP5);
  not not_165 (not_165_out, OP4);
  not not_166 (not_166_out, OP3);
  not not_167 (not_167_out, OP2);
  not not_168 (not_168_out, OP1);
  not not_169 (not_169_out, OP0);
  not not_170 (not_170_out, F4);
  not not_171 (not_171_out, F3);
  not not_172 (not_172_out, F2);
  not not_173 (not_173_out, OP4);
  not not_174 (not_174_out, OP3);
  not not_175 (not_175_out, OP1);
  not not_176 (not_176_out, OP0);
  not not_177 (not_177_out, OP5);
  not not_178 (not_178_out, OP4);
  not not_179 (not_179_out, OP3);
  not not_180 (not_180_out, OP2);
  not not_181 (not_181_out, OP1);
  not not_182 (not_182_out, OP5);
  not not_183 (not_183_out, OP4);
  not not_184 (not_184_out, OP3);
  not not_185 (not_185_out, OP2);
  not not_186 (not_186_out, OP1);
  not not_187 (not_187_out, OP0);
  not not_188 (not_188_out, F5);
  not not_189 (not_189_out, F4);
  not not_190 (not_190_out, F3);
  not not_191 (not_191_out, F2);
  not not_192 (not_192_out, F1);
  not not_193 (not_193_out, F0);
  not not_194 (not_194_out, OP5);
  not not_195 (not_195_out, OP4);
  not not_196 (not_196_out, OP3);
  not not_197 (not_197_out, OP2);
  not not_198 (not_198_out, OP1);
  not not_199 (not_199_out, OP0);
  not not_200 (not_200_out, F5);
  not not_201 (not_201_out, F4);
  not not_202 (not_202_out, F3);
  not not_203 (not_203_out, F2);
  not not_204 (not_204_out, OP5);
  not not_205 (not_205_out, OP4);
  not not_206 (not_206_out, OP3);
  not not_207 (not_207_out, OP2);
  not not_208 (not_208_out, OP1);
  not not_209 (not_209_out, OP0);
  not not_210 (not_210_out, F5);
  not not_211 (not_211_out, F4);
  not not_212 (not_212_out, F3);
  not not_213 (not_213_out, F2);
  not not_214 (not_214_out, F0);
  not not_215 (not_215_out, OP5);
  not not_216 (not_216_out, OP4);
  not not_217 (not_217_out, OP3);
  not not_218 (not_218_out, OP2);
  not not_219 (not_219_out, OP1);
  not not_220 (not_220_out, OP0);
  not not_221 (not_221_out, F4);
  not not_222 (not_222_out, F3);
  not not_223 (not_223_out, F2);
  not not_224 (not_224_out, F1);
  not not_225 (not_225_out, F0);
  not not_226 (not_226_out, OP5);
  not not_227 (not_227_out, OP4);
  not not_228 (not_228_out, OP3);
  not not_229 (not_229_out, OP2);
  not not_230 (not_230_out, OP1);
  not not_231 (not_231_out, OP0);
  not not_232 (not_232_out, F4);
  not not_233 (not_233_out, F3);
  not not_234 (not_234_out, F2);
  not not_235 (not_235_out, F1);
  not not_236 (not_236_out, OP5);
  not not_237 (not_237_out, OP4);
  not not_238 (not_238_out, OP3);
  not not_239 (not_239_out, OP2);
  not not_240 (not_240_out, OP1);
  not not_241 (not_241_out, OP0);
  not not_242 (not_242_out, F4);
  not not_243 (not_243_out, F3);
  not not_244 (not_244_out, F2);
  not not_245 (not_245_out, F0);
  not not_246 (not_246_out, OP5);
  not not_247 (not_247_out, OP4);
  not not_248 (not_248_out, OP3);
  not not_249 (not_249_out, OP2);
  not not_250 (not_250_out, OP1);
  not not_251 (not_251_out, OP0);
  not not_252 (not_252_out, F4);
  not not_253 (not_253_out, F3);
  not not_254 (not_254_out, F1);
  not not_255 (not_255_out, F0);
  not not_256 (not_256_out, OP5);
  not not_257 (not_257_out, OP4);
  not not_258 (not_258_out, OP3);
  not not_259 (not_259_out, OP2);
  not not_260 (not_260_out, OP1);
  not not_261 (not_261_out, OP0);
  not not_262 (not_262_out, F4);
  not not_263 (not_263_out, F3);
  not not_264 (not_264_out, F1);
  not not_265 (not_265_out, OP5);
  not not_266 (not_266_out, OP4);
  not not_267 (not_267_out, OP3);
  not not_268 (not_268_out, OP2);
  not not_269 (not_269_out, OP1);
  not not_270 (not_270_out, OP0);
  not not_271 (not_271_out, F4);
  not not_272 (not_272_out, F3);
  not not_273 (not_273_out, OP5);
  not not_274 (not_274_out, OP4);
  not not_275 (not_275_out, OP3);
  not not_276 (not_276_out, OP2);
  not not_277 (not_277_out, OP1);
  not not_278 (not_278_out, OP0);
  not not_279 (not_279_out, F4);
  not not_280 (not_280_out, F2);
  not not_281 (not_281_out, F0);
  not not_282 (not_282_out, OP5);
  not not_283 (not_283_out, OP4);
  not not_284 (not_284_out, OP3);
  not not_285 (not_285_out, OP2);
  not not_286 (not_286_out, OP1);
  not not_287 (not_287_out, OP0);
  not not_288 (not_288_out, F4);
  not not_289 (not_289_out, F2);
  not not_290 (not_290_out, OP5);
  not not_291 (not_291_out, OP4);
  not not_292 (not_292_out, OP3);
  not not_293 (not_293_out, OP2);
  not not_294 (not_294_out, OP1);
  not not_295 (not_295_out, OP0);
  not not_296 (not_296_out, F5);
  not not_297 (not_297_out, F4);
  not not_298 (not_298_out, F1);
  not not_299 (not_299_out, F0);
  not not_300 (not_300_out, OP5);
  not not_301 (not_301_out, OP4);
  not not_302 (not_302_out, OP3);
  not not_303 (not_303_out, OP1);
  not not_304 (not_304_out, OP0);
  not not_305 (not_305_out, OP5);
  not not_306 (not_306_out, OP4);
  not not_307 (not_307_out, OP3);
  not not_308 (not_308_out, OP1);
  not not_309 (not_309_out, OP4);
  not not_310 (not_310_out, OP3);
  not not_311 (not_311_out, OP2);
  not not_312 (not_312_out, OP4);
  not not_313 (not_313_out, OP2);
  not not_314 (not_314_out, OP5);
  not not_315 (not_315_out, OP4);
  not not_316 (not_316_out, OP3);
  not not_317 (not_317_out, OP2);
  not not_318 (not_318_out, OP1);
  not not_319 (not_319_out, OP0);
  not not_320 (not_320_out, F4);
  not not_321 (not_321_out, F3);
  not not_322 (not_322_out, F2);
  not not_323 (not_323_out, OP4);
  not not_324 (not_324_out, OP3);
  not not_325 (not_325_out, OP1);
  not not_326 (not_326_out, OP0);
  not not_327 (not_327_out, OP5);
  not not_328 (not_328_out, OP3);
  not not_329 (not_329_out, OP2);
  not not_330 (not_330_out, OP1);
  not not_331 (not_331_out, OP0);
  and and_1 (and_1_out, not_1_out, not_2_out, not_3_out, not_4_out, not_5_out, not_6_out, not_7_out, not_8_out, not_9_out, not_10_out, not_11_out, not_12_out);
  and and_2 (and_2_out, not_13_out, not_14_out, not_15_out, not_16_out, not_17_out, not_18_out, not_19_out, not_20_out, not_21_out, not_22_out, F1, F0);
  and and_3 (and_3_out, not_23_out, not_24_out, not_25_out, not_26_out, not_27_out, not_28_out, not_29_out, not_30_out, not_31_out, not_32_out, F1, not_33_out);
  and and_4 (and_4_out, not_34_out, not_35_out, not_36_out, not_37_out, not_38_out, not_39_out, F5, not_40_out, not_41_out, not_42_out, not_43_out, not_44_out);
  and and_5 (and_5_out, not_45_out, not_46_out, not_47_out, not_48_out, not_49_out, not_50_out, F5, not_51_out, not_52_out, not_53_out, not_54_out, F0);
  and and_6 (and_6_out, not_55_out, not_56_out, not_57_out, not_58_out, not_59_out, not_60_out, F5, not_61_out, not_62_out, not_63_out, F1, not_64_out);
  and and_7 (and_7_out, not_65_out, not_66_out, not_67_out, not_68_out, not_69_out, not_70_out, F5, not_71_out, not_72_out, F2, not_73_out, not_74_out);
  and and_8 (and_8_out, not_75_out, not_76_out, not_77_out, not_78_out, not_79_out, not_80_out, F5, not_81_out, not_82_out, F2, not_83_out, F0);
  and and_9 (and_9_out, not_84_out, not_85_out, not_86_out, not_87_out, not_88_out, not_89_out, F5, not_90_out, not_91_out, F2, F1, F0);
  and and_10 (and_10_out, not_92_out, not_93_out, not_94_out, not_95_out, not_96_out, not_97_out, F5, not_98_out, F3, not_99_out, F1, not_100_out);
  and and_11 (and_11_out, not_101_out, not_102_out, not_103_out, not_104_out, not_105_out, not_106_out, F5, not_107_out, F3, not_108_out, F1, F0);
  and and_12 (and_12_out, not_109_out, not_110_out, not_111_out, not_112_out, not_113_out, not_114_out, not_115_out, not_116_out, F3, not_117_out, not_118_out, not_119_out);
  and and_13 (and_13_out, not_120_out, not_121_out, not_122_out, not_123_out, not_124_out, not_125_out, not_126_out, not_127_out, F3, F2, not_128_out, not_129_out);
  and and_14 (and_14_out, not_130_out, not_131_out, not_132_out, OP2, not_133_out, not_134_out);
  and and_15 (and_15_out, not_135_out, not_136_out, not_137_out, OP2, not_138_out, OP0);
  and and_16 (and_16_out, not_139_out, not_140_out, OP3, not_141_out, not_142_out, not_143_out);
  and and_17 (and_17_out, not_144_out, not_145_out, OP3, OP2, not_146_out, not_147_out);
  and and_18 (and_18_out, not_148_out, not_149_out, OP3, not_150_out, not_151_out, OP0);
  and and_19 (and_19_out, not_152_out, not_153_out, OP3, not_154_out, OP1, not_155_out);
  and and_20 (and_20_out, not_156_out, not_157_out, OP3, OP2, not_158_out, OP0);
  and and_21 (and_21_out, OP5, not_159_out, not_160_out, not_161_out, OP1, OP0);
  and and_22 (and_22_out, OP5, not_162_out, OP3, not_163_out, OP1, OP0);
  and and_23 (and_23_out, not_164_out, not_165_out, not_166_out, not_167_out, not_168_out, not_169_out, F5, not_170_out, not_171_out, not_172_out, F1, F0);
  and and_24 (and_24_out, OP5, not_173_out, not_174_out, OP2, not_175_out, not_176_out);
  and and_25 (and_25_out, not_177_out, not_178_out, not_179_out, not_180_out, not_181_out, OP0);
  and and_26 (and_26_out, not_182_out, not_183_out, not_184_out, not_185_out, not_186_out, not_187_out, not_188_out, not_189_out, not_190_out, not_191_out, not_192_out, not_193_out);
  and and_27 (and_27_out, not_194_out, not_195_out, not_196_out, not_197_out, not_198_out, not_199_out, not_200_out, not_201_out, not_202_out, not_203_out, F1, F0);
  and and_28 (and_28_out, not_204_out, not_205_out, not_206_out, not_207_out, not_208_out, not_209_out, not_210_out, not_211_out, not_212_out, not_213_out, F1, not_214_out);
  and and_29 (and_29_out, not_215_out, not_216_out, not_217_out, not_218_out, not_219_out, not_220_out, F5, not_221_out, not_222_out, not_223_out, not_224_out, not_225_out);
  and and_30 (and_30_out, not_226_out, not_227_out, not_228_out, not_229_out, not_230_out, not_231_out, F5, not_232_out, not_233_out, not_234_out, not_235_out, F0);
  and and_31 (and_31_out, not_236_out, not_237_out, not_238_out, not_239_out, not_240_out, not_241_out, F5, not_242_out, not_243_out, not_244_out, F1, not_245_out);
  and and_32 (and_32_out, not_246_out, not_247_out, not_248_out, not_249_out, not_250_out, not_251_out, F5, not_252_out, not_253_out, F2, not_254_out, not_255_out);
  and and_33 (and_33_out, not_256_out, not_257_out, not_258_out, not_259_out, not_260_out, not_261_out, F5, not_262_out, not_263_out, F2, not_264_out, F0);
  and and_34 (and_34_out, not_265_out, not_266_out, not_267_out, not_268_out, not_269_out, not_270_out, F5, not_271_out, not_272_out, F2, F1, F0);
  and and_35 (and_35_out, not_273_out, not_274_out, not_275_out, not_276_out, not_277_out, not_278_out, F5, not_279_out, F3, not_280_out, F1, not_281_out);
  and and_36 (and_36_out, not_282_out, not_283_out, not_284_out, not_285_out, not_286_out, not_287_out, F5, not_288_out, F3, not_289_out, F1, F0);
  and and_37 (and_37_out, not_290_out, not_291_out, not_292_out, not_293_out, not_294_out, not_295_out, not_296_out, not_297_out, F3, F2, not_298_out, not_299_out);
  and and_38 (and_38_out, not_300_out, not_301_out, not_302_out, OP2, not_303_out, not_304_out);
  and and_39 (and_39_out, not_305_out, not_306_out, not_307_out, OP2, not_308_out, OP0);
  and and_40 (and_40_out, OP5, not_309_out, not_310_out, not_311_out, OP1, OP0);
  and and_41 (and_41_out, OP5, not_312_out, OP3, not_313_out, OP1, OP0);
  and and_42 (and_42_out, not_314_out, not_315_out, not_316_out, not_317_out, not_318_out, not_319_out, F5, not_320_out, not_321_out, not_322_out, F1, F0);
  and and_43 (and_43_out, OP5, not_323_out, not_324_out, OP2, not_325_out, not_326_out);
  and and_44 (and_44_out, not_327_out, OP4, not_328_out, not_329_out, not_330_out, not_331_out);
  or or_1 (R1_Used, and_1_out, and_2_out, and_3_out, and_4_out, and_5_out, and_6_out, and_7_out, and_8_out, and_9_out, and_10_out, and_11_out, and_12_out, and_13_out, and_14_out, and_15_out, and_16_out, and_17_out, and_18_out, and_19_out, and_20_out, and_21_out, and_22_out, and_23_out, and_24_out, and_25_out);
  or or_2 (R2_Used, and_26_out, and_27_out, and_28_out, and_29_out, and_30_out, and_31_out, and_32_out, and_33_out, and_34_out, and_35_out, and_36_out, and_37_out, and_38_out, and_39_out, and_40_out, and_41_out, and_42_out, and_43_out, and_44_out);
endmodule

// 数据相关检测
module \数据相关检测  (
  input  [4:0] ID_R1_num,
  input  [4:0] ID_R2_num,
  input  [4:0] EX_WriteReg_num,
  input  [4:0] MEM_WriteReg_num,
  input  EX_RegWrite,
  input  MEM__RegWrite,
  input  R1_Used,
  input  R2_Used,
  input  EX_MemToReg,
  input  MEM_MemToReg,
  output \数据相关 ,
  output [1:0] Forward1,
  output [1:0] Forward2,
  output Load_Use
);

  wire and_1_out, and_2_out, and_3_out, and_4_out, and_5_out, and_6_out, and_7_out, and_8_out,
       comparator_1_eq, comparator_2_eq, comparator_3_eq, comparator_4_eq, comparator_5_eq, comparator_6_eq,
       not_1_out, not_2_out, or_1_out, or_2_out, or_3_out;
  wire [1:0] multiplexer_1_out, multiplexer_2_out, multiplexer_4_out, multiplexer_6_out;

  Comparator #(.width(5), .mode("twosComplement")) comparator_1 (
    .a(ID_R1_num), .b(EX_WriteReg_num), .eq(comparator_1_eq));  // open: gt, lt
  Comparator #(.width(5), .mode("twosComplement")) comparator_2 (
    .a(ID_R1_num), .b(MEM_WriteReg_num), .eq(comparator_2_eq));  // open: gt, lt
  Comparator #(.width(5), .mode("twosComplement")) comparator_3 (
    .a(ID_R2_num), .b(EX_WriteReg_num), .eq(comparator_3_eq));  // open: gt, lt
  Comparator #(.width(5), .mode("twosComplement")) comparator_4 (
    .a(ID_R2_num), .b(MEM_WriteReg_num), .eq(comparator_4_eq));  // open: gt, lt
  Comparator #(.width(5), .mode("twosComplement")) comparator_5 (
    .a(EX_WriteReg_num), .b({5{1'b0}}), .eq(comparator_5_eq));  // open: gt, lt
  not not_1 (not_1_out, comparator_5_eq);
  not not_2 (not_2_out, comparator_6_eq);
  Comparator #(.width(5), .mode("twosComplement")) comparator_6 (
    .a(MEM_WriteReg_num), .b({5{1'b0}}), .eq(comparator_6_eq));  // open: gt, lt
  and and_1 (and_1_out, comparator_1_eq, not_1_out, EX_RegWrite);
  and and_2 (and_2_out, comparator_2_eq, not_2_out, MEM__RegWrite);
  and and_3 (and_3_out, comparator_3_eq, not_1_out, EX_RegWrite);
  and and_4 (and_4_out, comparator_4_eq, not_2_out, MEM__RegWrite);
  Multiplexer #(.select(1), .width(2), .disabled("Z"), .enable("false")) multiplexer_1 (
    .in0(2'b10), .in1(2'b11), .out(multiplexer_1_out), .sel(MEM_MemToReg));
  Multiplexer #(.select(1), .width(2), .disabled("Z"), .enable("false")) multiplexer_2 (
    .in0(2'b10), .in1(2'b11), .out(multiplexer_2_out), .sel(MEM_MemToReg));
  and and_5 (and_5_out, R1_Used, and_1_out);
  and and_6 (and_6_out, R2_Used, and_3_out);
  or or_1 (or_1_out, and_1_out, and_2_out);
  or or_2 (or_2_out, and_3_out, and_4_out);
  Multiplexer #(.select(1), .width(2), .disabled("Z"), .enable("false")) multiplexer_3 (
    .in0(2'b00), .in1(multiplexer_4_out), .out(Forward1), .sel(and_7_out));
  Multiplexer #(.select(1), .width(2), .disabled("Z"), .enable("false")) multiplexer_4 (
    .in0(multiplexer_1_out), .in1(2'b01), .out(multiplexer_4_out), .sel(comparator_1_eq));
  Multiplexer #(.select(1), .width(2), .disabled("Z"), .enable("false")) multiplexer_5 (
    .in0(2'b00), .in1(multiplexer_6_out), .out(Forward2), .sel(and_8_out));
  Multiplexer #(.select(1), .width(2), .disabled("Z"), .enable("false")) multiplexer_6 (
    .in0(multiplexer_2_out), .in1(2'b01), .out(multiplexer_6_out), .sel(comparator_3_eq));
  or or_3 (or_3_out, and_5_out, and_6_out);
  and and_7 (and_7_out, or_1_out, R1_Used);
  and and_8 (and_8_out, or_2_out, R2_Used);
  and and_9 (Load_Use, EX_MemToReg, or_3_out);
  or or_4 (\数据相关 , and_7_out, and_8_out);
endmodule
// 全相联BHT
module \全相联BHT  (
  input  [1:0] PRE,
  input  update,
  input  [31:0] IF_PC,
  input  [31:0] EX_PC,
  input  [31:0] DES,
  input  ex_hit,
  input  CLK,
  output Miss,
  output [1:0] PreData,
  output [31:0] DesData,
  output PredictJmp
);

  wire Change0, Change1, Change2, Change3, Change4, Change5, Change6, Change7, comparator_1_eq,
       comparator_2_eq, comparator_3_eq, comparator_4_eq, comparator_5_eq, comparator_6_eq, comparator_7_eq,
       comparator_8_eq, comparator_9_eq, comparator_10_eq, comparator_11_eq, comparator_12_eq,
       comparator_13_eq, comparator_14_eq, comparator_15_eq, comparator_16_eq, decoder_1_out0,
       decoder_1_out1, decoder_1_out2, decoder_1_out3, decoder_1_out4, decoder_1_out5, decoder_1_out6,
       decoder_1_out7, L0, L1, L2, L3, L4, L5, L6, L7, not_1_out, not_2_out, not_3_out, not_4_out, not_5_out,
       not_6_out, not_7_out, not_8_out, not_9_out, not_10_out, or_1_out, or_2_out, or_3_out, or_4_out,
       or_5_out, or_6_out, or_7_out, or_8_out, or_9_out, or_10_out, V0, V1, V2, V3, V4, V5, V6, V7, WriteL0,
       WriteL1, WriteL2, WriteL3, WriteL4, WriteL5, WriteL6, WriteL7;
  wire [1:0] \预测位_2_q , \预测位_3_q , \预测位_4_q , \预测位_5_q , \预测位_6_q , \预测位_7_q , \预测位_8_q , \预测位_q ;
  wire [2:0] controlled_buffer_17_out, \max3_归并比较_1_max_num , \max3_归并比较_2_max_num , \max3_归并比较_3_max_num ,
       \max3_归并比较_4_max_num , \max3_归并比较_5_max_num , \max3_归并比较_6_max_num , \max3_归并比较_7_max_num ,
       priority_encoder_1_out;
  wire [15:0] C0, C1, C2, C3, C4, C5, C6, C7, \max3_归并比较_1_max , \max3_归并比较_2_max , \max3_归并比较_3_max ,
       \max3_归并比较_4_max , \max3_归并比较_5_max , \max3_归并比较_6_max ;
  wire [31:0] EX_PC0, EX_PC1, EX_PC2, EX_PC3, EX_PC4, EX_PC5, EX_PC6, EX_PC7, \目标地址_2_q , \目标地址_3_q ,
       \目标地址_4_q , \目标地址_5_q , \目标地址_6_q , \目标地址_7_q , \目标地址_8_q , \目标地址_q ;

  Register #(.width(1), .trigger("rising"), .Select("low")) VALID (
    .D(1'b1), .en(WriteL0), .Q(V0), .clk(CLK));  // open: clr
  Register #(.width(1), .trigger("rising"), .Select("low")) VALID_2 (
    .D(1'b1), .en(WriteL1), .Q(V1), .clk(CLK));  // open: clr
  Register #(.width(1), .trigger("rising"), .Select("low")) VALID_3 (
    .D(1'b1), .en(WriteL2), .Q(V2), .clk(CLK));  // open: clr
  Register #(.width(1), .trigger("rising"), .Select("low")) VALID_4 (
    .D(1'b1), .en(WriteL3), .Q(V3), .clk(CLK));  // open: clr
  Register #(.width(1), .trigger("rising"), .Select("low")) VALID_5 (
    .D(1'b1), .en(WriteL4), .Q(V4), .clk(CLK));  // open: clr
  Register #(.width(1), .trigger("rising"), .Select("low")) VALID_6 (
    .D(1'b1), .en(WriteL5), .Q(V5), .clk(CLK));  // open: clr
  Register #(.width(1), .trigger("rising"), .Select("low")) VALID_7 (
    .D(1'b1), .en(WriteL6), .Q(V6), .clk(CLK));  // open: clr
  Register #(.width(1), .trigger("rising"), .Select("low")) VALID_8 (
    .D(1'b1), .en(WriteL7), .Q(V7), .clk(CLK));  // open: clr
  Register #(.width(32), .trigger("rising"), .Select("low")) \u_分支地址  (
    .D(EX_PC), .en(WriteL0), .Q(EX_PC0), .clk(CLK));  // open: clr
  Register #(.width(32), .trigger("rising"), .Select("low")) \u_分支地址_2  (
    .D(EX_PC), .en(WriteL1), .Q(EX_PC1), .clk(CLK));  // open: clr
  Register #(.width(32), .trigger("rising"), .Select("low")) \u_分支地址_3  (
    .D(EX_PC), .en(WriteL2), .Q(EX_PC2), .clk(CLK));  // open: clr
  Register #(.width(32), .trigger("rising"), .Select("low")) \u_分支地址_4  (
    .D(EX_PC), .en(WriteL3), .Q(EX_PC3), .clk(CLK));  // open: clr
  Register #(.width(32), .trigger("rising"), .Select("low")) \u_分支地址_5  (
    .D(EX_PC), .en(WriteL4), .Q(EX_PC4), .clk(CLK));  // open: clr
  Register #(.width(32), .trigger("rising"), .Select("low")) \u_分支地址_6  (
    .D(EX_PC), .en(WriteL5), .Q(EX_PC5), .clk(CLK));  // open: clr
  Register #(.width(32), .trigger("rising"), .Select("low")) \u_分支地址_7  (
    .D(EX_PC), .en(WriteL6), .Q(EX_PC6), .clk(CLK));  // open: clr
  Register #(.width(32), .trigger("rising"), .Select("low")) \u_分支地址_8  (
    .D(EX_PC), .en(WriteL7), .Q(EX_PC7), .clk(CLK));  // open: clr
  Register #(.width(32), .trigger("rising"), .Select("low")) \u_目标地址  (
    .D(DES), .en(WriteL0), .Q(\目标地址_q ), .clk(CLK));  // open: clr
  assign DesData = L0 ? \目标地址_q  : 32'bz;  // Controlled_Buffer controlled_buffer_1
  Register #(.width(32), .trigger("rising"), .Select("low")) \u_目标地址_2  (
    .D(DES), .en(WriteL1), .Q(\目标地址_2_q ), .clk(CLK));  // open: clr
  assign DesData = L1 ? \目标地址_2_q  : 32'bz;  // Controlled_Buffer controlled_buffer_2
  assign DesData = L2 ? \目标地址_3_q  : 32'bz;  // Controlled_Buffer controlled_buffer_3
  Register #(.width(32), .trigger("rising"), .Select("low")) \u_目标地址_3  (
    .D(DES), .en(WriteL2), .Q(\目标地址_3_q ), .clk(CLK));  // open: clr
  assign DesData = L3 ? \目标地址_4_q  : 32'bz;  // Controlled_Buffer controlled_buffer_4
  Register #(.width(32), .trigger("rising"), .Select("low")) \u_目标地址_4  (
    .D(DES), .en(WriteL3), .Q(\目标地址_4_q ), .clk(CLK));  // open: clr
  assign DesData = L4 ? \目标地址_5_q  : 32'bz;  // Controlled_Buffer controlled_buffer_5
  Register #(.width(32), .trigger("rising"), .Select("low")) \u_目标地址_5  (
    .D(DES), .en(WriteL4), .Q(\目标地址_5_q ), .clk(CLK));  // open: clr
  assign DesData = L5 ? \目标地址_6_q  : 32'bz;  // Controlled_Buffer controlled_buffer_6
  Register #(.width(32), .trigger("rising"), .Select("low")) \u_目标地址_6  (
    .D(DES), .en(WriteL5), .Q(\目标地址_6_q ), .clk(CLK));  // open: clr
  Register #(.width(32), .trigger("rising"), .Select("low")) \u_目标地址_7  (
    .D(DES), .en(WriteL6), .Q(\目标地址_7_q ), .clk(CLK));  // open: clr
  assign DesData = L6 ? \目标地址_7_q  : 32'bz;  // Controlled_Buffer controlled_buffer_7
  assign DesData = L7 ? \目标地址_8_q  : 32'bz;  // Controlled_Buffer controlled_buffer_8
  Register #(.width(32), .trigger("rising"), .Select("low")) \u_目标地址_8  (
    .D(DES), .en(WriteL7), .Q(\目标地址_8_q ), .clk(CLK));  // open: clr
  Counter #(.width(16), .max('hffff), .ongoal("wrap"), .trigger("rising"), .behavior("old")) \u_淘汰计数  (
    .Q(C0), .clk(CLK), .clr(L0));  // open: load, D, count, carry, preset
  Counter #(.width(16), .max('hffff), .ongoal("wrap"), .trigger("rising"), .behavior("old")) \u_淘汰计数_2  (
    .Q(C1), .clk(CLK), .clr(L1));  // open: load, D, count, carry, preset
  Counter #(.width(16), .max('hffff), .ongoal("wrap"), .trigger("rising"), .behavior("old")) \u_淘汰计数_3  (
    .Q(C2), .clk(CLK), .clr(L2));  // open: load, D, count, carry, preset
  Counter #(.width(16), .max('hffff), .ongoal("wrap"), .trigger("rising"), .behavior("old")) \u_淘汰计数_4  (
    .Q(C3), .clk(CLK), .clr(L3));  // open: load, D, count, carry, preset
  Counter #(.width(16), .max('hffff), .ongoal("wrap"), .trigger("rising"), .behavior("old")) \u_淘汰计数_5  (
    .Q(C4), .clk(CLK), .clr(L4));  // open: load, D, count, carry, preset
  Counter #(.width(16), .max('hffff), .ongoal("wrap"), .trigger("rising"), .behavior("old")) \u_淘汰计数_6  (
    .Q(C5), .clk(CLK), .clr(L5));  // open: load, D, count, carry, preset
  Counter #(.width(16), .max('hffff), .ongoal("wrap"), .trigger("rising"), .behavior("old")) \u_淘汰计数_7  (
    .Q(C6), .clk(CLK), .clr(L6));  // open: load, D, count, carry, preset
  Counter #(.width(16), .max('hffff), .ongoal("wrap"), .trigger("rising"), .behavior("old")) \u_淘汰计数_8  (
    .Q(C7), .clk(CLK), .clr(L7));  // open: load, D, count, carry, preset
  or or_1 (or_1_out, Change0, WriteL0);
  or or_2 (or_2_out, Change1, WriteL1);
  or or_3 (or_3_out, Change2, WriteL2);
  or or_4 (or_4_out, Change3, WriteL3);
  or or_5 (or_5_out, Change4, WriteL4);
  or or_6 (or_6_out, Change5, WriteL5);
  or or_7 (or_7_out, Change6, WriteL6);
  or or_8 (or_8_out, Change7, WriteL7);
  assign PreData = L0 ? \预测位_q  : 2'bz;  // Controlled_Buffer controlled_buffer_9
  Register #(.width(2), .trigger("rising"), .Select("low")) \u_预测位  (
    .D(PRE), .en(or_1_out), .Q(\预测位_q ), .clk(CLK));  // open: clr
  assign PreData = L1 ? \预测位_2_q  : 2'bz;  // Controlled_Buffer controlled_buffer_10
  Register #(.width(2), .trigger("rising"), .Select("low")) \u_预测位_2  (
    .D(PRE), .en(or_2_out), .Q(\预测位_2_q ), .clk(CLK));  // open: clr
  assign PreData = L2 ? \预测位_3_q  : 2'bz;  // Controlled_Buffer controlled_buffer_11
  Register #(.width(2), .trigger("rising"), .Select("low")) \u_预测位_3  (
    .D(PRE), .en(or_3_out), .Q(\预测位_3_q ), .clk(CLK));  // open: clr
  assign PreData = L3 ? \预测位_4_q  : 2'bz;  // Controlled_Buffer controlled_buffer_12
  Register #(.width(2), .trigger("rising"), .Select("low")) \u_预测位_4  (
    .D(PRE), .en(or_4_out), .Q(\预测位_4_q ), .clk(CLK));  // open: clr
  assign PreData = L4 ? \预测位_5_q  : 2'bz;  // Controlled_Buffer controlled_buffer_13
  Register #(.width(2), .trigger("rising"), .Select("low")) \u_预测位_5  (
    .D(PRE), .en(or_5_out), .Q(\预测位_5_q ), .clk(CLK));  // open: clr
  assign PreData = L5 ? \预测位_6_q  : 2'bz;  // Controlled_Buffer controlled_buffer_14
  Register #(.width(2), .trigger("rising"), .Select("low")) \u_预测位_6  (
    .D(PRE), .en(or_6_out), .Q(\预测位_6_q ), .clk(CLK));  // open: clr
  assign PreData = L6 ? \预测位_7_q  : 2'bz;  // Controlled_Buffer controlled_buffer_15
  Register #(.width(2), .trigger("rising"), .Select("low")) \u_预测位_7  (
    .D(PRE), .en(or_7_out), .Q(\预测位_7_q ), .clk(CLK));  // open: clr
  assign PreData = L7 ? \预测位_8_q  : 2'bz;  // Controlled_Buffer controlled_buffer_16
  Register #(.width(2), .trigger("rising"), .Select("low")) \u_预测位_8  (
    .D(PRE), .en(or_8_out), .Q(\预测位_8_q ), .clk(CLK));  // open: clr
  \Max3_归并比较  \max3_归并比较_1  (
    .Y(C1), .MAX(\max3_归并比较_1_max ), .X(C0), .Y_num(3'b001), .Max_num(\max3_归并比较_1_max_num ), .X_num(3'b000));
  \Max3_归并比较  \max3_归并比较_2  (
    .Y(C3), .MAX(\max3_归并比较_2_max ), .X(C2), .Y_num(3'b011), .Max_num(\max3_归并比较_2_max_num ), .X_num(3'b010));
  \Max3_归并比较  \max3_归并比较_3  (
    .Y(C5), .MAX(\max3_归并比较_3_max ), .X(C4), .Y_num(3'b101), .Max_num(\max3_归并比较_3_max_num ), .X_num(3'b100));
  \Max3_归并比较  \max3_归并比较_4  (
    .Y(C7), .MAX(\max3_归并比较_4_max ), .X(C6), .Y_num(3'b111), .Max_num(\max3_归并比较_4_max_num ), .X_num(3'b110));
  not not_1 (not_1_out, V0);
  not not_2 (not_2_out, V1);
  not not_3 (not_3_out, V2);
  not not_4 (not_4_out, V3);
  not not_5 (not_5_out, V4);
  not not_6 (not_6_out, V5);
  not not_7 (not_7_out, V6);
  not not_8 (not_8_out, V7);
  and and_1 (Change0, V0, comparator_1_eq);
  Comparator #(.width(32), .mode("twosComplement")) comparator_1 (
    .a(EX_PC0), .b(EX_PC), .eq(comparator_1_eq));  // open: gt, lt
  and and_2 (Change1, V1, comparator_2_eq);
  Comparator #(.width(32), .mode("twosComplement")) comparator_2 (
    .a(EX_PC1), .b(EX_PC), .eq(comparator_2_eq));  // open: gt, lt
  and and_3 (Change2, V2, comparator_3_eq);
  Comparator #(.width(32), .mode("twosComplement")) comparator_3 (
    .a(EX_PC2), .b(EX_PC), .eq(comparator_3_eq));  // open: gt, lt
  and and_4 (Change3, V3, comparator_4_eq);
  Comparator #(.width(32), .mode("twosComplement")) comparator_4 (
    .a(EX_PC3), .b(EX_PC), .eq(comparator_4_eq));  // open: gt, lt
  and and_5 (Change4, V4, comparator_5_eq);
  Comparator #(.width(32), .mode("twosComplement")) comparator_5 (
    .a(EX_PC4), .b(EX_PC), .eq(comparator_5_eq));  // open: gt, lt
  and and_6 (Change5, V5, comparator_6_eq);
  Comparator #(.width(32), .mode("twosComplement")) comparator_6 (
    .a(EX_PC5), .b(EX_PC), .eq(comparator_6_eq));  // open: gt, lt
  and and_7 (Change6, V6, comparator_7_eq);
  Comparator #(.width(32), .mode("twosComplement")) comparator_7 (
    .a(EX_PC6), .b(EX_PC), .eq(comparator_7_eq));  // open: gt, lt
  and and_8 (Change7, V7, comparator_8_eq);
  Comparator #(.width(32), .mode("twosComplement")) comparator_8 (
    .a(EX_PC7), .b(EX_PC), .eq(comparator_8_eq));  // open: gt, lt
  not not_9 (not_9_out, Miss);
  \Max3_归并比较  \max3_归并比较_5  (
    .Y(\max3_归并比较_2_max ), .MAX(\max3_归并比较_5_max ), .X(\max3_归并比较_1_max ), .Y_num(\max3_归并比较_2_max_num ),
    .Max_num(\max3_归并比较_5_max_num ), .X_num(\max3_归并比较_1_max_num ));
  \Max3_归并比较  \max3_归并比较_6  (
    .Y(\max3_归并比较_4_max ), .MAX(\max3_归并比较_6_max ), .X(\max3_归并比较_3_max ), .Y_num(\max3_归并比较_4_max_num ),
    .Max_num(\max3_归并比较_6_max_num ), .X_num(\max3_归并比较_3_max_num ));
  Priority_Encoder #(.select(3), .disabled("Z")) priority_encoder_1 (
    .in0(not_1_out), .in1(not_2_out), .in2(not_3_out), .in3(not_4_out), .in4(not_5_out), .in5(not_6_out),
    .in6(not_7_out), .in7(not_8_out), .out(priority_encoder_1_out));  // open: gs, en_out, en_in
  or or_9 (or_9_out, not_8_out, not_7_out, not_6_out, not_5_out, not_4_out, not_3_out, not_2_out, not_1_out);
  and and_9 (PredictJmp, not_9_out, PreData[1]);
  \Max3_归并比较  \max3_归并比较_7  (
    .Y(\max3_归并比较_6_max ), .X(\max3_归并比较_5_max ), .Y_num(\max3_归并比较_6_max_num ),
    .Max_num(\max3_归并比较_7_max_num ), .X_num(\max3_归并比较_5_max_num ));  // open: MAX
  assign controlled_buffer_17_out = not_10_out ? \max3_归并比较_7_max_num  : 3'bz;  // Controlled_Buffer controlled_buffer_17
  not not_10 (not_10_out, or_9_out);
  assign controlled_buffer_17_out = or_9_out ? priority_encoder_1_out : 3'bz;  // Controlled_Buffer controlled_buffer_18
  Decoder #(.select(3), .tristate("false"), .disabled("Z"), .enable("false")) decoder_1 (
    .out0(decoder_1_out0), .out1(decoder_1_out1), .out2(decoder_1_out2), .out3(decoder_1_out3),
    .out4(decoder_1_out4), .out5(decoder_1_out5), .out6(decoder_1_out6), .out7(decoder_1_out7),
    .sel(controlled_buffer_17_out));
  Comparator #(.width(32), .mode("twosComplement")) comparator_9 (
    .a(EX_PC0), .b(IF_PC), .eq(comparator_9_eq));  // open: gt, lt
  Comparator #(.width(32), .mode("twosComplement")) comparator_10 (
    .a(EX_PC1), .b(IF_PC), .eq(comparator_10_eq));  // open: gt, lt
  Comparator #(.width(32), .mode("twosComplement")) comparator_11 (
    .a(EX_PC2), .b(IF_PC), .eq(comparator_11_eq));  // open: gt, lt
  Comparator #(.width(32), .mode("twosComplement")) comparator_12 (
    .a(EX_PC3), .b(IF_PC), .eq(comparator_12_eq));  // open: gt, lt
  Comparator #(.width(32), .mode("twosComplement")) comparator_13 (
    .a(EX_PC4), .b(IF_PC), .eq(comparator_13_eq));  // open: gt, lt
  Comparator #(.width(32), .mode("twosComplement")) comparator_14 (
    .a(EX_PC5), .b(IF_PC), .eq(comparator_14_eq));  // open: gt, lt
  Comparator #(.width(32), .mode("twosComplement")) comparator_15 (
    .a(EX_PC6), .b(IF_PC), .eq(comparator_15_eq));  // open: gt, lt
  Comparator #(.width(32), .mode("twosComplement")) comparator_16 (
    .a(EX_PC7), .b(IF_PC), .eq(comparator_16_eq));  // open: gt, lt
  and and_10 (L0, V0, comparator_9_eq);
  and and_11 (L1, V1, comparator_10_eq);
  and and_12 (L2, V2, comparator_11_eq);
  and and_13 (L3, V3, comparator_12_eq);
  and and_14 (L4, V4, comparator_13_eq);
  and and_15 (L5, V5, comparator_14_eq);
  and and_16 (L6, V6, comparator_15_eq);
  and and_17 (L7, V7, comparator_16_eq);
  and and_18 (WriteL0, decoder_1_out0, update);
  and and_19 (WriteL1, decoder_1_out1, update);
  and and_20 (WriteL2, decoder_1_out2, update);
  and and_21 (WriteL3, decoder_1_out3, update);
  and and_22 (WriteL4, decoder_1_out4, update);
  and and_23 (WriteL5, decoder_1_out5, update);
  and and_24 (WriteL6, decoder_1_out6, update);
  and and_25 (WriteL7, decoder_1_out7, update);
  or or_10 (or_10_out, L0, L1, L2, L3, L4, L5, L6, L7);
  not not_11 (Miss, or_10_out);

  // Notes on the sheet:
  //   输入引脚区
  //   请勿增改引脚，请勿修改子电路封装
  //   电路功能：利用上面给定的隧道构建8行的Cache，cache映射方式自选
  //   输出引脚区
  //   请在下方利用上方输入输出引脚的隧道信号构建电路，ctrl+d复制选择部件
  //   预测跳转
  //   LRU算法
endmodule

// 状态变换
module \预测状态逻辑转换  (
  input  jmp,
  input  PreStatus1,
  input  PreStatus0,
  output AfterStatus1,
  output AfterStatus0,
  output fail
);

  wire and_1_out, and_2_out, and_3_out, and_4_out, and_5_out, and_6_out, not_1_out, not_2_out, not_3_out,
       not_4_out, not_5_out, not_6_out, not_7_out;

  not not_1 (not_1_out, PreStatus0);
  not not_2 (not_2_out, jmp);
  not not_3 (not_3_out, PreStatus0);
  not not_4 (not_4_out, PreStatus1);
  not not_5 (not_5_out, PreStatus0);
  not not_6 (not_6_out, jmp);
  not not_7 (not_7_out, PreStatus1);
  and and_1 (and_1_out, PreStatus1, not_1_out);
  and and_2 (and_2_out, jmp, PreStatus0);
  and and_3 (and_3_out, not_2_out, PreStatus1, not_3_out);
  and and_4 (and_4_out, jmp, not_4_out, not_5_out);
  and and_5 (and_5_out, not_6_out, PreStatus1);
  and and_6 (and_6_out, jmp, not_7_out);
  or or_1 (AfterStatus1, and_1_out, and_2_out);
  or or_2 (AfterStatus0, and_3_out, and_4_out);
  or or_3 (fail, and_5_out, and_6_out);
endmodule

// ALU
module MIPS_ALU (
  input  [4:0] shamt,
  input  [31:0] X,
  input  [31:0] Y,
  input  [3:0] AluOP,
  output Equal,
  output [31:0] Result,
  output [31:0] Result_2
);

  wire [0:0] comparator_1_lt, comparator_2_lt;
  wire [31:0] adder_1_out, AND_out, divider_1_out, divider_1_rem, multiplier_1_cout, multiplier_1_out,
       NOR_out, OR_out, shifter_1_out, shifter_2_out, shifter_3_out, subtractor_1_out, XOR_out;

  assign AND_out = X & Y;  // AND_Gate AND, 32 bits wide
  assign OR_out = X | Y;  // OR_Gate OR, 32 bits wide
  Shifter #(.width(32), .shift("ll")) shifter_1 (.in(Y), .\dist (shamt), .out(shifter_1_out));
  Shifter #(.width(32), .shift("ar")) shifter_2 (.in(Y), .\dist (shamt), .out(shifter_2_out));
  Shifter #(.width(32), .shift("lr")) shifter_3 (.in(Y), .\dist (shamt), .out(shifter_3_out));
  Multiplier #(.width(32)) multiplier_1 (.a(X), .b(Y), .out(multiplier_1_out), .cout(multiplier_1_cout));  // open: cin
  Divider #(.width(32)) divider_1 (.a(X), .b(Y), .out(divider_1_out), .rem(divider_1_rem));  // open: upper
  Adder #(.width(32)) adder_1 (.a(X), .b(Y), .out(adder_1_out));  // open: cin, cout
  Subtractor #(.width(32)) subtractor_1 (.a(X), .b(Y), .out(subtractor_1_out));  // open: bin, bout
  assign XOR_out = X ^ Y;  // XOR_Gate XOR, 32 bits wide
  assign NOR_out = ~(X | Y);  // NOR_Gate NOR, 32 bits wide
  Comparator #(.width(32), .mode("twosComplement")) comparator_1 (
    .a(X), .b(Y), .eq(Equal), .lt(comparator_1_lt[0]));  // open: gt
  Comparator #(.width(32), .mode("unsigned")) comparator_2 (.a(X), .b(Y), .lt(comparator_2_lt[0]));  // open: gt, eq
  Multiplexer #(.select(4), .width(32), .disabled("Z"), .enable("false")) multiplexer_1 (
    .in0(shifter_1_out), .in1(shifter_2_out), .in2(shifter_3_out), .in3(multiplier_1_out),
    .in4(divider_1_out), .in5(adder_1_out), .in6(subtractor_1_out), .in7(AND_out), .in8(OR_out),
    .in9(XOR_out), .in10(NOR_out), .in11({{31{1'b0}}, comparator_1_lt[0]}),
    .in12({{31{1'b0}}, comparator_2_lt[0]}), .in13({32{1'b0}}), .in14({32{1'b0}}), .in15({32{1'b0}}),
    .out(Result), .sel(AluOP));
  Multiplexer #(.select(4), .width(32), .disabled("Z"), .enable("false")) multiplexer_2 (
    .in0({32{1'b0}}), .in1({32{1'b0}}), .in2({32{1'b0}}), .in3(multiplier_1_cout), .in4(divider_1_rem),
    .in5({32{1'b0}}), .in6({32{1'b0}}), .in7({32{1'b0}}), .in8({32{1'b0}}), .in9({32{1'b0}}),
    .in10({32{1'b0}}), .in11({32{1'b0}}), .in12({32{1'b0}}), .in13({32{1'b0}}), .in14({32{1'b0}}),
    .in15({32{1'b0}}), .out(Result_2), .sel(AluOP));

  // Other names for the same wires on the sheet: Result2[31:0] = Result_2; S[3:0] = AluOP

  // Notes on the sheet:
  //   不要改变此引脚区域内容，也不要改变ALU封装形式
  //   输入引脚
  //   输出引脚
endmodule

module MIPS_Regifile (
  input  [31:0] Din,
  input  Clk,
  input  WE,
  input  [4:0] R1_num,
  input  [4:0] W_num,
  input  [4:0] R2_num,
  output [31:0] R1,
  output [31:0] R2
);

  // RegisterFile registerfile_1: pin names not known; wires that end beside it: Din, Clk, WE, W_num, R1_num, R2_num, R1, R2
endmodule

module \中断按键参考电路  (
  input  \同步清零信号 ,
  output \与中断屏蔽位与 
);

  wire \_1号中断_out , and_1_out, clock_1_out, d_ff_1_q, or_1_out, or_2_out;

  Clock #(.highDuration(1), .lowDuration(1)) clock_1 (.out(clock_1_out));
  Button \_1号中断  (.out(\_1号中断_out ));
  or or_1 (or_1_out, \与中断屏蔽位与 , d_ff_1_q);
  LED #(.active("true")) \_1号中断等待指示灯  (.in(or_1_out));
  D_Flip_Flop #(.trigger("rising"), .Pre_Clr_Positions("LEGACY"), .NegatePresetClear("false"), .enable("true"), .NewFFLayout("false")) d_ff_1 (
    .clk(\_1号中断_out ), .D(1'b1), .Q(d_ff_1_q), .reset(\与中断屏蔽位与 ));  // open: Qn, preset, en
  or or_2 (or_2_out, d_ff_1_q, \与中断屏蔽位与 );
  and and_1 (and_1_out, or_2_out, ~\同步清零信号 );  // AND_Gate
  D_Flip_Flop #(.trigger("rising"), .Pre_Clr_Positions("LEGACY"), .NegatePresetClear("false"), .enable("true"), .NewFFLayout("false")) IR1 (
    .clk(clock_1_out), .D(and_1_out), .Q(\与中断屏蔽位与 ));  // open: Qn, preset, en, reset

  // Notes on the sheet:
  //   中断信号采样参考电路
  //   Reset 
endmodule

// Max3
module \Max3_归并比较  (
  input  [15:0] Y,
  input  [15:0] X,
  input  [2:0] Y_num,
  input  [2:0] X_num,
  output [15:0] MAX,
  output [2:0] Max_num
);

  wire comparator_1_eq, comparator_1_gt, or_1_out;

  Multiplexer #(.select(1), .width(16), .disabled("Z"), .enable("false")) multiplexer_1 (
    .in0(Y), .in1(X), .out(MAX), .sel(or_1_out));
  Comparator #(.width(16), .mode("unsigned")) comparator_1 (
    .a(X), .b(Y), .gt(comparator_1_gt), .eq(comparator_1_eq));  // open: lt
  or or_1 (or_1_out, comparator_1_gt, comparator_1_eq);
  Multiplexer #(.select(1), .width(3), .disabled("Z"), .enable("false")) multiplexer_2 (
    .in0(Y_num), .in1(X_num), .out(Max_num), .sel(or_1_out));

  // Notes on the sheet:
  //   输出两个输入中的较大值，并输出较大值的3位编号
endmodule
