// Logisim project 推箱子游戏（小组任务）.circ as structural Verilog: 12 circuits, main circuit ◇重定向流水线+单级中断
module \重定向流水线_单级中断  (
);

  wire and_1_out, and_2_out, and_3_out, and_4_out, and_6_out, BRANCH, branch_t, CLK, \cpu控制器_1_alu_src ,
       \cpu控制器_1_beq , \cpu控制器_1_blez , \cpu控制器_1_bne , \cpu控制器_1_jal , \cpu控制器_1_jmp , \cpu控制器_1_jr ,
       \cpu控制器_1_lb , \cpu控制器_1_memtoreg , \cpu控制器_1_memwrite , \cpu控制器_1_regdst , \cpu控制器_1_regwrite ,
       \cpu控制器_1_srlv , \cpu控制器_1_syscall , en, eq, ERET, EX_ERET, EX_RegWrite, Go, INT, IR1, IR2, IR3, IR4,
       IR5, IR6, JAL, JMP, JR, LUI, MEM_MemtoReg, MEM_RegWrite, MemWrite, mips_alu_1_equal, not_1_out,
       not_2_out, not_3_out, or_1_out, or_2_out, or_3_out, or_4_out, or_7_out, or_8_out, or_9_out, or_10_out,
       RegWrite, RST, SignedExt, stall, syscall, sysen, UBRANCH, W1, W2, W3, W4, W5, W6, WB_JAL, WB_MemtoReg,
       \流水接口部件_1_传输状态out_表明当前传输数据有效 , \流水接口部件_2_alusrcbout , \流水接口部件_2_beqout , \流水接口部件_2_blezout ,
       \流水接口部件_2_bneout , \流水接口部件_2_lbout , \流水接口部件_2_memtoregout , \流水接口部件_2_memwriteout ,
       \流水接口部件_2_srlvout , \流水接口部件_2_syscallout , \流水接口部件_2_传输状态out_表明当前传输数据有效 , \流水接口部件_3_eqout ,
       \流水接口部件_3_jalout , \流水接口部件_3_lbout , \流水接口部件_3_syscallout , \流水接口部件_3_传输状态out_表明当前传输数据有效 ,
       \流水接口部件_4_传输状态out_表明当前传输数据有效 ;
  wire [1:0] forwardA, forwardB, priority_encoder_2_out;
  wire [2:0] priority_encoder_1_out;
  wire [3:0] \cpu控制器_1_alu_op , \流水接口部件_2_aluopout ;
  wire [4:0] EX_Rs, EX_Rt, EX_WriteReg_num, MEM_WriteReg_num, multiplexer_7_out, multiplexer_9_out,
       multiplexer_12_out, Rs, Rt, WB_WriteReg_num, \流水接口部件_2_shamtout ;
  wire [7:0] multiplexer_15_out;
  wire [23:0] ADDR_val;
  wire [31:0] a0out, adder_1_out, bit_extender_1_out, bit_extender_2_out, bit_extender_3_out,
       bit_extender_4_out, BJMP, controlled_buffer_1_out, data1, data2, data3, EPC, EX_IR, EX_PC, ID_IR,
       ID_PC, IDATA_val, IF_IR, IF_PC, IJMP, INT_ADDR, LedData, MEM_IR, MEM_PC, mips_alu_1_result,
       mips_regfile_1_r1, mips_regfile_1_r2, multiplexer_1_out, multiplexer_2_out, multiplexer_6_out,
       multiplexer_8_out, multiplexer_11_out, multiplexer_13_out, multiplexer_14_out, multiplexer_16_out,
       ODATA_val, PC, PC_4, RDin, RJMP, shifter_1_out, subtractor_1_out, WB_Din, WB_IR, WB_PC,
       \流水接口部件_1_pc4out , \流水接口部件_2_aout , \流水接口部件_2_bout , \流水接口部件_2_imm1out , \流水接口部件_2_imm2out ,
       \流水接口部件_3_pc4out ;

  // Mips_Probe mips_probe_1: pin names not known; wires that end beside it: IF_IR
  // Mips_Probe mips_probe_2: pin names not known; wires that end beside it: ID_IR
  ROM #(.addrWidth(16), .dataWidth(32), .Select("high")) rom_1 (.addr(IF_PC[17:2]), .data(IF_IR), .sel(1'b1));
  LED #(.active("true")) led_1 (.in(en));
  Button button_1 (.out(IR3));
  // Mips_Probe mips_probe_3: pin names not known; wires that end beside it: EX_IR
  Button button_2 (.out(RST));
  Button button_3 (.out(IR1));
  Button button_4 (.out(IR4));
  Button button_5 (.out(IR2));
  Button button_6 (.out(Go));
  Button button_7 (.out(IR5));
  // Mips_Probe mips_probe_4: pin names not known; wires that end beside it: MEM_IR, RST
  RAM #(.addrWidth(24), .dataWidth(32), .bus("separate"), .Select("high")) ram_1 (
    .addr(ADDR_val), .din(IDATA_val), .data(ODATA_val), .str(MemWrite), .sel(1'b1), .clk(CLK), .ld(1'b1));  // open: clr
  Button button_8 (.out(IR6));
  // Mips_Probe mips_probe_5: pin names not known; wires that end beside it: WB_IR
  // LCD_Video lcd_video_1: pin names not known; wires that end beside it: LedData[31], CLK, LedData[30], LedData[29:23], LedData[22:16], LedData[15:0]
  Clock #(.highDuration(1), .lowDuration(1)) clock_1 (.out(CLK));
  LED #(.active("true")) led_2 (.in(W1));
  LED #(.active("true")) led_3 (.in(W2));
  LED #(.active("true")) led_4 (.in(W3));
  LED #(.active("true")) led_5 (.in(W4));
  LED #(.active("true")) led_6 (.in(W5));
  LED #(.active("true")) led_7 (.in(W6));
  // Probe on EPC
  or or_1 (or_1_out, JAL, JMP);
  Priority_Encoder #(.select(3), .disabled("Z")) priority_encoder_1 (
    .in0(1'b1), .in1(branch_t), .in2(or_1_out), .in3(JR), .in4(EX_ERET), .in5(INT),
    .out(priority_encoder_1_out));  // open: in6, in7, gs, en_out, en_in
  or or_2 (or_2_out, JAL, JMP);
  Priority_Encoder #(.select(2), .disabled("Z")) priority_encoder_2 (
    .in0(1'b1), .in1(branch_t), .in2(or_2_out), .in3(JR), .out(priority_encoder_2_out));  // open: gs, en_out, en_in
  Multiplexer #(.select(2), .width(32), .disabled("Z"), .enable("false")) multiplexer_1 (
    .in0(PC_4), .in1(BJMP), .in2(IJMP), .in3(RJMP), .out(multiplexer_1_out), .sel(priority_encoder_2_out));
  // Probe on priority_encoder_1_out
  Multiplexer #(.select(3), .width(32), .disabled("Z"), .enable("false")) multiplexer_2 (
    .in0(adder_1_out), .in1(BJMP), .in2(IJMP), .in3(RJMP), .in4(EPC), .in5(INT_ADDR),
    .out(multiplexer_2_out), .sel(priority_encoder_1_out));  // open: in6, in7
  Register #(.width(32), .trigger("rising"), .Select("low")) u_PC (
    .D(multiplexer_2_out), .en(en), .Q(IF_PC), .clk(CLK), .clr(RST));
  \中断产生电路  \u_中断产生电路_1  (
    .CLK(CLK), .ERET(EX_ERET), .\_1号中断 (IR1), .\_1号中断等待指示灯 (W1), .\_2号中断 (IR2), .\_2号中断等待指示灯 (W2),
    .PC(multiplexer_1_out), .\_3号中断 (IR3), .\_3号中断等待指示灯 (W3), .INT(INT), .INT_ADDR(INT_ADDR), .EPC(EPC),
    .EX_IR(EX_IR), .\_4号中断 (IR4), .\_4号中断等待指示灯 (W4), .\_5号中断 (IR5), .\_5号中断等待指示灯 (W5), .\_6号中断 (IR6),
    .\_6号中断等待指示灯 (W6));
  Adder #(.width(32)) adder_1 (.a(IF_PC), .b(32'h4), .out(adder_1_out));  // open: cin, cout
  or or_3 (or_3_out, stall, ~sysen);  // OR_Gate
  or or_4 (or_4_out, EX_ERET, INT, BRANCH);
  \流水接口部件  \u_流水接口部件_1  (
    .IRin(IF_IR), .PC4in(adder_1_out), .\传输状态In_表明当前传输数据有效 (1'b1), .CLK(CLK), .IRout(ID_IR),
    .PC4out(\流水接口部件_1_pc4out ), .\传输状态Out_表明当前传输数据有效 (\流水接口部件_1_传输状态out_表明当前传输数据有效 ),
    .\同步清零_气泡_高电平有效 (or_4_out), .\使能端_低电平有效_stall_高电平有效 (or_3_out), .PCin(IF_PC), .PCout(ID_PC), .\异步清零端 (RST));  // open: BEQin, BLEZin, BNEin, MemtoRegin, MemWritein, AluOPin, AluSrcBin, RegWritein, LBin, SRLVin, Syscallin, Ain, Bin, SHAMTin, IMM1in, BEQout, BLEZout, BNEout, MemtoRegout, MemWriteout, AluOPout, AluSrcBout, RegWriteout, LBout, SRLVout, Syscallout, Aout, Bout, SHAMTout, IMM1out, IMM2in, IMM2out, JMPout, JALin, JALout, JMPin, JRout, JRin, Rin, Rout, MEMin, MEMout, WriteReg_in, WriteReg_out, eqin, eqout, Rsin, Rsout, Rtin, Rtout, ERETin, ERETout
  \CPU控制器  \cpu控制器_1  (
    .OP(ID_IR[31:26]), .Func(ID_IR[5:0]), .ALU_OP(\cpu控制器_1_alu_op ), .MemToReg(\cpu控制器_1_memtoreg ),
    .MemWrite(\cpu控制器_1_memwrite ), .ALU_SRC(\cpu控制器_1_alu_src ), .RegWrite(\cpu控制器_1_regwrite ),
    .SysCALL(\cpu控制器_1_syscall ), .SignedExt(SignedExt), .RegDst(\cpu控制器_1_regdst ), .Beq(\cpu控制器_1_beq ),
    .Bne(\cpu控制器_1_bne ), .JR(\cpu控制器_1_jr ), .JMP(\cpu控制器_1_jmp ), .JAL(\cpu控制器_1_jal ),
    .SRLV(\cpu控制器_1_srlv ), .LB(\cpu控制器_1_lb ), .BLEZ(\cpu控制器_1_blez ), .ERET(ERET), .LUI(LUI));
  assign bit_extender_1_out = {{16{ID_IR[15]}}, ID_IR[15:0]};  // Bit_Extender bit_extender_1
  assign bit_extender_2_out = {{16{1'b0}}, ID_IR[15:0]};  // Bit_Extender bit_extender_2
  Multiplexer #(.select(1), .width(5), .disabled("Z"), .enable("false")) multiplexer_3 (
    .in0(ID_IR[25:21]), .in1(5'b00010), .out(Rs), .sel(\cpu控制器_1_syscall ));
  Multiplexer #(.select(1), .width(5), .disabled("Z"), .enable("false")) multiplexer_4 (
    .in0(ID_IR[20:16]), .in1(5'b00100), .out(Rt), .sel(\cpu控制器_1_syscall ));
  Multiplexer #(.select(1), .width(32), .disabled("Z"), .enable("false")) multiplexer_5 (
    .in0(WB_Din), .in1(PC), .out(RDin), .sel(WB_JAL));
  Multiplexer #(.select(1), .width(32), .disabled("Z"), .enable("false")) multiplexer_6 (
    .in0(bit_extender_1_out), .in1(bit_extender_2_out), .out(multiplexer_6_out), .sel(SignedExt));
  assign bit_extender_3_out = {{6{ID_IR[25]}}, ID_IR[25:0]};  // Bit_Extender bit_extender_3
  and and_1 (and_1_out, syscall, eq);
  assign controlled_buffer_1_out = and_1_out ? a0out : 32'bz;  // Controlled_Buffer controlled_buffer_1
  Register #(.width(32), .trigger("rising"), .Select("low")) register_1 (
    .D(controlled_buffer_1_out), .Q(LedData), .clk(CLK), .clr(RST));  // open: en
  or or_5 (BRANCH, branch_t, JMP, JAL, JR);
  or or_6 (UBRANCH, JMP, JAL, JR);
  MIPS_Regfile mips_regfile_1 (
    .Din(RDin), .Clk(CLK), .R1(mips_regfile_1_r1), .R2(mips_regfile_1_r2), .WE(RegWrite),
    .W_num(WB_WriteReg_num), .R1_num(Rs), .R2_num(Rt));
  Multiplexer #(.select(1), .width(5), .disabled("Z"), .enable("false")) multiplexer_7 (
    .in0(ID_IR[20:16]), .in1(ID_IR[15:11]), .out(multiplexer_7_out), .sel(\cpu控制器_1_regdst ));
  Multiplexer #(.select(1), .width(32), .disabled("Z"), .enable("false")) multiplexer_8 (
    .in0(multiplexer_6_out), .in1({ID_IR[15:0], {16{1'b0}}}), .out(multiplexer_8_out), .sel(LUI));
  Multiplexer #(.select(1), .width(5), .disabled("Z"), .enable("false")) multiplexer_9 (
    .in0(multiplexer_7_out), .in1({5{1'b1}}), .out(multiplexer_9_out), .sel(\cpu控制器_1_jal ));
  or or_7 (or_7_out, EX_ERET, INT, stall, BRANCH);
  \流水接口部件  \u_流水接口部件_2  (
    .BEQin(\cpu控制器_1_beq ), .BLEZin(\cpu控制器_1_blez ), .BNEin(\cpu控制器_1_bne ),
    .MemtoRegin(\cpu控制器_1_memtoreg ), .MemWritein(\cpu控制器_1_memwrite ), .AluOPin(\cpu控制器_1_alu_op ),
    .AluSrcBin(\cpu控制器_1_alu_src ), .RegWritein(\cpu控制器_1_regwrite ), .LBin(\cpu控制器_1_lb ),
    .SRLVin(\cpu控制器_1_srlv ), .Syscallin(\cpu控制器_1_syscall ), .Ain(mips_regfile_1_r1),
    .Bin(mips_regfile_1_r2), .SHAMTin(ID_IR[10:6]), .IMM1in(multiplexer_8_out), .IRin(ID_IR),
    .PC4in(\流水接口部件_1_pc4out ), .\传输状态In_表明当前传输数据有效 (\流水接口部件_1_传输状态out_表明当前传输数据有效 ), .CLK(CLK),
    .BEQout(\流水接口部件_2_beqout ), .BLEZout(\流水接口部件_2_blezout ), .BNEout(\流水接口部件_2_bneout ),
    .MemtoRegout(\流水接口部件_2_memtoregout ), .MemWriteout(\流水接口部件_2_memwriteout ),
    .AluOPout(\流水接口部件_2_aluopout ), .AluSrcBout(\流水接口部件_2_alusrcbout ), .RegWriteout(EX_RegWrite),
    .LBout(\流水接口部件_2_lbout ), .SRLVout(\流水接口部件_2_srlvout ), .Syscallout(\流水接口部件_2_syscallout ),
    .Aout(\流水接口部件_2_aout ), .Bout(\流水接口部件_2_bout ), .SHAMTout(\流水接口部件_2_shamtout ),
    .IMM1out(\流水接口部件_2_imm1out ), .IRout(EX_IR), .PC4out(PC_4),
    .\传输状态Out_表明当前传输数据有效 (\流水接口部件_2_传输状态out_表明当前传输数据有效 ), .\同步清零_气泡_高电平有效 (or_7_out),
    .\使能端_低电平有效_stall_高电平有效 (not_1_out), .IMM2in(bit_extender_3_out), .IMM2out(\流水接口部件_2_imm2out ),
    .PCin(ID_PC), .PCout(EX_PC), .JMPout(JMP), .JALin(\cpu控制器_1_jal ), .JALout(JAL), .JMPin(\cpu控制器_1_jmp ),
    .JRout(JR), .JRin(\cpu控制器_1_jr ), .WriteReg_in(multiplexer_9_out), .WriteReg_out(EX_WriteReg_num),
    .\异步清零端 (RST), .Rsin(Rs), .Rsout(EX_Rs), .Rtin(Rt), .Rtout(EX_Rt), .ERETin(ERET), .ERETout(EX_ERET));  // open: Rin, Rout, MEMin, MEMout, eqin, eqout
  not not_1 (not_1_out, sysen);
  Multiplexer #(.select(2), .width(32), .disabled("Z"), .enable("false")) multiplexer_10 (
    .in0(\流水接口部件_2_aout ), .in1(data1), .in2(data2), .in3(data3), .out(RJMP), .sel(forwardA));
  Multiplexer #(.select(2), .width(32), .disabled("Z"), .enable("false")) multiplexer_11 (
    .in0(\流水接口部件_2_bout ), .in1(data1), .in2(data2), .in3(data3), .out(multiplexer_11_out), .sel(forwardB));
  Multiplexer #(.select(1), .width(5), .disabled("Z"), .enable("false")) multiplexer_12 (
    .in0(\流水接口部件_2_shamtout ), .in1(RJMP[4:0]), .out(multiplexer_12_out), .sel(\流水接口部件_2_srlvout ));
  Multiplexer #(.select(1), .width(32), .disabled("Z"), .enable("false")) multiplexer_13 (
    .in0(\流水接口部件_2_imm1out ), .in1(32'h22), .out(multiplexer_13_out), .sel(\流水接口部件_2_syscallout ));
  Shifter #(.width(32), .shift("ll")) shifter_1 (.in(\流水接口部件_2_imm1out ), .\dist (5'b00010), .out(shifter_1_out));
  Shifter #(.width(32), .shift("ll")) shifter_2 (.in(\流水接口部件_2_imm2out ), .\dist (5'b00010), .out(IJMP));
  D_Flip_Flop #(.trigger("rising"), .Pre_Clr_Positions("LEGACY"), .NegatePresetClear("false"), .enable("true"), .NewFFLayout("false")) d_ff_1 (
    .clk(CLK), .D(and_2_out), .Qn(sysen), .en(sysen), .reset(or_8_out));  // open: Q, preset
  and and_2 (and_2_out, syscall, ~eq);  // AND_Gate
  or or_8 (or_8_out, RST, Go);
  Multiplexer #(.select(1), .width(32), .disabled("Z"), .enable("false")) multiplexer_14 (
    .in0(multiplexer_11_out), .in1(multiplexer_13_out), .out(multiplexer_14_out), .sel(\流水接口部件_2_alusrcbout ));
  Adder #(.width(32)) adder_2 (.a(shifter_1_out), .b(PC_4), .out(BJMP));  // open: cin, cout
  and and_3 (and_3_out, mips_alu_1_equal, \流水接口部件_2_beqout );
  and and_4 (and_4_out, \流水接口部件_2_bneout , ~mips_alu_1_equal);  // AND_Gate
  MIPS_ALU mips_alu_1 (
    .shamt(multiplexer_12_out), .X(RJMP), .Y(multiplexer_14_out), .AluOP(\流水接口部件_2_aluopout ),
    .Equal(mips_alu_1_equal), .Result(mips_alu_1_result));  // open: Result_2
  or or_9 (or_9_out, BRANCH, ~stall);  // OR_Gate
  and and_5 (en, or_9_out, sysen);
  and and_6 (and_6_out, \流水接口部件_2_blezout , or_10_out);
  or or_10 (or_10_out, mips_alu_1_equal, mips_alu_1_result[0]);
  or or_11 (branch_t, and_4_out, and_6_out, and_3_out);
  \流水接口部件  \u_流水接口部件_3  (
    .MemtoRegin(\流水接口部件_2_memtoregout ), .MemWritein(\流水接口部件_2_memwriteout ), .RegWritein(EX_RegWrite),
    .LBin(\流水接口部件_2_lbout ), .Syscallin(\流水接口部件_2_syscallout ), .Bin(multiplexer_11_out), .IRin(EX_IR),
    .PC4in(PC_4), .\传输状态In_表明当前传输数据有效 (\流水接口部件_2_传输状态out_表明当前传输数据有效 ), .CLK(CLK), .MemtoRegout(MEM_MemtoReg),
    .MemWriteout(MemWrite), .RegWriteout(MEM_RegWrite), .LBout(\流水接口部件_3_lbout ),
    .Syscallout(\流水接口部件_3_syscallout ), .Bout(IDATA_val), .IRout(MEM_IR), .PC4out(\流水接口部件_3_pc4out ),
    .\传输状态Out_表明当前传输数据有效 (\流水接口部件_3_传输状态out_表明当前传输数据有效 ), .\使能端_低电平有效_stall_高电平有效 (not_2_out), .PCin(EX_PC),
    .PCout(MEM_PC), .JALin(JAL), .JALout(\流水接口部件_3_jalout ), .Rin(mips_alu_1_result), .Rout(data1),
    .WriteReg_in(EX_WriteReg_num), .WriteReg_out(MEM_WriteReg_num), .eqin(mips_alu_1_equal),
    .eqout(\流水接口部件_3_eqout ), .\异步清零端 (RST));  // open: BEQin, BLEZin, BNEin, AluOPin, AluSrcBin, SRLVin, Ain, SHAMTin, IMM1in, BEQout, BLEZout, BNEout, AluOPout, AluSrcBout, SRLVout, Aout, SHAMTout, IMM1out, 同步清零_气泡_高电平有效, IMM2in, IMM2out, JMPout, JMPin, JRout, JRin, MEMin, MEMout, Rsin, Rsout, Rtin, Rtout, ERETin, ERETout
  not not_2 (not_2_out, sysen);
  Subtractor #(.width(32)) subtractor_1 (
    .a(data1), .b(32'h10000), .out({subtractor_1_out[31:26], ADDR_val, subtractor_1_out[1:0]}));  // open: bin, bout
  \重定向检测电路  \u_重定向检测电路_1  (
    .OP(EX_IR[31:26]), .FUNC(EX_IR[5:0]), .Rs(EX_Rs), .Rt(EX_Rt), .MEM_WriteReg_num(MEM_WriteReg_num),
    .WB_WriteReg_num(WB_WriteReg_num), .MEM_RegWrite(MEM_RegWrite), .WB_RegWrite(RegWrite),
    .forwardA(forwardA), .MEM_MemtoReg(MEM_MemtoReg), .WB_MemtoReg(WB_MemtoReg), .forwardB(forwardB));
  Multiplexer #(.select(2), .width(8), .disabled("Z"), .enable("false")) multiplexer_15 (
    .in0(ODATA_val[7:0]), .in1(ODATA_val[15:8]), .in2(ODATA_val[23:16]), .in3(ODATA_val[31:24]),
    .out(multiplexer_15_out), .sel(data1[1:0]));
  assign bit_extender_4_out = {{24{multiplexer_15_out[7]}}, multiplexer_15_out};  // Bit_Extender bit_extender_4
  Multiplexer #(.select(1), .width(32), .disabled("Z"), .enable("false")) multiplexer_16 (
    .in0(ODATA_val), .in1(bit_extender_4_out), .out(multiplexer_16_out), .sel(\流水接口部件_3_lbout ));
  \流水接口部件  \u_流水接口部件_4  (
    .MemtoRegin(MEM_MemtoReg), .RegWritein(MEM_RegWrite), .Syscallin(\流水接口部件_3_syscallout ), .Bin(IDATA_val),
    .IRin(MEM_IR), .PC4in(\流水接口部件_3_pc4out ), .\传输状态In_表明当前传输数据有效 (\流水接口部件_3_传输状态out_表明当前传输数据有效 ), .CLK(CLK),
    .MemtoRegout(WB_MemtoReg), .RegWriteout(RegWrite), .Syscallout(syscall), .Bout(a0out), .IRout(WB_IR),
    .PC4out(PC), .\传输状态Out_表明当前传输数据有效 (\流水接口部件_4_传输状态out_表明当前传输数据有效 ), .\使能端_低电平有效_stall_高电平有效 (not_3_out),
    .PCin(MEM_PC), .PCout(WB_PC), .JALin(\流水接口部件_3_jalout ), .JALout(WB_JAL), .Rin(data1), .Rout(data2),
    .MEMin(multiplexer_16_out), .MEMout(data3), .WriteReg_in(MEM_WriteReg_num),
    .WriteReg_out(WB_WriteReg_num), .eqin(\流水接口部件_3_eqout ), .eqout(eq), .\异步清零端 (RST));  // open: BEQin, BLEZin, BNEin, MemWritein, AluOPin, AluSrcBin, LBin, SRLVin, Ain, SHAMTin, IMM1in, BEQout, BLEZout, BNEout, MemWriteout, AluOPout, AluSrcBout, LBout, SRLVout, Aout, SHAMTout, IMM1out, 同步清零_气泡_高电平有效, IMM2in, IMM2out, JMPout, JMPin, JRout, JRin, Rsin, Rsout, Rtin, Rtout, ERETin, ERETout
  not not_3 (not_3_out, sysen);
  Multiplexer #(.select(1), .width(32), .disabled("Z"), .enable("false")) multiplexer_17 (
    .in0(data2), .in1(data3), .out(WB_Din), .sel(WB_MemtoReg));
  \load_use检测电路  \load_use检测电路_1  (
    .ID_OP(ID_IR[31:26]), .ID_FUNC(ID_IR[5:0]), .EX_OP(EX_IR[31:26]), .ID_Rt(Rt),
    .EX_WriteReg_num(EX_WriteReg_num), .load_use(stall), .ID_Rs(Rs));
  // Probe on WB_Din

  // Other names for the same wires on the sheet: PC_val[15:0] = IF_PC[17:2]; IR_val[31:0] = IF_IR;
  //   MDin[31:0] = IDATA_val; WB_RegWrite = RegWrite

  // Notes on the sheet:
  //   指令存储器
  //   contents of rom_1 (hex, n*v repeats v):
  //   3c011001 343d3000 8100045 23bdfffc afa80000 24080001 3c011001 ac280628 24080001 3c011001 ac28062c
  //   8fa80000 23bd0004 42000018 23bdfffc afa80000 24080002 3c011001 ac280628 24080001 3c011001 ac28062c
  //   8fa80000 23bd0004 42000018 23bdfffc afa80000 24080003 3c011001 ac280628 24080001 3c011001 ac28062c
  //   8fa80000 23bd0004 42000018 23bdfffc afa80000 24080004 3c011001 ac280628 24080001 3c011001 ac28062c
  //   8fa80000 23bd0004 42000018 23bdfffc afa80000 24080005 3c011001 ac280628 24080001 3c011001 ac28062c
  //   8fa80000 23bd0004 42000018 23bdfffc afa80000 24080006 3c011001 ac280628 24080001 3c011001 ac28062c
  //   8fa80000 23bd0004 42000018 c1007cc 2402000a c 24190001 3c011001 ac3904d0 810004d 8100045 c1007cc
  //   3c011001 8c24041c c1007d1 24090000 3c011001 ac290630 3c011001 8c240454 3c011001 8c250484 3c011001
  //   8c260488 c1007e1 c10086f 3c011001 8c280628 20010001 1428002e 3c011001 8c290630 20010000 1029fff7
  //   3c011001 8c240480 3c011001 8c250484 3c011001 8c260488 3c011001 8c2a048c 23bdfffc afb80000 240b0000
  //   9c020 13000003 16a5820 2318ffff 1700fffd 8fb80000 23bd0004 cb3020 c1007e1 2129ffff 3c011001 ac290630
  //   3c011001 8c240454 3c011001 8c250484 3c011001 8c260488 23bdfffc afb80000 240b0000 9c020 13000003
  //   16a5820 2318ffff 1700fffd 8fb80000 23bd0004 cb3020 c1007e1 810005b 20010002 1428002e 3c011001
  //   8c290630 20010002 1029ffc7 3c011001 8c240480 3c011001 8c250484 3c011001 8c260488 3c011001 8c2a048c
  //   23bdfffc afb80000 240b0000 9c020 13000003 16a5820 2318ffff 1700fffd 8fb80000 23bd0004 cb3020 c1007e1
  //   21290001 3c011001 ac290630 3c011001 8c240454 3c011001 8c250484 3c011001 8c260488 23bdfffc afb80000
  //   240b0000 9c020 13000003 16a5820 2318ffff 1700fffd 8fb80000 23bd0004 cb3020 c1007e1 810005b 20010005
  //   1428000e 3c011001 8c290630 20010000 14290004 24190001 3c011001 ac3904d0 8100152 20010001 14290001
  //   81007bf 20010002 1429ff8e 81000d2 20010006 1428ff8b 8100045 810005b c1007cc 3c011001 8c240420
  //   c1007d1 3c011001 ac200634 3c011001 8c240454 3c011001 8c2504b8 3c011001 8c2604bc c1007e1 c10086f
  //   3c011001 8c280628 20010003 14280030 3c011001 8c290634 20010000 1029fff7 3c011001 8c240480 3c011001
  //   8c2504c4 3c011001 8c2604c8 3c011001 8c2a04cc 23bdfffc afb80000 240b0000 9c020 13000003 16a5820
  //   2318ffff 1700fffd 8fb80000 23bd0004 ab2820 c1007e1 2129ffff 3c011001 ac290634 3c011001 8c240454
  //   3c011001 8c2504b8 3c011001 8c2604bc 3c011001 8c2a04c0 23bdfffc afb80000 240b0000 9c020 13000003
  //   16a5820 2318ffff 1700fffd 8fb80000 23bd0004 ab2820 c1007e1 81000df 20010004 14280030 3c011001
  //   8c290634 20010002 1029ffc5 3c011001 8c240480 3c011001 8c2504c4 3c011001 8c2604c8 3c011001 8c2a04cc
  //   23bdfffc afb80000 240b0000 9c020 13000003 16a5820 2318ffff 1700fffd 8fb80000 23bd0004 ab2820 c1007e1
  //   21290001 3c011001 ac290634 3c011001 8c240454 3c011001 8c2504b8 3c011001 8c2604bc 3c011001 8c2a04c0
  //   23bdfffc afb80000 240b0000 9c020 13000003 16a5820 2318ffff 1700fffd 8fb80000 23bd0004 ab2820 c1007e1
  //   81000df 20010005 14280006 3c011001 8c290634 21390001 3c011001 ac3904d0 8100152 20010006 1428ff8f
  //   810004d 81000df c1007cc c100926 32021 c1007d1 c1007f9 3c011001 8c280624 20010000 14280005 3c011001
  //   8c2904d0 20010003 10290560 8100635 3c011001 8c280618 20010000 102805dd c10086f 3c011001 8c280628
  //   20010001 1428012d 3c011001 8c29061c 3c011001 8c2a0620 20010000 1029ffe8 3c011001 342404d4 92821
  //   a3021 3c011001 8c300418 3c011001 8c310418 c10087c 36021 20a5ffff c10087c 36821 20010001 102dffd9
  //   20010000 142d0022 3c011001 8c2b0618 216bffff 3c011001 ac2b0618 c1007f9 20010003 142c000c 3c011001
  //   8c240480 24120000 c1008da 2129ffff 3c011001 ac29061c 3c011001 8c240448 24120003 c1008da 8100157
  //   20010006 142cffc1 3c011001 8c240450 24120002 c1008da 2129ffff 3c011001 ac29061c 3c011001 8c240448
  //   24120003 c1008da 8100157 20010004 142d0066 20010000 1026ffb1 20a5ffff c10087c 37021 20010001
  //   102effac 20010004 102effaa 20010005 102effa8 3c011001 8c2b0618 216bffff 3c011001 ac2b0618 c1007f9
  //   20010000 142e0026 20010003 142c0011 3c011001 8c240480 24120000 c1008da 2129ffff 3c011001 ac29061c
  //   3c011001 8c240448 24120003 c1008da 2129ffff 3c011001 8c240444 24120004 c1008da 8100157 2001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
  //   左
  //   小组项目结果展示
  //   重置
  //   上
  //   下
  //   右
  //   游戏控制界面
  //   运行须知
  //   在正式运行本项目之前，需要向数据寄存器中添加我们编写好的数据
  //   要访问完整的项目，请访问网址：https://github.com/Mipsers/Box-Pushing-Game
  //   我们的数据寄存器存在于data/res.txt中
  //   确认
  //   数据存储器
  //   开始
  //   返回主页面
  //   中断等待指示
  //   指令字
  //   OP
  //   OP
  //   Func
  //   Func
  //   rs
  //   rt
  //   rd
  //   shamt
  //   imm
  //   J/JAL
  //   JMP
  //   JAL
  //   JR
  //   Beq
  //   Blez
  //   Bne
  //   AluOP
  //   AluSrcB
  //   RegWrite
  //   LB
  //   SRLV
  //   RegDst
  //   Syscall
  //   MemToReg
  //   MemWrite
  //   流水电路
  //   OP
  //   Func
  //   OP
  //   Func
  //   OP
endmodule

module \流水接口部件  (
  input  ERETin,
  input  [4:0] Rsin,
  input  [4:0] Rtin,
  input  JMPin,
  input  JALin,
  input  JRin,
  input  BEQin,
  input  BLEZin,
  input  BNEin,
  input  MemtoRegin,
  input  MemWritein,
  input  [3:0] AluOPin,
  input  AluSrcBin,
  input  RegWritein,
  input  LBin,
  input  SRLVin,
  input  Syscallin,
  input  [31:0] Rin,
  input  [31:0] MEMin,
  input  [31:0] Ain,
  input  [31:0] Bin,
  input  [4:0] SHAMTin,
  input  [31:0] IMM1in,
  input  [31:0] IMM2in,
  input  [31:0] PCin,
  input  [31:0] IRin,
  input  [31:0] PC4in,
  input  [4:0] WriteReg_in,
  input  eqin,
  input  \传输状态In_表明当前传输数据有效 ,
  input  \异步清零端 ,
  input  CLK,
  input  \同步清零_气泡_高电平有效 ,
  input  \使能端_低电平有效_stall_高电平有效 ,
  output ERETout,
  output [4:0] Rsout,
  output [4:0] Rtout,
  output JMPout,
  output JALout,
  output JRout,
  output BEQout,
  output BLEZout,
  output BNEout,
  output MemtoRegout,
  output MemWriteout,
  output [3:0] AluOPout,
  output AluSrcBout,
  output RegWriteout,
  output LBout,
  output SRLVout,
  output Syscallout,
  output [31:0] Rout,
  output [31:0] MEMout,
  output [31:0] Aout,
  output [31:0] Bout,
  output [4:0] SHAMTout,
  output [31:0] IMM1out,
  output [31:0] IMM2out,
  output [31:0] PCout,
  output [31:0] IRout,
  output [31:0] PC4out,
  output [4:0] WriteReg_out,
  output eqout,
  output \传输状态Out_表明当前传输数据有效 
);

  wire multiplexer_1_out, multiplexer_4_out, multiplexer_5_out, multiplexer_6_out, multiplexer_7_out,
       multiplexer_8_out, multiplexer_9_out, multiplexer_10_out, multiplexer_11_out, multiplexer_13_out,
       multiplexer_14_out, multiplexer_15_out, multiplexer_16_out, multiplexer_17_out, multiplexer_29_out,
       multiplexer_30_out, not_1_out;
  wire [3:0] multiplexer_12_out;
  wire [4:0] multiplexer_2_out, multiplexer_3_out, multiplexer_22_out, multiplexer_28_out;
  wire [31:0] multiplexer_18_out, multiplexer_19_out, multiplexer_20_out, multiplexer_21_out,
       multiplexer_23_out, multiplexer_24_out, multiplexer_25_out, multiplexer_26_out, multiplexer_27_out;

  Multiplexer #(.select(1), .width(1), .disabled("Z"), .enable("false")) multiplexer_1 (
    .in0(ERETin), .in1(1'b0), .out(multiplexer_1_out), .sel(\同步清零_气泡_高电平有效 ));
  Multiplexer #(.select(1), .width(5), .disabled("Z"), .enable("false")) multiplexer_2 (
    .in0(Rsin), .in1({5{1'b0}}), .out(multiplexer_2_out), .sel(\同步清零_气泡_高电平有效 ));
  Multiplexer #(.select(1), .width(5), .disabled("Z"), .enable("false")) multiplexer_3 (
    .in0(Rtin), .in1({5{1'b0}}), .out(multiplexer_3_out), .sel(\同步清零_气泡_高电平有效 ));
  Multiplexer #(.select(1), .width(1), .disabled("Z"), .enable("false")) multiplexer_4 (
    .in0(JMPin), .in1(1'b0), .out(multiplexer_4_out), .sel(\同步清零_气泡_高电平有效 ));
  Multiplexer #(.select(1), .width(1), .disabled("Z"), .enable("false")) multiplexer_5 (
    .in0(JALin), .in1(1'b0), .out(multiplexer_5_out), .sel(\同步清零_气泡_高电平有效 ));
  Multiplexer #(.select(1), .width(1), .disabled("Z"), .enable("false")) multiplexer_6 (
    .in0(JRin), .in1(1'b0), .out(multiplexer_6_out), .sel(\同步清零_气泡_高电平有效 ));
  Multiplexer #(.select(1), .width(1), .disabled("Z"), .enable("false")) multiplexer_7 (
    .in0(BEQin), .in1(1'b0), .out(multiplexer_7_out), .sel(\同步清零_气泡_高电平有效 ));
  Multiplexer #(.select(1), .width(1), .disabled("Z"), .enable("false")) multiplexer_8 (
    .in0(BLEZin), .in1(1'b0), .out(multiplexer_8_out), .sel(\同步清零_气泡_高电平有效 ));
  Multiplexer #(.select(1), .width(1), .disabled("Z"), .enable("false")) multiplexer_9 (
    .in0(BNEin), .in1(1'b0), .out(multiplexer_9_out), .sel(\同步清零_气泡_高电平有效 ));
  Multiplexer #(.select(1), .width(1), .disabled("Z"), .enable("false")) multiplexer_10 (
    .in0(MemtoRegin), .in1(1'b0), .out(multiplexer_10_out), .sel(\同步清零_气泡_高电平有效 ));
  Multiplexer #(.select(1), .width(1), .disabled("Z"), .enable("false")) multiplexer_11 (
    .in0(MemWritein), .in1(1'b0), .out(multiplexer_11_out), .sel(\同步清零_气泡_高电平有效 ));
  Multiplexer #(.select(1), .width(4), .disabled("Z"), .enable("false")) multiplexer_12 (
    .in0(AluOPin), .in1(4'b0000), .out(multiplexer_12_out), .sel(\同步清零_气泡_高电平有效 ));
  Multiplexer #(.select(1), .width(1), .disabled("Z"), .enable("false")) multiplexer_13 (
    .in0(AluSrcBin), .in1(1'b0), .out(multiplexer_13_out), .sel(\同步清零_气泡_高电平有效 ));
  Multiplexer #(.select(1), .width(1), .disabled("Z"), .enable("false")) multiplexer_14 (
    .in0(RegWritein), .in1(1'b0), .out(multiplexer_14_out), .sel(\同步清零_气泡_高电平有效 ));
  Multiplexer #(.select(1), .width(1), .disabled("Z"), .enable("false")) multiplexer_15 (
    .in0(LBin), .in1(1'b0), .out(multiplexer_15_out), .sel(\同步清零_气泡_高电平有效 ));
  Multiplexer #(.select(1), .width(1), .disabled("Z"), .enable("false")) multiplexer_16 (
    .in0(SRLVin), .in1(1'b0), .out(multiplexer_16_out), .sel(\同步清零_气泡_高电平有效 ));
  Multiplexer #(.select(1), .width(1), .disabled("Z"), .enable("false")) multiplexer_17 (
    .in0(Syscallin), .in1(1'b0), .out(multiplexer_17_out), .sel(\同步清零_气泡_高电平有效 ));
  Multiplexer #(.select(1), .width(32), .disabled("Z"), .enable("false")) multiplexer_18 (
    .in0(Rin), .in1({32{1'b0}}), .out(multiplexer_18_out), .sel(\同步清零_气泡_高电平有效 ));
  Multiplexer #(.select(1), .width(32), .disabled("Z"), .enable("false")) multiplexer_19 (
    .in0(MEMin), .in1({32{1'b0}}), .out(multiplexer_19_out), .sel(\同步清零_气泡_高电平有效 ));
  Multiplexer #(.select(1), .width(32), .disabled("Z"), .enable("false")) multiplexer_20 (
    .in0(Ain), .in1({32{1'b0}}), .out(multiplexer_20_out), .sel(\同步清零_气泡_高电平有效 ));
  Multiplexer #(.select(1), .width(32), .disabled("Z"), .enable("false")) multiplexer_21 (
    .in0(Bin), .in1({32{1'b0}}), .out(multiplexer_21_out), .sel(\同步清零_气泡_高电平有效 ));
  Multiplexer #(.select(1), .width(5), .disabled("Z"), .enable("false")) multiplexer_22 (
    .in0(SHAMTin), .in1({5{1'b0}}), .out(multiplexer_22_out), .sel(\同步清零_气泡_高电平有效 ));
  Multiplexer #(.select(1), .width(32), .disabled("Z"), .enable("false")) multiplexer_23 (
    .in0(IMM1in), .in1({32{1'b0}}), .out(multiplexer_23_out), .sel(\同步清零_气泡_高电平有效 ));
  Multiplexer #(.select(1), .width(32), .disabled("Z"), .enable("false")) multiplexer_24 (
    .in0(IMM2in), .in1({32{1'b0}}), .out(multiplexer_24_out), .sel(\同步清零_气泡_高电平有效 ));
  Multiplexer #(.select(1), .width(32), .disabled("Z"), .enable("false")) multiplexer_25 (
    .in0(PCin), .in1({32{1'b0}}), .out(multiplexer_25_out), .sel(\同步清零_气泡_高电平有效 ));
  Multiplexer #(.select(1), .width(32), .disabled("Z"), .enable("false")) multiplexer_26 (
    .in0(IRin), .in1({32{1'b0}}), .out(multiplexer_26_out), .sel(\同步清零_气泡_高电平有效 ));
  Multiplexer #(.select(1), .width(32), .disabled("Z"), .enable("false")) multiplexer_27 (
    .in0(PC4in), .in1({32{1'b0}}), .out(multiplexer_27_out), .sel(\同步清零_气泡_高电平有效 ));
  Multiplexer #(.select(1), .width(5), .disabled("Z"), .enable("false")) multiplexer_28 (
    .in0(WriteReg_in), .in1({5{1'b0}}), .out(multiplexer_28_out), .sel(\同步清零_气泡_高电平有效 ));
  Multiplexer #(.select(1), .width(1), .disabled("Z"), .enable("false")) multiplexer_29 (
    .in0(eqin), .in1(1'b0), .out(multiplexer_29_out), .sel(\同步清零_气泡_高电平有效 ));
  Multiplexer #(.select(1), .width(1), .disabled("Z"), .enable("false")) multiplexer_30 (
    .in0(\传输状态In_表明当前传输数据有效 ), .in1(1'b0), .out(multiplexer_30_out), .sel(\同步清零_气泡_高电平有效 ));
  Pull_Resistor #(.pull(0)) pull_resistor_1 (.node(\同步清零_气泡_高电平有效 ));
  not not_1 (not_1_out, \使能端_低电平有效_stall_高电平有效 );
  Register #(.width(1), .trigger("rising"), .Select("low")) register_1 (
    .D(multiplexer_1_out), .en(not_1_out), .Q(ERETout), .clk(CLK), .clr(\异步清零端 ));
  Register #(.width(5), .trigger("rising"), .Select("low")) register_2 (
    .D(multiplexer_2_out), .en(not_1_out), .Q(Rsout), .clk(CLK), .clr(\异步清零端 ));
  Register #(.width(5), .trigger("rising"), .Select("low")) register_3 (
    .D(multiplexer_3_out), .en(not_1_out), .Q(Rtout), .clk(CLK), .clr(\异步清零端 ));
  Register #(.width(1), .trigger("rising"), .Select("low")) register_4 (
    .D(multiplexer_4_out), .en(not_1_out), .Q(JMPout), .clk(CLK), .clr(\异步清零端 ));
  Register #(.width(1), .trigger("rising"), .Select("low")) register_5 (
    .D(multiplexer_5_out), .en(not_1_out), .Q(JALout), .clk(CLK), .clr(\异步清零端 ));
  Register #(.width(1), .trigger("rising"), .Select("low")) register_6 (
    .D(multiplexer_6_out), .en(not_1_out), .Q(JRout), .clk(CLK), .clr(\异步清零端 ));
  Register #(.width(1), .trigger("rising"), .Select("low")) register_7 (
    .D(multiplexer_7_out), .en(not_1_out), .Q(BEQout), .clk(CLK), .clr(\异步清零端 ));
  Register #(.width(1), .trigger("rising"), .Select("low")) register_8 (
    .D(multiplexer_8_out), .en(not_1_out), .Q(BLEZout), .clk(CLK), .clr(\异步清零端 ));
  Register #(.width(1), .trigger("rising"), .Select("low")) register_9 (
    .D(multiplexer_9_out), .en(not_1_out), .Q(BNEout), .clk(CLK), .clr(\异步清零端 ));
  Register #(.width(1), .trigger("rising"), .Select("low")) register_10 (
    .D(multiplexer_10_out), .en(not_1_out), .Q(MemtoRegout), .clk(CLK), .clr(\异步清零端 ));
  Register #(.width(1), .trigger("rising"), .Select("low")) register_11 (
    .D(multiplexer_11_out), .en(not_1_out), .Q(MemWriteout), .clk(CLK), .clr(\异步清零端 ));
  Register #(.width(4), .trigger("rising"), .Select("low")) register_12 (
    .D(multiplexer_12_out), .en(not_1_out), .Q(AluOPout), .clk(CLK), .clr(\异步清零端 ));
  Register #(.width(1), .trigger("rising"), .Select("low")) register_13 (
    .D(multiplexer_13_out), .en(not_1_out), .Q(AluSrcBout), .clk(CLK), .clr(\异步清零端 ));
  Register #(.width(1), .trigger("rising"), .Select("low")) register_14 (
    .D(multiplexer_14_out), .en(not_1_out), .Q(RegWriteout), .clk(CLK), .clr(\异步清零端 ));
  Register #(.width(1), .trigger("rising"), .Select("low")) register_15 (
    .D(multiplexer_15_out), .en(not_1_out), .Q(LBout), .clk(CLK), .clr(\异步清零端 ));
  Register #(.width(1), .trigger("rising"), .Select("low")) register_16 (
    .D(multiplexer_16_out), .en(not_1_out), .Q(SRLVout), .clk(CLK), .clr(\异步清零端 ));
  Register #(.width(1), .trigger("rising"), .Select("low")) register_17 (
    .D(multiplexer_17_out), .en(not_1_out), .Q(Syscallout), .clk(CLK), .clr(\异步清零端 ));
  Register #(.width(32), .trigger("rising"), .Select("low")) register_18 (
    .D(multiplexer_18_out), .en(not_1_out), .Q(Rout), .clk(CLK), .clr(\异步清零端 ));
  Register #(.width(32), .trigger("rising"), .Select("low")) register_19 (
    .D(multiplexer_19_out), .en(not_1_out), .Q(MEMout), .clk(CLK), .clr(\异步清零端 ));
  Register #(.width(32), .trigger("rising"), .Select("low")) register_20 (
    .D(multiplexer_20_out), .en(not_1_out), .Q(Aout), .clk(CLK), .clr(\异步清零端 ));
  Register #(.width(32), .trigger("rising"), .Select("low")) register_21 (
    .D(multiplexer_21_out), .en(not_1_out), .Q(Bout), .clk(CLK), .clr(\异步清零端 ));
  Register #(.width(5), .trigger("rising"), .Select("low")) register_22 (
    .D(multiplexer_22_out), .en(not_1_out), .Q(SHAMTout), .clk(CLK), .clr(\异步清零端 ));
  Register #(.width(32), .trigger("rising"), .Select("low")) register_23 (
    .D(multiplexer_23_out), .en(not_1_out), .Q(IMM1out), .clk(CLK), .clr(\异步清零端 ));
  Register #(.width(32), .trigger("rising"), .Select("low")) register_24 (
    .D(multiplexer_24_out), .en(not_1_out), .Q(IMM2out), .clk(CLK), .clr(\异步清零端 ));
  Register #(.width(32), .trigger("rising"), .Select("low")) register_25 (
    .D(multiplexer_25_out), .en(not_1_out), .Q(PCout), .clk(CLK), .clr(\异步清零端 ));
  Register #(.width(32), .trigger("rising"), .Select("low")) register_26 (
    .D(multiplexer_26_out), .en(not_1_out), .Q(IRout), .clk(CLK), .clr(\异步清零端 ));
  Register #(.width(32), .trigger("rising"), .Select("low")) register_27 (
    .D(multiplexer_27_out), .en(not_1_out), .Q(PC4out), .clk(CLK), .clr(\异步清零端 ));
  Register #(.width(5), .trigger("rising"), .Select("low")) register_28 (
    .D(multiplexer_28_out), .en(not_1_out), .Q(WriteReg_out), .clk(CLK), .clr(\异步清零端 ));
  Register #(.width(1), .trigger("rising"), .Select("low")) register_29 (
    .D(multiplexer_29_out), .en(not_1_out), .Q(eqout), .clk(CLK), .clr(\异步清零端 ));
  Register #(.width(1), .trigger("rising"), .Select("low")) register_30 (
    .D(multiplexer_30_out), .en(not_1_out), .Q(\传输状态Out_表明当前传输数据有效 ), .clk(CLK), .clr(\异步清零端 ));
  Pull_Resistor #(.pull(0)) pull_resistor_2 (.node(not_1_out));
endmodule

// 重定向检测单元
module \重定向检测电路  (
  input  [5:0] OP,
  input  [5:0] FUNC,
  input  [4:0] Rs,
  input  [4:0] Rt,
  input  [4:0] MEM_WriteReg_num,
  input  [4:0] WB_WriteReg_num,
  input  MEM_RegWrite,
  input  WB_RegWrite,
  input  MEM_MemtoReg,
  input  WB_MemtoReg,
  output [1:0] forwardA,
  output [1:0] forwardB
);

  wire \寄存器使用检测_1_rs_used , \寄存器使用检测_1_rt_used ;
  wire [4:0] controlled_buffer_1_out, controlled_buffer_2_out;

  \寄存器使用检测  \u_寄存器使用检测_1  (
    .OP0(OP[0]), .OP1(OP[1]), .OP2(OP[2]), .OP3(OP[3]), .OP4(OP[4]), .OP5(OP[5]), .F0(FUNC[0]), .F1(FUNC[1]),
    .F2(FUNC[2]), .F3(FUNC[3]), .F4(FUNC[4]), .F5(FUNC[5]), .Rs_used(\寄存器使用检测_1_rs_used ),
    .Rt_used(\寄存器使用检测_1_rt_used ));
  assign controlled_buffer_1_out = \寄存器使用检测_1_rs_used  ? Rs : 5'bz;  // Controlled_Buffer controlled_buffer_1
  assign controlled_buffer_2_out = \寄存器使用检测_1_rt_used  ? Rt : 5'bz;  // Controlled_Buffer controlled_buffer_2
  Pull_Resistor #(.pull(0)) pull_resistor_1 (.node(controlled_buffer_1_out));
  Pull_Resistor #(.pull(0)) pull_resistor_2 (.node(controlled_buffer_2_out));
  \数据相关检测  \u_数据相关检测_1  (
    .Rs_Rt(controlled_buffer_1_out), .MEM_RegWrite(MEM_RegWrite), .MEM_WriteReg_num(MEM_WriteReg_num),
    .WB_WriteReg_num(WB_WriteReg_num), .WB_RegWrite(WB_RegWrite), .MEM_MemtoReg(MEM_MemtoReg),
    .WB_MemtoReg(WB_MemtoReg), .forward(forwardA));
  \数据相关检测  \u_数据相关检测_2  (
    .Rs_Rt(controlled_buffer_2_out), .MEM_RegWrite(MEM_RegWrite), .MEM_WriteReg_num(MEM_WriteReg_num),
    .WB_WriteReg_num(WB_WriteReg_num), .WB_RegWrite(WB_RegWrite), .MEM_MemtoReg(MEM_MemtoReg),
    .WB_MemtoReg(WB_MemtoReg), .forward(forwardB));
endmodule

module \寄存器使用检测  (
  input  OP0,
  input  OP1,
  input  OP2,
  input  OP3,
  input  OP4,
  input  OP5,
  input  F0,
  input  F1,
  input  F2,
  input  F3,
  input  F4,
  input  F5,
  output Rs_used,
  output Rt_used
);

  wire and_1_out, and_2_out, and_3_out, and_4_out, and_5_out, and_6_out, and_7_out, and_8_out, and_9_out,
       and_10_out, and_11_out, and_12_out, and_13_out, and_14_out, and_15_out, and_16_out, and_17_out,
       and_18_out, and_19_out, and_20_out, and_21_out, and_22_out, and_23_out, and_24_out, and_25_out,
       and_26_out, and_27_out, and_28_out, and_29_out, not_1_out, not_2_out, not_3_out, not_4_out, not_5_out,
       not_6_out, not_7_out, not_8_out, not_9_out, not_10_out, not_11_out, not_12_out, not_13_out,
       not_14_out, not_15_out, not_16_out, not_17_out, not_18_out, not_19_out, not_20_out, not_21_out,
       not_22_out, not_23_out, not_24_out, not_25_out, not_26_out, not_27_out, not_28_out, not_29_out,
       not_30_out, not_31_out, not_32_out, not_33_out, not_34_out, not_35_out, not_36_out, not_37_out,
       not_38_out, not_39_out, not_40_out, not_41_out, not_42_out, not_43_out, not_44_out, not_45_out,
       not_46_out, not_47_out, not_48_out, not_49_out, not_50_out, not_51_out, not_52_out, not_53_out,
       not_54_out, not_55_out, not_56_out, not_57_out, not_58_out, not_59_out, not_60_out, not_61_out,
       not_62_out, not_63_out, not_64_out, not_65_out, not_66_out, not_67_out, not_68_out, not_69_out,
       not_70_out, not_71_out, not_72_out, not_73_out, not_74_out, not_75_out, not_76_out, not_77_out,
       not_78_out, not_79_out, not_80_out, not_81_out, not_82_out, not_83_out, not_84_out, not_85_out,
       not_86_out, not_87_out, not_88_out, not_89_out, not_90_out, not_91_out, not_92_out, not_93_out,
       not_94_out, not_95_out, not_96_out, not_97_out, not_98_out, not_99_out, not_100_out, not_101_out,
       not_102_out, not_103_out, not_104_out, not_105_out, not_106_out, not_107_out, not_108_out,
       not_109_out, not_110_out, not_111_out, not_112_out, not_113_out, not_114_out, not_115_out,
       not_116_out, not_117_out, not_118_out, not_119_out, not_120_out, not_121_out, not_122_out,
       not_123_out, not_124_out, not_125_out, not_126_out, not_127_out, not_128_out, not_129_out,
       not_130_out, not_131_out, not_132_out, not_133_out, not_134_out, not_135_out, not_136_out,
       not_137_out, not_138_out, not_139_out, not_140_out, not_141_out, not_142_out, not_143_out,
       not_144_out, not_145_out, not_146_out, not_147_out, not_148_out, not_149_out, not_150_out,
       not_151_out, not_152_out, not_153_out, not_154_out, not_155_out, not_156_out, not_157_out,
       not_158_out, not_159_out, not_160_out, not_161_out, not_162_out, not_163_out, not_164_out,
       not_165_out, not_166_out, not_167_out, not_168_out, not_169_out, not_170_out, not_171_out,
       not_172_out, not_173_out, not_174_out, not_175_out, not_176_out, not_177_out, not_178_out,
       not_179_out, not_180_out, not_181_out, not_182_out, not_183_out, not_184_out, not_185_out,
       not_186_out, not_187_out, not_188_out, not_189_out, not_190_out, not_191_out, not_192_out,
       not_193_out, not_194_out, not_195_out, not_196_out, not_197_out, not_198_out, not_199_out,
       not_200_out, not_201_out, not_202_out;

  not not_1 (not_1_out, OP0);
  not not_2 (not_2_out, OP1);
  not not_3 (not_3_out, OP4);
  not not_4 (not_4_out, OP5);
  not not_5 (not_5_out, F1);
  not not_6 (not_6_out, F3);
  not not_7 (not_7_out, F4);
  not not_8 (not_8_out, OP0);
  not not_9 (not_9_out, OP1);
  not not_10 (not_10_out, OP4);
  not not_11 (not_11_out, OP5);
  not not_12 (not_12_out, F0);
  not not_13 (not_13_out, F1);
  not not_14 (not_14_out, F4);
  not not_15 (not_15_out, F5);
  not not_16 (not_16_out, OP0);
  not not_17 (not_17_out, OP1);
  not not_18 (not_18_out, OP4);
  not not_19 (not_19_out, OP5);
  not not_20 (not_20_out, F0);
  not not_21 (not_21_out, F2);
  not not_22 (not_22_out, F4);
  not not_23 (not_23_out, OP0);
  not not_24 (not_24_out, OP1);
  not not_25 (not_25_out, OP4);
  not not_26 (not_26_out, OP5);
  not not_27 (not_27_out, F2);
  not not_28 (not_28_out, F4);
  not not_29 (not_29_out, OP0);
  not not_30 (not_30_out, OP1);
  not not_31 (not_31_out, OP4);
  not not_32 (not_32_out, OP5);
  not not_33 (not_33_out, F0);
  not not_34 (not_34_out, F3);
  not not_35 (not_35_out, F4);
  not not_36 (not_36_out, F5);
  not not_37 (not_37_out, OP0);
  not not_38 (not_38_out, OP1);
  not not_39 (not_39_out, OP4);
  not not_40 (not_40_out, OP5);
  not not_41 (not_41_out, F3);
  not not_42 (not_42_out, F4);
  not not_43 (not_43_out, OP0);
  not not_44 (not_44_out, OP1);
  not not_45 (not_45_out, OP2);
  not not_46 (not_46_out, OP3);
  not not_47 (not_47_out, OP4);
  not not_48 (not_48_out, OP0);
  not not_49 (not_49_out, OP4);
  not not_50 (not_50_out, OP5);
  not not_51 (not_51_out, OP1);
  not not_52 (not_52_out, OP4);
  not not_53 (not_53_out, OP5);
  not not_54 (not_54_out, OP0);
  not not_55 (not_55_out, OP4);
  not not_56 (not_56_out, OP5);
  not not_57 (not_57_out, OP1);
  not not_58 (not_58_out, OP4);
  not not_59 (not_59_out, OP5);
  not not_60 (not_60_out, OP2);
  not not_61 (not_61_out, OP4);
  not not_62 (not_62_out, OP5);
  not not_63 (not_63_out, OP4);
  not not_64 (not_64_out, OP3);
  not not_65 (not_65_out, OP2);
  not not_66 (not_66_out, OP1);
  not not_67 (not_67_out, OP0);
  not not_68 (not_68_out, F5);
  not not_69 (not_69_out, F4);
  not not_70 (not_70_out, F3);
  not not_71 (not_71_out, F2);
  not not_72 (not_72_out, F1);
  not not_73 (not_73_out, F0);
  not not_74 (not_74_out, OP5);
  not not_75 (not_75_out, OP4);
  not not_76 (not_76_out, OP3);
  not not_77 (not_77_out, OP2);
  not not_78 (not_78_out, OP1);
  not not_79 (not_79_out, OP0);
  not not_80 (not_80_out, F5);
  not not_81 (not_81_out, F4);
  not not_82 (not_82_out, F3);
  not not_83 (not_83_out, F2);
  not not_84 (not_84_out, OP5);
  not not_85 (not_85_out, OP4);
  not not_86 (not_86_out, OP3);
  not not_87 (not_87_out, OP2);
  not not_88 (not_88_out, OP1);
  not not_89 (not_89_out, OP0);
  not not_90 (not_90_out, F5);
  not not_91 (not_91_out, F4);
  not not_92 (not_92_out, F3);
  not not_93 (not_93_out, F2);
  not not_94 (not_94_out, F0);
  not not_95 (not_95_out, OP5);
  not not_96 (not_96_out, OP4);
  not not_97 (not_97_out, OP3);
  not not_98 (not_98_out, OP2);
  not not_99 (not_99_out, OP1);
  not not_100 (not_100_out, OP0);
  not not_101 (not_101_out, F4);
  not not_102 (not_102_out, F3);
  not not_103 (not_103_out, F2);
  not not_104 (not_104_out, F1);
  not not_105 (not_105_out, F0);
  not not_106 (not_106_out, OP5);
  not not_107 (not_107_out, OP4);
  not not_108 (not_108_out, OP3);
  not not_109 (not_109_out, OP2);
  not not_110 (not_110_out, OP1);
  not not_111 (not_111_out, OP0);
  not not_112 (not_112_out, F4);
  not not_113 (not_113_out, F3);
  not not_114 (not_114_out, F2);
  not not_115 (not_115_out, F1);
  not not_116 (not_116_out, OP5);
  not not_117 (not_117_out, OP4);
  not not_118 (not_118_out, OP3);
  not not_119 (not_119_out, OP2);
  not not_120 (not_120_out, OP1);
  not not_121 (not_121_out, OP0);
  not not_122 (not_122_out, F4);
  not not_123 (not_123_out, F3);
  not not_124 (not_124_out, F2);
  not not_125 (not_125_out, F0);
  not not_126 (not_126_out, OP5);
  not not_127 (not_127_out, OP4);
  not not_128 (not_128_out, OP3);
  not not_129 (not_129_out, OP2);
  not not_130 (not_130_out, OP1);
  not not_131 (not_131_out, OP0);
  not not_132 (not_132_out, F4);
  not not_133 (not_133_out, F3);
  not not_134 (not_134_out, F1);
  not not_135 (not_135_out, F0);
  not not_136 (not_136_out, OP5);
  not not_137 (not_137_out, OP4);
  not not_138 (not_138_out, OP3);
  not not_139 (not_139_out, OP2);
  not not_140 (not_140_out, OP1);
  not not_141 (not_141_out, OP0);
  not not_142 (not_142_out, F4);
  not not_143 (not_143_out, F3);
  not not_144 (not_144_out, F1);
  not not_145 (not_145_out, OP5);
  not not_146 (not_146_out, OP4);
  not not_147 (not_147_out, OP3);
  not not_148 (not_148_out, OP2);
  not not_149 (not_149_out, OP1);
  not not_150 (not_150_out, OP0);
  not not_151 (not_151_out, F4);
  not not_152 (not_152_out, F3);
  not not_153 (not_153_out, OP5);
  not not_154 (not_154_out, OP4);
  not not_155 (not_155_out, OP3);
  not not_156 (not_156_out, OP2);
  not not_157 (not_157_out, OP1);
  not not_158 (not_158_out, OP0);
  not not_159 (not_159_out, F4);
  not not_160 (not_160_out, F2);
  not not_161 (not_161_out, F0);
  not not_162 (not_162_out, OP5);
  not not_163 (not_163_out, OP4);
  not not_164 (not_164_out, OP3);
  not not_165 (not_165_out, OP2);
  not not_166 (not_166_out, OP1);
  not not_167 (not_167_out, OP0);
  not not_168 (not_168_out, F4);
  not not_169 (not_169_out, F2);
  not not_170 (not_170_out, OP5);
  not not_171 (not_171_out, OP4);
  not not_172 (not_172_out, OP3);
  not not_173 (not_173_out, OP2);
  not not_174 (not_174_out, OP1);
  not not_175 (not_175_out, OP0);
  not not_176 (not_176_out, F5);
  not not_177 (not_177_out, F4);
  not not_178 (not_178_out, F1);
  not not_179 (not_179_out, F0);
  not not_180 (not_180_out, OP5);
  not not_181 (not_181_out, OP4);
  not not_182 (not_182_out, OP3);
  not not_183 (not_183_out, OP1);
  not not_184 (not_184_out, OP0);
  not not_185 (not_185_out, OP5);
  not not_186 (not_186_out, OP4);
  not not_187 (not_187_out, OP3);
  not not_188 (not_188_out, OP1);
  not not_189 (not_189_out, OP4);
  not not_190 (not_190_out, OP2);
  not not_191 (not_191_out, OP5);
  not not_192 (not_192_out, OP4);
  not not_193 (not_193_out, OP3);
  not not_194 (not_194_out, OP2);
  not not_195 (not_195_out, OP1);
  not not_196 (not_196_out, OP0);
  not not_197 (not_197_out, F5);
  not not_198 (not_198_out, F4);
  not not_199 (not_199_out, F3);
  not not_200 (not_200_out, F0);
  not not_201 (not_201_out, OP5);
  not not_202 (not_202_out, OP4);
  and and_1 (and_1_out, not_1_out, not_2_out, not_3_out, not_4_out, not_5_out, not_6_out, not_7_out, F5);
  and and_2 (and_2_out, not_8_out, not_9_out, not_10_out, not_11_out, not_12_out, not_13_out, F3, not_14_out, not_15_out);
  and and_3 (and_3_out, not_16_out, not_17_out, not_18_out, not_19_out, not_20_out, F1, not_21_out, not_22_out, F5);
  and and_4 (and_4_out, not_23_out, not_24_out, not_25_out, not_26_out, F1, not_27_out, F3, not_28_out, F5);
  and and_5 (and_5_out, not_29_out, not_30_out, not_31_out, not_32_out, not_33_out, F1, F2, not_34_out, not_35_out, not_36_out);
  and and_6 (and_6_out, not_37_out, not_38_out, not_39_out, not_40_out, F0, F2, not_41_out, not_42_out, F5);
  and and_7 (and_7_out, not_43_out, not_44_out, not_45_out, not_46_out, not_47_out, OP5);
  and and_8 (and_8_out, not_48_out, OP3, not_49_out, not_50_out);
  and and_9 (and_9_out, not_51_out, OP3, not_52_out, not_53_out);
  and and_10 (and_10_out, not_54_out, OP2, not_55_out, not_56_out);
  and and_11 (and_11_out, not_57_out, OP2, not_58_out, not_59_out);
  and and_12 (and_12_out, OP0, OP1, not_60_out, not_61_out, OP5);
  and and_13 (and_13_out, not_62_out, not_63_out, not_64_out, not_65_out, not_66_out, not_67_out, not_68_out, not_69_out, not_70_out, not_71_out, not_72_out, not_73_out);
  and and_14 (and_14_out, not_74_out, not_75_out, not_76_out, not_77_out, not_78_out, not_79_out, not_80_out, not_81_out, not_82_out, not_83_out, F1, F0);
  and and_15 (and_15_out, not_84_out, not_85_out, not_86_out, not_87_out, not_88_out, not_89_out, not_90_out, not_91_out, not_92_out, not_93_out, F1, not_94_out);
  and and_16 (and_16_out, not_95_out, not_96_out, not_97_out, not_98_out, not_99_out, not_100_out, F5, not_101_out, not_102_out, not_103_out, not_104_out, not_105_out);
  and and_17 (and_17_out, not_106_out, not_107_out, not_108_out, not_109_out, not_110_out, not_111_out, F5, not_112_out, not_113_out, not_114_out, not_115_out, F0);
  and and_18 (and_18_out, not_116_out, not_117_out, not_118_out, not_119_out, not_120_out, not_121_out, F5, not_122_out, not_123_out, not_124_out, F1, not_125_out);
  and and_19 (and_19_out, not_126_out, not_127_out, not_128_out, not_129_out, not_130_out, not_131_out, F5, not_132_out, not_133_out, F2, not_134_out, not_135_out);
  and and_20 (and_20_out, not_136_out, not_137_out, not_138_out, not_139_out, not_140_out, not_141_out, F5, not_142_out, not_143_out, F2, not_144_out, F0);
  and and_21 (and_21_out, not_145_out, not_146_out, not_147_out, not_148_out, not_149_out, not_150_out, F5, not_151_out, not_152_out, F2, F1, F0);
  and and_22 (and_22_out, not_153_out, not_154_out, not_155_out, not_156_out, not_157_out, not_158_out, F5, not_159_out, F3, not_160_out, F1, not_161_out);
  and and_23 (and_23_out, not_162_out, not_163_out, not_164_out, not_165_out, not_166_out, not_167_out, F5, not_168_out, F3, not_169_out, F1, F0);
  and and_24 (and_24_out, not_170_out, not_171_out, not_172_out, not_173_out, not_174_out, not_175_out, not_176_out, not_177_out, F3, F2, not_178_out, not_179_out);
  and and_25 (and_25_out, not_180_out, not_181_out, not_182_out, OP2, not_183_out, not_184_out);
  and and_26 (and_26_out, not_185_out, not_186_out, not_187_out, OP2, not_188_out, OP0);
  and and_27 (and_27_out, OP5, not_189_out, OP3, not_190_out, OP1, OP0);
  and and_28 (and_28_out, not_191_out, not_192_out, not_193_out, not_194_out, not_195_out, not_196_out, not_197_out, not_198_out, not_199_out, F2, F1, not_200_out);
  and and_29 (and_29_out, not_201_out, not_202_out, OP3, OP2, OP1, OP0);
  or or_1 (Rs_used, and_1_out, and_2_out, and_3_out, and_4_out, and_5_out, and_6_out, and_7_out, and_8_out, and_9_out, and_10_out, and_11_out, and_12_out);
  or or_2 (Rt_used, and_13_out, and_14_out, and_15_out, and_16_out, and_17_out, and_18_out, and_19_out, and_20_out, and_21_out, and_22_out, and_23_out, and_24_out, and_25_out, and_26_out, and_27_out, and_28_out, and_29_out);
endmodule

module \数据相关检测  (
  input  [4:0] Rs_Rt,
  input  MEM_RegWrite,
  input  [4:0] MEM_WriteReg_num,
  input  MEM_MemtoReg,
  input  WB_MemtoReg,
  input  [4:0] WB_WriteReg_num,
  input  WB_RegWrite,
  output [1:0] forward
);

  wire and_4_out, and_5_out, comparator_1_eq, comparator_2_eq, comparator_3_eq, comparator_4_eq, out1, out2;

  Comparator #(.width(5), .mode("unsigned")) comparator_1 (
    .a(Rs_Rt), .b(MEM_WriteReg_num), .eq(comparator_1_eq));  // open: gt, lt
  Comparator #(.width(5), .mode("unsigned")) comparator_2 (
    .a(Rs_Rt), .b(WB_WriteReg_num), .eq(comparator_2_eq));  // open: gt, lt
  Comparator #(.width(5), .mode("unsigned")) comparator_3 (
    .a(MEM_WriteReg_num), .b({5{1'b0}}), .eq(comparator_3_eq));  // open: gt, lt
  Comparator #(.width(5), .mode("unsigned")) comparator_4 (
    .a(WB_WriteReg_num), .b({5{1'b0}}), .eq(comparator_4_eq));  // open: gt, lt
  and and_1 (out1, comparator_1_eq, ~comparator_3_eq, MEM_RegWrite);  // AND_Gate
  and and_2 (out2, comparator_2_eq, ~comparator_4_eq, WB_RegWrite);  // AND_Gate
  and and_3 (forward[1], ~out1, out2);  // AND_Gate
  and and_4 (and_4_out, ~out1, out2, WB_MemtoReg);  // AND_Gate
  and and_5 (and_5_out, ~MEM_MemtoReg, out1);  // AND_Gate
  or or_1 (forward[0], and_4_out, and_5_out);

  // Notes on the sheet:
  //   f1=out2*~out1
  //   F0=~out1*out2*wm+out1*~mm
endmodule

// load-use检测单元
module \load_use检测电路  (
  input  [5:0] ID_OP,
  input  [5:0] ID_FUNC,
  input  [4:0] ID_Rt,
  input  [4:0] EX_WriteReg_num,
  input  [4:0] ID_Rs,
  input  [5:0] EX_OP,
  output load_use
);

  wire and_1_out, and_2_out, comparator_1_eq, comparator_2_eq, comparator_3_eq, comparator_4_eq, or_1_out,
       or_2_out, \寄存器使用检测_1_rs_used , \寄存器使用检测_1_rt_used ;

  \寄存器使用检测  \u_寄存器使用检测_1  (
    .OP0(ID_OP[0]), .OP1(ID_OP[1]), .OP2(ID_OP[2]), .OP3(ID_OP[3]), .OP4(ID_OP[4]), .OP5(ID_OP[5]),
    .F0(ID_FUNC[0]), .F1(ID_FUNC[1]), .F2(ID_FUNC[2]), .F3(ID_FUNC[3]), .F4(ID_FUNC[4]), .F5(ID_FUNC[5]),
    .Rs_used(\寄存器使用检测_1_rs_used ), .Rt_used(\寄存器使用检测_1_rt_used ));
  Comparator #(.width(5), .mode("unsigned")) comparator_1 (
    .a(ID_Rt), .b(EX_WriteReg_num), .eq(comparator_1_eq));  // open: gt, lt
  Comparator #(.width(5), .mode("unsigned")) comparator_2 (
    .a(EX_WriteReg_num), .b(ID_Rs), .eq(comparator_2_eq));  // open: gt, lt
  Comparator #(.width(6), .mode("unsigned")) comparator_3 (
    .a(EX_OP), .b(6'b100000), .eq(comparator_3_eq));  // open: gt, lt
  Comparator #(.width(6), .mode("unsigned")) comparator_4 (
    .a(EX_OP), .b(6'b100011), .eq(comparator_4_eq));  // open: gt, lt
  and and_1 (and_1_out, \寄存器使用检测_1_rt_used , comparator_1_eq);
  and and_2 (and_2_out, \寄存器使用检测_1_rs_used , comparator_2_eq);
  or or_1 (or_1_out, comparator_3_eq, comparator_4_eq);
  or or_2 (or_2_out, and_1_out, and_2_out);
  and and_3 (load_use, or_2_out, or_1_out);
endmodule

// 重定向流水线控制器
module \CPU控制器  (
  input  [5:0] OP,
  input  [5:0] Func,
  output [3:0] ALU_OP,
  output MemToReg,
  output MemWrite,
  output ALU_SRC,
  output RegWrite,
  output SysCALL,
  output SignedExt,
  output RegDst,
  output Beq,
  output Bne,
  output JR,
  output JMP,
  output JAL,
  output SRLV,
  output LB,
  output BLEZ,
  output ERET,
  output LUI
);

  \运算控制器  \u_运算控制器_1  (
    .OP0(OP[0]), .OP1(OP[1]), .OP2(OP[2]), .OP3(OP[3]), .OP4(OP[4]), .OP5(OP[5]), .F0(Func[0]), .F1(Func[1]),
    .F2(Func[2]), .F3(Func[3]), .F4(Func[4]), .F5(Func[5]), .S0(ALU_OP[0]), .S1(ALU_OP[1]), .S2(ALU_OP[2]),
    .S3(ALU_OP[3]));
  \控制信号  \u_控制信号_1  (
    .OP0(OP[0]), .OP1(OP[1]), .OP2(OP[2]), .MemtoReg(MemToReg), .OP3(OP[3]), .OP4(OP[4]), .OP5(OP[5]),
    .MemWrite(MemWrite), .F0(Func[0]), .F1(Func[1]), .F2(Func[2]), .F3(Func[3]), .F4(Func[4]), .F5(Func[5]),
    .ALU_SRC(ALU_SRC), .RegWrite(RegWrite), .SYSCALL(SysCALL), .SignedExt(SignedExt), .RegDst(RegDst),
    .BEQ(Beq), .BNE(Bne), .JR(JR), .JMP(JMP), .JAL(JAL), .SRLV(SRLV), .LB(LB), .BLEZ(BLEZ), .ERET(ERET),
    .LUI(LUI));

  // Other names for the same wires on the sheet: OP_CODE[5:0] = OP

  // Notes on the sheet:
  //   控制信号生成，产生数据通路需要的其他控制信号
  //   运算器控制器，根据指令生成运算器功能选择信号
endmodule

module \运算控制器  (
  input  OP0,
  input  OP1,
  input  OP2,
  input  OP3,
  input  OP4,
  input  OP5,
  input  F0,
  input  F1,
  input  F2,
  input  F3,
  input  F4,
  input  F5,
  output S0,
  output S1,
  output S2,
  output S3
);

  wire and_1_out, and_2_out, and_3_out, and_4_out, and_5_out, and_6_out, and_7_out, and_8_out, and_9_out,
       and_10_out, and_11_out, and_12_out, and_13_out, and_14_out, and_15_out, and_16_out, and_17_out,
       and_18_out, and_19_out, and_20_out, and_21_out, and_22_out, and_23_out, and_24_out, and_25_out,
       and_26_out, and_27_out, and_28_out, and_29_out, and_30_out, and_31_out, and_32_out, and_33_out,
       and_34_out, and_35_out, and_36_out, and_37_out, and_38_out, and_39_out, and_40_out, and_41_out,
       and_42_out, and_43_out, and_44_out, not_1_out, not_2_out, not_3_out, not_4_out, not_5_out, not_6_out,
       not_7_out, not_8_out, not_9_out, not_10_out, not_11_out, not_12_out, not_13_out, not_14_out,
       not_15_out, not_16_out, not_17_out, not_18_out, not_19_out, not_20_out, not_21_out, not_22_out,
       not_23_out, not_24_out, not_25_out, not_26_out, not_27_out, not_28_out, not_29_out, not_30_out,
       not_31_out, not_32_out, not_33_out, not_34_out, not_35_out, not_36_out, not_37_out, not_38_out,
       not_39_out, not_40_out, not_41_out, not_42_out, not_43_out, not_44_out, not_45_out, not_46_out,
       not_47_out, not_48_out, not_49_out, not_50_out, not_51_out, not_52_out, not_53_out, not_54_out,
       not_55_out, not_56_out, not_57_out, not_58_out, not_59_out, not_60_out, not_61_out, not_62_out,
       not_63_out, not_64_out, not_65_out, not_66_out, not_67_out, not_68_out, not_69_out, not_70_out,
       not_71_out, not_72_out, not_73_out, not_74_out, not_75_out, not_76_out, not_77_out, not_78_out,
       not_79_out, not_80_out, not_81_out, not_82_out, not_83_out, not_84_out, not_85_out, not_86_out,
       not_87_out, not_88_out, not_89_out, not_90_out, not_91_out, not_92_out, not_93_out, not_94_out,
       not_95_out, not_96_out, not_97_out, not_98_out, not_99_out, not_100_out, not_101_out, not_102_out,
       not_103_out, not_104_out, not_105_out, not_106_out, not_107_out, not_108_out, not_109_out,
       not_110_out, not_111_out, not_112_out, not_113_out, not_114_out, not_115_out, not_116_out,
       not_117_out, not_118_out, not_119_out, not_120_out, not_121_out, not_122_out, not_123_out,
       not_124_out, not_125_out, not_126_out, not_127_out, not_128_out, not_129_out, not_130_out,
       not_131_out, not_132_out, not_133_out, not_134_out, not_135_out, not_136_out, not_137_out,
       not_138_out, not_139_out, not_140_out, not_141_out, not_142_out, not_143_out, not_144_out,
       not_145_out, not_146_out, not_147_out, not_148_out, not_149_out, not_150_out, not_151_out,
       not_152_out, not_153_out, not_154_out, not_155_out, not_156_out, not_157_out, not_158_out,
       not_159_out, not_160_out, not_161_out, not_162_out, not_163_out, not_164_out, not_165_out,
       not_166_out, not_167_out, not_168_out, not_169_out, not_170_out, not_171_out, not_172_out,
       not_173_out, not_174_out, not_175_out, not_176_out, not_177_out, not_178_out, not_179_out,
       not_180_out, not_181_out, not_182_out, not_183_out, not_184_out, not_185_out, not_186_out,
       not_187_out, not_188_out, not_189_out, not_190_out, not_191_out, not_192_out, not_193_out,
       not_194_out, not_195_out, not_196_out, not_197_out, not_198_out, not_199_out, not_200_out,
       not_201_out, not_202_out, not_203_out, not_204_out, not_205_out, not_206_out, not_207_out,
       not_208_out, not_209_out, not_210_out, not_211_out, not_212_out, not_213_out, not_214_out,
       not_215_out, not_216_out, not_217_out, not_218_out, not_219_out, not_220_out, not_221_out,
       not_222_out, not_223_out, not_224_out, not_225_out, not_226_out, not_227_out, not_228_out,
       not_229_out, not_230_out, not_231_out, not_232_out, not_233_out, not_234_out, not_235_out,
       not_236_out, not_237_out, not_238_out, not_239_out, not_240_out, not_241_out, not_242_out,
       not_243_out, not_244_out, not_245_out, not_246_out, not_247_out, not_248_out, not_249_out,
       not_250_out, not_251_out, not_252_out, not_253_out, not_254_out, not_255_out, not_256_out,
       not_257_out, not_258_out, not_259_out, not_260_out, not_261_out, not_262_out, not_263_out,
       not_264_out, not_265_out, not_266_out, not_267_out, not_268_out, not_269_out, not_270_out,
       not_271_out, not_272_out, not_273_out, not_274_out, not_275_out, not_276_out, not_277_out, not_278_out;

  not not_1 (not_1_out, OP5);
  not not_2 (not_2_out, OP4);
  not not_3 (not_3_out, OP3);
  not not_4 (not_4_out, OP2);
  not not_5 (not_5_out, OP1);
  not not_6 (not_6_out, OP0);
  not not_7 (not_7_out, F5);
  not not_8 (not_8_out, F4);
  not not_9 (not_9_out, F3);
  not not_10 (not_10_out, F2);
  not not_11 (not_11_out, OP5);
  not not_12 (not_12_out, OP4);
  not not_13 (not_13_out, OP3);
  not not_14 (not_14_out, OP2);
  not not_15 (not_15_out, OP1);
  not not_16 (not_16_out, OP0);
  not not_17 (not_17_out, F4);
  not not_18 (not_18_out, F3);
  not not_19 (not_19_out, F2);
  not not_20 (not_20_out, F1);
  not not_21 (not_21_out, F0);
  not not_22 (not_22_out, OP5);
  not not_23 (not_23_out, OP4);
  not not_24 (not_24_out, OP3);
  not not_25 (not_25_out, OP2);
  not not_26 (not_26_out, OP1);
  not not_27 (not_27_out, OP0);
  not not_28 (not_28_out, F4);
  not not_29 (not_29_out, F3);
  not not_30 (not_30_out, F2);
  not not_31 (not_31_out, F1);
  not not_32 (not_32_out, OP5);
  not not_33 (not_33_out, OP4);
  not not_34 (not_34_out, OP3);
  not not_35 (not_35_out, OP2);
  not not_36 (not_36_out, OP1);
  not not_37 (not_37_out, OP0);
  not not_38 (not_38_out, F4);
  not not_39 (not_39_out, F3);
  not not_40 (not_40_out, F1);
  not not_41 (not_41_out, F0);
  not not_42 (not_42_out, OP5);
  not not_43 (not_43_out, OP4);
  not not_44 (not_44_out, OP3);
  not not_45 (not_45_out, OP2);
  not not_46 (not_46_out, OP1);
  not not_47 (not_47_out, OP0);
  not not_48 (not_48_out, F4);
  not not_49 (not_49_out, F2);
  not not_50 (not_50_out, F0);
  not not_51 (not_51_out, OP5);
  not not_52 (not_52_out, OP4);
  not not_53 (not_53_out, OP2);
  not not_54 (not_54_out, OP1);
  not not_55 (not_55_out, OP0);
  not not_56 (not_56_out, OP5);
  not not_57 (not_57_out, OP4);
  not not_58 (not_58_out, OP1);
  not not_59 (not_59_out, OP0);
  not not_60 (not_60_out, OP5);
  not not_61 (not_61_out, OP4);
  not not_62 (not_62_out, OP2);
  not not_63 (not_63_out, OP1);
  not not_64 (not_64_out, OP5);
  not not_65 (not_65_out, OP4);
  not not_66 (not_66_out, OP2);
  not not_67 (not_67_out, OP0);
  not not_68 (not_68_out, OP4);
  not not_69 (not_69_out, OP3);
  not not_70 (not_70_out, OP2);
  not not_71 (not_71_out, OP4);
  not not_72 (not_72_out, OP2);
  not not_73 (not_73_out, OP5);
  not not_74 (not_74_out, OP4);
  not not_75 (not_75_out, OP0);
  not not_76 (not_76_out, OP4);
  not not_77 (not_77_out, OP3);
  not not_78 (not_78_out, OP2);
  not not_79 (not_79_out, OP1);
  not not_80 (not_80_out, OP0);
  not not_81 (not_81_out, OP5);
  not not_82 (not_82_out, OP4);
  not not_83 (not_83_out, OP3);
  not not_84 (not_84_out, OP0);
  not not_85 (not_85_out, OP5);
  not not_86 (not_86_out, OP4);
  not not_87 (not_87_out, OP5);
  not not_88 (not_88_out, OP4);
  not not_89 (not_89_out, OP3);
  not not_90 (not_90_out, OP2);
  not not_91 (not_91_out, OP1);
  not not_92 (not_92_out, OP0);
  not not_93 (not_93_out, F5);
  not not_94 (not_94_out, F4);
  not not_95 (not_95_out, F3);
  not not_96 (not_96_out, F2);
  not not_97 (not_97_out, F0);
  not not_98 (not_98_out, OP5);
  not not_99 (not_99_out, OP4);
  not not_100 (not_100_out, OP3);
  not not_101 (not_101_out, OP2);
  not not_102 (not_102_out, OP1);
  not not_103 (not_103_out, OP0);
  not not_104 (not_104_out, F4);
  not not_105 (not_105_out, F3);
  not not_106 (not_106_out, F2);
  not not_107 (not_107_out, F0);
  not not_108 (not_108_out, OP5);
  not not_109 (not_109_out, OP4);
  not not_110 (not_110_out, OP3);
  not not_111 (not_111_out, OP2);
  not not_112 (not_112_out, OP1);
  not not_113 (not_113_out, OP0);
  not not_114 (not_114_out, F4);
  not not_115 (not_115_out, F3);
  not not_116 (not_116_out, F1);
  not not_117 (not_117_out, F0);
  not not_118 (not_118_out, OP5);
  not not_119 (not_119_out, OP4);
  not not_120 (not_120_out, OP3);
  not not_121 (not_121_out, OP2);
  not not_122 (not_122_out, OP1);
  not not_123 (not_123_out, OP0);
  not not_124 (not_124_out, F4);
  not not_125 (not_125_out, F3);
  not not_126 (not_126_out, OP5);
  not not_127 (not_127_out, OP4);
  not not_128 (not_128_out, OP3);
  not not_129 (not_129_out, OP2);
  not not_130 (not_130_out, OP1);
  not not_131 (not_131_out, OP0);
  not not_132 (not_132_out, F4);
  not not_133 (not_133_out, F2);
  not not_134 (not_134_out, F0);
  not not_135 (not_135_out, OP5);
  not not_136 (not_136_out, OP4);
  not not_137 (not_137_out, OP1);
  not not_138 (not_138_out, OP0);
  not not_139 (not_139_out, OP5);
  not not_140 (not_140_out, OP4);
  not not_141 (not_141_out, OP2);
  not not_142 (not_142_out, OP0);
  not not_143 (not_143_out, OP5);
  not not_144 (not_144_out, OP4);
  not not_145 (not_145_out, OP3);
  not not_146 (not_146_out, OP2);
  not not_147 (not_147_out, OP1);
  not not_148 (not_148_out, OP0);
  not not_149 (not_149_out, F5);
  not not_150 (not_150_out, F4);
  not not_151 (not_151_out, F3);
  not not_152 (not_152_out, F0);
  not not_153 (not_153_out, OP5);
  not not_154 (not_154_out, OP4);
  not not_155 (not_155_out, OP3);
  not not_156 (not_156_out, OP0);
  not not_157 (not_157_out, OP5);
  not not_158 (not_158_out, OP4);
  not not_159 (not_159_out, OP3);
  not not_160 (not_160_out, OP2);
  not not_161 (not_161_out, OP1);
  not not_162 (not_162_out, OP0);
  not not_163 (not_163_out, F4);
  not not_164 (not_164_out, F3);
  not not_165 (not_165_out, F2);
  not not_166 (not_166_out, F1);
  not not_167 (not_167_out, F0);
  not not_168 (not_168_out, OP5);
  not not_169 (not_169_out, OP4);
  not not_170 (not_170_out, OP3);
  not not_171 (not_171_out, OP2);
  not not_172 (not_172_out, OP1);
  not not_173 (not_173_out, OP0);
  not not_174 (not_174_out, F4);
  not not_175 (not_175_out, F3);
  not not_176 (not_176_out, F2);
  not not_177 (not_177_out, F1);
  not not_178 (not_178_out, OP5);
  not not_179 (not_179_out, OP4);
  not not_180 (not_180_out, OP3);
  not not_181 (not_181_out, OP2);
  not not_182 (not_182_out, OP1);
  not not_183 (not_183_out, OP0);
  not not_184 (not_184_out, F4);
  not not_185 (not_185_out, F3);
  not not_186 (not_186_out, F2);
  not not_187 (not_187_out, F0);
  not not_188 (not_188_out, OP5);
  not not_189 (not_189_out, OP4);
  not not_190 (not_190_out, OP3);
  not not_191 (not_191_out, OP2);
  not not_192 (not_192_out, OP1);
  not not_193 (not_193_out, OP0);
  not not_194 (not_194_out, F4);
  not not_195 (not_195_out, F3);
  not not_196 (not_196_out, F1);
  not not_197 (not_197_out, F0);
  not not_198 (not_198_out, OP5);
  not not_199 (not_199_out, OP4);
  not not_200 (not_200_out, OP3);
  not not_201 (not_201_out, OP2);
  not not_202 (not_202_out, OP1);
  not not_203 (not_203_out, OP0);
  not not_204 (not_204_out, F4);
  not not_205 (not_205_out, F2);
  not not_206 (not_206_out, OP5);
  not not_207 (not_207_out, OP4);
  not not_208 (not_208_out, OP2);
  not not_209 (not_209_out, OP1);
  not not_210 (not_210_out, OP0);
  not not_211 (not_211_out, OP5);
  not not_212 (not_212_out, OP4);
  not not_213 (not_213_out, OP1);
  not not_214 (not_214_out, OP0);
  not not_215 (not_215_out, OP5);
  not not_216 (not_216_out, OP4);
  not not_217 (not_217_out, OP2);
  not not_218 (not_218_out, OP1);
  not not_219 (not_219_out, OP4);
  not not_220 (not_220_out, OP3);
  not not_221 (not_221_out, OP2);
  not not_222 (not_222_out, OP4);
  not not_223 (not_223_out, OP2);
  not not_224 (not_224_out, OP4);
  not not_225 (not_225_out, OP3);
  not not_226 (not_226_out, OP2);
  not not_227 (not_227_out, OP1);
  not not_228 (not_228_out, OP0);
  not not_229 (not_229_out, OP5);
  not not_230 (not_230_out, OP4);
  not not_231 (not_231_out, OP5);
  not not_232 (not_232_out, OP4);
  not not_233 (not_233_out, OP3);
  not not_234 (not_234_out, OP2);
  not not_235 (not_235_out, OP1);
  not not_236 (not_236_out, OP0);
  not not_237 (not_237_out, F4);
  not not_238 (not_238_out, F3);
  not not_239 (not_239_out, F1);
  not not_240 (not_240_out, OP5);
  not not_241 (not_241_out, OP4);
  not not_242 (not_242_out, OP3);
  not not_243 (not_243_out, OP2);
  not not_244 (not_244_out, OP1);
  not not_245 (not_245_out, OP0);
  not not_246 (not_246_out, F4);
  not not_247 (not_247_out, F3);
  not not_248 (not_248_out, OP5);
  not not_249 (not_249_out, OP4);
  not not_250 (not_250_out, OP3);
  not not_251 (not_251_out, OP2);
  not not_252 (not_252_out, OP1);
  not not_253 (not_253_out, OP0);
  not not_254 (not_254_out, F4);
  not not_255 (not_255_out, F2);
  not not_256 (not_256_out, F0);
  not not_257 (not_257_out, OP5);
  not not_258 (not_258_out, OP4);
  not not_259 (not_259_out, OP3);
  not not_260 (not_260_out, OP2);
  not not_261 (not_261_out, OP1);
  not not_262 (not_262_out, OP0);
  not not_263 (not_263_out, F4);
  not not_264 (not_264_out, F2);
  not not_265 (not_265_out, OP5);
  not not_266 (not_266_out, OP4);
  not not_267 (not_267_out, OP2);
  not not_268 (not_268_out, OP0);
  not not_269 (not_269_out, OP5);
  not not_270 (not_270_out, OP4);
  not not_271 (not_271_out, OP1);
  not not_272 (not_272_out, OP5);
  not not_273 (not_273_out, OP4);
  not not_274 (not_274_out, OP0);
  not not_275 (not_275_out, OP5);
  not not_276 (not_276_out, OP4);
  not not_277 (not_277_out, OP3);
  not not_278 (not_278_out, OP0);
  and and_1 (and_1_out, not_1_out, not_2_out, not_3_out, not_4_out, not_5_out, not_6_out, not_7_out, not_8_out, not_9_out, not_10_out, F1, F0);
  and and_2 (and_2_out, not_11_out, not_12_out, not_13_out, not_14_out, not_15_out, not_16_out, F5, not_17_out, not_18_out, not_19_out, not_20_out, not_21_out);
  and and_3 (and_3_out, not_22_out, not_23_out, not_24_out, not_25_out, not_26_out, not_27_out, F5, not_28_out, not_29_out, not_30_out, not_31_out, F0);
  and and_4 (and_4_out, not_32_out, not_33_out, not_34_out, not_35_out, not_36_out, not_37_out, F5, not_38_out, not_39_out, F2, not_40_out, not_41_out);
  and and_5 (and_5_out, not_42_out, not_43_out, not_44_out, not_45_out, not_46_out, not_47_out, F5, not_48_out, F3, not_49_out, F1, not_50_out);
  and and_6 (and_6_out, not_51_out, not_52_out, OP3, not_53_out, not_54_out, not_55_out);
  and and_7 (and_7_out, not_56_out, not_57_out, OP3, OP2, not_58_out, not_59_out);
  and and_8 (and_8_out, not_60_out, not_61_out, OP3, not_62_out, not_63_out, OP0);
  and and_9 (and_9_out, not_64_out, not_65_out, OP3, not_66_out, OP1, not_67_out);
  and and_10 (and_10_out, OP5, not_68_out, not_69_out, not_70_out, OP1, OP0);
  and and_11 (and_11_out, OP5, not_71_out, OP3, not_72_out, OP1, OP0);
  and and_12 (and_12_out, not_73_out, not_74_out, OP3, OP2, OP1, not_75_out);
  and and_13 (and_13_out, OP5, not_76_out, not_77_out, not_78_out, not_79_out, not_80_out);
  and and_14 (and_14_out, not_81_out, not_82_out, not_83_out, OP2, OP1, not_84_out);
  and and_15 (and_15_out, not_85_out, not_86_out, OP3, OP2, OP1, OP0);
  and and_16 (and_16_out, not_87_out, not_88_out, not_89_out, not_90_out, not_91_out, not_92_out, not_93_out, not_94_out, not_95_out, not_96_out, F1, not_97_out);
  and and_17 (and_17_out, not_98_out, not_99_out, not_100_out, not_101_out, not_102_out, not_103_out, F5, not_104_out, not_105_out, not_106_out, F1, not_107_out);
  and and_18 (and_18_out, not_108_out, not_109_out, not_110_out, not_111_out, not_112_out, not_113_out, F5, not_114_out, not_115_out, F2, not_116_out, not_117_out);
  and and_19 (and_19_out, not_118_out, not_119_out, not_120_out, not_121_out, not_122_out, not_123_out, F5, not_124_out, not_125_out, F2, F1, F0);
  and and_20 (and_20_out, not_126_out, not_127_out, not_128_out, not_129_out, not_130_out, not_131_out, F5, not_132_out, F3, not_133_out, F1, not_134_out);
  and and_21 (and_21_out, not_135_out, not_136_out, OP3, OP2, not_137_out, not_138_out);
  and and_22 (and_22_out, not_139_out, not_140_out, OP3, not_141_out, OP1, not_142_out);
  and and_23 (and_23_out, not_143_out, not_144_out, not_145_out, not_146_out, not_147_out, not_148_out, not_149_out, not_150_out, not_151_out, F2, F1, not_152_out);
  and and_24 (and_24_out, not_153_out, not_154_out, not_155_out, OP2, OP1, not_156_out);
  and and_25 (and_25_out, not_157_out, not_158_out, not_159_out, not_160_out, not_161_out, not_162_out, F5, not_163_out, not_164_out, not_165_out, not_166_out, not_167_out);
  and and_26 (and_26_out, not_168_out, not_169_out, not_170_out, not_171_out, not_172_out, not_173_out, F5, not_174_out, not_175_out, not_176_out, not_177_out, F0);
  and and_27 (and_27_out, not_178_out, not_179_out, not_180_out, not_181_out, not_182_out, not_183_out, F5, not_184_out, not_185_out, not_186_out, F1, not_187_out);
  and and_28 (and_28_out, not_188_out, not_189_out, not_190_out, not_191_out, not_192_out, not_193_out, F5, not_194_out, not_195_out, F2, not_196_out, not_197_out);
  and and_29 (and_29_out, not_198_out, not_199_out, not_200_out, not_201_out, not_202_out, not_203_out, F5, not_204_out, F3, not_205_out, F1, F0);
  and and_30 (and_30_out, not_206_out, not_207_out, OP3, not_208_out, not_209_out, not_210_out);
  and and_31 (and_31_out, not_211_out, not_212_out, OP3, OP2, not_213_out, not_214_out);
  and and_32 (and_32_out, not_215_out, not_216_out, OP3, not_217_out, not_218_out, OP0);
  and and_33 (and_33_out, OP5, not_219_out, not_220_out, not_221_out, OP1, OP0);
  and and_34 (and_34_out, OP5, not_222_out, OP3, not_223_out, OP1, OP0);
  and and_35 (and_35_out, OP5, not_224_out, not_225_out, not_226_out, not_227_out, not_228_out);
  and and_36 (and_36_out, not_229_out, not_230_out, OP3, OP2, OP1, OP0);
  and and_37 (and_37_out, not_231_out, not_232_out, not_233_out, not_234_out, not_235_out, not_236_out, F5, not_237_out, not_238_out, F2, not_239_out, F0);
  and and_38 (and_38_out, not_240_out, not_241_out, not_242_out, not_243_out, not_244_out, not_245_out, F5, not_246_out, not_247_out, F2, F1, F0);
  and and_39 (and_39_out, not_248_out, not_249_out, not_250_out, not_251_out, not_252_out, not_253_out, F5, not_254_out, F3, not_255_out, F1, not_256_out);
  and and_40 (and_40_out, not_257_out, not_258_out, not_259_out, not_260_out, not_261_out, not_262_out, F5, not_263_out, F3, not_264_out, F1, F0);
  and and_41 (and_41_out, not_265_out, not_266_out, OP3, not_267_out, OP1, not_268_out);
  and and_42 (and_42_out, not_269_out, not_270_out, OP3, OP2, not_271_out, OP0);
  and and_43 (and_43_out, not_272_out, not_273_out, OP3, OP2, OP1, not_274_out);
  and and_44 (and_44_out, not_275_out, not_276_out, not_277_out, OP2, OP1, not_278_out);
  or or_1 (S1, and_16_out, and_17_out, and_18_out, and_19_out, and_20_out, and_21_out, and_22_out, and_23_out, and_24_out);
  or or_2 (S3, and_37_out, and_38_out, and_39_out, and_40_out, and_41_out, and_42_out, and_43_out, and_44_out);
  or or_3 (S0, and_1_out, and_2_out, and_3_out, and_4_out, and_5_out, and_6_out, and_7_out, and_8_out, and_9_out, and_10_out, and_11_out, and_12_out, and_13_out, and_14_out, and_15_out);
  or or_4 (S2, and_25_out, and_26_out, and_27_out, and_28_out, and_29_out, and_30_out, and_31_out, and_32_out, and_33_out, and_34_out, and_35_out, and_36_out);
endmodule

module \控制信号  (
  input  OP0,
  input  OP1,
  input  OP2,
  input  OP3,
  input  OP4,
  input  OP5,
  input  F0,
  input  F1,
  input  F2,
  input  F3,
  input  F4,
  input  F5,
  output MemtoReg,
  output MemWrite,
  output ALU_SRC,
  output RegWrite,
  output SYSCALL,
  output SignedExt,
  output RegDst,
  output BEQ,
  output BNE,
  output JR,
  output JMP,
  output JAL,
  output SRLV,
  output LB,
  output BLEZ,
  output ERET,
  output LUI
);

  wire and_1_out, and_2_out, and_4_out, and_5_out, and_6_out, and_7_out, and_8_out, and_9_out, and_10_out,
       and_11_out, and_12_out, and_13_out, and_14_out, and_15_out, and_16_out, and_17_out, and_18_out,
       and_19_out, and_20_out, and_21_out, and_22_out, and_23_out, and_24_out, and_25_out, and_26_out,
       and_27_out, and_28_out, and_29_out, and_30_out, and_31_out, and_32_out, and_33_out, and_34_out,
       and_35_out, and_36_out, and_38_out, and_39_out, and_40_out, and_41_out, and_42_out, and_43_out,
       and_44_out, and_45_out, not_1_out, not_2_out, not_3_out, not_4_out, not_5_out, not_6_out, not_7_out,
       not_8_out, not_9_out, not_10_out, not_11_out, not_12_out, not_13_out, not_14_out, not_15_out,
       not_16_out, not_17_out, not_18_out, not_19_out, not_20_out, not_21_out, not_22_out, not_23_out,
       not_24_out, not_25_out, not_26_out, not_27_out, not_28_out, not_29_out, not_30_out, not_31_out,
       not_32_out, not_33_out, not_34_out, not_35_out, not_36_out, not_37_out, not_38_out, not_39_out,
       not_40_out, not_41_out, not_42_out, not_43_out, not_44_out, not_45_out, not_46_out, not_47_out,
       not_48_out, not_49_out, not_50_out, not_51_out, not_52_out, not_53_out, not_54_out, not_55_out,
       not_56_out, not_57_out, not_58_out, not_59_out, not_60_out, not_61_out, not_62_out, not_63_out,
       not_64_out, not_65_out, not_66_out, not_67_out, not_68_out, not_69_out, not_70_out, not_71_out,
       not_72_out, not_73_out, not_74_out, not_75_out, not_76_out, not_77_out, not_78_out, not_79_out,
       not_80_out, not_81_out, not_82_out, not_83_out, not_84_out, not_85_out, not_86_out, not_87_out,
       not_88_out, not_89_out, not_90_out, not_91_out, not_92_out, not_93_out, not_94_out, not_95_out,
       not_96_out, not_97_out, not_98_out, not_99_out, not_100_out, not_101_out, not_102_out, not_103_out,
       not_104_out, not_105_out, not_106_out, not_107_out, not_108_out, not_109_out, not_110_out,
       not_111_out, not_112_out, not_113_out, not_114_out, not_115_out, not_116_out, not_117_out,
       not_118_out, not_119_out, not_120_out, not_121_out, not_122_out, not_123_out, not_124_out,
       not_125_out, not_126_out, not_127_out, not_128_out, not_129_out, not_130_out, not_131_out,
       not_132_out, not_133_out, not_134_out, not_135_out, not_136_out, not_137_out, not_138_out,
       not_139_out, not_140_out, not_141_out, not_142_out, not_143_out, not_144_out, not_145_out,
       not_146_out, not_147_out, not_148_out, not_149_out, not_150_out, not_151_out, not_152_out,
       not_153_out, not_154_out, not_155_out, not_156_out, not_157_out, not_158_out, not_159_out,
       not_160_out, not_161_out, not_162_out, not_163_out, not_164_out, not_165_out, not_166_out,
       not_167_out, not_168_out, not_169_out, not_170_out, not_171_out, not_172_out, not_173_out,
       not_174_out, not_175_out, not_176_out, not_177_out, not_178_out, not_179_out, not_180_out,
       not_181_out, not_182_out, not_183_out, not_184_out, not_185_out, not_186_out, not_187_out,
       not_188_out, not_189_out, not_190_out, not_191_out, not_192_out, not_193_out, not_194_out,
       not_195_out, not_196_out, not_197_out, not_198_out, not_199_out, not_200_out, not_201_out,
       not_202_out, not_203_out, not_204_out, not_205_out, not_206_out, not_207_out, not_208_out,
       not_209_out, not_210_out, not_211_out, not_212_out, not_213_out, not_214_out, not_215_out,
       not_216_out, not_217_out, not_218_out, not_219_out, not_220_out, not_221_out, not_222_out,
       not_223_out, not_224_out, not_225_out, not_226_out, not_227_out, not_228_out, not_229_out,
       not_230_out, not_231_out, not_232_out, not_233_out, not_234_out, not_235_out, not_236_out,
       not_237_out, not_238_out, not_239_out, not_240_out, not_241_out, not_242_out, not_243_out,
       not_244_out, not_245_out, not_246_out, not_247_out, not_248_out, not_249_out, not_250_out,
       not_251_out, not_252_out, not_253_out, not_254_out, not_255_out, not_256_out, not_257_out,
       not_258_out, not_259_out, not_260_out, not_261_out, not_262_out, not_263_out, not_264_out,
       not_265_out, not_266_out, not_267_out, not_268_out, not_269_out, not_270_out, not_271_out,
       not_272_out, not_273_out, not_274_out, not_275_out, not_276_out, not_277_out, not_278_out,
       not_279_out, not_280_out, not_281_out, not_282_out, not_283_out, not_284_out, not_285_out,
       not_286_out, not_287_out, not_288_out, not_289_out, not_290_out, not_291_out, not_292_out,
       not_293_out, not_294_out, not_295_out, not_296_out, not_297_out, not_298_out, not_299_out,
       not_300_out, not_301_out, not_302_out, not_303_out, not_304_out, not_305_out, not_306_out,
       not_307_out, not_308_out, not_309_out, not_310_out, not_311_out, not_312_out, not_313_out,
       not_314_out, not_315_out, not_316_out, not_317_out, not_318_out, not_319_out, not_320_out,
       not_321_out, not_322_out, not_323_out, not_324_out, not_325_out, not_326_out, not_327_out,
       not_328_out, not_329_out, not_330_out, not_331_out, not_332_out, not_333_out, not_334_out,
       not_335_out, not_336_out, not_337_out, not_338_out, not_339_out, not_340_out;

  not not_1 (not_1_out, OP0);
  not not_2 (not_2_out, OP1);
  not not_3 (not_3_out, OP2);
  not not_4 (not_4_out, OP3);
  not not_5 (not_5_out, OP4);
  not not_6 (not_6_out, OP2);
  not not_7 (not_7_out, OP3);
  not not_8 (not_8_out, OP4);
  not not_9 (not_9_out, OP2);
  not not_10 (not_10_out, OP4);
  not not_11 (not_11_out, OP5);
  not not_12 (not_12_out, OP4);
  not not_13 (not_13_out, OP3);
  not not_14 (not_14_out, OP2);
  not not_15 (not_15_out, OP1);
  not not_16 (not_16_out, OP0);
  not not_17 (not_17_out, F5);
  not not_18 (not_18_out, F4);
  not not_19 (not_19_out, F1);
  not not_20 (not_20_out, F0);
  not not_21 (not_21_out, OP5);
  not not_22 (not_22_out, OP4);
  not not_23 (not_23_out, OP2);
  not not_24 (not_24_out, OP1);
  not not_25 (not_25_out, OP0);
  not not_26 (not_26_out, OP5);
  not not_27 (not_27_out, OP4);
  not not_28 (not_28_out, OP1);
  not not_29 (not_29_out, OP0);
  not not_30 (not_30_out, OP5);
  not not_31 (not_31_out, OP4);
  not not_32 (not_32_out, OP2);
  not not_33 (not_33_out, OP1);
  not not_34 (not_34_out, OP5);
  not not_35 (not_35_out, OP4);
  not not_36 (not_36_out, OP2);
  not not_37 (not_37_out, OP0);
  not not_38 (not_38_out, OP5);
  not not_39 (not_39_out, OP4);
  not not_40 (not_40_out, OP1);
  not not_41 (not_41_out, OP4);
  not not_42 (not_42_out, OP3);
  not not_43 (not_43_out, OP2);
  not not_44 (not_44_out, OP4);
  not not_45 (not_45_out, OP2);
  not not_46 (not_46_out, OP5);
  not not_47 (not_47_out, OP4);
  not not_48 (not_48_out, OP0);
  not not_49 (not_49_out, OP4);
  not not_50 (not_50_out, OP3);
  not not_51 (not_51_out, OP2);
  not not_52 (not_52_out, OP1);
  not not_53 (not_53_out, OP0);
  not not_54 (not_54_out, OP5);
  not not_55 (not_55_out, OP4);
  not not_56 (not_56_out, OP5);
  not not_57 (not_57_out, OP4);
  not not_58 (not_58_out, OP3);
  not not_59 (not_59_out, OP2);
  not not_60 (not_60_out, OP1);
  not not_61 (not_61_out, OP0);
  not not_62 (not_62_out, F5);
  not not_63 (not_63_out, F4);
  not not_64 (not_64_out, F3);
  not not_65 (not_65_out, F2);
  not not_66 (not_66_out, F1);
  not not_67 (not_67_out, F0);
  not not_68 (not_68_out, OP5);
  not not_69 (not_69_out, OP4);
  not not_70 (not_70_out, OP3);
  not not_71 (not_71_out, OP2);
  not not_72 (not_72_out, OP1);
  not not_73 (not_73_out, OP0);
  not not_74 (not_74_out, F5);
  not not_75 (not_75_out, F4);
  not not_76 (not_76_out, F3);
  not not_77 (not_77_out, F2);
  not not_78 (not_78_out, OP5);
  not not_79 (not_79_out, OP4);
  not not_80 (not_80_out, OP3);
  not not_81 (not_81_out, OP2);
  not not_82 (not_82_out, OP1);
  not not_83 (not_83_out, OP0);
  not not_84 (not_84_out, F5);
  not not_85 (not_85_out, F4);
  not not_86 (not_86_out, F3);
  not not_87 (not_87_out, F2);
  not not_88 (not_88_out, F0);
  not not_89 (not_89_out, OP5);
  not not_90 (not_90_out, OP4);
  not not_91 (not_91_out, OP3);
  not not_92 (not_92_out, OP2);
  not not_93 (not_93_out, OP1);
  not not_94 (not_94_out, OP0);
  not not_95 (not_95_out, F4);
  not not_96 (not_96_out, F3);
  not not_97 (not_97_out, F2);
  not not_98 (not_98_out, F1);
  not not_99 (not_99_out, F0);
  not not_100 (not_100_out, OP5);
  not not_101 (not_101_out, OP4);
  not not_102 (not_102_out, OP3);
  not not_103 (not_103_out, OP2);
  not not_104 (not_104_out, OP1);
  not not_105 (not_105_out, OP0);
  not not_106 (not_106_out, F4);
  not not_107 (not_107_out, F3);
  not not_108 (not_108_out, F2);
  not not_109 (not_109_out, F1);
  not not_110 (not_110_out, OP5);
  not not_111 (not_111_out, OP4);
  not not_112 (not_112_out, OP3);
  not not_113 (not_113_out, OP2);
  not not_114 (not_114_out, OP1);
  not not_115 (not_115_out, OP0);
  not not_116 (not_116_out, F4);
  not not_117 (not_117_out, F3);
  not not_118 (not_118_out, F2);
  not not_119 (not_119_out, F0);
  not not_120 (not_120_out, OP5);
  not not_121 (not_121_out, OP4);
  not not_122 (not_122_out, OP3);
  not not_123 (not_123_out, OP2);
  not not_124 (not_124_out, OP1);
  not not_125 (not_125_out, OP0);
  not not_126 (not_126_out, F4);
  not not_127 (not_127_out, F3);
  not not_128 (not_128_out, F1);
  not not_129 (not_129_out, F0);
  not not_130 (not_130_out, OP5);
  not not_131 (not_131_out, OP4);
  not not_132 (not_132_out, OP3);
  not not_133 (not_133_out, OP2);
  not not_134 (not_134_out, OP1);
  not not_135 (not_135_out, OP0);
  not not_136 (not_136_out, F4);
  not not_137 (not_137_out, F3);
  not not_138 (not_138_out, F1);
  not not_139 (not_139_out, OP5);
  not not_140 (not_140_out, OP4);
  not not_141 (not_141_out, OP3);
  not not_142 (not_142_out, OP2);
  not not_143 (not_143_out, OP1);
  not not_144 (not_144_out, OP0);
  not not_145 (not_145_out, F4);
  not not_146 (not_146_out, F3);
  not not_147 (not_147_out, OP5);
  not not_148 (not_148_out, OP4);
  not not_149 (not_149_out, OP3);
  not not_150 (not_150_out, OP2);
  not not_151 (not_151_out, OP1);
  not not_152 (not_152_out, OP0);
  not not_153 (not_153_out, F4);
  not not_154 (not_154_out, F2);
  not not_155 (not_155_out, F0);
  not not_156 (not_156_out, OP5);
  not not_157 (not_157_out, OP4);
  not not_158 (not_158_out, OP3);
  not not_159 (not_159_out, OP2);
  not not_160 (not_160_out, OP1);
  not not_161 (not_161_out, OP0);
  not not_162 (not_162_out, F4);
  not not_163 (not_163_out, F2);
  not not_164 (not_164_out, OP5);
  not not_165 (not_165_out, OP4);
  not not_166 (not_166_out, OP3);
  not not_167 (not_167_out, OP2);
  not not_168 (not_168_out, OP5);
  not not_169 (not_169_out, OP4);
  not not_170 (not_170_out, OP2);
  not not_171 (not_171_out, OP1);
  not not_172 (not_172_out, OP0);
  not not_173 (not_173_out, OP5);
  not not_174 (not_174_out, OP4);
  not not_175 (not_175_out, OP1);
  not not_176 (not_176_out, OP0);
  not not_177 (not_177_out, OP5);
  not not_178 (not_178_out, OP4);
  not not_179 (not_179_out, OP2);
  not not_180 (not_180_out, OP1);
  not not_181 (not_181_out, OP5);
  not not_182 (not_182_out, OP4);
  not not_183 (not_183_out, OP2);
  not not_184 (not_184_out, OP0);
  not not_185 (not_185_out, OP5);
  not not_186 (not_186_out, OP4);
  not not_187 (not_187_out, OP1);
  not not_188 (not_188_out, OP4);
  not not_189 (not_189_out, OP3);
  not not_190 (not_190_out, OP2);
  not not_191 (not_191_out, OP5);
  not not_192 (not_192_out, OP4);
  not not_193 (not_193_out, OP3);
  not not_194 (not_194_out, OP2);
  not not_195 (not_195_out, OP1);
  not not_196 (not_196_out, OP0);
  not not_197 (not_197_out, F5);
  not not_198 (not_198_out, F4);
  not not_199 (not_199_out, F3);
  not not_200 (not_200_out, F0);
  not not_201 (not_201_out, OP5);
  not not_202 (not_202_out, OP4);
  not not_203 (not_203_out, OP0);
  not not_204 (not_204_out, OP4);
  not not_205 (not_205_out, OP3);
  not not_206 (not_206_out, OP2);
  not not_207 (not_207_out, OP1);
  not not_208 (not_208_out, OP0);
  not not_209 (not_209_out, OP5);
  not not_210 (not_210_out, OP4);
  not not_211 (not_211_out, OP0);
  not not_212 (not_212_out, OP1);
  not not_213 (not_213_out, OP2);
  not not_214 (not_214_out, OP3);
  not not_215 (not_215_out, OP4);
  not not_216 (not_216_out, OP5);
  not not_217 (not_217_out, F0);
  not not_218 (not_218_out, F1);
  not not_219 (not_219_out, F4);
  not not_220 (not_220_out, F5);
  not not_221 (not_221_out, OP0);
  not not_222 (not_222_out, OP4);
  not not_223 (not_223_out, OP5);
  not not_224 (not_224_out, OP1);
  not not_225 (not_225_out, OP4);
  not not_226 (not_226_out, OP5);
  not not_227 (not_227_out, OP0);
  not not_228 (not_228_out, OP1);
  not not_229 (not_229_out, OP2);
  not not_230 (not_230_out, OP3);
  not not_231 (not_231_out, OP4);
  not not_232 (not_232_out, OP5);
  not not_233 (not_233_out, F0);
  not not_234 (not_234_out, F2);
  not not_235 (not_235_out, F3);
  not not_236 (not_236_out, F4);
  not not_237 (not_237_out, OP0);
  not not_238 (not_238_out, OP1);
  not not_239 (not_239_out, OP2);
  not not_240 (not_240_out, OP3);
  not not_241 (not_241_out, OP4);
  not not_242 (not_242_out, OP5);
  not not_243 (not_243_out, F1);
  not not_244 (not_244_out, F3);
  not not_245 (not_245_out, F4);
  not not_246 (not_246_out, OP0);
  not not_247 (not_247_out, OP1);
  not not_248 (not_248_out, OP2);
  not not_249 (not_249_out, OP3);
  not not_250 (not_250_out, OP4);
  not not_251 (not_251_out, OP5);
  not not_252 (not_252_out, F0);
  not not_253 (not_253_out, F3);
  not not_254 (not_254_out, F4);
  not not_255 (not_255_out, F5);
  not not_256 (not_256_out, OP0);
  not not_257 (not_257_out, OP1);
  not not_258 (not_258_out, OP2);
  not not_259 (not_259_out, OP3);
  not not_260 (not_260_out, OP4);
  not not_261 (not_261_out, OP5);
  not not_262 (not_262_out, F2);
  not not_263 (not_263_out, F3);
  not not_264 (not_264_out, F4);
  not not_265 (not_265_out, F5);
  not not_266 (not_266_out, OP0);
  not not_267 (not_267_out, OP1);
  not not_268 (not_268_out, OP2);
  not not_269 (not_269_out, OP3);
  not not_270 (not_270_out, OP4);
  not not_271 (not_271_out, OP5);
  not not_272 (not_272_out, F2);
  not not_273 (not_273_out, F4);
  not not_274 (not_274_out, OP0);
  not not_275 (not_275_out, OP1);
  not not_276 (not_276_out, OP2);
  not not_277 (not_277_out, OP3);
  not not_278 (not_278_out, OP4);
  not not_279 (not_279_out, OP5);
  not not_280 (not_280_out, F3);
  not not_281 (not_281_out, F4);
  not not_282 (not_282_out, OP0);
  not not_283 (not_283_out, OP1);
  not not_284 (not_284_out, OP3);
  not not_285 (not_285_out, OP4);
  not not_286 (not_286_out, OP5);
  not not_287 (not_287_out, OP1);
  not not_288 (not_288_out, OP3);
  not not_289 (not_289_out, OP4);
  not not_290 (not_290_out, OP5);
  not not_291 (not_291_out, OP0);
  not not_292 (not_292_out, OP1);
  not not_293 (not_293_out, OP2);
  not not_294 (not_294_out, OP3);
  not not_295 (not_295_out, OP4);
  not not_296 (not_296_out, OP5);
  not not_297 (not_297_out, F0);
  not not_298 (not_298_out, F1);
  not not_299 (not_299_out, F2);
  not not_300 (not_300_out, F4);
  not not_301 (not_301_out, F5);
  not not_302 (not_302_out, OP0);
  not not_303 (not_303_out, OP2);
  not not_304 (not_304_out, OP3);
  not not_305 (not_305_out, OP4);
  not not_306 (not_306_out, OP5);
  not not_307 (not_307_out, OP2);
  not not_308 (not_308_out, OP3);
  not not_309 (not_309_out, OP4);
  not not_310 (not_310_out, OP5);
  not not_311 (not_311_out, OP0);
  not not_312 (not_312_out, OP1);
  not not_313 (not_313_out, OP2);
  not not_314 (not_314_out, OP3);
  not not_315 (not_315_out, OP4);
  not not_316 (not_316_out, OP5);
  not not_317 (not_317_out, F0);
  not not_318 (not_318_out, F3);
  not not_319 (not_319_out, F4);
  not not_320 (not_320_out, F5);
  not not_321 (not_321_out, OP0);
  not not_322 (not_322_out, OP1);
  not not_323 (not_323_out, OP2);
  not not_324 (not_324_out, OP3);
  not not_325 (not_325_out, OP4);
  not not_326 (not_326_out, OP0);
  not not_327 (not_327_out, OP3);
  not not_328 (not_328_out, OP4);
  not not_329 (not_329_out, OP5);
  not not_330 (not_330_out, OP0);
  not not_331 (not_331_out, OP1);
  not not_332 (not_332_out, OP2);
  not not_333 (not_333_out, OP3);
  not not_334 (not_334_out, OP5);
  not not_335 (not_335_out, F0);
  not not_336 (not_336_out, F1);
  not not_337 (not_337_out, F2);
  not not_338 (not_338_out, F5);
  not not_339 (not_339_out, OP5);
  not not_340 (not_340_out, OP4);
  and and_1 (and_1_out, not_1_out, not_2_out, not_3_out, not_4_out, not_5_out, OP5);
  and and_2 (and_2_out, OP0, OP1, not_6_out, not_7_out, not_8_out, OP5);
  and and_3 (MemWrite, OP0, OP1, not_9_out, OP3, not_10_out, OP5);
  and and_4 (and_4_out, not_11_out, not_12_out, not_13_out, not_14_out, not_15_out, not_16_out, not_17_out, not_18_out, F3, F2, not_19_out, not_20_out);
  and and_5 (and_5_out, not_21_out, not_22_out, OP3, not_23_out, not_24_out, not_25_out);
  and and_6 (and_6_out, not_26_out, not_27_out, OP3, OP2, not_28_out, not_29_out);
  and and_7 (and_7_out, not_30_out, not_31_out, OP3, not_32_out, not_33_out, OP0);
  and and_8 (and_8_out, not_34_out, not_35_out, OP3, not_36_out, OP1, not_37_out);
  and and_9 (and_9_out, not_38_out, not_39_out, OP3, OP2, not_40_out, OP0);
  and and_10 (and_10_out, OP5, not_41_out, not_42_out, not_43_out, OP1, OP0);
  and and_11 (and_11_out, OP5, not_44_out, OP3, not_45_out, OP1, OP0);
  and and_12 (and_12_out, not_46_out, not_47_out, OP3, OP2, OP1, not_48_out);
  and and_13 (and_13_out, OP5, not_49_out, not_50_out, not_51_out, not_52_out, not_53_out);
  and and_14 (and_14_out, not_54_out, not_55_out, OP3, OP2, OP1, OP0);
  and and_15 (and_15_out, not_56_out, not_57_out, not_58_out, not_59_out, not_60_out, not_61_out, not_62_out, not_63_out, not_64_out, not_65_out, not_66_out, not_67_out);
  and and_16 (and_16_out, not_68_out, not_69_out, not_70_out, not_71_out, not_72_out, not_73_out, not_74_out, not_75_out, not_76_out, not_77_out, F1, F0);
  and and_17 (and_17_out, not_78_out, not_79_out, not_80_out, not_81_out, not_82_out, not_83_out, not_84_out, not_85_out, not_86_out, not_87_out, F1, not_88_out);
  and and_18 (and_18_out, not_89_out, not_90_out, not_91_out, not_92_out, not_93_out, not_94_out, F5, not_95_out, not_96_out, not_97_out, not_98_out, not_99_out);
  and and_19 (and_19_out, not_100_out, not_101_out, not_102_out, not_103_out, not_104_out, not_105_out, F5, not_106_out, not_107_out, not_108_out, not_109_out, F0);
  and and_20 (and_20_out, not_110_out, not_111_out, not_112_out, not_113_out, not_114_out, not_115_out, F5, not_116_out, not_117_out, not_118_out, F1, not_119_out);
  and and_21 (and_21_out, not_120_out, not_121_out, not_122_out, not_123_out, not_124_out, not_125_out, F5, not_126_out, not_127_out, F2, not_128_out, not_129_out);
  and and_22 (and_22_out, not_130_out, not_131_out, not_132_out, not_133_out, not_134_out, not_135_out, F5, not_136_out, not_137_out, F2, not_138_out, F0);
  and and_23 (and_23_out, not_139_out, not_140_out, not_141_out, not_142_out, not_143_out, not_144_out, F5, not_145_out, not_146_out, F2, F1, F0);
  and and_24 (and_24_out, not_147_out, not_148_out, not_149_out, not_150_out, not_151_out, not_152_out, F5, not_153_out, F3, not_154_out, F1, not_155_out);
  and and_25 (and_25_out, not_156_out, not_157_out, not_158_out, not_159_out, not_160_out, not_161_out, F5, not_162_out, F3, not_163_out, F1, F0);
  and and_26 (and_26_out, not_164_out, not_165_out, not_166_out, not_167_out, OP1, OP0);
  and and_27 (and_27_out, not_168_out, not_169_out, OP3, not_170_out, not_171_out, not_172_out);
  and and_28 (and_28_out, not_173_out, not_174_out, OP3, OP2, not_175_out, not_176_out);
  and and_29 (and_29_out, not_177_out, not_178_out, OP3, not_179_out, not_180_out, OP0);
  and and_30 (and_30_out, not_181_out, not_182_out, OP3, not_183_out, OP1, not_184_out);
  and and_31 (and_31_out, not_185_out, not_186_out, OP3, OP2, not_187_out, OP0);
  and and_32 (and_32_out, OP5, not_188_out, not_189_out, not_190_out, OP1, OP0);
  and and_33 (and_33_out, not_191_out, not_192_out, not_193_out, not_194_out, not_195_out, not_196_out, not_197_out, not_198_out, not_199_out, F2, F1, not_200_out);
  and and_34 (and_34_out, not_201_out, not_202_out, OP3, OP2, OP1, not_203_out);
  and and_35 (and_35_out, OP5, not_204_out, not_205_out, not_206_out, not_207_out, not_208_out);
  and and_36 (and_36_out, not_209_out, not_210_out, OP3, OP2, OP1, OP0);
  and and_37 (SYSCALL, not_211_out, not_212_out, not_213_out, not_214_out, not_215_out, not_216_out, not_217_out, not_218_out, F2, F3, not_219_out, not_220_out);
  and and_38 (and_38_out, not_221_out, OP2, OP3, not_222_out, not_223_out);
  or or_1 (SignedExt, and_38_out, and_39_out);
  and and_39 (and_39_out, OP0, not_224_out, OP3, not_225_out, not_226_out);
  and and_40 (and_40_out, not_227_out, not_228_out, not_229_out, not_230_out, not_231_out, not_232_out, not_233_out, not_234_out, not_235_out, not_236_out);
  and and_41 (and_41_out, not_237_out, not_238_out, not_239_out, not_240_out, not_241_out, not_242_out, not_243_out, not_244_out, not_245_out, F5);
  and and_42 (and_42_out, not_246_out, not_247_out, not_248_out, not_249_out, not_250_out, not_251_out, not_252_out, F1, not_253_out, not_254_out, not_255_out);
  and and_43 (and_43_out, not_256_out, not_257_out, not_258_out, not_259_out, not_260_out, not_261_out, F1, not_262_out, not_263_out, not_264_out, not_265_out);
  and and_44 (and_44_out, not_266_out, not_267_out, not_268_out, not_269_out, not_270_out, not_271_out, F1, not_272_out, F3, not_273_out, F5);
  and and_45 (and_45_out, not_274_out, not_275_out, not_276_out, not_277_out, not_278_out, not_279_out, F0, F2, not_280_out, not_281_out, F5);
  and and_46 (BEQ, not_282_out, not_283_out, OP2, not_284_out, not_285_out, not_286_out);
  and and_47 (BNE, OP0, not_287_out, OP2, not_288_out, not_289_out, not_290_out);
  and and_48 (JR, not_291_out, not_292_out, not_293_out, not_294_out, not_295_out, not_296_out, not_297_out, not_298_out, not_299_out, F3, not_300_out, not_301_out);
  and and_49 (JMP, not_302_out, OP1, not_303_out, not_304_out, not_305_out, not_306_out);
  and and_50 (JAL, OP0, OP1, not_307_out, not_308_out, not_309_out, not_310_out);
  and and_51 (SRLV, not_311_out, not_312_out, not_313_out, not_314_out, not_315_out, not_316_out, not_317_out, F1, F2, not_318_out, not_319_out, not_320_out);
  and and_52 (LB, not_321_out, not_322_out, not_323_out, not_324_out, not_325_out, OP5);
  and and_53 (BLEZ, not_326_out, OP1, OP2, not_327_out, not_328_out, not_329_out);
  and and_54 (ERET, not_330_out, not_331_out, not_332_out, not_333_out, OP4, not_334_out, not_335_out, not_336_out, not_337_out, F3, F4, not_338_out);
  and and_55 (LUI, not_339_out, not_340_out, OP3, OP2, OP1, OP0);
  or or_2 (MemtoReg, and_1_out, and_2_out);
  or or_3 (ALU_SRC, and_4_out, and_5_out, and_6_out, and_7_out, and_8_out, and_9_out, and_10_out, and_11_out, and_12_out, and_13_out, and_14_out);
  or or_4 (RegDst, and_40_out, and_41_out, and_42_out, and_43_out, and_44_out, and_45_out);
  or or_5 (RegWrite, and_15_out, and_16_out, and_17_out, and_18_out, and_19_out, and_20_out, and_21_out, and_22_out, and_23_out, and_24_out, and_25_out, and_26_out, and_27_out, and_28_out, and_29_out, and_30_out, and_31_out, and_32_out, and_33_out, and_34_out, and_35_out, and_36_out);
endmodule

module MIPS_ALU (
  input  [4:0] shamt,
  input  [31:0] X,
  input  [31:0] Y,
  input  [3:0] AluOP,
  output Equal,
  output [31:0] Result,
  output [31:0] Result_2
);

  wire [0:0] comparator_1_lt, comparator_2_lt;
  wire [31:0] adder_1_out, AND_out, divider_1_out, divider_1_rem, multiplier_1_cout, multiplier_1_out,
       NOR_out, OR_out, shifter_1_out, shifter_2_out, shifter_3_out, subtractor_1_out, XOR_out;

  assign AND_out = X & Y;  // AND_Gate AND, 32 bits wide
  assign OR_out = X | Y;  // OR_Gate OR, 32 bits wide
  Shifter #(.width(32), .shift("ll")) shifter_1 (.in(Y), .\dist (shamt), .out(shifter_1_out));
  Shifter #(.width(32), .shift("ar")) shifter_2 (.in(Y), .\dist (shamt), .out(shifter_2_out));
  Shifter #(.width(32), .shift("lr")) shifter_3 (.in(Y), .\dist (shamt), .out(shifter_3_out));
  Multiplier #(.width(32)) multiplier_1 (.a(X), .b(Y), .out(multiplier_1_out), .cout(multiplier_1_cout));  // open: cin
  Divider #(.width(32)) divider_1 (.a(X), .b(Y), .out(divider_1_out), .rem(divider_1_rem));  // open: upper
  Adder #(.width(32)) adder_1 (.a(X), .b(Y), .out(adder_1_out));  // open: cin, cout
  Subtractor #(.width(32)) subtractor_1 (.a(X), .b(Y), .out(subtractor_1_out));  // open: bin, bout
  assign XOR_out = X ^ Y;  // XOR_Gate XOR, 32 bits wide
  assign NOR_out = ~(X | Y);  // NOR_Gate NOR, 32 bits wide
  Comparator #(.width(32), .mode("twosComplement")) comparator_1 (
    .a(X), .b(Y), .eq(Equal), .lt(comparator_1_lt[0]));  // open: gt
  Comparator #(.width(32), .mode("unsigned")) comparator_2 (.a(X), .b(Y), .lt(comparator_2_lt[0]));  // open: gt, eq
  Multiplexer #(.select(4), .width(32), .disabled("Z"), .enable("false")) multiplexer_1 (
    .in0(shifter_1_out), .in1(shifter_2_out), .in2(shifter_3_out), .in3(multiplier_1_out),
    .in4(divider_1_out), .in5(adder_1_out), .in6(subtractor_1_out), .in7(AND_out), .in8(OR_out),
    .in9(XOR_out), .in10(NOR_out), .in11({{31{1'b0}}, comparator_1_lt[0]}),
    .in12({{31{1'b0}}, comparator_2_lt[0]}), .in13({32{1'b0}}), .in14({32{1'b0}}), .in15({32{1'b0}}),
    .out(Result), .sel(AluOP));
  Multiplexer #(.select(4), .width(32), .disabled("Z"), .enable("false")) multiplexer_2 (
    .in0({32{1'b0}}), .in1({32{1'b0}}), .in2({32{1'b0}}), .in3(multiplier_1_cout), .in4(divider_1_rem),
    .in5({32{1'b0}}), .in6({32{1'b0}}), .in7({32{1'b0}}), .in8({32{1'b0}}), .in9({32{1'b0}}),
    .in10({32{1'b0}}), .in11({32{1'b0}}), .in12({32{1'b0}}), .in13({32{1'b0}}), .in14({32{1'b0}}),
    .in15({32{1'b0}}), .out(Result_2), .sel(AluOP));

  // Other names for the same wires on the sheet: Result2[31:0] = Result_2; S[3:0] = AluOP

  // Notes on the sheet:
  //   不要改变此引脚区域内容，也不要改变ALU封装形式
  //   输入引脚
  //   输出引脚
endmodule

module MIPS_Regfile (
  input  [31:0] Din,
  input  Clk,
  input  WE,
  input  [4:0] R1_num,
  input  [4:0] W_num,
  input  [4:0] R2_num,
  output [31:0] R1,
  output [31:0] R2
);

  // RegisterFile registerfile_1: pin names not known; wires that end beside it: Din, Clk, WE, W_num, R1_num, R2_num, R1, R2
endmodule
module \中断产生电路  (
  input  CLK,
  input  ERET,
  input  \_1号中断 ,
  input  \_2号中断 ,
  input  \_3号中断 ,
  input  \_4号中断 ,
  input  [31:0] PC,
  input  \_5号中断 ,
  input  [31:0] EX_IR,
  input  \_6号中断 ,
  output \_1号中断等待指示灯 ,
  output INT,
  output \_2号中断等待指示灯 ,
  output [31:0] INT_ADDR,
  output \_3号中断等待指示灯 ,
  output [31:0] EPC,
  output \_4号中断等待指示灯 ,
  output \_5号中断等待指示灯 ,
  output \_6号中断等待指示灯 
);

  wire and_1_out, and_2_out, and_3_out, and_4_out, and_5_out, and_6_out, and_7_out, and_8_out, and_9_out,
       and_10_out, and_11_out, and_12_out, d_ff_1_q, d_ff_2_q, d_ff_3_q, d_ff_4_q, d_ff_5_q, d_ff_6_q, IE,
       INT_en, IR1, IR1CLR, IR2, IR2CLR, IR3, IR3CLR, IR4, IR4CLR, IR5, IR5CLR, IR6, IR6CLR,
       multiplexer_1_out, nIE_q, not_1_out, or_7_out, or_8_out, or_9_out, or_10_out, or_11_out, or_12_out,
       priority_encoder_1_gs;
  wire [2:0] INT_CODE_q, priority_encoder_1_out;

  or or_1 (\_1号中断等待指示灯 , IR1, d_ff_1_q);
  or or_2 (\_2号中断等待指示灯 , IR2, d_ff_2_q);
  or or_3 (\_3号中断等待指示灯 , IR3, d_ff_3_q);
  or or_4 (\_4号中断等待指示灯 , IR4, d_ff_4_q);
  or or_5 (\_5号中断等待指示灯 , IR5, d_ff_5_q);
  or or_6 (\_6号中断等待指示灯 , IR6, d_ff_6_q);
  D_Flip_Flop #(.trigger("rising"), .Pre_Clr_Positions("LEGACY"), .NegatePresetClear("false"), .enable("true"), .NewFFLayout("false")) d_ff_1 (
    .clk(\_1号中断 ), .D(1'b1), .Q(d_ff_1_q), .reset(IR1));  // open: Qn, preset, en
  D_Flip_Flop #(.trigger("rising"), .Pre_Clr_Positions("LEGACY"), .NegatePresetClear("false"), .enable("true"), .NewFFLayout("false")) d_ff_2 (
    .clk(\_2号中断 ), .D(1'b1), .Q(d_ff_2_q), .reset(IR2));  // open: Qn, preset, en
  D_Flip_Flop #(.trigger("rising"), .Pre_Clr_Positions("LEGACY"), .NegatePresetClear("false"), .enable("true"), .NewFFLayout("false")) d_ff_3 (
    .clk(\_3号中断 ), .D(1'b1), .Q(d_ff_3_q), .reset(IR3));  // open: Qn, preset, en
  D_Flip_Flop #(.trigger("rising"), .Pre_Clr_Positions("LEGACY"), .NegatePresetClear("false"), .enable("true"), .NewFFLayout("false")) d_ff_4 (
    .clk(\_4号中断 ), .D(1'b1), .Q(d_ff_4_q), .reset(IR4));  // open: Qn, preset, en
  D_Flip_Flop #(.trigger("rising"), .Pre_Clr_Positions("LEGACY"), .NegatePresetClear("false"), .enable("true"), .NewFFLayout("false")) d_ff_5 (
    .clk(\_5号中断 ), .D(1'b1), .Q(d_ff_5_q), .reset(IR5));  // open: Qn, preset, en
  D_Flip_Flop #(.trigger("rising"), .Pre_Clr_Positions("LEGACY"), .NegatePresetClear("false"), .enable("true"), .NewFFLayout("false")) d_ff_6 (
    .clk(\_6号中断 ), .D(1'b1), .Q(d_ff_6_q), .reset(IR6));  // open: Qn, preset, en
  or or_7 (or_7_out, d_ff_1_q, IR1);
  and and_1 (and_1_out, ERET, IR1CLR);
  or or_8 (or_8_out, d_ff_2_q, IR2);
  and and_2 (and_2_out, ERET, IR2CLR);
  or or_9 (or_9_out, d_ff_3_q, IR3);
  and and_3 (and_3_out, ERET, IR3CLR);
  or or_10 (or_10_out, d_ff_4_q, IR4);
  and and_4 (and_4_out, ERET, IR4CLR);
  or or_11 (or_11_out, d_ff_5_q, IR5);
  and and_5 (and_5_out, ERET, IR5CLR);
  or or_12 (or_12_out, d_ff_6_q, IR6);
  and and_6 (and_6_out, ERET, IR6CLR);
  and and_7 (and_7_out, or_7_out, ~and_1_out);  // AND_Gate
  and and_8 (and_8_out, or_8_out, ~and_2_out);  // AND_Gate
  and and_9 (and_9_out, or_9_out, ~and_3_out);  // AND_Gate
  and and_10 (and_10_out, or_10_out, ~and_4_out);  // AND_Gate
  and and_11 (and_11_out, or_11_out, ~and_5_out);  // AND_Gate
  and and_12 (and_12_out, or_12_out, ~and_6_out);  // AND_Gate
  D_Flip_Flop #(.trigger("rising"), .Pre_Clr_Positions("LEGACY"), .NegatePresetClear("false"), .enable("true"), .NewFFLayout("false")) u_IR1 (
    .clk(CLK), .D(and_7_out), .Q(IR1));  // open: Qn, preset, en, reset
  D_Flip_Flop #(.trigger("rising"), .Pre_Clr_Positions("LEGACY"), .NegatePresetClear("false"), .enable("true"), .NewFFLayout("false")) u_IR2 (
    .clk(CLK), .D(and_8_out), .Q(IR2));  // open: Qn, preset, en, reset
  D_Flip_Flop #(.trigger("rising"), .Pre_Clr_Positions("LEGACY"), .NegatePresetClear("false"), .enable("true"), .NewFFLayout("false")) u_IR3 (
    .clk(CLK), .D(and_9_out), .Q(IR3));  // open: Qn, preset, en, reset
  D_Flip_Flop #(.trigger("rising"), .Pre_Clr_Positions("LEGACY"), .NegatePresetClear("false"), .enable("true"), .NewFFLayout("false")) u_IR4 (
    .clk(CLK), .D(and_10_out), .Q(IR4));  // open: Qn, preset, en, reset
  D_Flip_Flop #(.trigger("rising"), .Pre_Clr_Positions("LEGACY"), .NegatePresetClear("false"), .enable("true"), .NewFFLayout("false")) u_IR5 (
    .clk(CLK), .D(and_11_out), .Q(IR5));  // open: Qn, preset, en, reset
  D_Flip_Flop #(.trigger("rising"), .Pre_Clr_Positions("LEGACY"), .NegatePresetClear("false"), .enable("true"), .NewFFLayout("false")) u_IR6 (
    .clk(CLK), .D(and_12_out), .Q(IR6));  // open: Qn, preset, en, reset
  not not_1 (not_1_out, IE);
  Priority_Encoder #(.select(3), .disabled("Z")) priority_encoder_1 (
    .in0(1'b0), .in1(IR1), .in2(IR2), .in3(IR3), .in4(IR4), .in5(IR5), .in6(IR6),
    .out(priority_encoder_1_out), .gs(priority_encoder_1_gs));  // open: in7, en_out, en_in
  and and_13 (INT, priority_encoder_1_gs, IE, ~INT_en);  // AND_Gate
  Multiplexer #(.select(2), .width(1), .disabled("Z"), .enable("false")) multiplexer_1 (
    .in0(not_1_out), .in1(IE), .in2(1'b0), .in3(1'b0), .out(multiplexer_1_out), .sel({ERET, INT}));
  Pull_Resistor #(.pull(0)) pull_resistor_1 (.node(priority_encoder_1_out));
  not not_2 (IE, nIE_q);
  Register #(.width(1), .trigger("rising"), .Select("low")) nIE (
    .D(multiplexer_1_out), .Q(nIE_q), .clk(CLK));  // open: en, clr
  Comparator #(.width(32), .mode("unsigned")) comparator_1 (.a(EX_IR), .b({32{1'b0}}), .eq(INT_en));  // open: gt, lt
  Multiplexer #(.select(3), .width(32), .disabled("Z"), .enable("false")) multiplexer_2 (
    .in1(32'h40000c), .in2(32'h400038), .in3(32'h400064), .in4(32'h400090), .in5(32'h4000bc),
    .in6(32'h4000e8), .out(INT_ADDR), .sel(priority_encoder_1_out));  // open: in0, in7
  Register #(.width(3), .trigger("rising"), .Select("low")) INT_CODE (
    .D(priority_encoder_1_out), .en(IE), .Q(INT_CODE_q), .clk(CLK));  // open: clr
  Decoder #(.select(3), .tristate("false"), .disabled("Z"), .enable("false")) decoder_1 (
    .out1(IR1CLR), .out2(IR2CLR), .out3(IR3CLR), .out4(IR4CLR), .out5(IR5CLR), .out6(IR6CLR), .sel(INT_CODE_q));  // open: out0, out7
  Register #(.width(32), .trigger("rising"), .Select("low")) u_EPC (.D(PC), .en(IE), .Q(EPC), .clk(CLK));  // open: clr

  // Notes on the sheet:
  //   Reset 
  //   Reset 
  //   Reset 
  //   Reset 
  //   Reset 
  //   Reset 
endmodule
